// Logisim project cpu24+4-重定向流水线+动态分支预测.circ as structural Verilog: 26 circuits, main circuit ◇单周期MIPS
module \单周期MIPS  (
  input  IR1,
  input  IR2,
  input  IR3,
  output RegWrite,
  output MemWrite,
  output [31:0] PC,
  output [31:0] IR,
  output [31:0] RDin,
  output [31:0] MDin,
  output [31:0] LedData
);

  wire and_3_out, and_4_out, and_5_out, Branch, CLK, clock_2_out, comparator_1_eq, comparator_2_eq,
       comparator_2_lt, comparator_3_eq, comparator_3_lt, d_ff_1_q, Go, Halt, IR1_t, IR2_t, IR3_t, IRA, IRB,
       IRC, JAL, JMP, JR, LedOut, mips_alu_1_equal, nand_1_out, not_1_out, or_4_out, SignedExt, Syscall, W1,
       W2, W3, \单周期硬布线控制器_1_alu_src , \单周期硬布线控制器_1_beq , \单周期硬布线控制器_1_blez , \单周期硬布线控制器_1_bne ,
       \单周期硬布线控制器_1_lh , \单周期硬布线控制器_1_lui , \单周期硬布线控制器_1_memtoreg , \单周期硬布线控制器_1_regdst ;
  wire [3:0] \单周期硬布线控制器_1_alu_op ;
  wire [4:0] multiplexer_4_out, multiplexer_5_out, multiplexer_6_out, multiplexer_8_out;
  wire [12:0] CNT_num;
  wire [15:0] adder_1_out, multiplexer_14_out, register_1_q, \总周期数 ;
  wire [31:0] adder_3_out, adder_4_out, bit_extender_1_out, bit_extender_2_out, bit_extender_3_out,
       mips_alu_1_result, multiplexer_1_out, multiplexer_2_out, multiplexer_3_out, multiplexer_9_out,
       multiplexer_10_out, multiplexer_11_out, multiplexer_12_out, multiplexer_13_out, ram_1_data,
       shifter_1_out, shifter_2_out, v0;

  Clock #(.highDuration(1), .lowDuration(1)) clock_1 ();  // open: out
  Button _1 (.out(IRA));
  Button _2 (.out(IRB));
  Button _3 (.out(IRC));
  Button \u_继续运行  (.out(Go));
  LED #(.active("true")) led_1 (.in(W1));
  LED #(.active("true")) led_2 (.in(W2));
  LED #(.active("true")) led_3 (.in(W3));
  Hex_Digit_Display hex_digit_display_1 (.value(LedData[31:28]));  // open: dp
  Register #(.width(16), .trigger("rising"), .Select("low")) register_1 (
    .D(adder_1_out), .Q(register_1_q), .clk(CLK));  // open: en, clr
  Multiplexer #(.select(1), .width(32), .disabled("Z"), .enable("false")) multiplexer_1 (
    .in0(adder_3_out), .in1(adder_4_out), .out(multiplexer_1_out), .sel(Branch));
  Hex_Digit_Display hex_digit_display_2 (.value(LedData[23:20]));  // open: dp
  Hex_Digit_Display hex_digit_display_3 (.value(LedData[27:24]));  // open: dp
  Multiplexer #(.select(1), .width(32), .disabled("Z"), .enable("false")) multiplexer_2 (
    .in0(multiplexer_1_out), .in1({PC[31:28], IR[25:0], 2'b00}), .out(multiplexer_2_out), .sel(JMP));
  Multiplexer #(.select(1), .width(32), .disabled("Z"), .enable("false")) multiplexer_3 (
    .in0(multiplexer_2_out), .in1(v0), .out(multiplexer_3_out), .sel(JR));
  Hex_Digit_Display hex_digit_display_4 (.value(LedData[19:16]));  // open: dp
  Hex_Digit_Display hex_digit_display_5 (.value(LedData[15:12]));  // open: dp
  Adder #(.width(16)) adder_1 (.a(16'h1), .b(register_1_q), .out(adder_1_out));  // open: cin, cout
  not not_1 (not_1_out, Halt);
  Hex_Digit_Display hex_digit_display_6 (.value(LedData[7:4]));  // open: dp
  Hex_Digit_Display hex_digit_display_7 (.value(LedData[11:8]));  // open: dp
  // Probe on \总周期数 
  Register #(.width(32), .trigger("rising"), .Select("low")) u_PC (
    .D(multiplexer_3_out), .en(not_1_out), .Q(PC), .clk(CLK));  // open: clr
  Hex_Digit_Display hex_digit_display_8 (.value(LedData[3:0]));  // open: dp
  Adder #(.width(16)) adder_2 (.a({16{1'b1}}), .b(adder_1_out), .out(\总周期数 ));  // open: cin, cout
  Adder #(.width(32)) adder_3 (.a(PC), .b(32'h4), .out(adder_3_out));  // open: cin, cout
  // Mips_Probe mips_probe_1: pin names not known; wires that end beside it: IR
  or or_1 (IR1_t, IR1, IRA);
  ROM #(.addrWidth(10), .dataWidth(32), .Select("high")) rom_1 (.addr(PC[11:2]), .data(IR));
  or or_2 (IR2_t, IR2, IRB);
  \单周期硬布线控制器  \u_单周期硬布线控制器_1  (
    .Func(IR[5:0]), .OP(IR[31:26]), .ALU_OP(\单周期硬布线控制器_1_alu_op ), .MemToReg(\单周期硬布线控制器_1_memtoreg ),
    .MemWrite(MemWrite), .ALU_SRC(\单周期硬布线控制器_1_alu_src ), .RegWrite(RegWrite), .SysCALL(Syscall),
    .SignedExt(SignedExt), .RegDst(\单周期硬布线控制器_1_regdst ), .JR(JR), .JMP(JMP), .Beq(\单周期硬布线控制器_1_beq ),
    .JAL(JAL), .Bne(\单周期硬布线控制器_1_bne ), .LUI(\单周期硬布线控制器_1_lui ), .LH(\单周期硬布线控制器_1_lh ),
    .BLEZ(\单周期硬布线控制器_1_blez ));
  Multiplexer #(.select(1), .width(5), .disabled("Z"), .enable("false")) multiplexer_4 (
    .in0(IR[25:21]), .in1(5'b00010), .out(multiplexer_4_out), .sel(Syscall));
  Multiplexer #(.select(1), .width(5), .disabled("Z"), .enable("false")) multiplexer_5 (
    .in0(IR[20:16]), .in1(5'b00100), .out(multiplexer_5_out), .sel(Syscall));
  Multiplexer #(.select(1), .width(5), .disabled("Z"), .enable("false")) multiplexer_6 (
    .in0(IR[20:16]), .in1(IR[15:11]), .out(multiplexer_6_out), .sel(\单周期硬布线控制器_1_regdst ));
  Multiplexer #(.select(1), .width(32), .disabled("Z"), .enable("false")) multiplexer_7 (
    .in0(multiplexer_10_out), .in1(adder_3_out), .out(RDin), .sel(JAL));
  or or_3 (IR3_t, IR3, IRC);
  Multiplexer #(.select(1), .width(5), .disabled("Z"), .enable("false")) multiplexer_8 (
    .in0(multiplexer_6_out), .in1({5{1'b1}}), .out(multiplexer_8_out), .sel(JAL));
  assign bit_extender_1_out = {{16{1'b0}}, IR[15:0]};  // Bit_Extender bit_extender_1
  assign bit_extender_2_out = {{16{IR[15]}}, IR[15:0]};  // Bit_Extender bit_extender_2
  MIPS_Regifile mips_regifile_1 (
    .Din(RDin), .Clk(CLK), .R1(v0), .R2(MDin), .WE(RegWrite), .W_num(multiplexer_8_out),
    .R1_num(multiplexer_4_out), .R2_num(multiplexer_5_out));
  Multiplexer #(.select(1), .width(32), .disabled("Z"), .enable("false")) multiplexer_9 (
    .in0(bit_extender_1_out), .in1(bit_extender_2_out), .out(multiplexer_9_out), .sel(SignedExt));
  Comparator #(.width(32), .mode("twosComplement")) comparator_1 (
    .a(32'ha), .b(v0), .eq(comparator_1_eq));  // open: gt, lt
  Multiplexer #(.select(1), .width(32), .disabled("Z"), .enable("false")) multiplexer_10 (
    .in0(multiplexer_12_out), .in1(shifter_2_out), .out(multiplexer_10_out), .sel(\单周期硬布线控制器_1_lui ));
  Shifter #(.width(32), .shift("ll")) shifter_1 (.in(bit_extender_2_out), .\dist (5'b00010), .out(shifter_1_out));
  and and_1 (Halt, Syscall, comparator_1_eq);
  and and_2 (LedOut, Syscall, ~comparator_1_eq);  // AND_Gate
  Shifter #(.width(32), .shift("ll")) shifter_2 (.in(multiplexer_9_out), .\dist (5'b10000), .out(shifter_2_out));
  Adder #(.width(32)) adder_4 (.a(shifter_1_out), .b(adder_3_out), .out(adder_4_out));  // open: cin, cout
  Comparator #(.width(32), .mode("twosComplement")) comparator_2 (
    .a(v0), .b({32{1'b0}}), .eq(comparator_2_eq), .lt(comparator_2_lt));  // open: gt
  Multiplexer #(.select(1), .width(32), .disabled("Z"), .enable("false")) multiplexer_11 (
    .in0(MDin), .in1(multiplexer_9_out), .out(multiplexer_11_out), .sel(\单周期硬布线控制器_1_alu_src ));
  or or_4 (or_4_out, comparator_2_eq, comparator_2_lt);
  and and_3 (and_3_out, or_4_out, \单周期硬布线控制器_1_blez );
  and and_4 (and_4_out, mips_alu_1_equal, \单周期硬布线控制器_1_beq );
  and and_5 (and_5_out, ~mips_alu_1_equal, \单周期硬布线控制器_1_bne );  // AND_Gate
  MIPS_ALU mips_alu_1 (
    .X(v0), .Y(multiplexer_11_out), .AluOP(\单周期硬布线控制器_1_alu_op ), .Equal(mips_alu_1_equal),
    .Result(mips_alu_1_result), .shamt(IR[10:6]));  // open: Result_2
  D_Flip_Flop #(.trigger("high"), .Pre_Clr_Positions("LEGACY"), .NegatePresetClear("false"), .enable("true"), .NewFFLayout("false")) d_ff_1 (.Q(d_ff_1_q));  // open: clk, D, Qn, preset, en, reset
  // Probe on 13'hc
  or or_5 (Branch, and_3_out, and_4_out, and_5_out);
  Register #(.width(32), .trigger("rising"), .Select("low")) register_2 (
    .D(MDin), .en(LedOut), .Q(LedData), .clk(CLK));  // open: clr
  Comparator #(.width(13), .mode("twosComplement")) comparator_3 (
    .a(CNT_num), .b(13'hc), .eq(comparator_3_eq), .lt(comparator_3_lt));  // open: gt
  Clock #(.highDuration(1), .lowDuration(1)) clock_2 (.out(clock_2_out));
  nand nand_1 (nand_1_out, d_ff_1_q, comparator_3_eq);
  Counter #(.width(13), .max('h1fff), .ongoal("stay"), .trigger("rising"), .behavior("old")) counter_1 (
    .count(comparator_3_lt), .Q(CNT_num), .clk(clock_2_out));  // open: load, D, carry, clr, preset
  RAM #(.addrWidth(10), .dataWidth(32), .bus("separate"), .Select("high")) ram_1 (
    .addr(mips_alu_1_result[11:2]), .din(MDin), .data(ram_1_data), .str(MemWrite), .clk(CLK));  // open: sel, ld, clr
  assign CLK = nand_1_out ? clock_2_out : 1'bz;  // Controlled_Buffer controlled_buffer_1
  Multiplexer #(.select(1), .width(32), .disabled("Z"), .enable("false")) multiplexer_12 (
    .in0(multiplexer_13_out), .in1(bit_extender_3_out), .out(multiplexer_12_out), .sel(\单周期硬布线控制器_1_lh ));
  Pull_Resistor #(.pull(1)) pull_resistor_1 (.node(CLK));
  Multiplexer #(.select(1), .width(32), .disabled("Z"), .enable("false")) multiplexer_13 (
    .in0(mips_alu_1_result), .in1(ram_1_data), .out(multiplexer_13_out), .sel(\单周期硬布线控制器_1_memtoreg ));
  Multiplexer #(.select(1), .width(16), .disabled("Z"), .enable("false")) multiplexer_14 (
    .in0(multiplexer_13_out[15:0]), .in1(multiplexer_13_out[31:16]), .out(multiplexer_14_out),
    .sel(mips_alu_1_result[1]));
  assign bit_extender_3_out = {{16{multiplexer_14_out[15]}}, multiplexer_14_out};  // Bit_Extender bit_extender_3

  // Notes on the sheet:
  //   中断源
  //   中断等待指示
  //   总复位信号应将除ROM以外所有存储组件全部清零
  //   数码管输出
  //   数码管输出应该用寄存器锁存，否则显示数据只能一闪而过
  //   指令存储器
  //   指令字
  //   contents of rom_1 (hex, n*v repeats v):
  //   20110001 8000c05 20110001 20120002 20130003 8000c09 20110001 20120002 20130003 8000c0d 20110001
  //   20120002 20130003 8000c11 20110001 20120002 20130003 c000cf6 20100001 20110001 118fc0 112020
  //   20020022 c 118882 12200001 8000c15 112020 20020022 c 20110001 118880 112020 20020022 c 12200001
  //   8000c1f 20110001 118fc0 112020 20020022 c 1188c3 112020 20020022 c 118903 112020 20020022 c 118903
  //   112020 20020022 c 118903 112020 20020022 c 118903 112020 20020022 c 118903 112020 20020022 c 118903
  //   112020 20020022 c 118903 112020 20020022 c 20100001 109fc0 139fc3 8021 2012000c 24160003 26100001
  //   3210000f 20080008 20090001 139900 2709825 132020 20020022 c 1094022 1500fff9 22100001 2018000f
  //   2188024 108700 20080008 20090001 139902 2709825 132021 20020022 c 1094022 1500fff9 108702 2c9b022
  //   12c00001 8000c50 4020 1084027 84400 3508ffff 82021 20020022 c 2010ffff 20110000 ae300000 22100001
  //   22310004 ae300000 22100001 22310004 ae300000 22100001 22310004 ae300000 22100001 22310004 ae300000
  //   22100001 22310004 ae300000 22100001 22310004 ae300000 22100001 22310004 ae300000 22100001 22310004
  //   ae300000 22100001 22310004 ae300000 22100001 22310004 ae300000 22100001 22310004 ae300000 22100001
  //   22310004 ae300000 22100001 22310004 ae300000 22100001 22310004 ae300000 22100001 22310004 ae300000
  //   22100001 22310004 22100001 8020 2011003c 8e130000 8e340000 274402a 11000002 ae330000 ae140000
  //   2231fffc 1611fff8 102020 20020022 c 22100004 2011003c 1611fff2 20020032 c 200b0008 3c11fedc 3631ffff
  //   112020 20020022 c 3c11ba98 112020 c 3c117654 112020 c 3c113210 112020 c 216bffff 1560fff0 20020032 c
  //   2008ffff 20090000 20111997 112020 20020022 c 2288820 2e291949 1120fffa 20020032 c 20090000 200b0010
  //   34118483 20120404 118c00 129400 36318281 22520404 ad310000 2328820 21290004 216bffff 1560fffb
  //   200b0020 20090000 85310000 112020 20020022 c 21290002 216bffff 1560fff9 20020032 c 2011fff1 112020
  //   20020022 c 22310001 1a20fffb 2002000a c 20100000 22100001 102020 20020022 c 22100002 102020 20020022
  //   c 22100003 102020 20020022 c 22100004 102020 20020022 c 22100005 102020 20020022 c 22100006 102020
  //   20020022 c 22100007 102020 20020022 c 22100008 102020 20020022 20020022 c 3e00008
  //   JMP
  //   JR
  //   OP
  //   OP
  //   Func
  //   Func
  //   rs
  //   rt
  //   rd
  //   imm16
  //   imm26
  //   shamt
  //   Blez
  //   LH
  //   LUI
  //   Beq
  //   Bne
  //   AluOP
  //   AluSrcB
  //   RegWrite
  //   JAL
  //   RegDst
  //   Syscall
  //   MemToReg
  //   MemWrite
  //   为方便自动评测，需要输出PC，IR，寄存器堆写如数据RDin
  //   RAM写使能MemWrite、RAM写入数据MDin等信号
  //   控制位
  //   暂停节拍，不能为0
  //   戳工具置1进入计数暂停模式，ctrl+k时钟自动运行到对应节拍暂停
  //   ctrl+k关闭时钟连续运行，将控制位置零，进入单步调试模式调试
  //   用这个时钟源需要去掉电路中的其他时钟源
  //   可计数暂停的时钟源
endmodule

// 单周期硬布线控制器
module \单周期硬布线控制器  (
  input  [5:0] OP,
  input  [5:0] Func,
  output [3:0] ALU_OP,
  output MemToReg,
  output MemWrite,
  output ALU_SRC,
  output RegWrite,
  output SysCALL,
  output SignedExt,
  output RegDst,
  output Beq,
  output Bne,
  output JR,
  output JMP,
  output JAL,
  output LUI,
  output LH,
  output BLEZ
);

  \运算控制器自动生成  \u_运算控制器自动生成_1  (
    .OP0(OP[0]), .OP1(OP[1]), .OP2(OP[2]), .OP3(OP[3]), .OP4(OP[4]), .OP5(OP[5]), .F0(Func[0]), .F1(Func[1]),
    .F2(Func[2]), .F3(Func[3]), .F4(Func[4]), .F5(Func[5]), .S0(ALU_OP[0]), .S1(ALU_OP[1]), .S2(ALU_OP[2]),
    .S3(ALU_OP[3]));
  \控制信号自动生成  \u_控制信号自动生成_1  (
    .OP0(OP[0]), .OP1(OP[1]), .OP2(OP[2]), .OP3(OP[3]), .OP4(OP[4]), .OP5(OP[5]), .F0(Func[0]), .F1(Func[1]),
    .F2(Func[2]), .F3(Func[3]), .F4(Func[4]), .F5(Func[5]), .MemToReg(MemToReg), .MemWrite(MemWrite),
    .ALU_SRC(ALU_SRC), .RegWrite(RegWrite), .SysCALL(SysCALL), .SignedExt(SignedExt), .RegDst(RegDst),
    .BEQ(Beq), .BNE(Bne), .JR(JR), .JUMP(JMP), .JAL(JAL), .LUI(LUI), .LH(LH), .BLEZ(BLEZ));

  // Other names for the same wires on the sheet: OP_CODE[5:0] = OP

  // Notes on the sheet:
  //   运算器控制器，根据指令生成运算器功能选择信号
  //   控制信号生成，产生数据通路需要的其他控制信号
endmodule

// 运算器控制器
module \运算控制器自动生成  (
  input  OP0,
  input  OP1,
  input  OP2,
  input  OP3,
  input  OP4,
  input  OP5,
  input  F0,
  input  F1,
  input  F2,
  input  F3,
  input  F4,
  input  F5,
  output S0,
  output S1,
  output S2,
  output S3
);

  wire and_1_out, and_2_out, and_3_out, and_4_out, and_5_out, and_6_out, and_7_out, and_8_out, and_9_out,
       and_10_out, and_11_out, and_12_out, and_13_out, and_14_out, and_15_out, and_16_out, and_17_out,
       and_18_out, and_19_out, and_20_out, and_21_out, and_22_out, and_23_out, and_24_out, and_25_out,
       and_26_out, and_27_out, and_28_out, and_29_out, and_30_out, and_31_out, and_32_out, and_33_out,
       and_34_out, and_35_out, and_36_out, and_37_out, and_38_out, not_1_out, not_2_out, not_3_out,
       not_4_out, not_5_out, not_6_out, not_7_out, not_8_out, not_9_out, not_10_out, not_11_out, not_12_out,
       not_13_out, not_14_out, not_15_out, not_16_out, not_17_out, not_18_out, not_19_out, not_20_out,
       not_21_out, not_22_out, not_23_out, not_24_out, not_25_out, not_26_out, not_27_out, not_28_out,
       not_29_out, not_30_out, not_31_out, not_32_out, not_33_out, not_34_out, not_35_out, not_36_out,
       not_37_out, not_38_out, not_39_out, not_40_out, not_41_out, not_42_out, not_43_out, not_44_out,
       not_45_out, not_46_out, not_47_out, not_48_out, not_49_out, not_50_out, not_51_out, not_52_out,
       not_53_out, not_54_out, not_55_out, not_56_out, not_57_out, not_58_out, not_59_out, not_60_out,
       not_61_out, not_62_out, not_63_out, not_64_out, not_65_out, not_66_out, not_67_out, not_68_out,
       not_69_out, not_70_out, not_71_out, not_72_out, not_73_out, not_74_out, not_75_out, not_76_out,
       not_77_out, not_78_out, not_79_out, not_80_out, not_81_out, not_82_out, not_83_out, not_84_out,
       not_85_out, not_86_out, not_87_out, not_88_out, not_89_out, not_90_out, not_91_out, not_92_out,
       not_93_out, not_94_out, not_95_out, not_96_out, not_97_out, not_98_out, not_99_out, not_100_out,
       not_101_out, not_102_out, not_103_out, not_104_out, not_105_out, not_106_out, not_107_out,
       not_108_out, not_109_out, not_110_out, not_111_out, not_112_out, not_113_out, not_114_out,
       not_115_out, not_116_out, not_117_out, not_118_out, not_119_out, not_120_out, not_121_out,
       not_122_out, not_123_out, not_124_out, not_125_out, not_126_out, not_127_out, not_128_out,
       not_129_out, not_130_out, not_131_out, not_132_out, not_133_out, not_134_out, not_135_out,
       not_136_out, not_137_out, not_138_out, not_139_out, not_140_out, not_141_out, not_142_out,
       not_143_out, not_144_out, not_145_out, not_146_out, not_147_out, not_148_out, not_149_out,
       not_150_out, not_151_out, not_152_out, not_153_out, not_154_out, not_155_out, not_156_out,
       not_157_out, not_158_out, not_159_out, not_160_out, not_161_out, not_162_out, not_163_out,
       not_164_out, not_165_out, not_166_out, not_167_out, not_168_out, not_169_out, not_170_out,
       not_171_out, not_172_out, not_173_out, not_174_out, not_175_out, not_176_out, not_177_out,
       not_178_out, not_179_out, not_180_out, not_181_out, not_182_out, not_183_out, not_184_out,
       not_185_out, not_186_out, not_187_out, not_188_out, not_189_out, not_190_out, not_191_out,
       not_192_out, not_193_out, not_194_out, not_195_out, not_196_out, not_197_out, not_198_out,
       not_199_out, not_200_out, not_201_out, not_202_out, not_203_out, not_204_out, not_205_out,
       not_206_out, not_207_out, not_208_out, not_209_out, not_210_out, not_211_out, not_212_out,
       not_213_out, not_214_out, not_215_out, not_216_out, not_217_out, not_218_out, not_219_out,
       not_220_out, not_221_out, not_222_out, not_223_out, not_224_out, not_225_out, not_226_out,
       not_227_out, not_228_out, not_229_out, not_230_out, not_231_out, not_232_out, not_233_out,
       not_234_out, not_235_out, not_236_out, not_237_out, not_238_out, not_239_out, not_240_out,
       not_241_out, not_242_out, not_243_out, not_244_out, not_245_out, not_246_out, not_247_out,
       not_248_out, not_249_out, not_250_out;

  not not_1 (not_1_out, OP5);
  not not_2 (not_2_out, OP4);
  not not_3 (not_3_out, OP3);
  not not_4 (not_4_out, OP2);
  not not_5 (not_5_out, OP1);
  not not_6 (not_6_out, OP0);
  not not_7 (not_7_out, F5);
  not not_8 (not_8_out, F4);
  not not_9 (not_9_out, F3);
  not not_10 (not_10_out, F2);
  not not_11 (not_11_out, OP5);
  not not_12 (not_12_out, OP4);
  not not_13 (not_13_out, OP3);
  not not_14 (not_14_out, OP2);
  not not_15 (not_15_out, OP1);
  not not_16 (not_16_out, OP0);
  not not_17 (not_17_out, F4);
  not not_18 (not_18_out, F3);
  not not_19 (not_19_out, F2);
  not not_20 (not_20_out, F1);
  not not_21 (not_21_out, F0);
  not not_22 (not_22_out, OP5);
  not not_23 (not_23_out, OP4);
  not not_24 (not_24_out, OP3);
  not not_25 (not_25_out, OP2);
  not not_26 (not_26_out, OP1);
  not not_27 (not_27_out, OP0);
  not not_28 (not_28_out, F4);
  not not_29 (not_29_out, F3);
  not not_30 (not_30_out, F2);
  not not_31 (not_31_out, F1);
  not not_32 (not_32_out, OP5);
  not not_33 (not_33_out, OP4);
  not not_34 (not_34_out, OP3);
  not not_35 (not_35_out, OP2);
  not not_36 (not_36_out, OP1);
  not not_37 (not_37_out, OP0);
  not not_38 (not_38_out, F4);
  not not_39 (not_39_out, F3);
  not not_40 (not_40_out, F1);
  not not_41 (not_41_out, F0);
  not not_42 (not_42_out, OP5);
  not not_43 (not_43_out, OP4);
  not not_44 (not_44_out, OP3);
  not not_45 (not_45_out, OP2);
  not not_46 (not_46_out, OP1);
  not not_47 (not_47_out, OP0);
  not not_48 (not_48_out, F4);
  not not_49 (not_49_out, F2);
  not not_50 (not_50_out, F0);
  not not_51 (not_51_out, OP5);
  not not_52 (not_52_out, OP4);
  not not_53 (not_53_out, OP2);
  not not_54 (not_54_out, OP1);
  not not_55 (not_55_out, OP0);
  not not_56 (not_56_out, OP5);
  not not_57 (not_57_out, OP4);
  not not_58 (not_58_out, OP1);
  not not_59 (not_59_out, OP0);
  not not_60 (not_60_out, OP5);
  not not_61 (not_61_out, OP4);
  not not_62 (not_62_out, OP2);
  not not_63 (not_63_out, OP1);
  not not_64 (not_64_out, OP5);
  not not_65 (not_65_out, OP4);
  not not_66 (not_66_out, OP2);
  not not_67 (not_67_out, OP0);
  not not_68 (not_68_out, OP4);
  not not_69 (not_69_out, OP3);
  not not_70 (not_70_out, OP2);
  not not_71 (not_71_out, OP4);
  not not_72 (not_72_out, OP2);
  not not_73 (not_73_out, OP4);
  not not_74 (not_74_out, OP3);
  not not_75 (not_75_out, OP2);
  not not_76 (not_76_out, OP1);
  not not_77 (not_77_out, OP5);
  not not_78 (not_78_out, OP4);
  not not_79 (not_79_out, OP3);
  not not_80 (not_80_out, OP2);
  not not_81 (not_81_out, OP1);
  not not_82 (not_82_out, OP0);
  not not_83 (not_83_out, F5);
  not not_84 (not_84_out, F4);
  not not_85 (not_85_out, F3);
  not not_86 (not_86_out, F2);
  not not_87 (not_87_out, F0);
  not not_88 (not_88_out, OP5);
  not not_89 (not_89_out, OP4);
  not not_90 (not_90_out, OP3);
  not not_91 (not_91_out, OP2);
  not not_92 (not_92_out, OP1);
  not not_93 (not_93_out, OP0);
  not not_94 (not_94_out, F4);
  not not_95 (not_95_out, F3);
  not not_96 (not_96_out, F2);
  not not_97 (not_97_out, F0);
  not not_98 (not_98_out, OP5);
  not not_99 (not_99_out, OP4);
  not not_100 (not_100_out, OP3);
  not not_101 (not_101_out, OP2);
  not not_102 (not_102_out, OP1);
  not not_103 (not_103_out, OP0);
  not not_104 (not_104_out, F4);
  not not_105 (not_105_out, F3);
  not not_106 (not_106_out, F1);
  not not_107 (not_107_out, F0);
  not not_108 (not_108_out, OP5);
  not not_109 (not_109_out, OP4);
  not not_110 (not_110_out, OP3);
  not not_111 (not_111_out, OP2);
  not not_112 (not_112_out, OP1);
  not not_113 (not_113_out, OP0);
  not not_114 (not_114_out, F4);
  not not_115 (not_115_out, F3);
  not not_116 (not_116_out, OP5);
  not not_117 (not_117_out, OP4);
  not not_118 (not_118_out, OP3);
  not not_119 (not_119_out, OP2);
  not not_120 (not_120_out, OP1);
  not not_121 (not_121_out, OP0);
  not not_122 (not_122_out, F4);
  not not_123 (not_123_out, F2);
  not not_124 (not_124_out, F0);
  not not_125 (not_125_out, OP5);
  not not_126 (not_126_out, OP4);
  not not_127 (not_127_out, OP1);
  not not_128 (not_128_out, OP0);
  not not_129 (not_129_out, OP5);
  not not_130 (not_130_out, OP4);
  not not_131 (not_131_out, OP2);
  not not_132 (not_132_out, OP0);
  not not_133 (not_133_out, OP5);
  not not_134 (not_134_out, OP4);
  not not_135 (not_135_out, OP3);
  not not_136 (not_136_out, OP2);
  not not_137 (not_137_out, OP1);
  not not_138 (not_138_out, OP0);
  not not_139 (not_139_out, F4);
  not not_140 (not_140_out, F3);
  not not_141 (not_141_out, F2);
  not not_142 (not_142_out, F1);
  not not_143 (not_143_out, F0);
  not not_144 (not_144_out, OP5);
  not not_145 (not_145_out, OP4);
  not not_146 (not_146_out, OP3);
  not not_147 (not_147_out, OP2);
  not not_148 (not_148_out, OP1);
  not not_149 (not_149_out, OP0);
  not not_150 (not_150_out, F4);
  not not_151 (not_151_out, F3);
  not not_152 (not_152_out, F2);
  not not_153 (not_153_out, F1);
  not not_154 (not_154_out, OP5);
  not not_155 (not_155_out, OP4);
  not not_156 (not_156_out, OP3);
  not not_157 (not_157_out, OP2);
  not not_158 (not_158_out, OP1);
  not not_159 (not_159_out, OP0);
  not not_160 (not_160_out, F4);
  not not_161 (not_161_out, F3);
  not not_162 (not_162_out, F2);
  not not_163 (not_163_out, F0);
  not not_164 (not_164_out, OP5);
  not not_165 (not_165_out, OP4);
  not not_166 (not_166_out, OP3);
  not not_167 (not_167_out, OP2);
  not not_168 (not_168_out, OP1);
  not not_169 (not_169_out, OP0);
  not not_170 (not_170_out, F4);
  not not_171 (not_171_out, F3);
  not not_172 (not_172_out, F1);
  not not_173 (not_173_out, F0);
  not not_174 (not_174_out, OP5);
  not not_175 (not_175_out, OP4);
  not not_176 (not_176_out, OP3);
  not not_177 (not_177_out, OP2);
  not not_178 (not_178_out, OP1);
  not not_179 (not_179_out, OP0);
  not not_180 (not_180_out, F4);
  not not_181 (not_181_out, F2);
  not not_182 (not_182_out, OP5);
  not not_183 (not_183_out, OP4);
  not not_184 (not_184_out, OP2);
  not not_185 (not_185_out, OP1);
  not not_186 (not_186_out, OP0);
  not not_187 (not_187_out, OP5);
  not not_188 (not_188_out, OP4);
  not not_189 (not_189_out, OP1);
  not not_190 (not_190_out, OP0);
  not not_191 (not_191_out, OP5);
  not not_192 (not_192_out, OP4);
  not not_193 (not_193_out, OP2);
  not not_194 (not_194_out, OP1);
  not not_195 (not_195_out, OP4);
  not not_196 (not_196_out, OP3);
  not not_197 (not_197_out, OP2);
  not not_198 (not_198_out, OP4);
  not not_199 (not_199_out, OP2);
  not not_200 (not_200_out, OP5);
  not not_201 (not_201_out, OP4);
  not not_202 (not_202_out, OP2);
  not not_203 (not_203_out, OP4);
  not not_204 (not_204_out, OP3);
  not not_205 (not_205_out, OP2);
  not not_206 (not_206_out, OP1);
  not not_207 (not_207_out, OP5);
  not not_208 (not_208_out, OP4);
  not not_209 (not_209_out, OP3);
  not not_210 (not_210_out, OP2);
  not not_211 (not_211_out, OP1);
  not not_212 (not_212_out, OP0);
  not not_213 (not_213_out, F4);
  not not_214 (not_214_out, F3);
  not not_215 (not_215_out, F1);
  not not_216 (not_216_out, OP5);
  not not_217 (not_217_out, OP4);
  not not_218 (not_218_out, OP3);
  not not_219 (not_219_out, OP2);
  not not_220 (not_220_out, OP1);
  not not_221 (not_221_out, OP0);
  not not_222 (not_222_out, F4);
  not not_223 (not_223_out, F3);
  not not_224 (not_224_out, OP5);
  not not_225 (not_225_out, OP4);
  not not_226 (not_226_out, OP3);
  not not_227 (not_227_out, OP2);
  not not_228 (not_228_out, OP1);
  not not_229 (not_229_out, OP0);
  not not_230 (not_230_out, F4);
  not not_231 (not_231_out, F2);
  not not_232 (not_232_out, F0);
  not not_233 (not_233_out, OP5);
  not not_234 (not_234_out, OP4);
  not not_235 (not_235_out, OP3);
  not not_236 (not_236_out, OP2);
  not not_237 (not_237_out, OP1);
  not not_238 (not_238_out, OP0);
  not not_239 (not_239_out, F4);
  not not_240 (not_240_out, F2);
  not not_241 (not_241_out, OP5);
  not not_242 (not_242_out, OP4);
  not not_243 (not_243_out, OP2);
  not not_244 (not_244_out, OP0);
  not not_245 (not_245_out, OP5);
  not not_246 (not_246_out, OP4);
  not not_247 (not_247_out, OP1);
  not not_248 (not_248_out, OP5);
  not not_249 (not_249_out, OP4);
  not not_250 (not_250_out, OP2);
  and and_1 (and_1_out, not_1_out, not_2_out, not_3_out, not_4_out, not_5_out, not_6_out, not_7_out, not_8_out, not_9_out, not_10_out, F1, F0);
  and and_2 (and_2_out, not_11_out, not_12_out, not_13_out, not_14_out, not_15_out, not_16_out, F5, not_17_out, not_18_out, not_19_out, not_20_out, not_21_out);
  and and_3 (and_3_out, not_22_out, not_23_out, not_24_out, not_25_out, not_26_out, not_27_out, F5, not_28_out, not_29_out, not_30_out, not_31_out, F0);
  and and_4 (and_4_out, not_32_out, not_33_out, not_34_out, not_35_out, not_36_out, not_37_out, F5, not_38_out, not_39_out, F2, not_40_out, not_41_out);
  and and_5 (and_5_out, not_42_out, not_43_out, not_44_out, not_45_out, not_46_out, not_47_out, F5, not_48_out, F3, not_49_out, F1, not_50_out);
  and and_6 (and_6_out, not_51_out, not_52_out, OP3, not_53_out, not_54_out, not_55_out);
  and and_7 (and_7_out, not_56_out, not_57_out, OP3, OP2, not_58_out, not_59_out);
  and and_8 (and_8_out, not_60_out, not_61_out, OP3, not_62_out, not_63_out, OP0);
  and and_9 (and_9_out, not_64_out, not_65_out, OP3, not_66_out, OP1, not_67_out);
  and and_10 (and_10_out, OP5, not_68_out, not_69_out, not_70_out, OP1, OP0);
  and and_11 (and_11_out, OP5, not_71_out, OP3, not_72_out, OP1, OP0);
  and and_12 (and_12_out, OP5, not_73_out, not_74_out, not_75_out, not_76_out, OP0);
  and and_13 (and_13_out, not_77_out, not_78_out, not_79_out, not_80_out, not_81_out, not_82_out, not_83_out, not_84_out, not_85_out, not_86_out, F1, not_87_out);
  and and_14 (and_14_out, not_88_out, not_89_out, not_90_out, not_91_out, not_92_out, not_93_out, F5, not_94_out, not_95_out, not_96_out, F1, not_97_out);
  and and_15 (and_15_out, not_98_out, not_99_out, not_100_out, not_101_out, not_102_out, not_103_out, F5, not_104_out, not_105_out, F2, not_106_out, not_107_out);
  and and_16 (and_16_out, not_108_out, not_109_out, not_110_out, not_111_out, not_112_out, not_113_out, F5, not_114_out, not_115_out, F2, F1, F0);
  and and_17 (and_17_out, not_116_out, not_117_out, not_118_out, not_119_out, not_120_out, not_121_out, F5, not_122_out, F3, not_123_out, F1, not_124_out);
  and and_18 (and_18_out, not_125_out, not_126_out, OP3, OP2, not_127_out, not_128_out);
  and and_19 (and_19_out, not_129_out, not_130_out, OP3, not_131_out, OP1, not_132_out);
  and and_20 (and_20_out, not_133_out, not_134_out, not_135_out, not_136_out, not_137_out, not_138_out, F5, not_139_out, not_140_out, not_141_out, not_142_out, not_143_out);
  and and_21 (and_21_out, not_144_out, not_145_out, not_146_out, not_147_out, not_148_out, not_149_out, F5, not_150_out, not_151_out, not_152_out, not_153_out, F0);
  and and_22 (and_22_out, not_154_out, not_155_out, not_156_out, not_157_out, not_158_out, not_159_out, F5, not_160_out, not_161_out, not_162_out, F1, not_163_out);
  and and_23 (and_23_out, not_164_out, not_165_out, not_166_out, not_167_out, not_168_out, not_169_out, F5, not_170_out, not_171_out, F2, not_172_out, not_173_out);
  and and_24 (and_24_out, not_174_out, not_175_out, not_176_out, not_177_out, not_178_out, not_179_out, F5, not_180_out, F3, not_181_out, F1, F0);
  and and_25 (and_25_out, not_182_out, not_183_out, OP3, not_184_out, not_185_out, not_186_out);
  and and_26 (and_26_out, not_187_out, not_188_out, OP3, OP2, not_189_out, not_190_out);
  and and_27 (and_27_out, not_191_out, not_192_out, OP3, not_193_out, not_194_out, OP0);
  and and_28 (and_28_out, OP5, not_195_out, not_196_out, not_197_out, OP1, OP0);
  and and_29 (and_29_out, OP5, not_198_out, OP3, not_199_out, OP1, OP0);
  and and_30 (and_30_out, not_200_out, not_201_out, OP3, not_202_out, OP1, OP0);
  and and_31 (and_31_out, OP5, not_203_out, not_204_out, not_205_out, not_206_out, OP0);
  and and_32 (and_32_out, not_207_out, not_208_out, not_209_out, not_210_out, not_211_out, not_212_out, F5, not_213_out, not_214_out, F2, not_215_out, F0);
  and and_33 (and_33_out, not_216_out, not_217_out, not_218_out, not_219_out, not_220_out, not_221_out, F5, not_222_out, not_223_out, F2, F1, F0);
  and and_34 (and_34_out, not_224_out, not_225_out, not_226_out, not_227_out, not_228_out, not_229_out, F5, not_230_out, F3, not_231_out, F1, not_232_out);
  and and_35 (and_35_out, not_233_out, not_234_out, not_235_out, not_236_out, not_237_out, not_238_out, F5, not_239_out, F3, not_240_out, F1, F0);
  and and_36 (and_36_out, not_241_out, not_242_out, OP3, not_243_out, OP1, not_244_out);
  and and_37 (and_37_out, not_245_out, not_246_out, OP3, OP2, not_247_out, OP0);
  and and_38 (and_38_out, not_248_out, not_249_out, OP3, not_250_out, OP1, OP0);
  or or_1 (S1, and_13_out, and_14_out, and_15_out, and_16_out, and_17_out, and_18_out, and_19_out);
  or or_2 (S3, and_32_out, and_33_out, and_34_out, and_35_out, and_36_out, and_37_out, and_38_out);
  or or_3 (S0, and_1_out, and_2_out, and_3_out, and_4_out, and_5_out, and_6_out, and_7_out, and_8_out, and_9_out, and_10_out, and_11_out, and_12_out);
  or or_4 (S2, and_20_out, and_21_out, and_22_out, and_23_out, and_24_out, and_25_out, and_26_out, and_27_out, and_28_out, and_29_out, and_30_out, and_31_out);
endmodule

// 控制信号生成
module \控制信号自动生成  (
  input  OP0,
  input  OP1,
  input  OP2,
  input  OP3,
  input  OP4,
  input  OP5,
  input  F0,
  input  F1,
  input  F2,
  input  F3,
  input  F4,
  input  F5,
  output MemToReg,
  output MemWrite,
  output ALU_SRC,
  output RegWrite,
  output SysCALL,
  output SignedExt,
  output RegDst,
  output BEQ,
  output BNE,
  output JR,
  output JUMP,
  output JAL,
  output LUI,
  output LH,
  output BLEZ
);

  wire and_1_out, and_2_out, and_4_out, and_5_out, and_6_out, and_7_out, and_8_out, and_9_out, and_10_out,
       and_11_out, and_12_out, and_13_out, and_14_out, and_15_out, and_16_out, and_17_out, and_18_out,
       and_19_out, and_20_out, and_21_out, and_22_out, and_23_out, and_24_out, and_25_out, and_26_out,
       and_27_out, and_28_out, and_29_out, and_30_out, and_31_out, and_32_out, and_33_out, and_35_out,
       and_36_out, and_37_out, and_38_out, and_39_out, and_40_out, and_41_out, and_42_out, and_43_out,
       and_44_out, and_45_out, and_46_out, and_47_out, and_48_out, and_49_out, and_50_out, and_51_out,
       and_52_out, and_53_out, and_54_out, and_55_out, and_59_out, and_60_out, and_61_out, not_1_out,
       not_2_out, not_3_out, not_4_out, not_5_out, not_6_out, not_7_out, not_8_out, not_9_out, not_10_out,
       not_11_out, not_12_out, not_13_out, not_14_out, not_15_out, not_16_out, not_17_out, not_18_out,
       not_19_out, not_20_out, not_21_out, not_22_out, not_23_out, not_24_out, not_25_out, not_26_out,
       not_27_out, not_28_out, not_29_out, not_30_out, not_31_out, not_32_out, not_33_out, not_34_out,
       not_35_out, not_36_out, not_37_out, not_38_out, not_39_out, not_40_out, not_41_out, not_42_out,
       not_43_out, not_44_out, not_45_out, not_46_out, not_47_out, not_48_out, not_49_out, not_50_out,
       not_51_out, not_52_out, not_53_out, not_54_out, not_55_out, not_56_out, not_57_out, not_58_out,
       not_59_out, not_60_out, not_61_out, not_62_out, not_63_out, not_64_out, not_65_out, not_66_out,
       not_67_out, not_68_out, not_69_out, not_70_out, not_71_out, not_72_out, not_73_out, not_74_out,
       not_75_out, not_76_out, not_77_out, not_78_out, not_79_out, not_80_out, not_81_out, not_82_out,
       not_83_out, not_84_out, not_85_out, not_86_out, not_87_out, not_88_out, not_89_out, not_90_out,
       not_91_out, not_92_out, not_93_out, not_94_out, not_95_out, not_96_out, not_97_out, not_98_out,
       not_99_out, not_100_out, not_101_out, not_102_out, not_103_out, not_104_out, not_105_out, not_106_out,
       not_107_out, not_108_out, not_109_out, not_110_out, not_111_out, not_112_out, not_113_out,
       not_114_out, not_115_out, not_116_out, not_117_out, not_118_out, not_119_out, not_120_out,
       not_121_out, not_122_out, not_123_out, not_124_out, not_125_out, not_126_out, not_127_out,
       not_128_out, not_129_out, not_130_out, not_131_out, not_132_out, not_133_out, not_134_out,
       not_135_out, not_136_out, not_137_out, not_138_out, not_139_out, not_140_out, not_141_out,
       not_142_out, not_143_out, not_144_out, not_145_out, not_146_out, not_147_out, not_148_out,
       not_149_out, not_150_out, not_151_out, not_152_out, not_153_out, not_154_out, not_155_out,
       not_156_out, not_157_out, not_158_out, not_159_out, not_160_out, not_161_out, not_162_out,
       not_163_out, not_164_out, not_165_out, not_166_out, not_167_out, not_168_out, not_169_out,
       not_170_out, not_171_out, not_172_out, not_173_out, not_174_out, not_175_out, not_176_out,
       not_177_out, not_178_out, not_179_out, not_180_out, not_181_out, not_182_out, not_183_out,
       not_184_out, not_185_out, not_186_out, not_187_out, not_188_out, not_189_out, not_190_out,
       not_191_out, not_192_out, not_193_out, not_194_out, not_195_out, not_196_out, not_197_out,
       not_198_out, not_199_out, not_200_out, not_201_out, not_202_out, not_203_out, not_204_out,
       not_205_out, not_206_out, not_207_out, not_208_out, not_209_out, not_210_out, not_211_out,
       not_212_out, not_213_out, not_214_out, not_215_out, not_216_out, not_217_out, not_218_out,
       not_219_out, not_220_out, not_221_out, not_222_out, not_223_out, not_224_out, not_225_out,
       not_226_out, not_227_out, not_228_out, not_229_out, not_230_out, not_231_out, not_232_out,
       not_233_out, not_234_out, not_235_out, not_236_out, not_237_out, not_238_out, not_239_out,
       not_240_out, not_241_out, not_242_out, not_243_out, not_244_out, not_245_out, not_246_out,
       not_247_out, not_248_out, not_249_out, not_250_out, not_251_out, not_252_out, not_253_out,
       not_254_out, not_255_out, not_256_out, not_257_out, not_258_out, not_259_out, not_260_out,
       not_261_out, not_262_out, not_263_out, not_264_out, not_265_out, not_266_out, not_267_out,
       not_268_out, not_269_out, not_270_out, not_271_out, not_272_out, not_273_out, not_274_out,
       not_275_out, not_276_out, not_277_out, not_278_out, not_279_out, not_280_out, not_281_out,
       not_282_out, not_283_out, not_284_out, not_285_out, not_286_out, not_287_out, not_288_out,
       not_289_out, not_290_out, not_291_out, not_292_out, not_293_out, not_294_out, not_295_out,
       not_296_out, not_297_out, not_298_out, not_299_out, not_300_out, not_301_out, not_302_out,
       not_303_out, not_304_out, not_305_out, not_306_out, not_307_out, not_308_out, not_309_out,
       not_310_out, not_311_out, not_312_out, not_313_out, not_314_out, not_315_out, not_316_out,
       not_317_out, not_318_out, not_319_out, not_320_out, not_321_out, not_322_out, not_323_out,
       not_324_out, not_325_out, not_326_out, not_327_out, not_328_out, not_329_out, not_330_out,
       not_331_out, not_332_out, not_333_out, not_334_out, not_335_out, not_336_out, not_337_out,
       not_338_out, not_339_out, not_340_out, not_341_out, not_342_out, not_343_out, not_344_out,
       not_345_out, not_346_out, not_347_out, not_348_out, not_349_out, not_350_out, not_351_out,
       not_352_out, not_353_out, not_354_out, not_355_out, not_356_out, not_357_out, not_358_out,
       not_359_out, not_360_out, not_361_out, not_362_out, not_363_out, not_364_out, not_365_out,
       not_366_out, not_367_out, not_368_out, not_369_out, not_370_out, not_371_out, not_372_out,
       not_373_out, not_374_out, not_375_out, not_376_out, not_377_out, not_378_out, not_379_out,
       not_380_out, not_381_out, not_382_out, not_383_out, not_384_out, not_385_out, not_386_out,
       not_387_out, not_388_out, not_389_out, not_390_out, not_391_out, not_392_out, not_393_out,
       not_394_out, not_395_out;

  not not_1 (not_1_out, OP4);
  not not_2 (not_2_out, OP3);
  not not_3 (not_3_out, OP2);
  not not_4 (not_4_out, OP4);
  not not_5 (not_5_out, OP3);
  not not_6 (not_6_out, OP2);
  not not_7 (not_7_out, OP1);
  not not_8 (not_8_out, OP4);
  not not_9 (not_9_out, OP2);
  not not_10 (not_10_out, OP5);
  not not_11 (not_11_out, OP4);
  not not_12 (not_12_out, OP2);
  not not_13 (not_13_out, OP1);
  not not_14 (not_14_out, OP0);
  not not_15 (not_15_out, OP5);
  not not_16 (not_16_out, OP4);
  not not_17 (not_17_out, OP1);
  not not_18 (not_18_out, OP0);
  not not_19 (not_19_out, OP5);
  not not_20 (not_20_out, OP4);
  not not_21 (not_21_out, OP2);
  not not_22 (not_22_out, OP1);
  not not_23 (not_23_out, OP5);
  not not_24 (not_24_out, OP4);
  not not_25 (not_25_out, OP2);
  not not_26 (not_26_out, OP0);
  not not_27 (not_27_out, OP5);
  not not_28 (not_28_out, OP4);
  not not_29 (not_29_out, OP1);
  not not_30 (not_30_out, OP4);
  not not_31 (not_31_out, OP3);
  not not_32 (not_32_out, OP2);
  not not_33 (not_33_out, OP4);
  not not_34 (not_34_out, OP2);
  not not_35 (not_35_out, OP5);
  not not_36 (not_36_out, OP4);
  not not_37 (not_37_out, OP2);
  not not_38 (not_38_out, OP4);
  not not_39 (not_39_out, OP3);
  not not_40 (not_40_out, OP2);
  not not_41 (not_41_out, OP1);
  not not_42 (not_42_out, OP5);
  not not_43 (not_43_out, OP4);
  not not_44 (not_44_out, OP3);
  not not_45 (not_45_out, OP2);
  not not_46 (not_46_out, OP1);
  not not_47 (not_47_out, OP0);
  not not_48 (not_48_out, F5);
  not not_49 (not_49_out, F4);
  not not_50 (not_50_out, F3);
  not not_51 (not_51_out, F2);
  not not_52 (not_52_out, F1);
  not not_53 (not_53_out, F0);
  not not_54 (not_54_out, OP5);
  not not_55 (not_55_out, OP4);
  not not_56 (not_56_out, OP3);
  not not_57 (not_57_out, OP2);
  not not_58 (not_58_out, OP1);
  not not_59 (not_59_out, OP0);
  not not_60 (not_60_out, F5);
  not not_61 (not_61_out, F4);
  not not_62 (not_62_out, F3);
  not not_63 (not_63_out, F2);
  not not_64 (not_64_out, OP5);
  not not_65 (not_65_out, OP4);
  not not_66 (not_66_out, OP3);
  not not_67 (not_67_out, OP2);
  not not_68 (not_68_out, OP1);
  not not_69 (not_69_out, OP0);
  not not_70 (not_70_out, F5);
  not not_71 (not_71_out, F4);
  not not_72 (not_72_out, F3);
  not not_73 (not_73_out, F2);
  not not_74 (not_74_out, F0);
  not not_75 (not_75_out, OP5);
  not not_76 (not_76_out, OP4);
  not not_77 (not_77_out, OP3);
  not not_78 (not_78_out, OP2);
  not not_79 (not_79_out, OP1);
  not not_80 (not_80_out, OP0);
  not not_81 (not_81_out, F4);
  not not_82 (not_82_out, F3);
  not not_83 (not_83_out, F2);
  not not_84 (not_84_out, F1);
  not not_85 (not_85_out, F0);
  not not_86 (not_86_out, OP5);
  not not_87 (not_87_out, OP4);
  not not_88 (not_88_out, OP3);
  not not_89 (not_89_out, OP2);
  not not_90 (not_90_out, OP1);
  not not_91 (not_91_out, OP0);
  not not_92 (not_92_out, F4);
  not not_93 (not_93_out, F3);
  not not_94 (not_94_out, F2);
  not not_95 (not_95_out, F1);
  not not_96 (not_96_out, OP5);
  not not_97 (not_97_out, OP4);
  not not_98 (not_98_out, OP3);
  not not_99 (not_99_out, OP2);
  not not_100 (not_100_out, OP1);
  not not_101 (not_101_out, OP0);
  not not_102 (not_102_out, F4);
  not not_103 (not_103_out, F3);
  not not_104 (not_104_out, F2);
  not not_105 (not_105_out, F0);
  not not_106 (not_106_out, OP5);
  not not_107 (not_107_out, OP4);
  not not_108 (not_108_out, OP3);
  not not_109 (not_109_out, OP2);
  not not_110 (not_110_out, OP1);
  not not_111 (not_111_out, OP0);
  not not_112 (not_112_out, F4);
  not not_113 (not_113_out, F3);
  not not_114 (not_114_out, F1);
  not not_115 (not_115_out, F0);
  not not_116 (not_116_out, OP5);
  not not_117 (not_117_out, OP4);
  not not_118 (not_118_out, OP3);
  not not_119 (not_119_out, OP2);
  not not_120 (not_120_out, OP1);
  not not_121 (not_121_out, OP0);
  not not_122 (not_122_out, F4);
  not not_123 (not_123_out, F3);
  not not_124 (not_124_out, F1);
  not not_125 (not_125_out, OP5);
  not not_126 (not_126_out, OP4);
  not not_127 (not_127_out, OP3);
  not not_128 (not_128_out, OP2);
  not not_129 (not_129_out, OP1);
  not not_130 (not_130_out, OP0);
  not not_131 (not_131_out, F4);
  not not_132 (not_132_out, F3);
  not not_133 (not_133_out, OP5);
  not not_134 (not_134_out, OP4);
  not not_135 (not_135_out, OP3);
  not not_136 (not_136_out, OP2);
  not not_137 (not_137_out, OP1);
  not not_138 (not_138_out, OP0);
  not not_139 (not_139_out, F4);
  not not_140 (not_140_out, F2);
  not not_141 (not_141_out, F0);
  not not_142 (not_142_out, OP5);
  not not_143 (not_143_out, OP4);
  not not_144 (not_144_out, OP3);
  not not_145 (not_145_out, OP2);
  not not_146 (not_146_out, OP1);
  not not_147 (not_147_out, OP0);
  not not_148 (not_148_out, F4);
  not not_149 (not_149_out, F2);
  not not_150 (not_150_out, OP5);
  not not_151 (not_151_out, OP4);
  not not_152 (not_152_out, OP3);
  not not_153 (not_153_out, OP2);
  not not_154 (not_154_out, OP5);
  not not_155 (not_155_out, OP4);
  not not_156 (not_156_out, OP2);
  not not_157 (not_157_out, OP1);
  not not_158 (not_158_out, OP0);
  not not_159 (not_159_out, OP5);
  not not_160 (not_160_out, OP4);
  not not_161 (not_161_out, OP1);
  not not_162 (not_162_out, OP0);
  not not_163 (not_163_out, OP5);
  not not_164 (not_164_out, OP4);
  not not_165 (not_165_out, OP2);
  not not_166 (not_166_out, OP1);
  not not_167 (not_167_out, OP5);
  not not_168 (not_168_out, OP4);
  not not_169 (not_169_out, OP2);
  not not_170 (not_170_out, OP0);
  not not_171 (not_171_out, OP5);
  not not_172 (not_172_out, OP4);
  not not_173 (not_173_out, OP1);
  not not_174 (not_174_out, OP4);
  not not_175 (not_175_out, OP3);
  not not_176 (not_176_out, OP2);
  not not_177 (not_177_out, OP5);
  not not_178 (not_178_out, OP4);
  not not_179 (not_179_out, OP5);
  not not_180 (not_180_out, OP4);
  not not_181 (not_181_out, OP2);
  not not_182 (not_182_out, OP4);
  not not_183 (not_183_out, OP3);
  not not_184 (not_184_out, OP2);
  not not_185 (not_185_out, OP1);
  not not_186 (not_186_out, OP5);
  not not_187 (not_187_out, OP4);
  not not_188 (not_188_out, OP3);
  not not_189 (not_189_out, OP2);
  not not_190 (not_190_out, OP1);
  not not_191 (not_191_out, OP0);
  not not_192 (not_192_out, F5);
  not not_193 (not_193_out, F4);
  not not_194 (not_194_out, F1);
  not not_195 (not_195_out, F0);
  not not_196 (not_196_out, OP5);
  not not_197 (not_197_out, OP4);
  not not_198 (not_198_out, OP3);
  not not_199 (not_199_out, OP1);
  not not_200 (not_200_out, OP0);
  not not_201 (not_201_out, OP5);
  not not_202 (not_202_out, OP4);
  not not_203 (not_203_out, OP3);
  not not_204 (not_204_out, OP1);
  not not_205 (not_205_out, OP5);
  not not_206 (not_206_out, OP4);
  not not_207 (not_207_out, OP2);
  not not_208 (not_208_out, OP1);
  not not_209 (not_209_out, OP0);
  not not_210 (not_210_out, OP5);
  not not_211 (not_211_out, OP4);
  not not_212 (not_212_out, OP2);
  not not_213 (not_213_out, OP1);
  not not_214 (not_214_out, OP5);
  not not_215 (not_215_out, OP4);
  not not_216 (not_216_out, OP2);
  not not_217 (not_217_out, OP0);
  not not_218 (not_218_out, OP4);
  not not_219 (not_219_out, OP3);
  not not_220 (not_220_out, OP2);
  not not_221 (not_221_out, OP4);
  not not_222 (not_222_out, OP2);
  not not_223 (not_223_out, OP5);
  not not_224 (not_224_out, OP4);
  not not_225 (not_225_out, OP2);
  not not_226 (not_226_out, OP4);
  not not_227 (not_227_out, OP3);
  not not_228 (not_228_out, OP2);
  not not_229 (not_229_out, OP1);
  not not_230 (not_230_out, OP5);
  not not_231 (not_231_out, OP4);
  not not_232 (not_232_out, OP3);
  not not_233 (not_233_out, OP0);
  not not_234 (not_234_out, OP5);
  not not_235 (not_235_out, OP4);
  not not_236 (not_236_out, OP3);
  not not_237 (not_237_out, OP2);
  not not_238 (not_238_out, OP1);
  not not_239 (not_239_out, OP0);
  not not_240 (not_240_out, F5);
  not not_241 (not_241_out, F4);
  not not_242 (not_242_out, F3);
  not not_243 (not_243_out, F2);
  not not_244 (not_244_out, F1);
  not not_245 (not_245_out, F0);
  not not_246 (not_246_out, OP5);
  not not_247 (not_247_out, OP4);
  not not_248 (not_248_out, OP3);
  not not_249 (not_249_out, OP2);
  not not_250 (not_250_out, OP1);
  not not_251 (not_251_out, OP0);
  not not_252 (not_252_out, F5);
  not not_253 (not_253_out, F4);
  not not_254 (not_254_out, F3);
  not not_255 (not_255_out, F2);
  not not_256 (not_256_out, OP5);
  not not_257 (not_257_out, OP4);
  not not_258 (not_258_out, OP3);
  not not_259 (not_259_out, OP2);
  not not_260 (not_260_out, OP1);
  not not_261 (not_261_out, OP0);
  not not_262 (not_262_out, F5);
  not not_263 (not_263_out, F4);
  not not_264 (not_264_out, F3);
  not not_265 (not_265_out, F2);
  not not_266 (not_266_out, F0);
  not not_267 (not_267_out, OP5);
  not not_268 (not_268_out, OP4);
  not not_269 (not_269_out, OP3);
  not not_270 (not_270_out, OP2);
  not not_271 (not_271_out, OP1);
  not not_272 (not_272_out, OP0);
  not not_273 (not_273_out, F4);
  not not_274 (not_274_out, F3);
  not not_275 (not_275_out, F2);
  not not_276 (not_276_out, F1);
  not not_277 (not_277_out, F0);
  not not_278 (not_278_out, OP5);
  not not_279 (not_279_out, OP4);
  not not_280 (not_280_out, OP3);
  not not_281 (not_281_out, OP2);
  not not_282 (not_282_out, OP1);
  not not_283 (not_283_out, OP0);
  not not_284 (not_284_out, F4);
  not not_285 (not_285_out, F3);
  not not_286 (not_286_out, F2);
  not not_287 (not_287_out, F1);
  not not_288 (not_288_out, OP5);
  not not_289 (not_289_out, OP4);
  not not_290 (not_290_out, OP3);
  not not_291 (not_291_out, OP2);
  not not_292 (not_292_out, OP1);
  not not_293 (not_293_out, OP0);
  not not_294 (not_294_out, F4);
  not not_295 (not_295_out, F3);
  not not_296 (not_296_out, F2);
  not not_297 (not_297_out, F0);
  not not_298 (not_298_out, OP5);
  not not_299 (not_299_out, OP4);
  not not_300 (not_300_out, OP3);
  not not_301 (not_301_out, OP2);
  not not_302 (not_302_out, OP1);
  not not_303 (not_303_out, OP0);
  not not_304 (not_304_out, F4);
  not not_305 (not_305_out, F3);
  not not_306 (not_306_out, F1);
  not not_307 (not_307_out, F0);
  not not_308 (not_308_out, OP5);
  not not_309 (not_309_out, OP4);
  not not_310 (not_310_out, OP3);
  not not_311 (not_311_out, OP2);
  not not_312 (not_312_out, OP1);
  not not_313 (not_313_out, OP0);
  not not_314 (not_314_out, F4);
  not not_315 (not_315_out, F3);
  not not_316 (not_316_out, F1);
  not not_317 (not_317_out, OP5);
  not not_318 (not_318_out, OP4);
  not not_319 (not_319_out, OP3);
  not not_320 (not_320_out, OP2);
  not not_321 (not_321_out, OP1);
  not not_322 (not_322_out, OP0);
  not not_323 (not_323_out, F4);
  not not_324 (not_324_out, F3);
  not not_325 (not_325_out, OP5);
  not not_326 (not_326_out, OP4);
  not not_327 (not_327_out, OP3);
  not not_328 (not_328_out, OP2);
  not not_329 (not_329_out, OP1);
  not not_330 (not_330_out, OP0);
  not not_331 (not_331_out, F4);
  not not_332 (not_332_out, F2);
  not not_333 (not_333_out, F0);
  not not_334 (not_334_out, OP5);
  not not_335 (not_335_out, OP4);
  not not_336 (not_336_out, OP3);
  not not_337 (not_337_out, OP2);
  not not_338 (not_338_out, OP1);
  not not_339 (not_339_out, OP0);
  not not_340 (not_340_out, F4);
  not not_341 (not_341_out, F2);
  not not_342 (not_342_out, OP5);
  not not_343 (not_343_out, OP4);
  not not_344 (not_344_out, OP3);
  not not_345 (not_345_out, OP1);
  not not_346 (not_346_out, OP0);
  not not_347 (not_347_out, OP5);
  not not_348 (not_348_out, OP4);
  not not_349 (not_349_out, OP3);
  not not_350 (not_350_out, OP1);
  not not_351 (not_351_out, OP5);
  not not_352 (not_352_out, OP4);
  not not_353 (not_353_out, OP3);
  not not_354 (not_354_out, OP2);
  not not_355 (not_355_out, OP1);
  not not_356 (not_356_out, OP0);
  not not_357 (not_357_out, F5);
  not not_358 (not_358_out, F4);
  not not_359 (not_359_out, F2);
  not not_360 (not_360_out, F1);
  not not_361 (not_361_out, F0);
  not not_362 (not_362_out, OP5);
  not not_363 (not_363_out, OP4);
  not not_364 (not_364_out, OP3);
  not not_365 (not_365_out, OP2);
  not not_366 (not_366_out, OP1);
  not not_367 (not_367_out, OP0);
  not not_368 (not_368_out, F5);
  not not_369 (not_369_out, F4);
  not not_370 (not_370_out, F2);
  not not_371 (not_371_out, F1);
  not not_372 (not_372_out, F0);
  not not_373 (not_373_out, OP5);
  not not_374 (not_374_out, OP4);
  not not_375 (not_375_out, OP3);
  not not_376 (not_376_out, OP2);
  not not_377 (not_377_out, OP0);
  not not_378 (not_378_out, OP5);
  not not_379 (not_379_out, OP4);
  not not_380 (not_380_out, OP3);
  not not_381 (not_381_out, OP2);
  not not_382 (not_382_out, OP5);
  not not_383 (not_383_out, OP4);
  not not_384 (not_384_out, OP3);
  not not_385 (not_385_out, OP2);
  not not_386 (not_386_out, OP5);
  not not_387 (not_387_out, OP4);
  not not_388 (not_388_out, OP4);
  not not_389 (not_389_out, OP3);
  not not_390 (not_390_out, OP2);
  not not_391 (not_391_out, OP1);
  not not_392 (not_392_out, OP5);
  not not_393 (not_393_out, OP4);
  not not_394 (not_394_out, OP3);
  not not_395 (not_395_out, OP0);
  and and_1 (and_1_out, OP5, not_1_out, not_2_out, not_3_out, OP1, OP0);
  and and_2 (and_2_out, OP5, not_4_out, not_5_out, not_6_out, not_7_out, OP0);
  and and_3 (MemWrite, OP5, not_8_out, OP3, not_9_out, OP1, OP0);
  and and_4 (and_4_out, not_10_out, not_11_out, OP3, not_12_out, not_13_out, not_14_out);
  and and_5 (and_5_out, not_15_out, not_16_out, OP3, OP2, not_17_out, not_18_out);
  and and_6 (and_6_out, not_19_out, not_20_out, OP3, not_21_out, not_22_out, OP0);
  and and_7 (and_7_out, not_23_out, not_24_out, OP3, not_25_out, OP1, not_26_out);
  and and_8 (and_8_out, not_27_out, not_28_out, OP3, OP2, not_29_out, OP0);
  and and_9 (and_9_out, OP5, not_30_out, not_31_out, not_32_out, OP1, OP0);
  and and_10 (and_10_out, OP5, not_33_out, OP3, not_34_out, OP1, OP0);
  and and_11 (and_11_out, not_35_out, not_36_out, OP3, not_37_out, OP1, OP0);
  and and_12 (and_12_out, OP5, not_38_out, not_39_out, not_40_out, not_41_out, OP0);
  and and_13 (and_13_out, not_42_out, not_43_out, not_44_out, not_45_out, not_46_out, not_47_out, not_48_out, not_49_out, not_50_out, not_51_out, not_52_out, not_53_out);
  and and_14 (and_14_out, not_54_out, not_55_out, not_56_out, not_57_out, not_58_out, not_59_out, not_60_out, not_61_out, not_62_out, not_63_out, F1, F0);
  and and_15 (and_15_out, not_64_out, not_65_out, not_66_out, not_67_out, not_68_out, not_69_out, not_70_out, not_71_out, not_72_out, not_73_out, F1, not_74_out);
  and and_16 (and_16_out, not_75_out, not_76_out, not_77_out, not_78_out, not_79_out, not_80_out, F5, not_81_out, not_82_out, not_83_out, not_84_out, not_85_out);
  and and_17 (and_17_out, not_86_out, not_87_out, not_88_out, not_89_out, not_90_out, not_91_out, F5, not_92_out, not_93_out, not_94_out, not_95_out, F0);
  and and_18 (and_18_out, not_96_out, not_97_out, not_98_out, not_99_out, not_100_out, not_101_out, F5, not_102_out, not_103_out, not_104_out, F1, not_105_out);
  and and_19 (and_19_out, not_106_out, not_107_out, not_108_out, not_109_out, not_110_out, not_111_out, F5, not_112_out, not_113_out, F2, not_114_out, not_115_out);
  and and_20 (and_20_out, not_116_out, not_117_out, not_118_out, not_119_out, not_120_out, not_121_out, F5, not_122_out, not_123_out, F2, not_124_out, F0);
  and and_21 (and_21_out, not_125_out, not_126_out, not_127_out, not_128_out, not_129_out, not_130_out, F5, not_131_out, not_132_out, F2, F1, F0);
  and and_22 (and_22_out, not_133_out, not_134_out, not_135_out, not_136_out, not_137_out, not_138_out, F5, not_139_out, F3, not_140_out, F1, not_141_out);
  and and_23 (and_23_out, not_142_out, not_143_out, not_144_out, not_145_out, not_146_out, not_147_out, F5, not_148_out, F3, not_149_out, F1, F0);
  and and_24 (and_24_out, not_150_out, not_151_out, not_152_out, not_153_out, OP1, OP0);
  and and_25 (and_25_out, not_154_out, not_155_out, OP3, not_156_out, not_157_out, not_158_out);
  and and_26 (and_26_out, not_159_out, not_160_out, OP3, OP2, not_161_out, not_162_out);
  and and_27 (and_27_out, not_163_out, not_164_out, OP3, not_165_out, not_166_out, OP0);
  and and_28 (and_28_out, not_167_out, not_168_out, OP3, not_169_out, OP1, not_170_out);
  and and_29 (and_29_out, not_171_out, not_172_out, OP3, OP2, not_173_out, OP0);
  and and_30 (and_30_out, OP5, not_174_out, not_175_out, not_176_out, OP1, OP0);
  and and_31 (and_31_out, not_177_out, not_178_out, OP3, OP2, OP1, OP0);
  and and_32 (and_32_out, not_179_out, not_180_out, OP3, not_181_out, OP1, OP0);
  and and_33 (and_33_out, OP5, not_182_out, not_183_out, not_184_out, not_185_out, OP0);
  and and_34 (SysCALL, not_186_out, not_187_out, not_188_out, not_189_out, not_190_out, not_191_out, not_192_out, not_193_out, F3, F2, not_194_out, not_195_out);
  and and_35 (and_35_out, not_196_out, not_197_out, not_198_out, OP2, not_199_out, not_200_out);
  and and_36 (and_36_out, not_201_out, not_202_out, not_203_out, OP2, not_204_out, OP0);
  and and_37 (and_37_out, not_205_out, not_206_out, OP3, not_207_out, not_208_out, not_209_out);
  and and_38 (and_38_out, not_210_out, not_211_out, OP3, not_212_out, not_213_out, OP0);
  and and_39 (and_39_out, not_214_out, not_215_out, OP3, not_216_out, OP1, not_217_out);
  and and_40 (and_40_out, OP5, not_218_out, not_219_out, not_220_out, OP1, OP0);
  and and_41 (and_41_out, OP5, not_221_out, OP3, not_222_out, OP1, OP0);
  and and_42 (and_42_out, not_223_out, not_224_out, OP3, not_225_out, OP1, OP0);
  and and_43 (and_43_out, OP5, not_226_out, not_227_out, not_228_out, not_229_out, OP0);
  and and_44 (and_44_out, not_230_out, not_231_out, not_232_out, OP2, OP1, not_233_out);
  and and_45 (and_45_out, not_234_out, not_235_out, not_236_out, not_237_out, not_238_out, not_239_out, not_240_out, not_241_out, not_242_out, not_243_out, not_244_out, not_245_out);
  and and_46 (and_46_out, not_246_out, not_247_out, not_248_out, not_249_out, not_250_out, not_251_out, not_252_out, not_253_out, not_254_out, not_255_out, F1, F0);
  and and_47 (and_47_out, not_256_out, not_257_out, not_258_out, not_259_out, not_260_out, not_261_out, not_262_out, not_263_out, not_264_out, not_265_out, F1, not_266_out);
  and and_48 (and_48_out, not_267_out, not_268_out, not_269_out, not_270_out, not_271_out, not_272_out, F5, not_273_out, not_274_out, not_275_out, not_276_out, not_277_out);
  and and_49 (and_49_out, not_278_out, not_279_out, not_280_out, not_281_out, not_282_out, not_283_out, F5, not_284_out, not_285_out, not_286_out, not_287_out, F0);
  and and_50 (and_50_out, not_288_out, not_289_out, not_290_out, not_291_out, not_292_out, not_293_out, F5, not_294_out, not_295_out, not_296_out, F1, not_297_out);
  and and_51 (and_51_out, not_298_out, not_299_out, not_300_out, not_301_out, not_302_out, not_303_out, F5, not_304_out, not_305_out, F2, not_306_out, not_307_out);
  and and_52 (and_52_out, not_308_out, not_309_out, not_310_out, not_311_out, not_312_out, not_313_out, F5, not_314_out, not_315_out, F2, not_316_out, F0);
  and and_53 (and_53_out, not_317_out, not_318_out, not_319_out, not_320_out, not_321_out, not_322_out, F5, not_323_out, not_324_out, F2, F1, F0);
  and and_54 (and_54_out, not_325_out, not_326_out, not_327_out, not_328_out, not_329_out, not_330_out, F5, not_331_out, F3, not_332_out, F1, not_333_out);
  and and_55 (and_55_out, not_334_out, not_335_out, not_336_out, not_337_out, not_338_out, not_339_out, F5, not_340_out, F3, not_341_out, F1, F0);
  and and_56 (BEQ, not_342_out, not_343_out, not_344_out, OP2, not_345_out, not_346_out);
  and and_57 (BNE, not_347_out, not_348_out, not_349_out, OP2, not_350_out, OP0);
  and and_58 (JR, not_351_out, not_352_out, not_353_out, not_354_out, not_355_out, not_356_out, not_357_out, not_358_out, F3, not_359_out, not_360_out, not_361_out);
  and and_59 (and_59_out, not_362_out, not_363_out, not_364_out, not_365_out, not_366_out, not_367_out, not_368_out, not_369_out, F3, not_370_out, not_371_out, not_372_out);
  and and_60 (and_60_out, not_373_out, not_374_out, not_375_out, not_376_out, OP1, not_377_out);
  and and_61 (and_61_out, not_378_out, not_379_out, not_380_out, not_381_out, OP1, OP0);
  and and_62 (JAL, not_382_out, not_383_out, not_384_out, not_385_out, OP1, OP0);
  and and_63 (LUI, not_386_out, not_387_out, OP3, OP2, OP1, OP0);
  and and_64 (LH, OP5, not_388_out, not_389_out, not_390_out, not_391_out, OP0);
  and and_65 (BLEZ, not_392_out, not_393_out, not_394_out, OP2, OP1, not_395_out);
  or or_1 (MemToReg, and_1_out, and_2_out);
  or or_2 (ALU_SRC, and_4_out, and_5_out, and_6_out, and_7_out, and_8_out, and_9_out, and_10_out, and_11_out, and_12_out);
  or or_3 (SignedExt, and_35_out, and_36_out, and_37_out, and_38_out, and_39_out, and_40_out, and_41_out, and_42_out, and_43_out, and_44_out);
  or or_4 (RegDst, and_45_out, and_46_out, and_47_out, and_48_out, and_49_out, and_50_out, and_51_out, and_52_out, and_53_out, and_54_out, and_55_out);
  or or_5 (JUMP, and_59_out, and_60_out, and_61_out);
  or or_6 (RegWrite, and_13_out, and_14_out, and_15_out, and_16_out, and_17_out, and_18_out, and_19_out, and_20_out, and_21_out, and_22_out, and_23_out, and_24_out, and_25_out, and_26_out, and_27_out, and_28_out, and_29_out, and_30_out, and_31_out, and_32_out, and_33_out);
endmodule

// ALU
module MIPS_ALU (
  input  [4:0] shamt,
  input  [31:0] X,
  input  [31:0] Y,
  input  [3:0] AluOP,
  output Equal,
  output [31:0] Result,
  output [31:0] Result_2
);

  wire [0:0] comparator_1_lt, comparator_2_lt;
  wire [31:0] adder_1_out, AND_out, divider_1_out, divider_1_rem, multiplier_1_cout, multiplier_1_out,
       NOR_out, OR_out, shifter_1_out, shifter_2_out, shifter_3_out, subtractor_1_out, XOR_out;

  assign AND_out = X & Y;  // AND_Gate AND, 32 bits wide
  assign OR_out = X | Y;  // OR_Gate OR, 32 bits wide
  Shifter #(.width(32), .shift("ll")) shifter_1 (.in(Y), .\dist (shamt), .out(shifter_1_out));
  Shifter #(.width(32), .shift("ar")) shifter_2 (.in(Y), .\dist (shamt), .out(shifter_2_out));
  Shifter #(.width(32), .shift("lr")) shifter_3 (.in(Y), .\dist (shamt), .out(shifter_3_out));
  Multiplier #(.width(32)) multiplier_1 (.a(X), .b(Y), .out(multiplier_1_out), .cout(multiplier_1_cout));  // open: cin
  Divider #(.width(32)) divider_1 (.a(X), .b(Y), .out(divider_1_out), .rem(divider_1_rem));  // open: upper
  Adder #(.width(32)) adder_1 (.a(X), .b(Y), .out(adder_1_out));  // open: cin, cout
  Subtractor #(.width(32)) subtractor_1 (.a(X), .b(Y), .out(subtractor_1_out));  // open: bin, bout
  assign XOR_out = X ^ Y;  // XOR_Gate XOR, 32 bits wide
  assign NOR_out = ~(X | Y);  // NOR_Gate NOR, 32 bits wide
  Comparator #(.width(32), .mode("twosComplement")) comparator_1 (
    .a(X), .b(Y), .eq(Equal), .lt(comparator_1_lt[0]));  // open: gt
  Comparator #(.width(32), .mode("unsigned")) comparator_2 (.a(X), .b(Y), .lt(comparator_2_lt[0]));  // open: gt, eq
  Multiplexer #(.select(4), .width(32), .disabled("Z"), .enable("false")) multiplexer_1 (
    .in0(shifter_1_out), .in1(shifter_2_out), .in2(shifter_3_out), .in3(multiplier_1_out),
    .in4(divider_1_out), .in5(adder_1_out), .in6(subtractor_1_out), .in7(AND_out), .in8(OR_out),
    .in9(XOR_out), .in10(NOR_out), .in11({{31{1'b0}}, comparator_1_lt[0]}),
    .in12({{31{1'b0}}, comparator_2_lt[0]}), .in13({32{1'b0}}), .in14({32{1'b0}}), .in15({32{1'b0}}),
    .out(Result), .sel(AluOP));
  Multiplexer #(.select(4), .width(32), .disabled("Z"), .enable("false")) multiplexer_2 (
    .in0({32{1'b0}}), .in1({32{1'b0}}), .in2({32{1'b0}}), .in3(multiplier_1_cout), .in4(divider_1_rem),
    .in5({32{1'b0}}), .in6({32{1'b0}}), .in7({32{1'b0}}), .in8({32{1'b0}}), .in9({32{1'b0}}),
    .in10({32{1'b0}}), .in11({32{1'b0}}), .in12({32{1'b0}}), .in13({32{1'b0}}), .in14({32{1'b0}}),
    .in15({32{1'b0}}), .out(Result_2), .sel(AluOP));

  // Other names for the same wires on the sheet: Result2[31:0] = Result_2; S[3:0] = AluOP

  // Notes on the sheet:
  //   不要改变此引脚区域内容，也不要改变ALU封装形式
  //   输入引脚
  //   输出引脚
endmodule

module MIPS_Regifile (
  input  [31:0] Din,
  input  Clk,
  input  WE,
  input  [4:0] R1_num,
  input  [4:0] W_num,
  input  [4:0] R2_num,
  output [31:0] R1,
  output [31:0] R2
);

  // RegisterFile registerfile_1: pin names not known; wires that end beside it: Din, Clk, WE, W_num, R1_num, R2_num, R1, R2
endmodule

module \理想流水线  (
  output RegWrite,
  output MemWrite,
  output [31:0] IF_PC,
  output [31:0] ID_PC,
  output [31:0] EX_PC,
  output [31:0] M_PC,
  output [31:0] WB_PC,
  output [31:0] RDin,
  output [31:0] MDin,
  output [31:0] LedData
);

  wire and_3_out, and_4_out, and_5_out, and_6_out, Branch, CLK, clock_1_out, clock_2_out, comparator_1_eq,
       comparator_1_lt, comparator_2_eq, comparator_3_eq, comparator_3_lt, d_ff_1_q, END, ex_mem_1_jal_2,
       ex_mem_1_lh_2, ex_mem_1_lui_2, ex_mem_1_memtoreg_2, ex_mem_1_regwrite_2, ex_mem_1_syscall_2, Go, Halt,
       id_ex_1_alu_srcb_2, id_ex_1_beq_2, id_ex_1_blez_2, id_ex_1_bne_2, id_ex_1_jal_2, id_ex_1_lh_2,
       id_ex_1_lui_2, id_ex_1_memtoreg_2, id_ex_1_memwrite_2, id_ex_1_regwrite_2, id_ex_1_syscall_2, IR1,
       IR2, IR3, JMP, JR, LedOut, mem_wb_1_jal_2, mem_wb_1_lh_2, mem_wb_1_lui_2, mem_wb_1_memtoreg_2,
       mips_alu_1_equal, nand_1_out, not_1_out, not_2_out, or_1_out, register_1_q, RST, SignedExt, Stop, W1,
       W2, W3, \单周期硬布线控制器_1_alu_src , \单周期硬布线控制器_1_beq , \单周期硬布线控制器_1_blez , \单周期硬布线控制器_1_bne ,
       \单周期硬布线控制器_1_jal , \单周期硬布线控制器_1_jmp , \单周期硬布线控制器_1_jr , \单周期硬布线控制器_1_lh , \单周期硬布线控制器_1_lui ,
       \单周期硬布线控制器_1_memtoreg , \单周期硬布线控制器_1_memwrite , \单周期硬布线控制器_1_regdst , \单周期硬布线控制器_1_regwrite ,
       \单周期硬布线控制器_1_syscall ;
  wire [3:0] id_ex_1_alu_op_2, \单周期硬布线控制器_1_alu_op ;
  wire [4:0] ex_mem_1_w_num_2, id_ex_1_w_num_2, mem_wb_1_w_num_2, multiplexer_4_out, multiplexer_5_out,
       multiplexer_6_out, multiplexer_7_out;
  wire [12:0] CNT_num;
  wire [15:0] adder_2_out, \LoadUse次数 , multiplexer_11_out, register_2_q, \总周期数 , \插入气泡数 , \无条件分支数 ,
       \条件分支成功数 ;
  wire [25:0] id_ex_1_imm26_2;
  wire [31:0] adder_1_out, adder_4_out, bit_extender_1_out, bit_extender_2_out, bit_extender_3_out, EX_IR,
       ex_mem_1_alu_result_2, ex_mem_1_pc_4_2, ex_mem_1_sign_imm_2, id_ex_1_pc_4_2, id_ex_1_rt_2,
       id_ex_1_sign_imm_2, ID_IR, if_id_1_pc_4_2, IF_IR, MEM_IR, mem_wb_1_alu_result_2, mem_wb_1_mem_data_2,
       mem_wb_1_pc_4_2, mem_wb_1_sign_imm_2, mips_alu_1_result, mips_regifile_1_r1, mips_regifile_1_r2,
       multiplexer_1_out, multiplexer_2_out, multiplexer_3_out, multiplexer_8_out, multiplexer_9_out,
       multiplexer_10_out, multiplexer_12_out, multiplexer_13_out, ram_1_data, shifter_1_out, shifter_2_out,
       v0, WB_IR;

  Button \u_总复位  (.out(RST));
  Button _1 (.out(IR1));
  Button _2 (.out(IR2));
  Button _3 (.out(IR3));
  // Probe on \总周期数 
  // Probe on \总周期数 
  Button \u_继续运行  (.out(Go));
  LED #(.active("true")) led_1 (.in(W1));
  LED #(.active("true")) led_2 (.in(W2));
  LED #(.active("true")) led_3 (.in(W3));
  Hex_Digit_Display hex_digit_display_1 (.value(LedData[31:28]));  // open: dp
  // Probe on IF_PC[19:0]
  // Mips_Probe mips_probe_1: pin names not known; wires that end beside it: IF_IR
  Multiplexer #(.select(1), .width(32), .disabled("Z"), .enable("false")) multiplexer_1 (
    .in0(adder_1_out), .in1(adder_4_out), .out(multiplexer_1_out), .sel(Branch));
  Hex_Digit_Display hex_digit_display_2 (.value(LedData[23:20]));  // open: dp
  Hex_Digit_Display hex_digit_display_3 (.value(LedData[27:24]));  // open: dp
  // Probe on ID_PC[19:0]
  // Mips_Probe mips_probe_2: pin names not known; wires that end beside it: ID_IR
  Register #(.width(1), .trigger("rising"), .Select("low")) register_1 (
    .D(1'b1), .Q(register_1_q), .clk(Halt));  // open: en, clr
  Multiplexer #(.select(1), .width(32), .disabled("Z"), .enable("false")) multiplexer_2 (
    .in0(multiplexer_1_out), .in1({EX_PC[31:28], id_ex_1_imm26_2, 2'b00}), .out(multiplexer_2_out), .sel(JMP));
  Hex_Digit_Display hex_digit_display_4 (.value(LedData[19:16]));  // open: dp
  Hex_Digit_Display hex_digit_display_5 (.value(LedData[15:12]));  // open: dp
  and and_1 (END, Stop, register_1_q);
  not not_1 (not_1_out, END);
  Multiplexer #(.select(1), .width(32), .disabled("Z"), .enable("false")) multiplexer_3 (
    .in0(multiplexer_2_out), .in1(v0), .out(multiplexer_3_out), .sel(JR));
  Hex_Digit_Display hex_digit_display_6 (.value(LedData[11:8]));  // open: dp
  Hex_Digit_Display hex_digit_display_7 (.value(LedData[7:4]));  // open: dp
  Clock #(.highDuration(1), .lowDuration(1)) clock_1 (.out(clock_1_out));
  // Probe on EX_PC[19:0]
  // Mips_Probe mips_probe_3: pin names not known; wires that end beside it: clock_1_out, EX_IR, CLK
  Register #(.width(32), .trigger("rising"), .Select("low")) PC (
    .D(multiplexer_3_out), .en(not_1_out), .Q(IF_PC), .clk(CLK));  // open: clr
  Hex_Digit_Display hex_digit_display_8 (.value(LedData[3:0]));  // open: dp
  Adder #(.width(32)) adder_1 (.a(IF_PC), .b(32'h4), .out(adder_1_out));  // open: cin, cout
  // Probe on \总周期数 
  // Probe on M_PC[19:0]
  // Mips_Probe mips_probe_4: pin names not known; wires that end beside it: MEM_IR
  // Probe on \总周期数 
  // Probe on \无条件分支数 
  // Probe on \条件分支成功数 
  // Probe on \插入气泡数 
  // Probe on \LoadUse次数 
  ROM #(.addrWidth(10), .dataWidth(32), .Select("high")) rom_1 (.addr(IF_PC[11:2]), .data(IF_IR));
  // Probe on IF_PC[11:0]
  // Probe on WB_PC[19:0]
  // Mips_Probe mips_probe_5: pin names not known; wires that end beside it: WB_IR
  // Mips_Probe mips_probe_6: pin names not known; wires that end beside it: IF_IR
  // Probe on EX_PC[11:0]
  // Probe on ID_PC[11:0]
  IF_ID if_id_1 (
    .CLK(CLK), .PC_4(adder_1_out), .IR(IF_IR), .PC(IF_PC), .PC_4_2(if_id_1_pc_4_2), .IR_2(ID_IR),
    .PC_2(ID_PC), .\同步清零_高电平有效 (1'b0), .\使能端_低电平有效 (END));  // open: MISS, MISS_2, Branch_Pre, Branch_Pre_2, Now_State_Pre, Now_State_Pre_2, Row_Pre, Row_Pre_2
  // Probe on M_PC[11:0]
  D_Flip_Flop #(.trigger("high"), .Pre_Clr_Positions("LEGACY"), .NegatePresetClear("false"), .enable("true"), .NewFFLayout("false")) d_ff_1 (.Q(d_ff_1_q));  // open: clk, D, Qn, preset, en, reset
  // Probe on 13'hc
  // Probe on WB_PC[11:0]
  Comparator #(.width(13), .mode("twosComplement")) comparator_1 (
    .a(CNT_num), .b(13'hc), .eq(comparator_1_eq), .lt(comparator_1_lt));  // open: gt
  Clock #(.highDuration(1), .lowDuration(1)) clock_2 (.out(clock_2_out));
  nand nand_1 (nand_1_out, d_ff_1_q, comparator_1_eq);
  Counter #(.width(13), .max('h1fff), .ongoal("stay"), .trigger("rising"), .behavior("old")) counter_1 (
    .count(comparator_1_lt), .Q(CNT_num), .clk(clock_2_out));  // open: load, D, carry, clr, preset
  \单周期硬布线控制器  \u_单周期硬布线控制器_1  (
    .Func(ID_IR[5:0]), .OP(ID_IR[31:26]), .ALU_OP(\单周期硬布线控制器_1_alu_op ), .MemToReg(\单周期硬布线控制器_1_memtoreg ),
    .MemWrite(\单周期硬布线控制器_1_memwrite ), .ALU_SRC(\单周期硬布线控制器_1_alu_src ), .RegWrite(\单周期硬布线控制器_1_regwrite ),
    .SysCALL(\单周期硬布线控制器_1_syscall ), .SignedExt(SignedExt), .RegDst(\单周期硬布线控制器_1_regdst ),
    .JR(\单周期硬布线控制器_1_jr ), .JMP(\单周期硬布线控制器_1_jmp ), .Beq(\单周期硬布线控制器_1_beq ), .JAL(\单周期硬布线控制器_1_jal ),
    .Bne(\单周期硬布线控制器_1_bne ), .LUI(\单周期硬布线控制器_1_lui ), .LH(\单周期硬布线控制器_1_lh ), .BLEZ(\单周期硬布线控制器_1_blez ));
  Multiplexer #(.select(1), .width(5), .disabled("Z"), .enable("false")) multiplexer_4 (
    .in0(ID_IR[25:21]), .in1(5'b00010), .out(multiplexer_4_out), .sel(\单周期硬布线控制器_1_syscall ));
  Multiplexer #(.select(1), .width(5), .disabled("Z"), .enable("false")) multiplexer_5 (
    .in0(ID_IR[20:16]), .in1(5'b00100), .out(multiplexer_5_out), .sel(\单周期硬布线控制器_1_syscall ));
  Multiplexer #(.select(1), .width(5), .disabled("Z"), .enable("false")) multiplexer_6 (
    .in0(ID_IR[20:16]), .in1(ID_IR[15:11]), .out(multiplexer_6_out), .sel(\单周期硬布线控制器_1_regdst ));
  Multiplexer #(.select(1), .width(5), .disabled("Z"), .enable("false")) multiplexer_7 (
    .in0(multiplexer_6_out), .in1({5{1'b1}}), .out(multiplexer_7_out), .sel(\单周期硬布线控制器_1_jal ));
  assign bit_extender_1_out = {{16{1'b0}}, ID_IR[15:0]};  // Bit_Extender bit_extender_1
  assign bit_extender_2_out = {{16{ID_IR[15]}}, ID_IR[15:0]};  // Bit_Extender bit_extender_2
  assign CLK = nand_1_out ? clock_2_out : 1'bz;  // Controlled_Buffer controlled_buffer_1
  Pull_Resistor #(.pull(1)) pull_resistor_1 (.node(CLK));
  not not_2 (not_2_out, END);
  MIPS_Regifile mips_regifile_1 (
    .Din(RDin), .Clk(CLK), .R1(mips_regifile_1_r1), .R2(mips_regifile_1_r2), .WE(RegWrite),
    .W_num(mem_wb_1_w_num_2), .R1_num(multiplexer_4_out), .R2_num(multiplexer_5_out));
  Multiplexer #(.select(1), .width(32), .disabled("Z"), .enable("false")) multiplexer_8 (
    .in0(bit_extender_1_out), .in1(bit_extender_2_out), .out(multiplexer_8_out), .sel(SignedExt));
  Register #(.width(16), .trigger("rising"), .Select("low")) register_2 (
    .D(adder_2_out), .en(not_2_out), .Q(register_2_q), .clk(CLK));  // open: clr
  Adder #(.width(16)) adder_2 (.a(16'h1), .b(register_2_q), .out(adder_2_out));  // open: cin, cout
  ID_EX id_ex_1 (
    .CLK(CLK), .RS(mips_regifile_1_r1), .RS_2(v0), .RT(mips_regifile_1_r2), .RT_2(id_ex_1_rt_2),
    .W_num(multiplexer_7_out), .W_num_2(id_ex_1_w_num_2), .PC_4(if_id_1_pc_4_2), .PC_4_2(id_ex_1_pc_4_2),
    .SIGN_IMM(multiplexer_8_out), .SIGN_IMM_2(id_ex_1_sign_imm_2), .IMM26(ID_IR[25:0]),
    .IMM26_2(id_ex_1_imm26_2), .PC(ID_PC), .PC_2(EX_PC), .JMP(\单周期硬布线控制器_1_jmp ), .JMP_2(JMP),
    .JR(\单周期硬布线控制器_1_jr ), .JR_2(JR), .BLEZ(\单周期硬布线控制器_1_blez ), .BLEZ_2(id_ex_1_blez_2),
    .LH(\单周期硬布线控制器_1_lh ), .LH_2(id_ex_1_lh_2), .LUI(\单周期硬布线控制器_1_lui ), .LUI_2(id_ex_1_lui_2),
    .BEQ(\单周期硬布线控制器_1_beq ), .BEQ_2(id_ex_1_beq_2), .BNE(\单周期硬布线控制器_1_bne ), .BNE_2(id_ex_1_bne_2),
    .MemToReg(\单周期硬布线控制器_1_memtoreg ), .MemToReg_2(id_ex_1_memtoreg_2), .MemWrite(\单周期硬布线控制器_1_memwrite ),
    .MemWrite_2(id_ex_1_memwrite_2), .ALU_OP(\单周期硬布线控制器_1_alu_op ), .ALU_OP_2(id_ex_1_alu_op_2),
    .ALU_SrcB(\单周期硬布线控制器_1_alu_src ), .ALU_SrcB_2(id_ex_1_alu_srcb_2), .RegWrite(\单周期硬布线控制器_1_regwrite ),
    .RegWrite_2(id_ex_1_regwrite_2), .JAL(\单周期硬布线控制器_1_jal ), .JAL_2(id_ex_1_jal_2),
    .Syscall(\单周期硬布线控制器_1_syscall ), .Syscall_2(id_ex_1_syscall_2), .\使能端_低电平有效 (END), .\同步清零_高电平有效 (1'b0),
    .IR(ID_IR), .IR_2(EX_IR));  // open: RsForward, RsForward_2, RtForward, RtForward_2, MISS, MISS_2, Branch_Pre, Branch_Pre_2, Now_State_Pre, Now_State_Pre_2, Row_Pre, Row_Pre_2
  Adder #(.width(16)) adder_3 (.a(adder_2_out), .b({16{1'b1}}), .out(\总周期数 ));  // open: cin, cout
  Comparator #(.width(32), .mode("twosComplement")) comparator_2 (
    .a(32'ha), .b(v0), .eq(comparator_2_eq));  // open: gt, lt
  and and_2 (Halt, id_ex_1_syscall_2, comparator_2_eq);
  and and_3 (and_3_out, id_ex_1_syscall_2, ~comparator_2_eq);  // AND_Gate
  Shifter #(.width(32), .shift("ll")) shifter_1 (.in(id_ex_1_sign_imm_2), .\dist (5'b00010), .out(shifter_1_out));
  Register #(.width(32), .trigger("rising"), .Select("low")) register_3 (
    .D(MDin), .en(LedOut), .Q(LedData), .clk(CLK));  // open: clr
  Comparator #(.width(32), .mode("twosComplement")) comparator_3 (
    .a(v0), .b({32{1'b0}}), .eq(comparator_3_eq), .lt(comparator_3_lt));  // open: gt
  Adder #(.width(32)) adder_4 (.a(shifter_1_out), .b(id_ex_1_pc_4_2), .out(adder_4_out));  // open: cin, cout
  or or_1 (or_1_out, comparator_3_eq, comparator_3_lt);
  Multiplexer #(.select(1), .width(32), .disabled("Z"), .enable("false")) multiplexer_9 (
    .in0(id_ex_1_rt_2), .in1(id_ex_1_sign_imm_2), .out(multiplexer_9_out), .sel(id_ex_1_alu_srcb_2));
  and and_4 (and_4_out, or_1_out, id_ex_1_blez_2);
  and and_5 (and_5_out, mips_alu_1_equal, id_ex_1_beq_2);
  and and_6 (and_6_out, ~mips_alu_1_equal, id_ex_1_bne_2);  // AND_Gate
  MIPS_ALU mips_alu_1 (
    .X(v0), .Y(multiplexer_9_out), .AluOP(id_ex_1_alu_op_2), .Equal(mips_alu_1_equal),
    .Result(mips_alu_1_result), .shamt(id_ex_1_imm26_2[10:6]));  // open: Result_2
  or or_2 (Branch, and_4_out, and_5_out, and_6_out);
  EX_MEM ex_mem_1 (
    .CLK(CLK), .W_num(id_ex_1_w_num_2), .W_num_2(ex_mem_1_w_num_2), .Write_Data(id_ex_1_rt_2),
    .Write_Data_2(MDin), .SIGN_IMM(id_ex_1_sign_imm_2), .SIGN_IMM_2(ex_mem_1_sign_imm_2),
    .ALU_RESULT(mips_alu_1_result), .ALU_RESULT_2(ex_mem_1_alu_result_2), .PC(EX_PC), .PC_2(M_PC),
    .LH(id_ex_1_lh_2), .LH_2(ex_mem_1_lh_2), .LUI(id_ex_1_lui_2), .LUI_2(ex_mem_1_lui_2),
    .MemToReg(id_ex_1_memtoreg_2), .MemToReg_2(ex_mem_1_memtoreg_2), .MemWrite(id_ex_1_memwrite_2),
    .MemWrite_2(MemWrite), .RegWrite(id_ex_1_regwrite_2), .RegWrite_2(ex_mem_1_regwrite_2),
    .PC_4(id_ex_1_pc_4_2), .PC_4_2(ex_mem_1_pc_4_2), .JAL(id_ex_1_jal_2), .JAL_2(ex_mem_1_jal_2),
    .\使能端_低电平有效 (END), .\同步清零_高电平有效 (1'b0), .Syscall(id_ex_1_syscall_2), .Syscall_2(ex_mem_1_syscall_2),
    .IR(EX_IR), .IR_2(MEM_IR), .Ledout(and_3_out), .Ledout_2(LedOut));
  RAM #(.addrWidth(10), .dataWidth(32), .bus("separate"), .Select("high")) ram_1 (
    .addr(ex_mem_1_alu_result_2[11:2]), .din(MDin), .data(ram_1_data), .str(MemWrite), .clk(CLK));  // open: sel, ld, clr
  MEM_WB mem_wb_1 (
    .CLK(CLK), .W_num(ex_mem_1_w_num_2), .W_num_2(mem_wb_1_w_num_2), .MEM_Data(ram_1_data),
    .MEM_Data_2(mem_wb_1_mem_data_2), .SIGN_IMM(ex_mem_1_sign_imm_2), .SIGN_IMM_2(mem_wb_1_sign_imm_2),
    .ALU_RESULT(ex_mem_1_alu_result_2), .ALU_RESULT_2(mem_wb_1_alu_result_2), .PC(M_PC), .PC_2(WB_PC),
    .LH(ex_mem_1_lh_2), .LH_2(mem_wb_1_lh_2), .LUI(ex_mem_1_lui_2), .LUI_2(mem_wb_1_lui_2),
    .MemToReg(ex_mem_1_memtoreg_2), .MemToReg_2(mem_wb_1_memtoreg_2), .RegWrite(ex_mem_1_regwrite_2),
    .RegWrite_2(RegWrite), .PC_4(ex_mem_1_pc_4_2), .PC_4_2(mem_wb_1_pc_4_2), .JAL(ex_mem_1_jal_2),
    .JAL_2(mem_wb_1_jal_2), .\使能端_低电平有效 (END), .\同步清零_高电平有效 (1'b0), .Syscall(ex_mem_1_syscall_2),
    .Syscall_2(Stop), .IR(MEM_IR), .IR_2(WB_IR));
  Multiplexer #(.select(1), .width(32), .disabled("Z"), .enable("false")) multiplexer_10 (
    .in0(mem_wb_1_alu_result_2), .in1(mem_wb_1_mem_data_2), .out(multiplexer_10_out),
    .sel(mem_wb_1_memtoreg_2));
  Multiplexer #(.select(1), .width(16), .disabled("Z"), .enable("false")) multiplexer_11 (
    .in0(multiplexer_10_out[15:0]), .in1(multiplexer_10_out[31:16]), .out(multiplexer_11_out),
    .sel(mem_wb_1_alu_result_2[1]));
  assign bit_extender_3_out = {{16{multiplexer_11_out[15]}}, multiplexer_11_out};  // Bit_Extender bit_extender_3
  Multiplexer #(.select(1), .width(32), .disabled("Z"), .enable("false")) multiplexer_12 (
    .in0(multiplexer_10_out), .in1(bit_extender_3_out), .out(multiplexer_12_out), .sel(mem_wb_1_lh_2));
  Shifter #(.width(32), .shift("ll")) shifter_2 (.in(mem_wb_1_sign_imm_2), .\dist (5'b10000), .out(shifter_2_out));
  Multiplexer #(.select(1), .width(32), .disabled("Z"), .enable("false")) multiplexer_13 (
    .in0(multiplexer_12_out), .in1(shifter_2_out), .out(multiplexer_13_out), .sel(mem_wb_1_lui_2));
  Multiplexer #(.select(1), .width(32), .disabled("Z"), .enable("false")) multiplexer_14 (
    .in0(multiplexer_13_out), .in1(mem_wb_1_pc_4_2), .out(RDin), .sel(mem_wb_1_jal_2));

  // Other names for the same wires on the sheet: MEM_PC[31:0] = M_PC

  // Notes on the sheet:
  //   中断源
  //   时空图监测，可删除
  //   中断等待指示
  //   数码管输出
  //   指令存储器
  //   contents of rom_1 (hex, n*v repeats v):
  //   20100000 20110000 20120000 20130000 36100000 36310001 36520002 36730003 ae100000 ae110004 ae120008
  //   ae13000c 2002000a 20110000 20120000 20130000 c
  //   控制位
  //   IR
  //   流水调试日志用
  //   暂停节拍，不能为0
  //   戳工具置1进入计数暂停模式，ctrl+k时钟自动运行到对应节拍暂停
  //   ctrl+k关闭时钟连续运行，将控制位置零，进入单步调试模式调试
  //   用这个时钟源需要去掉电路中的其他时钟源
  //   JMP
  //   JR
  //   OP
  //   OP
  //   Func
  //   Func
  //   rs
  //   rt
  //   rd
  //   imm16
  //   imm26
  //   Blez
  //   LH
  //   LUI
  //   Beq
  //   Bne
  //   AluOP
  //   AluSrcB
  //   RegWrite
  //   JAL
  //   RegDst
  //   Syscall
  //   可计数暂停的时钟源
  //   MemToReg
  //   MemWrite
  //   为方便自动评测，需要输出流水线各段保存的PC值，注意是PC不是PC+4，另外ID段寄存器写入信息，Mem段内存写入信息也要输出
  //   Blez
  //   LH
  //   LUI
  //   Beq
  //   Bne
  //   MemToReg
  //   MemWrite
  //   AluOP
  //   AluSrcB
  //   RegWrite
  //   JAL
  //   Syscall
  //   RS
  //   RT
  //   W#
  //   SIGN_IMM
  //   PC+4
  //   IMM26
  //   shamt
  //   LH
  //   LUI
  //   MemToReg
  //   MemWrite
  //   RegWrite
  //   JAL
  //   Syscall
  //   Ledout
  //   ALU_RESULT
  //   Write_Data
  //   W#
  //   SIGN_IMM
  //   PC+4
  //   LH
  //   LUI
  //   MemToReg
  //   RegWrite
  //   JAL
  //   Syscall
  //   MEM_Data
  //   W#
  //   SIGN_IMM
  //   PC+4
  //   ALU_RESULT
endmodule

module \气泡流水线  (
  output RegWrite,
  output MemWrite,
  output [31:0] IF_PC,
  output [31:0] ID_PC,
  output [31:0] EX_PC,
  output [31:0] M_PC,
  output [31:0] WB_PC,
  output [31:0] RDin,
  output [31:0] MDin,
  output [31:0] LedData
);

  wire and_2_out, and_4_out, and_5_out, and_6_out, and_7_out, Branch, CLK, clock_1_out, clock_2_out,
       comparator_1_eq, comparator_1_lt, comparator_2_eq, comparator_3_eq, comparator_3_lt, d_ff_1_q,
       DataHazzrd, END, ex_mem_1_jal_2, ex_mem_1_lh_2, ex_mem_1_lui_2, ex_mem_1_memtoreg_2,
       ex_mem_1_syscall_2, EX_RegWrite, Go, Halt, id_ex_1_alu_srcb_2, id_ex_1_beq_2, id_ex_1_blez_2,
       id_ex_1_bne_2, id_ex_1_jal_2, id_ex_1_lh_2, id_ex_1_lui_2, id_ex_1_memtoreg_2, id_ex_1_memwrite_2,
       id_ex_1_syscall_2, ID_EX_Flush, IF_ID_Flush, IR1, IR2, IR3, JMP, JR, LedOut, MEM_RegWrite,
       mem_wb_1_jal_2, mem_wb_1_lh_2, mem_wb_1_lui_2, mem_wb_1_memtoreg_2, mips_alu_1_equal, nand_1_out,
       not_1_out, not_2_out, not_3_out, or_1_out, or_4_out, register_1_q, RST, SignedExt, Stop, W1, W2, W3,
       \单周期硬布线控制器_1_alu_src , \单周期硬布线控制器_1_beq , \单周期硬布线控制器_1_blez , \单周期硬布线控制器_1_bne , \单周期硬布线控制器_1_jal ,
       \单周期硬布线控制器_1_jmp , \单周期硬布线控制器_1_jr , \单周期硬布线控制器_1_lh , \单周期硬布线控制器_1_lui , \单周期硬布线控制器_1_memtoreg ,
       \单周期硬布线控制器_1_memwrite , \单周期硬布线控制器_1_regdst , \单周期硬布线控制器_1_regwrite , \单周期硬布线控制器_1_syscall ,
       \源寄存器使用情况_1_r1_used , \源寄存器使用情况_1_r2_used ;
  wire [3:0] id_ex_1_alu_op_2, \单周期硬布线控制器_1_alu_op ;
  wire [4:0] EX_WriteReg_num, id_ex_1_imm26_2_2, mem_wb_1_w_num_2, MEM_WriteReg_num, multiplexer_4_out,
       multiplexer_7_out, R1, R2;
  wire [5:0] Func;
  wire [12:0] CNT_num;
  wire [15:0] adder_2_out, \LoadUse次数 , multiplexer_11_out, register_2_q, \总周期数 , \插入气泡数 , \无条件分支数 ,
       \条件分支成功数 ;
  wire [27:2] id_ex_1_imm26_2;
  wire [31:0] adder_1_out, adder_4_out, bit_extender_1_out, bit_extender_2_out, bit_extender_3_out, EX_IR,
       ex_mem_1_alu_result_2, ex_mem_1_pc_4_2, ex_mem_1_sign_imm_2, id_ex_1_pc_4_2, id_ex_1_rt_2,
       id_ex_1_sign_imm_2, if_id_1_pc_4_2, IF_IR, MEM_IR, mem_wb_1_alu_result_2, mem_wb_1_mem_data_2,
       mem_wb_1_pc_4_2, mem_wb_1_sign_imm_2, mips_alu_1_result, mips_regifile_1_r1, mips_regifile_1_r2,
       multiplexer_1_out, multiplexer_2_out, multiplexer_3_out, multiplexer_8_out, multiplexer_9_out,
       multiplexer_10_out, multiplexer_12_out, multiplexer_13_out, ram_1_data, shifter_1_out, shifter_2_out,
       v0, WB_IR;
  wire [31:6] ID_IR;

  Button \u_总复位  (.out(RST));
  Button _1 (.out(IR1));
  Button _2 (.out(IR2));
  Button _3 (.out(IR3));
  // Probe on \总周期数 
  // Probe on \总周期数 
  Button \u_继续运行  (.out(Go));
  LED #(.active("true")) led_1 (.in(W1));
  LED #(.active("true")) led_2 (.in(W2));
  LED #(.active("true")) led_3 (.in(W3));
  Hex_Digit_Display hex_digit_display_1 (.value(LedData[31:28]));  // open: dp
  // Probe on IF_PC[19:0]
  // Mips_Probe mips_probe_1: pin names not known; wires that end beside it: IF_IR
  Hex_Digit_Display hex_digit_display_2 (.value(LedData[27:24]));  // open: dp
  Hex_Digit_Display hex_digit_display_3 (.value(LedData[23:20]));  // open: dp
  // Probe on ID_PC[19:0]
  // Mips_Probe mips_probe_2: pin names not known; wires that end beside it: {ID_IR, Func}
  Register #(.width(1), .trigger("rising"), .Select("low")) register_1 (
    .D(1'b1), .Q(register_1_q), .clk(Halt));  // open: en, clr
  Multiplexer #(.select(1), .width(32), .disabled("Z"), .enable("false")) multiplexer_1 (
    .in0(adder_1_out), .in1(adder_4_out), .out(multiplexer_1_out), .sel(Branch));
  Hex_Digit_Display hex_digit_display_4 (.value(LedData[15:12]));  // open: dp
  Hex_Digit_Display hex_digit_display_5 (.value(LedData[19:16]));  // open: dp
  Multiplexer #(.select(1), .width(32), .disabled("Z"), .enable("false")) multiplexer_2 (
    .in0(multiplexer_1_out),
    .in1({EX_PC[31:28], id_ex_1_imm26_2[27:13], id_ex_1_imm26_2_2, id_ex_1_imm26_2[7:2], 2'b00}),
    .out(multiplexer_2_out), .sel(JMP));
  Multiplexer #(.select(1), .width(32), .disabled("Z"), .enable("false")) multiplexer_3 (
    .in0(multiplexer_2_out), .in1(v0), .out(multiplexer_3_out), .sel(JR));
  Hex_Digit_Display hex_digit_display_6 (.value(LedData[7:4]));  // open: dp
  Hex_Digit_Display hex_digit_display_7 (.value(LedData[11:8]));  // open: dp
  Clock #(.highDuration(1), .lowDuration(1)) clock_1 (.out(clock_1_out));
  // Probe on EX_PC[19:0]
  // Mips_Probe mips_probe_3: pin names not known; wires that end beside it: clock_1_out, EX_IR, CLK
  and and_1 (END, Stop, register_1_q);
  not not_1 (not_1_out, END);
  and and_2 (and_2_out, not_1_out, not_2_out);
  Hex_Digit_Display hex_digit_display_8 (.value(LedData[3:0]));  // open: dp
  \源寄存器使用情况  \u_源寄存器使用情况_1  (
    .OP0(ID_IR[26]), .OP1(ID_IR[27]), .OP2(ID_IR[28]), .OP3(ID_IR[29]), .OP4(ID_IR[30]), .OP5(ID_IR[31]),
    .F0(Func[0]), .F1(Func[1]), .F2(Func[2]), .F3(Func[3]), .F4(Func[4]), .F5(Func[5]),
    .R1_used(\源寄存器使用情况_1_r1_used ), .R2_used(\源寄存器使用情况_1_r2_used ));
  not not_2 (not_2_out, DataHazzrd);
  Register #(.width(32), .trigger("rising"), .Select("low")) PC (
    .D(multiplexer_3_out), .en(and_2_out), .Q(IF_PC), .clk(CLK));  // open: clr
  // Probe on \总周期数 
  // Probe on M_PC[19:0]
  // Mips_Probe mips_probe_4: pin names not known; wires that end beside it: MEM_IR
  Adder #(.width(32)) adder_1 (.a(IF_PC), .b(32'h4), .out(adder_1_out));  // open: cin, cout
  // Probe on \总周期数 
  // Probe on \无条件分支数 
  // Probe on \条件分支成功数 
  // Probe on \插入气泡数 
  // Probe on \LoadUse次数 
  ROM #(.addrWidth(10), .dataWidth(32), .Select("high")) rom_1 (.addr(IF_PC[11:2]), .data(IF_IR));
  // Probe on IF_PC[11:0]
  // Probe on WB_PC[19:0]
  // Mips_Probe mips_probe_5: pin names not known; wires that end beside it: WB_IR
  // Mips_Probe mips_probe_6: pin names not known; wires that end beside it: IF_IR
  or or_1 (or_1_out, DataHazzrd, END);
  // Probe on ID_PC[11:0]
  // Probe on EX_PC[11:0]
  \数据相关检测  \u_数据相关检测_1  (
    .R1_num(R1), .R2_num(R2), .EX_WriteReg_num(EX_WriteReg_num), .EX_RegWrite(EX_RegWrite),
    .MEM_WriteReg_num(MEM_WriteReg_num), .MEM_RegWrite(MEM_RegWrite), .R1_Used(\源寄存器使用情况_1_r1_used ),
    .R2_Used(\源寄存器使用情况_1_r2_used ), .DataHazzard(DataHazzrd));
  // Probe on M_PC[11:0]
  D_Flip_Flop #(.trigger("high"), .Pre_Clr_Positions("LEGACY"), .NegatePresetClear("false"), .enable("true"), .NewFFLayout("false")) d_ff_1 (.Q(d_ff_1_q));  // open: clk, D, Qn, preset, en, reset
  // Probe on 13'hc
  IF_ID if_id_1 (
    .CLK(CLK), .PC_4(adder_1_out), .IR(IF_IR), .PC(IF_PC), .PC_4_2(if_id_1_pc_4_2), .IR_2({ID_IR, Func}),
    .PC_2(ID_PC), .\同步清零_高电平有效 (IF_ID_Flush), .\使能端_低电平有效 (or_1_out));  // open: MISS, MISS_2, Branch_Pre, Branch_Pre_2, Now_State_Pre, Now_State_Pre_2, Row_Pre, Row_Pre_2
  // Probe on WB_PC[11:0]
  Comparator #(.width(13), .mode("twosComplement")) comparator_1 (
    .a(CNT_num), .b(13'hc), .eq(comparator_1_eq), .lt(comparator_1_lt));  // open: gt
  Clock #(.highDuration(1), .lowDuration(1)) clock_2 (.out(clock_2_out));
  nand nand_1 (nand_1_out, d_ff_1_q, comparator_1_eq);
  Counter #(.width(13), .max('h1fff), .ongoal("stay"), .trigger("rising"), .behavior("old")) counter_1 (
    .count(comparator_1_lt), .Q(CNT_num), .clk(clock_2_out));  // open: load, D, carry, clr, preset
  Multiplexer #(.select(1), .width(5), .disabled("Z"), .enable("false")) multiplexer_4 (
    .in0(ID_IR[20:16]), .in1(ID_IR[15:11]), .out(multiplexer_4_out), .sel(\单周期硬布线控制器_1_regdst ));
  assign CLK = nand_1_out ? clock_2_out : 1'bz;  // Controlled_Buffer controlled_buffer_1
  \单周期硬布线控制器  \u_单周期硬布线控制器_1  (
    .Func(Func), .OP(ID_IR[31:26]), .ALU_OP(\单周期硬布线控制器_1_alu_op ), .MemToReg(\单周期硬布线控制器_1_memtoreg ),
    .MemWrite(\单周期硬布线控制器_1_memwrite ), .ALU_SRC(\单周期硬布线控制器_1_alu_src ), .RegWrite(\单周期硬布线控制器_1_regwrite ),
    .SysCALL(\单周期硬布线控制器_1_syscall ), .SignedExt(SignedExt), .RegDst(\单周期硬布线控制器_1_regdst ),
    .JR(\单周期硬布线控制器_1_jr ), .JMP(\单周期硬布线控制器_1_jmp ), .Beq(\单周期硬布线控制器_1_beq ), .JAL(\单周期硬布线控制器_1_jal ),
    .Bne(\单周期硬布线控制器_1_bne ), .LUI(\单周期硬布线控制器_1_lui ), .LH(\单周期硬布线控制器_1_lh ), .BLEZ(\单周期硬布线控制器_1_blez ));
  Multiplexer #(.select(1), .width(5), .disabled("Z"), .enable("false")) multiplexer_5 (
    .in0(ID_IR[25:21]), .in1(5'b00010), .out(R1), .sel(\单周期硬布线控制器_1_syscall ));
  Multiplexer #(.select(1), .width(5), .disabled("Z"), .enable("false")) multiplexer_6 (
    .in0(ID_IR[20:16]), .in1(5'b00100), .out(R2), .sel(\单周期硬布线控制器_1_syscall ));
  Multiplexer #(.select(1), .width(5), .disabled("Z"), .enable("false")) multiplexer_7 (
    .in0(multiplexer_4_out), .in1({5{1'b1}}), .out(multiplexer_7_out), .sel(\单周期硬布线控制器_1_jal ));
  assign bit_extender_1_out = {{16{1'b0}}, {ID_IR[15:6], Func}};  // Bit_Extender bit_extender_1
  assign bit_extender_2_out = {{16{ID_IR[15]}}, {ID_IR[15:6], Func}};  // Bit_Extender bit_extender_2
  Pull_Resistor #(.pull(1)) pull_resistor_1 (.node(CLK));
  or or_2 (IF_ID_Flush, Branch, JR, JMP);
  not not_3 (not_3_out, END);
  MIPS_Regifile mips_regifile_1 (
    .Din(RDin), .Clk(CLK), .R1(mips_regifile_1_r1), .R2(mips_regifile_1_r2), .WE(RegWrite),
    .W_num(mem_wb_1_w_num_2), .R1_num(R1), .R2_num(R2));
  Register #(.width(16), .trigger("rising"), .Select("low")) register_2 (
    .D(adder_2_out), .en(not_3_out), .Q(register_2_q), .clk(CLK));  // open: clr
  or or_3 (ID_EX_Flush, IF_ID_Flush, DataHazzrd);
  Multiplexer #(.select(1), .width(32), .disabled("Z"), .enable("false")) multiplexer_8 (
    .in0(bit_extender_1_out), .in1(bit_extender_2_out), .out(multiplexer_8_out), .sel(SignedExt));
  Adder #(.width(16)) adder_2 (.a(16'h1), .b(register_2_q), .out(adder_2_out));  // open: cin, cout
  ID_EX id_ex_1 (
    .CLK(CLK), .RS(mips_regifile_1_r1), .RS_2(v0), .RT(mips_regifile_1_r2), .RT_2(id_ex_1_rt_2),
    .W_num(multiplexer_7_out), .W_num_2(EX_WriteReg_num), .PC_4(if_id_1_pc_4_2), .PC_4_2(id_ex_1_pc_4_2),
    .SIGN_IMM(multiplexer_8_out), .SIGN_IMM_2(id_ex_1_sign_imm_2), .IMM26({ID_IR[25:6], Func}),
    .IMM26_2({id_ex_1_imm26_2[27:13], id_ex_1_imm26_2_2, id_ex_1_imm26_2[7:2]}), .PC(ID_PC), .PC_2(EX_PC),
    .JMP(\单周期硬布线控制器_1_jmp ), .JMP_2(JMP), .JR(\单周期硬布线控制器_1_jr ), .JR_2(JR), .BLEZ(\单周期硬布线控制器_1_blez ),
    .BLEZ_2(id_ex_1_blez_2), .LH(\单周期硬布线控制器_1_lh ), .LH_2(id_ex_1_lh_2), .LUI(\单周期硬布线控制器_1_lui ),
    .LUI_2(id_ex_1_lui_2), .BEQ(\单周期硬布线控制器_1_beq ), .BEQ_2(id_ex_1_beq_2), .BNE(\单周期硬布线控制器_1_bne ),
    .BNE_2(id_ex_1_bne_2), .MemToReg(\单周期硬布线控制器_1_memtoreg ), .MemToReg_2(id_ex_1_memtoreg_2),
    .MemWrite(\单周期硬布线控制器_1_memwrite ), .MemWrite_2(id_ex_1_memwrite_2), .ALU_OP(\单周期硬布线控制器_1_alu_op ),
    .ALU_OP_2(id_ex_1_alu_op_2), .ALU_SrcB(\单周期硬布线控制器_1_alu_src ), .ALU_SrcB_2(id_ex_1_alu_srcb_2),
    .RegWrite(\单周期硬布线控制器_1_regwrite ), .RegWrite_2(EX_RegWrite), .JAL(\单周期硬布线控制器_1_jal ),
    .JAL_2(id_ex_1_jal_2), .Syscall(\单周期硬布线控制器_1_syscall ), .Syscall_2(id_ex_1_syscall_2), .\使能端_低电平有效 (END),
    .\同步清零_高电平有效 (ID_EX_Flush), .IR({ID_IR, Func}), .IR_2(EX_IR));  // open: RsForward, RsForward_2, RtForward, RtForward_2, MISS, MISS_2, Branch_Pre, Branch_Pre_2, Now_State_Pre, Now_State_Pre_2, Row_Pre, Row_Pre_2
  Adder #(.width(16)) adder_3 (.a(adder_2_out), .b({16{1'b1}}), .out(\总周期数 ));  // open: cin, cout
  Comparator #(.width(32), .mode("twosComplement")) comparator_2 (
    .a(32'ha), .b(v0), .eq(comparator_2_eq));  // open: gt, lt
  Register #(.width(32), .trigger("rising"), .Select("low")) register_3 (
    .D(MDin), .en(LedOut), .Q(LedData), .clk(CLK));  // open: clr
  and and_3 (Halt, id_ex_1_syscall_2, comparator_2_eq);
  and and_4 (and_4_out, id_ex_1_syscall_2, ~comparator_2_eq);  // AND_Gate
  Shifter #(.width(32), .shift("ll")) shifter_1 (.in(id_ex_1_sign_imm_2), .\dist (5'b00010), .out(shifter_1_out));
  Comparator #(.width(32), .mode("twosComplement")) comparator_3 (
    .a(v0), .b({32{1'b0}}), .eq(comparator_3_eq), .lt(comparator_3_lt));  // open: gt
  Multiplexer #(.select(1), .width(32), .disabled("Z"), .enable("false")) multiplexer_9 (
    .in0(id_ex_1_rt_2), .in1(id_ex_1_sign_imm_2), .out(multiplexer_9_out), .sel(id_ex_1_alu_srcb_2));
  Adder #(.width(32)) adder_4 (.a(shifter_1_out), .b(id_ex_1_pc_4_2), .out(adder_4_out));  // open: cin, cout
  or or_4 (or_4_out, comparator_3_eq, comparator_3_lt);
  and and_5 (and_5_out, or_4_out, id_ex_1_blez_2);
  and and_6 (and_6_out, mips_alu_1_equal, id_ex_1_beq_2);
  and and_7 (and_7_out, ~mips_alu_1_equal, id_ex_1_bne_2);  // AND_Gate
  MIPS_ALU mips_alu_1 (
    .X(v0), .Y(multiplexer_9_out), .AluOP(id_ex_1_alu_op_2), .Equal(mips_alu_1_equal),
    .Result(mips_alu_1_result), .shamt(id_ex_1_imm26_2_2));  // open: Result_2
  or or_5 (Branch, and_5_out, and_6_out, and_7_out);
  EX_MEM ex_mem_1 (
    .CLK(CLK), .W_num(EX_WriteReg_num), .W_num_2(MEM_WriteReg_num), .Write_Data(id_ex_1_rt_2),
    .Write_Data_2(MDin), .SIGN_IMM(id_ex_1_sign_imm_2), .SIGN_IMM_2(ex_mem_1_sign_imm_2),
    .ALU_RESULT(mips_alu_1_result), .ALU_RESULT_2(ex_mem_1_alu_result_2), .PC(EX_PC), .PC_2(M_PC),
    .LH(id_ex_1_lh_2), .LH_2(ex_mem_1_lh_2), .LUI(id_ex_1_lui_2), .LUI_2(ex_mem_1_lui_2),
    .MemToReg(id_ex_1_memtoreg_2), .MemToReg_2(ex_mem_1_memtoreg_2), .MemWrite(id_ex_1_memwrite_2),
    .MemWrite_2(MemWrite), .RegWrite(EX_RegWrite), .RegWrite_2(MEM_RegWrite), .PC_4(id_ex_1_pc_4_2),
    .PC_4_2(ex_mem_1_pc_4_2), .JAL(id_ex_1_jal_2), .JAL_2(ex_mem_1_jal_2), .\使能端_低电平有效 (END),
    .\同步清零_高电平有效 (1'b0), .Syscall(id_ex_1_syscall_2), .Syscall_2(ex_mem_1_syscall_2), .IR(EX_IR),
    .IR_2(MEM_IR), .Ledout(and_4_out), .Ledout_2(LedOut));
  RAM #(.addrWidth(10), .dataWidth(32), .bus("separate"), .Select("high")) ram_1 (
    .addr(ex_mem_1_alu_result_2[11:2]), .din(MDin), .data(ram_1_data), .str(MemWrite), .clk(CLK));  // open: sel, ld, clr
  MEM_WB mem_wb_1 (
    .CLK(CLK), .W_num(MEM_WriteReg_num), .W_num_2(mem_wb_1_w_num_2), .MEM_Data(ram_1_data),
    .MEM_Data_2(mem_wb_1_mem_data_2), .SIGN_IMM(ex_mem_1_sign_imm_2), .SIGN_IMM_2(mem_wb_1_sign_imm_2),
    .ALU_RESULT(ex_mem_1_alu_result_2), .ALU_RESULT_2(mem_wb_1_alu_result_2), .PC(M_PC), .PC_2(WB_PC),
    .LH(ex_mem_1_lh_2), .LH_2(mem_wb_1_lh_2), .LUI(ex_mem_1_lui_2), .LUI_2(mem_wb_1_lui_2),
    .MemToReg(ex_mem_1_memtoreg_2), .MemToReg_2(mem_wb_1_memtoreg_2), .RegWrite(MEM_RegWrite),
    .RegWrite_2(RegWrite), .PC_4(ex_mem_1_pc_4_2), .PC_4_2(mem_wb_1_pc_4_2), .JAL(ex_mem_1_jal_2),
    .JAL_2(mem_wb_1_jal_2), .\使能端_低电平有效 (END), .\同步清零_高电平有效 (1'b0), .Syscall(ex_mem_1_syscall_2),
    .Syscall_2(Stop), .IR(MEM_IR), .IR_2(WB_IR));
  Multiplexer #(.select(1), .width(32), .disabled("Z"), .enable("false")) multiplexer_10 (
    .in0(mem_wb_1_alu_result_2), .in1(mem_wb_1_mem_data_2), .out(multiplexer_10_out),
    .sel(mem_wb_1_memtoreg_2));
  Multiplexer #(.select(1), .width(16), .disabled("Z"), .enable("false")) multiplexer_11 (
    .in0(multiplexer_10_out[15:0]), .in1(multiplexer_10_out[31:16]), .out(multiplexer_11_out),
    .sel(mem_wb_1_alu_result_2[1]));
  assign bit_extender_3_out = {{16{multiplexer_11_out[15]}}, multiplexer_11_out};  // Bit_Extender bit_extender_3
  Multiplexer #(.select(1), .width(32), .disabled("Z"), .enable("false")) multiplexer_12 (
    .in0(multiplexer_10_out), .in1(bit_extender_3_out), .out(multiplexer_12_out), .sel(mem_wb_1_lh_2));
  Shifter #(.width(32), .shift("ll")) shifter_2 (.in(mem_wb_1_sign_imm_2), .\dist (5'b10000), .out(shifter_2_out));
  Multiplexer #(.select(1), .width(32), .disabled("Z"), .enable("false")) multiplexer_13 (
    .in0(multiplexer_12_out), .in1(shifter_2_out), .out(multiplexer_13_out), .sel(mem_wb_1_lui_2));
  Multiplexer #(.select(1), .width(32), .disabled("Z"), .enable("false")) multiplexer_14 (
    .in0(multiplexer_13_out), .in1(mem_wb_1_pc_4_2), .out(RDin), .sel(mem_wb_1_jal_2));

  // Other names for the same wires on the sheet: ID_IR[5:0] = Func; OP[5:0] = ID_IR[31:26]; MEM_PC[31:0] = M_PC;
  //   Stall = DataHazzrd

  // Notes on the sheet:
  //   中断源
  //   时空图监测，可删除
  //   中断等待指示
  //   数码管输出
  //   指令存储器
  //   R1_used
  //   R2_used
  //   contents of rom_1 (hex, n*v repeats v):
  //   20110001 8000c05 20110001 20120002 20130003 8000c09 20110001 20120002 20130003 8000c0d 20110001
  //   20120002 20130003 8000c11 20110001 20120002 20130003 c000cf6 20100001 20110001 118fc0 112020
  //   20020022 c 118882 12200001 8000c15 112020 20020022 c 20110001 118880 112020 20020022 c 12200001
  //   8000c1f 20110001 118fc0 112020 20020022 c 1188c3 112020 20020022 c 118903 112020 20020022 c 118903
  //   112020 20020022 c 118903 112020 20020022 c 118903 112020 20020022 c 118903 112020 20020022 c 118903
  //   112020 20020022 c 118903 112020 20020022 c 20100001 109fc0 139fc3 8021 2012000c 24160003 26100001
  //   3210000f 20080008 20090001 139900 2709825 132020 20020022 c 1094022 1500fff9 22100001 2018000f
  //   2188024 108700 20080008 20090001 139902 2709825 132021 20020022 c 1094022 1500fff9 108702 2c9b022
  //   12c00001 8000c50 4020 1084027 84400 3508ffff 82021 20020022 c 2010ffff 20110000 ae300000 22100001
  //   22310004 ae300000 22100001 22310004 ae300000 22100001 22310004 ae300000 22100001 22310004 ae300000
  //   22100001 22310004 ae300000 22100001 22310004 ae300000 22100001 22310004 ae300000 22100001 22310004
  //   ae300000 22100001 22310004 ae300000 22100001 22310004 ae300000 22100001 22310004 ae300000 22100001
  //   22310004 ae300000 22100001 22310004 ae300000 22100001 22310004 ae300000 22100001 22310004 ae300000
  //   22100001 22310004 22100001 8020 2011003c 8e130000 8e340000 274402a 11000002 ae330000 ae140000
  //   2231fffc 1611fff8 102020 20020022 c 22100004 2011003c 1611fff2 20020032 c 200b0008 3c11fedc 3631ffff
  //   112020 20020022 c 3c11ba98 112020 c 3c117654 112020 c 3c113210 112020 c 216bffff 1560fff0 20020032 c
  //   2008ffff 20090000 20111997 112020 20020022 c 2288820 2e291949 1120fffa 20020032 c 20090000 200b0010
  //   34118483 20120404 118c00 129400 36318281 22520404 ad310000 2328820 21290004 216bffff 1560fffb
  //   200b0020 20090000 85310000 112020 20020022 c 21290002 216bffff 1560fff9 20020032 c 2011fff1 112020
  //   20020022 c 22310001 1a20fffb 2002000a c 20100000 22100001 102020 20020022 c 22100002 102020 20020022
  //   c 22100003 102020 20020022 c 22100004 102020 20020022 c 22100005 102020 20020022 c 22100006 102020
  //   20020022 c 22100007 102020 20020022 c 22100008 102020 20020022 20020022 c 3e00008
  //   控制位
  //   流水调试日志用
  //   暂停节拍，不能为0
  //   IR
  //   戳工具置1进入计数暂停模式，ctrl+k时钟自动运行到对应节拍暂停
  //   ctrl+k关闭时钟连续运行，将控制位置零，进入单步调试模式调试
  //   用这个时钟源需要去掉电路中的其他时钟源
  //   OP
  //   Func
  //   rs
  //   rt
  //   rd
  //   JMP
  //   JR
  //   OP
  //   Func
  //   Syscall
  //   imm16
  //   imm26
  //   可计数暂停的时钟源
  //   Blez
  //   LH
  //   LUI
  //   Beq
  //   Bne
  //   MemToReg
  //   MemWrite
  //   AluOP
  //   AluSrcB
  //   RegWrite
  //   JAL
  //   RegDst
  //   为方便自动评测，需要输出流水线各段保存的PC值，注意是PC不是PC+4，另外ID段寄存器写入信息，Mem段内存写入信息也要输出
  //   Blez
  //   LH
  //   LUI
  //   Beq
  //   Bne
  //   MemToReg
  //   MemWrite
  //   AluOP
  //   AluSrcB
  //   RegWrite
  //   JAL
  //   Syscall
  //   RS
  //   RT
  //   W#
  //   SIGN_IMM
  //   PC+4
  //   IMM26
  //   shamt
  //   LH
  //   LUI
  //   MemToReg
  //   MemWrite
  //   RegWrite
  //   JAL
  //   Syscall
  //   Ledout
  //   ALU_RESULT
  //   Write_Data
  //   W#
  //   SIGN_IMM
  //   PC+4
  //   LH
  //   LUI
  //   MemToReg
  //   RegWrite
  //   JAL
  //   Syscall
  //   ALU_RESULT
  //   MEM_Data
  //   W#
  //   SIGN_IMM
  //   PC+4
endmodule
module \重定向流水线  (
  output RegWrite,
  output MemWrite,
  output [31:0] IF_PC,
  output [31:0] ID_PC,
  output [31:0] EX_PC,
  output [31:0] M_PC,
  output [31:0] WB_PC,
  output [31:0] RDin,
  output [31:0] MDin,
  output [31:0] LedData
);

  wire and_2_out, and_4_out, and_5_out, and_6_out, and_7_out, Branch, CLK, clock_1_out, clock_2_out,
       comparator_1_eq, comparator_1_lt, comparator_2_eq, comparator_3_eq, comparator_3_lt, d_ff_1_q,
       DataHazzard, END, ex_mem_1_jal_2, ex_mem_1_lh_2, ex_mem_1_lui_2, ex_mem_1_memtoreg_2,
       ex_mem_1_syscall_2, EX_MemToReg, EX_RegWrite, Go, Halt, id_ex_1_alu_srcb_2, id_ex_1_beq_2,
       id_ex_1_blez_2, id_ex_1_bne_2, id_ex_1_jal_2, id_ex_1_lh_2, id_ex_1_lui_2, id_ex_1_memwrite_2,
       id_ex_1_syscall_2, ID_EX_Flush, IF_ID_Flush, IR1, IR2, IR3, JMP, JR, LedOut, LoadUse, MEM_RegWrite,
       MEM_Syscall, mem_wb_1_jal_2, mem_wb_1_lh_2, mem_wb_1_lui_2, mem_wb_1_memtoreg_2, mips_alu_1_equal,
       nand_1_out, not_1_out, not_2_out, not_3_out, or_1_out, or_4_out, register_1_q, RST, SignedExt, W1, W2,
       W3, \单周期硬布线控制器_1_alu_src , \单周期硬布线控制器_1_beq , \单周期硬布线控制器_1_blez , \单周期硬布线控制器_1_bne ,
       \单周期硬布线控制器_1_jal , \单周期硬布线控制器_1_jmp , \单周期硬布线控制器_1_jr , \单周期硬布线控制器_1_lh , \单周期硬布线控制器_1_lui ,
       \单周期硬布线控制器_1_memtoreg , \单周期硬布线控制器_1_memwrite , \单周期硬布线控制器_1_regdst , \单周期硬布线控制器_1_regwrite ,
       \单周期硬布线控制器_1_syscall , \源寄存器使用情况_1_r1_used , \源寄存器使用情况_1_r2_used ;
  wire [1:0] id_ex_1_rsforward_2, id_ex_1_rtforward_2, ID_RsForward, ID_RtForward;
  wire [3:0] id_ex_1_alu_op_2, \单周期硬布线控制器_1_alu_op ;
  wire [4:0] EX_WriteReg_num, id_ex_1_imm26_2_2, mem_wb_1_w_num_2, MEM_WriteReg_num, multiplexer_4_out,
       multiplexer_7_out, R1, R2;
  wire [5:0] Func;
  wire [12:0] CNT_num;
  wire [15:0] adder_2_out, \LoadUse次数 , multiplexer_14_out, register_2_q, \总周期数 , \插入气泡数 , \无条件分支数 ,
       \条件分支成功数 ;
  wire [27:2] id_ex_1_imm26_2;
  wire [31:0] adder_1_out, adder_4_out, bit_extender_1_out, bit_extender_2_out, bit_extender_3_out, EX_IR,
       ex_mem_1_alu_result_2, ex_mem_1_pc_4_2, ex_mem_1_sign_imm_2, id_ex_1_pc_4_2, id_ex_1_rs_2,
       id_ex_1_rt_2, id_ex_1_sign_imm_2, if_id_1_pc_4_2, IF_IR, MEM_ALU, MEM_IR, mem_wb_1_alu_result_2,
       mem_wb_1_mem_data_2, mem_wb_1_pc_4_2, mem_wb_1_sign_imm_2, mips_alu_1_result, mips_regifile_1_r1,
       mips_regifile_1_r2, multiplexer_1_out, multiplexer_2_out, multiplexer_3_out, multiplexer_8_out,
       multiplexer_9_out, multiplexer_10_out, multiplexer_11_out, multiplexer_13_out, multiplexer_15_out,
       multiplexer_16_out, ram_1_data, shifter_1_out, shifter_2_out, v0, WB_IR;
  wire [31:6] ID_IR;

  Button \u_总复位  (.out(RST));
  Button _1 (.out(IR1));
  Button _2 (.out(IR2));
  Button _3 (.out(IR3));
  // Probe on \总周期数 
  // Probe on \总周期数 
  Button \u_继续运行  (.out(Go));
  LED #(.active("true")) led_1 (.in(W1));
  LED #(.active("true")) led_2 (.in(W2));
  LED #(.active("true")) led_3 (.in(W3));
  Hex_Digit_Display hex_digit_display_1 (.value(LedData[31:28]));  // open: dp
  // Probe on IF_PC[19:0]
  // Mips_Probe mips_probe_1: pin names not known; wires that end beside it: IF_IR
  Hex_Digit_Display hex_digit_display_2 (.value(LedData[27:24]));  // open: dp
  Hex_Digit_Display hex_digit_display_3 (.value(LedData[23:20]));  // open: dp
  // Probe on ID_PC[19:0]
  // Mips_Probe mips_probe_2: pin names not known; wires that end beside it: {ID_IR, Func}
  Register #(.width(1), .trigger("rising"), .Select("low")) register_1 (
    .D(1'b1), .Q(register_1_q), .clk(Halt), .clr(Go));  // open: en
  Multiplexer #(.select(1), .width(32), .disabled("Z"), .enable("false")) multiplexer_1 (
    .in0(adder_1_out), .in1(adder_4_out), .out(multiplexer_1_out), .sel(Branch));
  Multiplexer #(.select(1), .width(32), .disabled("Z"), .enable("false")) multiplexer_2 (
    .in0(multiplexer_1_out),
    .in1({EX_PC[31:28], id_ex_1_imm26_2[27:13], id_ex_1_imm26_2_2, id_ex_1_imm26_2[7:2], 2'b00}),
    .out(multiplexer_2_out), .sel(JMP));
  Hex_Digit_Display hex_digit_display_4 (.value(LedData[19:16]));  // open: dp
  Hex_Digit_Display hex_digit_display_5 (.value(LedData[15:12]));  // open: dp
  and and_1 (END, MEM_Syscall, register_1_q);
  Multiplexer #(.select(1), .width(32), .disabled("Z"), .enable("false")) multiplexer_3 (
    .in0(multiplexer_2_out), .in1(multiplexer_9_out), .out(multiplexer_3_out), .sel(JR));
  Hex_Digit_Display hex_digit_display_6 (.value(LedData[11:8]));  // open: dp
  Hex_Digit_Display hex_digit_display_7 (.value(LedData[7:4]));  // open: dp
  Clock #(.highDuration(1), .lowDuration(1)) clock_1 (.out(clock_1_out));
  // Probe on EX_PC[19:0]
  // Mips_Probe mips_probe_3: pin names not known; wires that end beside it: clock_1_out, EX_IR, CLK
  not not_1 (not_1_out, END);
  and and_2 (and_2_out, not_1_out, not_2_out);
  Register #(.width(32), .trigger("rising"), .Select("low")) PC (
    .D(multiplexer_3_out), .en(and_2_out), .Q(IF_PC), .clk(CLK));  // open: clr
  Hex_Digit_Display hex_digit_display_8 (.value(LedData[3:0]));  // open: dp
  \源寄存器使用情况  \u_源寄存器使用情况_1  (
    .OP0(ID_IR[26]), .OP1(ID_IR[27]), .OP2(ID_IR[28]), .OP3(ID_IR[29]), .OP4(ID_IR[30]), .OP5(ID_IR[31]),
    .F0(Func[0]), .F1(Func[1]), .F2(Func[2]), .F3(Func[3]), .F4(Func[4]), .F5(Func[5]),
    .R1_used(\源寄存器使用情况_1_r1_used ), .R2_used(\源寄存器使用情况_1_r2_used ));
  not not_2 (not_2_out, LoadUse);
  // Probe on \总周期数 
  // Probe on M_PC[19:0]
  // Mips_Probe mips_probe_4: pin names not known; wires that end beside it: MEM_IR
  Adder #(.width(32)) adder_1 (.a(IF_PC), .b(32'h4), .out(adder_1_out));  // open: cin, cout
  // Probe on \总周期数 
  // Probe on \无条件分支数 
  // Probe on \条件分支成功数 
  // Probe on \插入气泡数 
  // Probe on \LoadUse次数 
  ROM #(.addrWidth(10), .dataWidth(32), .Select("high")) rom_1 (.addr(IF_PC[11:2]), .data(IF_IR));
  or or_1 (or_1_out, LoadUse, END);
  // Probe on IF_PC[11:0]
  // Probe on WB_PC[19:0]
  // Mips_Probe mips_probe_5: pin names not known; wires that end beside it: WB_IR
  // Mips_Probe mips_probe_6: pin names not known; wires that end beside it: IF_IR
  // Probe on ID_PC[11:0]
  // Probe on EX_PC[11:0]
  \数据相关检测_重定向  \u_数据相关检测_重定向_1  (
    .R1_Used(\源寄存器使用情况_1_r1_used ), .R2_Used(\源寄存器使用情况_1_r2_used ), .DataHazzard(DataHazzard), .R1_num(R1),
    .R2_num(R2), .LoadUse(LoadUse), .EX_WriteReg_num(EX_WriteReg_num), .EX_RegWrite(EX_RegWrite),
    .MEM_WriteReg_num(MEM_WriteReg_num), .MEM_RegWrite(MEM_RegWrite), .EX_MemToReg(EX_MemToReg),
    .RsForward(ID_RsForward), .RtForward(ID_RtForward));
  IF_ID if_id_1 (
    .CLK(CLK), .PC_4(adder_1_out), .IR(IF_IR), .PC(IF_PC), .PC_4_2(if_id_1_pc_4_2), .IR_2({ID_IR, Func}),
    .PC_2(ID_PC), .\同步清零_高电平有效 (IF_ID_Flush), .\使能端_低电平有效 (or_1_out));  // open: MISS, MISS_2, Branch_Pre, Branch_Pre_2, Now_State_Pre, Now_State_Pre_2, Row_Pre, Row_Pre_2
  // Probe on M_PC[11:0]
  D_Flip_Flop #(.trigger("high"), .Pre_Clr_Positions("LEGACY"), .NegatePresetClear("false"), .enable("true"), .NewFFLayout("false")) d_ff_1 (.Q(d_ff_1_q));  // open: clk, D, Qn, preset, en, reset
  // Probe on 13'h8f8
  // Probe on WB_PC[11:0]
  Comparator #(.width(13), .mode("twosComplement")) comparator_1 (
    .a(CNT_num), .b(13'h8f8), .eq(comparator_1_eq), .lt(comparator_1_lt));  // open: gt
  Clock #(.highDuration(1), .lowDuration(1)) clock_2 (.out(clock_2_out));
  nand nand_1 (nand_1_out, d_ff_1_q, comparator_1_eq);
  Counter #(.width(13), .max('h1fff), .ongoal("stay"), .trigger("rising"), .behavior("old")) counter_1 (
    .count(comparator_1_lt), .Q(CNT_num), .clk(clock_2_out));  // open: load, D, carry, clr, preset
  Multiplexer #(.select(1), .width(5), .disabled("Z"), .enable("false")) multiplexer_4 (
    .in0(ID_IR[20:16]), .in1(ID_IR[15:11]), .out(multiplexer_4_out), .sel(\单周期硬布线控制器_1_regdst ));
  assign bit_extender_1_out = {{16{1'b0}}, {ID_IR[15:6], Func}};  // Bit_Extender bit_extender_1
  assign bit_extender_2_out = {{16{ID_IR[15]}}, {ID_IR[15:6], Func}};  // Bit_Extender bit_extender_2
  assign CLK = nand_1_out ? clock_2_out : 1'bz;  // Controlled_Buffer controlled_buffer_1
  or or_2 (IF_ID_Flush, Branch, JR, JMP);
  \单周期硬布线控制器  \u_单周期硬布线控制器_1  (
    .Func(Func), .OP(ID_IR[31:26]), .ALU_OP(\单周期硬布线控制器_1_alu_op ), .MemToReg(\单周期硬布线控制器_1_memtoreg ),
    .MemWrite(\单周期硬布线控制器_1_memwrite ), .ALU_SRC(\单周期硬布线控制器_1_alu_src ), .RegWrite(\单周期硬布线控制器_1_regwrite ),
    .SysCALL(\单周期硬布线控制器_1_syscall ), .SignedExt(SignedExt), .RegDst(\单周期硬布线控制器_1_regdst ),
    .JR(\单周期硬布线控制器_1_jr ), .JMP(\单周期硬布线控制器_1_jmp ), .Beq(\单周期硬布线控制器_1_beq ), .JAL(\单周期硬布线控制器_1_jal ),
    .Bne(\单周期硬布线控制器_1_bne ), .LUI(\单周期硬布线控制器_1_lui ), .LH(\单周期硬布线控制器_1_lh ), .BLEZ(\单周期硬布线控制器_1_blez ));
  Multiplexer #(.select(1), .width(5), .disabled("Z"), .enable("false")) multiplexer_5 (
    .in0(ID_IR[25:21]), .in1(5'b00010), .out(R1), .sel(\单周期硬布线控制器_1_syscall ));
  Multiplexer #(.select(1), .width(5), .disabled("Z"), .enable("false")) multiplexer_6 (
    .in0(ID_IR[20:16]), .in1(5'b00100), .out(R2), .sel(\单周期硬布线控制器_1_syscall ));
  Multiplexer #(.select(1), .width(5), .disabled("Z"), .enable("false")) multiplexer_7 (
    .in0(multiplexer_4_out), .in1({5{1'b1}}), .out(multiplexer_7_out), .sel(\单周期硬布线控制器_1_jal ));
  Pull_Resistor #(.pull(1)) pull_resistor_1 (.node(CLK));
  not not_3 (not_3_out, END);
  or or_3 (ID_EX_Flush, IF_ID_Flush, LoadUse);
  MIPS_Regifile mips_regifile_1 (
    .Din(RDin), .Clk(CLK), .R1(mips_regifile_1_r1), .R2(mips_regifile_1_r2), .WE(RegWrite),
    .W_num(mem_wb_1_w_num_2), .R1_num(R1), .R2_num(R2));
  Multiplexer #(.select(1), .width(32), .disabled("Z"), .enable("false")) multiplexer_8 (
    .in0(bit_extender_1_out), .in1(bit_extender_2_out), .out(multiplexer_8_out), .sel(SignedExt));
  Register #(.width(16), .trigger("rising"), .Select("low")) register_2 (
    .D(adder_2_out), .en(not_3_out), .Q(register_2_q), .clk(CLK));  // open: clr
  Adder #(.width(16)) adder_2 (.a(16'h1), .b(register_2_q), .out(adder_2_out));  // open: cin, cout
  ID_EX id_ex_1 (
    .CLK(CLK), .RS(mips_regifile_1_r1), .RS_2(id_ex_1_rs_2), .RT(mips_regifile_1_r2), .RT_2(id_ex_1_rt_2),
    .W_num(multiplexer_7_out), .W_num_2(EX_WriteReg_num), .PC_4(if_id_1_pc_4_2), .PC_4_2(id_ex_1_pc_4_2),
    .SIGN_IMM(multiplexer_8_out), .SIGN_IMM_2(id_ex_1_sign_imm_2), .IMM26({ID_IR[25:6], Func}),
    .IMM26_2({id_ex_1_imm26_2[27:13], id_ex_1_imm26_2_2, id_ex_1_imm26_2[7:2]}), .PC(ID_PC), .PC_2(EX_PC),
    .JMP(\单周期硬布线控制器_1_jmp ), .JMP_2(JMP), .JR(\单周期硬布线控制器_1_jr ), .JR_2(JR), .BLEZ(\单周期硬布线控制器_1_blez ),
    .BLEZ_2(id_ex_1_blez_2), .LH(\单周期硬布线控制器_1_lh ), .LH_2(id_ex_1_lh_2), .LUI(\单周期硬布线控制器_1_lui ),
    .LUI_2(id_ex_1_lui_2), .BEQ(\单周期硬布线控制器_1_beq ), .BEQ_2(id_ex_1_beq_2), .BNE(\单周期硬布线控制器_1_bne ),
    .BNE_2(id_ex_1_bne_2), .MemToReg(\单周期硬布线控制器_1_memtoreg ), .MemToReg_2(EX_MemToReg),
    .MemWrite(\单周期硬布线控制器_1_memwrite ), .MemWrite_2(id_ex_1_memwrite_2), .ALU_OP(\单周期硬布线控制器_1_alu_op ),
    .ALU_OP_2(id_ex_1_alu_op_2), .ALU_SrcB(\单周期硬布线控制器_1_alu_src ), .ALU_SrcB_2(id_ex_1_alu_srcb_2),
    .RegWrite(\单周期硬布线控制器_1_regwrite ), .RegWrite_2(EX_RegWrite), .JAL(\单周期硬布线控制器_1_jal ),
    .JAL_2(id_ex_1_jal_2), .Syscall(\单周期硬布线控制器_1_syscall ), .Syscall_2(id_ex_1_syscall_2), .\使能端_低电平有效 (END),
    .\同步清零_高电平有效 (ID_EX_Flush), .IR({ID_IR, Func}), .IR_2(EX_IR), .RsForward(ID_RsForward),
    .RsForward_2(id_ex_1_rsforward_2), .RtForward(ID_RtForward), .RtForward_2(id_ex_1_rtforward_2));  // open: MISS, MISS_2, Branch_Pre, Branch_Pre_2, Now_State_Pre, Now_State_Pre_2, Row_Pre, Row_Pre_2
  Adder #(.width(16)) adder_3 (.a(adder_2_out), .b({16{1'b1}}), .out(\总周期数 ));  // open: cin, cout
  Multiplexer #(.select(2), .width(32), .disabled("Z"), .enable("false")) multiplexer_9 (
    .in0(id_ex_1_rs_2), .in1(MEM_ALU), .in2(RDin), .in3(MEM_ALU), .out(multiplexer_9_out),
    .sel(id_ex_1_rsforward_2));
  Multiplexer #(.select(2), .width(32), .disabled("Z"), .enable("false")) multiplexer_10 (
    .in0(id_ex_1_rt_2), .in1(MEM_ALU), .in2(RDin), .in3(MEM_ALU), .out(multiplexer_10_out),
    .sel(id_ex_1_rtforward_2));
  Comparator #(.width(32), .mode("twosComplement")) comparator_2 (
    .a(32'ha), .b(v0), .eq(comparator_2_eq));  // open: gt, lt
  Shifter #(.width(32), .shift("ll")) shifter_1 (.in(id_ex_1_sign_imm_2), .\dist (5'b00010), .out(shifter_1_out));
  Register #(.width(32), .trigger("rising"), .Select("low")) register_3 (
    .D(MDin), .en(LedOut), .Q(LedData), .clk(CLK));  // open: clr
  Comparator #(.width(32), .mode("twosComplement")) comparator_3 (
    .a(v0), .b({32{1'b0}}), .eq(comparator_3_eq), .lt(comparator_3_lt));  // open: gt
  and and_3 (Halt, id_ex_1_syscall_2, comparator_2_eq);
  and and_4 (and_4_out, id_ex_1_syscall_2, ~comparator_2_eq);  // AND_Gate
  Register #(.width(32), .trigger("falling"), .Select("low")) register_4 (
    .D(multiplexer_9_out), .Q(v0), .clk(CLK));  // open: en, clr
  Adder #(.width(32)) adder_4 (.a(shifter_1_out), .b(id_ex_1_pc_4_2), .out(adder_4_out));  // open: cin, cout
  or or_4 (or_4_out, comparator_3_eq, comparator_3_lt);
  Multiplexer #(.select(1), .width(32), .disabled("Z"), .enable("false")) multiplexer_11 (
    .in0(multiplexer_10_out), .in1(id_ex_1_sign_imm_2), .out(multiplexer_11_out), .sel(id_ex_1_alu_srcb_2));
  and and_5 (and_5_out, or_4_out, id_ex_1_blez_2);
  MIPS_ALU mips_alu_1 (
    .X(multiplexer_9_out), .Y(multiplexer_11_out), .AluOP(id_ex_1_alu_op_2), .Equal(mips_alu_1_equal),
    .Result(mips_alu_1_result), .shamt(id_ex_1_imm26_2_2));  // open: Result_2
  and and_6 (and_6_out, mips_alu_1_equal, id_ex_1_beq_2);
  and and_7 (and_7_out, ~mips_alu_1_equal, id_ex_1_bne_2);  // AND_Gate
  Shifter #(.width(32), .shift("ll")) shifter_2 (.in(id_ex_1_sign_imm_2), .\dist (5'b10000), .out(shifter_2_out));
  or or_5 (Branch, and_5_out, and_6_out, and_7_out);
  EX_MEM ex_mem_1 (
    .CLK(CLK), .W_num(EX_WriteReg_num), .W_num_2(MEM_WriteReg_num), .Write_Data(multiplexer_10_out),
    .Write_Data_2(MDin), .SIGN_IMM(shifter_2_out), .SIGN_IMM_2(ex_mem_1_sign_imm_2),
    .ALU_RESULT(mips_alu_1_result), .ALU_RESULT_2(ex_mem_1_alu_result_2), .PC(EX_PC), .PC_2(M_PC),
    .LH(id_ex_1_lh_2), .LH_2(ex_mem_1_lh_2), .LUI(id_ex_1_lui_2), .LUI_2(ex_mem_1_lui_2),
    .MemToReg(EX_MemToReg), .MemToReg_2(ex_mem_1_memtoreg_2), .MemWrite(id_ex_1_memwrite_2),
    .MemWrite_2(MemWrite), .RegWrite(EX_RegWrite), .RegWrite_2(MEM_RegWrite), .PC_4(id_ex_1_pc_4_2),
    .PC_4_2(ex_mem_1_pc_4_2), .JAL(id_ex_1_jal_2), .JAL_2(ex_mem_1_jal_2), .\使能端_低电平有效 (END),
    .\同步清零_高电平有效 (1'b0), .Syscall(id_ex_1_syscall_2), .Syscall_2(ex_mem_1_syscall_2), .IR(EX_IR),
    .IR_2(MEM_IR), .Ledout(and_4_out), .Ledout_2(LedOut));
  Multiplexer #(.select(1), .width(32), .disabled("Z"), .enable("false")) multiplexer_12 (
    .in0(ex_mem_1_alu_result_2), .in1(ex_mem_1_sign_imm_2), .out(MEM_ALU), .sel(ex_mem_1_lui_2));
  RAM #(.addrWidth(10), .dataWidth(32), .bus("separate"), .Select("high")) ram_1 (
    .addr(ex_mem_1_alu_result_2[11:2]), .din(MDin), .data(ram_1_data), .str(MemWrite), .clk(CLK));  // open: sel, ld, clr
  MEM_WB mem_wb_1 (
    .CLK(CLK), .W_num(MEM_WriteReg_num), .W_num_2(mem_wb_1_w_num_2), .MEM_Data(ram_1_data),
    .MEM_Data_2(mem_wb_1_mem_data_2), .SIGN_IMM(ex_mem_1_sign_imm_2), .SIGN_IMM_2(mem_wb_1_sign_imm_2),
    .ALU_RESULT(ex_mem_1_alu_result_2), .ALU_RESULT_2(mem_wb_1_alu_result_2), .PC(M_PC), .PC_2(WB_PC),
    .LH(ex_mem_1_lh_2), .LH_2(mem_wb_1_lh_2), .LUI(ex_mem_1_lui_2), .LUI_2(mem_wb_1_lui_2),
    .MemToReg(ex_mem_1_memtoreg_2), .MemToReg_2(mem_wb_1_memtoreg_2), .RegWrite(MEM_RegWrite),
    .RegWrite_2(RegWrite), .PC_4(ex_mem_1_pc_4_2), .PC_4_2(mem_wb_1_pc_4_2), .JAL(ex_mem_1_jal_2),
    .JAL_2(mem_wb_1_jal_2), .\使能端_低电平有效 (END), .\同步清零_高电平有效 (1'b0), .Syscall(ex_mem_1_syscall_2),
    .Syscall_2(MEM_Syscall), .IR(MEM_IR), .IR_2(WB_IR));
  Multiplexer #(.select(1), .width(32), .disabled("Z"), .enable("false")) multiplexer_13 (
    .in0(mem_wb_1_alu_result_2), .in1(mem_wb_1_mem_data_2), .out(multiplexer_13_out),
    .sel(mem_wb_1_memtoreg_2));
  Multiplexer #(.select(1), .width(16), .disabled("Z"), .enable("false")) multiplexer_14 (
    .in0(multiplexer_13_out[15:0]), .in1(multiplexer_13_out[31:16]), .out(multiplexer_14_out),
    .sel(mem_wb_1_alu_result_2[1]));
  assign bit_extender_3_out = {{16{multiplexer_14_out[15]}}, multiplexer_14_out};  // Bit_Extender bit_extender_3
  Multiplexer #(.select(1), .width(32), .disabled("Z"), .enable("false")) multiplexer_15 (
    .in0(multiplexer_13_out), .in1(bit_extender_3_out), .out(multiplexer_15_out), .sel(mem_wb_1_lh_2));
  Multiplexer #(.select(1), .width(32), .disabled("Z"), .enable("false")) multiplexer_16 (
    .in0(multiplexer_15_out), .in1(mem_wb_1_sign_imm_2), .out(multiplexer_16_out), .sel(mem_wb_1_lui_2));
  Multiplexer #(.select(1), .width(32), .disabled("Z"), .enable("false")) multiplexer_17 (
    .in0(multiplexer_16_out), .in1(mem_wb_1_pc_4_2), .out(RDin), .sel(mem_wb_1_jal_2));

  // Other names for the same wires on the sheet: ID_IR[5:0] = Func; OP[5:0] = ID_IR[31:26]; MEM_PC[31:0] = M_PC;
  //   Stall = LoadUse; WB_WD[31:0] = RDin

  // Notes on the sheet:
  //   中断源
  //   时空图监测，可删除
  //   中断等待指示
  //   数码管输出
  //   指令存储器
  //   contents of rom_1 (hex, n*v repeats v):
  //   20110001 8000c05 20110001 20120002 20130003 8000c09 20110001 20120002 20130003 8000c0d 20110001
  //   20120002 20130003 8000c11 20110001 20120002 20130003 c000cf6 20100001 20110001 118fc0 112020
  //   20020022 c 118882 12200001 8000c15 112020 20020022 c 20110001 118880 112020 20020022 c 12200001
  //   8000c1f 20110001 118fc0 112020 20020022 c 1188c3 112020 20020022 c 118903 112020 20020022 c 118903
  //   112020 20020022 c 118903 112020 20020022 c 118903 112020 20020022 c 118903 112020 20020022 c 118903
  //   112020 20020022 c 118903 112020 20020022 c 20100001 109fc0 139fc3 8021 2012000c 24160003 26100001
  //   3210000f 20080008 20090001 139900 2709825 132020 20020022 c 1094022 1500fff9 22100001 2018000f
  //   2188024 108700 20080008 20090001 139902 2709825 132021 20020022 c 1094022 1500fff9 108702 2c9b022
  //   12c00001 8000c50 4020 1084027 84400 3508ffff 82021 20020022 c 2010ffff 20110000 ae300000 22100001
  //   22310004 ae300000 22100001 22310004 ae300000 22100001 22310004 ae300000 22100001 22310004 ae300000
  //   22100001 22310004 ae300000 22100001 22310004 ae300000 22100001 22310004 ae300000 22100001 22310004
  //   ae300000 22100001 22310004 ae300000 22100001 22310004 ae300000 22100001 22310004 ae300000 22100001
  //   22310004 ae300000 22100001 22310004 ae300000 22100001 22310004 ae300000 22100001 22310004 ae300000
  //   22100001 22310004 22100001 8020 2011003c 8e130000 8e340000 274402a 11000002 ae330000 ae140000
  //   2231fffc 1611fff8 102020 20020022 c 22100004 2011003c 1611fff2 2002000a c 200b0008 3c11fedc 3631ffff
  //   112020 20020022 c 3c11ba98 112020 c 3c117654 112020 c 3c113210 112020 c 216bffff 1560fff0 2002000a c
  //   2008ffff 20090000 20111997 112020 20020022 c 2288820 2e291949 1120fffa 2002000a c 20090000 200b0010
  //   34118483 20120404 118c00 129400 36318281 22520404 ad310000 2328820 21290004 216bffff 1560fffb
  //   200b0020 20090000 85310000 112020 20020022 c 21290002 216bffff 1560fff9 2002000a c 2011fff1 112020
  //   20020022 c 22310001 1a20fffb 2002000a c 20100000 22100001 102020 20020022 c 22100002 102020 20020022
  //   c 22100003 102020 20020022 c 22100004 102020 20020022 c 22100005 102020 20020022 c 22100006 102020
  //   20020022 c 22100007 102020 20020022 c 22100008 102020 20020022 20020022 c 3e00008
  //   控制位
  //   IR
  //   流水调试日志用
  //   暂停节拍，不能为0
  //   戳工具置1进入计数暂停模式，ctrl+k时钟自动运行到对应节拍暂停
  //   ctrl+k关闭时钟连续运行，将控制位置零，进入单步调试模式调试
  //   OP
  //   Func
  //   rs
  //   rt
  //   rd
  //   imm16
  //   imm26
  //   JMP
  //   JR
  //   OP
  //   Func
  //   Syscall
  //   可计数暂停的时钟源
  //   Blez
  //   LH
  //   LUI
  //   Beq
  //   Bne
  //   MemToReg
  //   MemWrite
  //   AluOP
  //   AluSrcB
  //   RegWrite
  //   JAL
  //   RegDst
  //   为方便自动评测，需要输出流水线各段保存的PC值，注意是PC不是PC+4，另外ID段寄存器写入信息，Mem段内存写入信息也要输出
  //   Blez
  //   LH
  //   LUI
  //   Beq
  //   Bne
  //   MemToReg
  //   MemWrite
  //   AluOP
  //   AluSrcB
  //   RegWrite
  //   JAL
  //   Syscall
  //   RS
  //   RT
  //   W#
  //   SIGN_IMM
  //   PC+4
  //   IMM26
  //   shamt
  //   LH
  //   LUI
  //   MemToReg
  //   MemWrite
  //   RegWrite
  //   JAL
  //   Syscall
  //   Ledout
  //   Write_Data
  //   W#
  //   LUI_IMM
  //   PC+4
  //   ALU_RESULT
  //   LH
  //   LUI
  //   MemToReg
  //   RegWrite
  //   JAL
  //   Syscall
  //   ALU_RESULT
  //   MEM_Data
  //   W#
  //   LUI_IMM
  //   PC+4
endmodule

module \中断按键参考电路  (
  input  \同步清零信号 ,
  output \与中断屏蔽位与 
);

  wire \_1号中断_out , and_1_out, clock_1_out, d_ff_1_q, or_1_out, or_2_out;

  Clock #(.highDuration(1), .lowDuration(1)) clock_1 (.out(clock_1_out));
  Button \_1号中断  (.out(\_1号中断_out ));
  or or_1 (or_1_out, \与中断屏蔽位与 , d_ff_1_q);
  LED #(.active("true")) \_1号中断等待指示灯  (.in(or_1_out));
  D_Flip_Flop #(.trigger("rising"), .Pre_Clr_Positions("LEGACY"), .NegatePresetClear("false"), .enable("true"), .NewFFLayout("false")) d_ff_1 (
    .clk(\_1号中断_out ), .D(1'b1), .Q(d_ff_1_q), .reset(\与中断屏蔽位与 ));  // open: Qn, preset, en
  or or_2 (or_2_out, d_ff_1_q, \与中断屏蔽位与 );
  and and_1 (and_1_out, or_2_out, ~\同步清零信号 );  // AND_Gate
  D_Flip_Flop #(.trigger("rising"), .Pre_Clr_Positions("LEGACY"), .NegatePresetClear("false"), .enable("true"), .NewFFLayout("false")) IR1 (
    .clk(clock_1_out), .D(and_1_out), .Q(\与中断屏蔽位与 ));  // open: Qn, preset, en, reset
  \单周期硬布线控制器  \u_单周期硬布线控制器_1  ();  // open: Func, OP, ALU_OP, MemToReg, MemWrite, ALU_SRC, RegWrite, SysCALL, SignedExt, RegDst, JR, JMP, Beq, JAL, Bne, LUI, LH, BLEZ

  // Notes on the sheet:
  //   中断信号采样参考电路
  //   Reset 
endmodule

module \单周期MIPS_单级中断  (
  input  IR1,
  input  IR2,
  input  IR3,
  output RegWrite,
  output MemWrite,
  output [31:0] PC,
  output [31:0] IR,
  output [31:0] RDin,
  output [31:0] MDin,
  output [31:0] LedData
);

  wire CLK, comparator_1_eq, comparator_2_eq, comparator_3_eq, comparator_4_eq, Go, IR1_t, IR2_t, IR3_t, IRA,
       IRB, IRC, or_1_out, W1, W2, W3;
  wire [15:0] \总周期数 ;

  Clock #(.highDuration(1), .lowDuration(1)) clock_1 (.out(CLK));
  Button _1 ();  // open: out
  Button _2 ();  // open: out
  Button _3 ();  // open: out
  Button \u_继续运行  (.out(Go));
  LED #(.active("true")) led_1 (.in(W1));
  LED #(.active("true")) led_2 (.in(W2));
  LED #(.active("true")) led_3 (.in(W3));
  Hex_Digit_Display hex_digit_display_1 (.value(LedData[31:28]));  // open: dp
  Comparator #(.width(16), .mode("twosComplement")) comparator_1 (
    .a(16'h23b), .b(\总周期数 ), .eq(comparator_1_eq));  // open: gt, lt
  Comparator #(.width(16), .mode("twosComplement")) comparator_2 (
    .a(\总周期数 ), .b(16'h1), .eq(comparator_2_eq));  // open: gt, lt
  Comparator #(.width(16), .mode("twosComplement")) comparator_3 (
    .a(\总周期数 ), .b(16'h4), .eq(comparator_3_eq));  // open: gt, lt
  Comparator #(.width(16), .mode("twosComplement")) comparator_4 (
    .a(\总周期数 ), .b(16'h7), .eq(comparator_4_eq));  // open: gt, lt
  Hex_Digit_Display hex_digit_display_2 (.value(LedData[23:20]));  // open: dp
  Hex_Digit_Display hex_digit_display_3 (.value(LedData[27:24]));  // open: dp
  or or_1 (or_1_out, comparator_1_eq, comparator_2_eq);
  assign IRA = or_1_out ? ~CLK : 1'bz;  // Controlled_Inverter controlled_inverter_1
  assign IRB = comparator_3_eq ? ~CLK : 1'bz;  // Controlled_Inverter controlled_inverter_2
  assign IRC = comparator_4_eq ? ~CLK : 1'bz;  // Controlled_Inverter controlled_inverter_3
  Hex_Digit_Display hex_digit_display_4 (.value(LedData[19:16]));  // open: dp
  Hex_Digit_Display hex_digit_display_5 (.value(LedData[15:12]));  // open: dp
  Pull_Resistor #(.pull(0)) pull_resistor_1 (.node(IRA));
  Pull_Resistor #(.pull(0)) pull_resistor_2 (.node(IRB));
  Pull_Resistor #(.pull(0)) pull_resistor_3 (.node(IRC));
  Hex_Digit_Display hex_digit_display_6 (.value(LedData[7:4]));  // open: dp
  Hex_Digit_Display hex_digit_display_7 (.value(LedData[11:8]));  // open: dp
  // Probe on \总周期数 
  Hex_Digit_Display hex_digit_display_8 (.value(LedData[3:0]));  // open: dp
  or or_2 (IR1_t, IR1, IRA);
  or or_3 (IR2_t, IR2, IRB);
  or or_4 (IR3_t, IR3, IRC);

  // Notes on the sheet:
  //   中断源
  //   中断等待指示
  //   总复位信号应将除ROM以外所有存储组件全部清零
  //   单级中断测试信号模拟器
  //   数码管输出
  //   数码管输出应该用寄存器锁存，否则显示数据只能一闪而过
  //   为方便自动评测，需要输出PC，IR，寄存器堆写如数据RDin
  //   RAM写使能MemWrite、RAM写入数据MDin等信号
endmodule

module \单周期MIPS_多级中断  (
  input  IR1,
  input  IR2,
  input  IR3,
  output RegWrite,
  output MemWrite,
  output [31:0] PC,
  output [31:0] IR,
  output [31:0] RDin,
  output [31:0] MDin,
  output [31:0] LedData
);

  wire CLK, comparator_1_eq, comparator_2_eq, comparator_3_eq, comparator_4_eq, comparator_5_eq, Go, IR1_t,
       IR2_t, IR3_t, IRA, IRB, IRC, or_1_out, or_2_out, W1, W2, W3;
  wire [15:0] \总周期数 ;

  Clock #(.highDuration(1), .lowDuration(1)) clock_1 (.out(CLK));
  Button _1 ();  // open: out
  Button _2 ();  // open: out
  Button _3 ();  // open: out
  Button \u_继续运行  (.out(Go));
  LED #(.active("true")) led_1 (.in(W1));
  LED #(.active("true")) led_2 (.in(W2));
  LED #(.active("true")) led_3 (.in(W3));
  Hex_Digit_Display hex_digit_display_1 (.value(LedData[31:28]));  // open: dp
  Comparator #(.width(16), .mode("twosComplement")) comparator_1 (
    .a(\总周期数 ), .b(16'h7), .eq(comparator_1_eq));  // open: gt, lt
  Comparator #(.width(16), .mode("twosComplement")) comparator_2 (
    .a(\总周期数 ), .b(16'h241), .eq(comparator_2_eq));  // open: gt, lt
  Hex_Digit_Display hex_digit_display_2 (.value(LedData[23:20]));  // open: dp
  Hex_Digit_Display hex_digit_display_3 (.value(LedData[27:24]));  // open: dp
  Comparator #(.width(16), .mode("twosComplement")) comparator_3 (
    .a(16'h258), .b(\总周期数 ), .eq(comparator_3_eq));  // open: gt, lt
  or or_1 (or_1_out, comparator_3_eq, comparator_4_eq);
  Comparator #(.width(16), .mode("twosComplement")) comparator_4 (
    .a(\总周期数 ), .b(16'h1), .eq(comparator_4_eq));  // open: gt, lt
  Comparator #(.width(16), .mode("twosComplement")) comparator_5 (
    .a(\总周期数 ), .b(16'h4), .eq(comparator_5_eq));  // open: gt, lt
  or or_2 (or_2_out, comparator_1_eq, comparator_2_eq);
  Hex_Digit_Display hex_digit_display_4 (.value(LedData[15:12]));  // open: dp
  Hex_Digit_Display hex_digit_display_5 (.value(LedData[19:16]));  // open: dp
  Pull_Resistor #(.pull(0)) pull_resistor_1 (.node(IRA));
  assign IRA = or_1_out ? ~CLK : 1'bz;  // Controlled_Inverter controlled_inverter_1
  Pull_Resistor #(.pull(0)) pull_resistor_2 (.node(IRB));
  assign IRB = comparator_5_eq ? ~CLK : 1'bz;  // Controlled_Inverter controlled_inverter_2
  Pull_Resistor #(.pull(0)) pull_resistor_3 (.node(IRC));
  assign IRC = or_2_out ? ~CLK : 1'bz;  // Controlled_Inverter controlled_inverter_3
  Hex_Digit_Display hex_digit_display_6 (.value(LedData[11:8]));  // open: dp
  Hex_Digit_Display hex_digit_display_7 (.value(LedData[7:4]));  // open: dp
  // Probe on \总周期数 
  Hex_Digit_Display hex_digit_display_8 (.value(LedData[3:0]));  // open: dp
  or or_3 (IR1_t, IR1, IRA);
  or or_4 (IR2_t, IR2, IRB);
  or or_5 (IR3_t, IR3, IRC);

  // Notes on the sheet:
  //   中断源
  //   中断等待指示
  //   总复位信号应将除ROM以外所有存储组件全部清零
  //   多级中断测试信号模拟器
  //   数码管输出
  //   数码管输出应该用寄存器锁存，否则显示数据只能一闪而过
  //   为方便自动评测，需要输出PC，IR，寄存器堆写如数据RDin
  //   RAM写使能MemWrite、RAM写入数据MDin等信号
endmodule

module \封装正确性测试  (
);

  wire IR1, IR2, IR3, MemW, RegW;
  wire [31:0] EX_PC, ID_PC, IF_PC, IR, LED, MDin, MDinr, MEM_PC, PC, RDin, RDinr, WB_PC;

  \单周期MIPS  \u_单周期mips_1  (
    .IR1(IR1), .IR2(IR2), .IR3(IR3), .RegWrite(RegW), .MemWrite(MemW), .PC(PC), .IR(IR), .RDin(RDin),
    .MDin(MDin), .LedData(LED));
  \气泡流水线  \u_气泡流水线_1  (
    .RegWrite(RegW), .MemWrite(MemW), .IF_PC(IF_PC), .ID_PC(ID_PC), .EX_PC(EX_PC), .M_PC(MEM_PC),
    .WB_PC(WB_PC), .RDin(RDinr), .MDin(MDinr), .LedData(LED));
  \单周期MIPS_单级中断  \u_单周期mips_单级中断_1  (
    .IR1(IR1), .IR2(IR2), .IR3(IR3), .RegWrite(RegW), .MemWrite(MemW), .PC(PC), .IR(IR), .RDin(RDin),
    .MDin(MDin), .LedData(LED));
  \理想流水线  \u_理想流水线_1  (
    .RegWrite(RegW), .MemWrite(MemW), .IF_PC(IF_PC), .ID_PC(ID_PC), .EX_PC(EX_PC), .M_PC(MEM_PC),
    .WB_PC(WB_PC), .RDin(RDinr), .MDin(MDinr), .LedData(LED));
  \重定向流水线  \u_重定向流水线_1  (
    .RegWrite(RegW), .MemWrite(MemW), .IF_PC(IF_PC), .ID_PC(ID_PC), .EX_PC(EX_PC), .M_PC(MEM_PC),
    .WB_PC(WB_PC), .RDin(RDinr), .MDin(MDinr), .LedData(LED));
  \单周期MIPS_多级中断  \u_单周期mips_多级中断_1  (
    .IR1(IR1), .IR2(IR2), .IR3(IR3), .RegWrite(RegW), .MemWrite(MemW), .PC(PC), .IR(IR), .RDin(RDin),
    .MDin(MDin), .LedData(LED));

  // Notes on the sheet:
  //   单周期封装测试
  //   气泡流水封装测试
  //   单周期+单级中断封装测试
  //   请检查上面封装有无位宽不匹配，引脚标签是否和连接的标签相对应，否则无法在educoder平台上正确测试
  //   理想流水封装测试
  //   重定向流水封装测试
  //   单周期+多级中断封装测试
endmodule

module IF_ID (
  input  \使能端_低电平有效 ,
  input  \同步清零_高电平有效 ,
  input  CLK,
  input  [31:0] PC_4,
  input  [31:0] IR,
  input  [31:0] PC,
  input  MISS,
  input  Branch_Pre,
  input  [1:0] Now_State_Pre,
  input  [7:0] Row_Pre,
  output [31:0] PC_4_2,
  output [31:0] IR_2,
  output [31:0] PC_2,
  output MISS_2,
  output Branch_Pre_2,
  output [1:0] Now_State_Pre_2,
  output [7:0] Row_Pre_2
);

  wire multiplexer_4_out, multiplexer_5_out, not_1_out;
  wire [1:0] multiplexer_6_out;
  wire [7:0] multiplexer_7_out;
  wire [31:0] multiplexer_1_out, multiplexer_2_out, multiplexer_3_out;

  not not_1 (not_1_out, \使能端_低电平有效 );
  Multiplexer #(.select(1), .width(32), .disabled("Z"), .enable("false")) multiplexer_1 (
    .in0(PC_4), .in1({32{1'b0}}), .out(multiplexer_1_out), .sel(\同步清零_高电平有效 ));
  Multiplexer #(.select(1), .width(32), .disabled("Z"), .enable("false")) multiplexer_2 (
    .in0(IR), .in1({32{1'b0}}), .out(multiplexer_2_out), .sel(\同步清零_高电平有效 ));
  Multiplexer #(.select(1), .width(32), .disabled("Z"), .enable("false")) multiplexer_3 (
    .in0(PC), .in1({32{1'b0}}), .out(multiplexer_3_out), .sel(\同步清零_高电平有效 ));
  Multiplexer #(.select(1), .width(1), .disabled("Z"), .enable("false")) multiplexer_4 (
    .in0(MISS), .in1(1'b0), .out(multiplexer_4_out), .sel(\同步清零_高电平有效 ));
  Multiplexer #(.select(1), .width(1), .disabled("Z"), .enable("false")) multiplexer_5 (
    .in0(Branch_Pre), .in1(1'b0), .out(multiplexer_5_out), .sel(\同步清零_高电平有效 ));
  Multiplexer #(.select(1), .width(2), .disabled("Z"), .enable("false")) multiplexer_6 (
    .in0(Now_State_Pre), .in1(2'b00), .out(multiplexer_6_out), .sel(\同步清零_高电平有效 ));
  Multiplexer #(.select(1), .width(8), .disabled("Z"), .enable("false")) multiplexer_7 (
    .in0(Row_Pre), .in1({8{1'b0}}), .out(multiplexer_7_out), .sel(\同步清零_高电平有效 ));
  Register #(.width(32), .trigger("rising"), .Select("low")) register_1 (
    .D(multiplexer_1_out), .en(not_1_out), .Q(PC_4_2), .clk(CLK));  // open: clr
  Register #(.width(32), .trigger("rising"), .Select("low")) register_2 (
    .D(multiplexer_2_out), .en(not_1_out), .Q(IR_2), .clk(CLK));  // open: clr
  Register #(.width(32), .trigger("rising"), .Select("low")) register_3 (
    .D(multiplexer_3_out), .en(not_1_out), .Q(PC_2), .clk(CLK));  // open: clr
  Register #(.width(1), .trigger("rising"), .Select("low")) register_4 (
    .D(multiplexer_4_out), .en(not_1_out), .Q(MISS_2), .clk(CLK));  // open: clr
  Register #(.width(1), .trigger("rising"), .Select("low")) register_5 (
    .D(multiplexer_5_out), .en(not_1_out), .Q(Branch_Pre_2), .clk(CLK));  // open: clr
  Register #(.width(2), .trigger("rising"), .Select("low")) register_6 (
    .D(multiplexer_6_out), .en(not_1_out), .Q(Now_State_Pre_2), .clk(CLK));  // open: clr
  Register #(.width(8), .trigger("rising"), .Select("low")) register_7 (
    .D(multiplexer_7_out), .en(not_1_out), .Q(Row_Pre_2), .clk(CLK));  // open: clr
endmodule

module ID_EX (
  input  \使能端_低电平有效 ,
  input  \同步清零_高电平有效 ,
  input  CLK,
  input  [31:0] IR,
  input  [31:0] RS,
  input  [31:0] RT,
  input  [4:0] W_num,
  input  [31:0] PC_4,
  input  [31:0] SIGN_IMM,
  input  [25:0] IMM26,
  input  [31:0] PC,
  input  JMP,
  input  JR,
  input  BLEZ,
  input  LH,
  input  LUI,
  input  BEQ,
  input  BNE,
  input  MemToReg,
  input  MemWrite,
  input  [3:0] ALU_OP,
  input  ALU_SrcB,
  input  RegWrite,
  input  JAL,
  input  Syscall,
  input  [1:0] RsForward,
  input  [1:0] RtForward,
  input  MISS,
  input  Branch_Pre,
  input  [1:0] Now_State_Pre,
  input  [7:0] Row_Pre,
  output [31:0] IR_2,
  output [31:0] RS_2,
  output [31:0] RT_2,
  output [4:0] W_num_2,
  output [31:0] PC_4_2,
  output [31:0] SIGN_IMM_2,
  output [25:0] IMM26_2,
  output [31:0] PC_2,
  output JMP_2,
  output JR_2,
  output BLEZ_2,
  output LH_2,
  output LUI_2,
  output BEQ_2,
  output BNE_2,
  output MemToReg_2,
  output MemWrite_2,
  output [3:0] ALU_OP_2,
  output ALU_SrcB_2,
  output RegWrite_2,
  output JAL_2,
  output Syscall_2,
  output [1:0] RsForward_2,
  output [1:0] RtForward_2,
  output MISS_2,
  output Branch_Pre_2,
  output [1:0] Now_State_Pre_2,
  output [7:0] Row_Pre_2
);

  wire multiplexer_9_out, multiplexer_10_out, multiplexer_11_out, multiplexer_12_out, multiplexer_13_out,
       multiplexer_14_out, multiplexer_15_out, multiplexer_16_out, multiplexer_17_out, multiplexer_19_out,
       multiplexer_20_out, multiplexer_21_out, multiplexer_22_out, multiplexer_25_out, multiplexer_26_out,
       not_1_out;
  wire [1:0] multiplexer_23_out, multiplexer_24_out, multiplexer_27_out;
  wire [3:0] multiplexer_18_out;
  wire [4:0] multiplexer_4_out;
  wire [7:0] multiplexer_28_out;
  wire [25:0] multiplexer_7_out;
  wire [31:0] multiplexer_1_out, multiplexer_2_out, multiplexer_3_out, multiplexer_5_out, multiplexer_6_out,
       multiplexer_8_out;

  not not_1 (not_1_out, \使能端_低电平有效 );
  Multiplexer #(.select(1), .width(32), .disabled("Z"), .enable("false")) multiplexer_1 (
    .in0(IR), .in1({32{1'b0}}), .out(multiplexer_1_out), .sel(\同步清零_高电平有效 ));
  Multiplexer #(.select(1), .width(32), .disabled("Z"), .enable("false")) multiplexer_2 (
    .in0(RS), .in1({32{1'b0}}), .out(multiplexer_2_out), .sel(\同步清零_高电平有效 ));
  Multiplexer #(.select(1), .width(32), .disabled("Z"), .enable("false")) multiplexer_3 (
    .in0(RT), .in1({32{1'b0}}), .out(multiplexer_3_out), .sel(\同步清零_高电平有效 ));
  Multiplexer #(.select(1), .width(5), .disabled("Z"), .enable("false")) multiplexer_4 (
    .in0(W_num), .in1({5{1'b0}}), .out(multiplexer_4_out), .sel(\同步清零_高电平有效 ));
  Multiplexer #(.select(1), .width(32), .disabled("Z"), .enable("false")) multiplexer_5 (
    .in0(PC_4), .in1({32{1'b0}}), .out(multiplexer_5_out), .sel(\同步清零_高电平有效 ));
  Multiplexer #(.select(1), .width(32), .disabled("Z"), .enable("false")) multiplexer_6 (
    .in0(SIGN_IMM), .in1({32{1'b0}}), .out(multiplexer_6_out), .sel(\同步清零_高电平有效 ));
  Multiplexer #(.select(1), .width(26), .disabled("Z"), .enable("false")) multiplexer_7 (
    .in0(IMM26), .in1({26{1'b0}}), .out(multiplexer_7_out), .sel(\同步清零_高电平有效 ));
  Multiplexer #(.select(1), .width(32), .disabled("Z"), .enable("false")) multiplexer_8 (
    .in0(PC), .in1({32{1'b0}}), .out(multiplexer_8_out), .sel(\同步清零_高电平有效 ));
  Multiplexer #(.select(1), .width(1), .disabled("Z"), .enable("false")) multiplexer_9 (
    .in0(JMP), .in1(1'b0), .out(multiplexer_9_out), .sel(\同步清零_高电平有效 ));
  Multiplexer #(.select(1), .width(1), .disabled("Z"), .enable("false")) multiplexer_10 (
    .in0(JR), .in1(1'b0), .out(multiplexer_10_out), .sel(\同步清零_高电平有效 ));
  Multiplexer #(.select(1), .width(1), .disabled("Z"), .enable("false")) multiplexer_11 (
    .in0(BLEZ), .in1(1'b0), .out(multiplexer_11_out), .sel(\同步清零_高电平有效 ));
  Multiplexer #(.select(1), .width(1), .disabled("Z"), .enable("false")) multiplexer_12 (
    .in0(LH), .in1(1'b0), .out(multiplexer_12_out), .sel(\同步清零_高电平有效 ));
  Multiplexer #(.select(1), .width(1), .disabled("Z"), .enable("false")) multiplexer_13 (
    .in0(LUI), .in1(1'b0), .out(multiplexer_13_out), .sel(\同步清零_高电平有效 ));
  Multiplexer #(.select(1), .width(1), .disabled("Z"), .enable("false")) multiplexer_14 (
    .in0(BEQ), .in1(1'b0), .out(multiplexer_14_out), .sel(\同步清零_高电平有效 ));
  Multiplexer #(.select(1), .width(1), .disabled("Z"), .enable("false")) multiplexer_15 (
    .in0(BNE), .in1(1'b0), .out(multiplexer_15_out), .sel(\同步清零_高电平有效 ));
  Multiplexer #(.select(1), .width(1), .disabled("Z"), .enable("false")) multiplexer_16 (
    .in0(MemToReg), .in1(1'b0), .out(multiplexer_16_out), .sel(\同步清零_高电平有效 ));
  Multiplexer #(.select(1), .width(1), .disabled("Z"), .enable("false")) multiplexer_17 (
    .in0(MemWrite), .in1(1'b0), .out(multiplexer_17_out), .sel(\同步清零_高电平有效 ));
  Multiplexer #(.select(1), .width(4), .disabled("Z"), .enable("false")) multiplexer_18 (
    .in0(ALU_OP), .in1(4'b0000), .out(multiplexer_18_out), .sel(\同步清零_高电平有效 ));
  Multiplexer #(.select(1), .width(1), .disabled("Z"), .enable("false")) multiplexer_19 (
    .in0(ALU_SrcB), .in1(1'b0), .out(multiplexer_19_out), .sel(\同步清零_高电平有效 ));
  Multiplexer #(.select(1), .width(1), .disabled("Z"), .enable("false")) multiplexer_20 (
    .in0(RegWrite), .in1(1'b0), .out(multiplexer_20_out), .sel(\同步清零_高电平有效 ));
  Multiplexer #(.select(1), .width(1), .disabled("Z"), .enable("false")) multiplexer_21 (
    .in0(JAL), .in1(1'b0), .out(multiplexer_21_out), .sel(\同步清零_高电平有效 ));
  Multiplexer #(.select(1), .width(1), .disabled("Z"), .enable("false")) multiplexer_22 (
    .in0(Syscall), .in1(1'b0), .out(multiplexer_22_out), .sel(\同步清零_高电平有效 ));
  Multiplexer #(.select(1), .width(2), .disabled("Z"), .enable("false")) multiplexer_23 (
    .in0(RsForward), .in1(2'b00), .out(multiplexer_23_out), .sel(\同步清零_高电平有效 ));
  Multiplexer #(.select(1), .width(2), .disabled("Z"), .enable("false")) multiplexer_24 (
    .in0(RtForward), .in1(2'b00), .out(multiplexer_24_out), .sel(\同步清零_高电平有效 ));
  Multiplexer #(.select(1), .width(1), .disabled("Z"), .enable("false")) multiplexer_25 (
    .in0(MISS), .in1(1'b0), .out(multiplexer_25_out), .sel(\同步清零_高电平有效 ));
  Multiplexer #(.select(1), .width(1), .disabled("Z"), .enable("false")) multiplexer_26 (
    .in0(Branch_Pre), .in1(1'b0), .out(multiplexer_26_out), .sel(\同步清零_高电平有效 ));
  Multiplexer #(.select(1), .width(2), .disabled("Z"), .enable("false")) multiplexer_27 (
    .in0(Now_State_Pre), .in1(2'b00), .out(multiplexer_27_out), .sel(\同步清零_高电平有效 ));
  Multiplexer #(.select(1), .width(8), .disabled("Z"), .enable("false")) multiplexer_28 (
    .in0(Row_Pre), .in1({8{1'b0}}), .out(multiplexer_28_out), .sel(\同步清零_高电平有效 ));
  Register #(.width(32), .trigger("rising"), .Select("low")) register_1 (
    .D(multiplexer_1_out), .en(not_1_out), .Q(IR_2), .clk(CLK));  // open: clr
  Register #(.width(32), .trigger("rising"), .Select("low")) register_2 (
    .D(multiplexer_2_out), .en(not_1_out), .Q(RS_2), .clk(CLK));  // open: clr
  Register #(.width(32), .trigger("rising"), .Select("low")) register_3 (
    .D(multiplexer_3_out), .en(not_1_out), .Q(RT_2), .clk(CLK));  // open: clr
  Register #(.width(5), .trigger("rising"), .Select("low")) register_4 (
    .D(multiplexer_4_out), .en(not_1_out), .Q(W_num_2), .clk(CLK));  // open: clr
  Register #(.width(32), .trigger("rising"), .Select("low")) register_5 (
    .D(multiplexer_5_out), .en(not_1_out), .Q(PC_4_2), .clk(CLK));  // open: clr
  Register #(.width(32), .trigger("rising"), .Select("low")) register_6 (
    .D(multiplexer_6_out), .en(not_1_out), .Q(SIGN_IMM_2), .clk(CLK));  // open: clr
  Register #(.width(26), .trigger("rising"), .Select("low")) register_7 (
    .D(multiplexer_7_out), .en(not_1_out), .Q(IMM26_2), .clk(CLK));  // open: clr
  Register #(.width(32), .trigger("rising"), .Select("low")) register_8 (
    .D(multiplexer_8_out), .en(not_1_out), .Q(PC_2), .clk(CLK));  // open: clr
  Register #(.width(1), .trigger("rising"), .Select("low")) register_9 (
    .D(multiplexer_9_out), .en(not_1_out), .Q(JMP_2), .clk(CLK));  // open: clr
  Register #(.width(1), .trigger("rising"), .Select("low")) register_10 (
    .D(multiplexer_10_out), .Q(JR_2), .clk(CLK));  // open: en, clr
  Register #(.width(1), .trigger("rising"), .Select("low")) register_11 (
    .D(multiplexer_11_out), .en(not_1_out), .Q(BLEZ_2), .clk(CLK));  // open: clr
  Register #(.width(1), .trigger("rising"), .Select("low")) register_12 (
    .D(multiplexer_12_out), .en(not_1_out), .Q(LH_2), .clk(CLK));  // open: clr
  Register #(.width(1), .trigger("rising"), .Select("low")) register_13 (
    .D(multiplexer_13_out), .en(not_1_out), .Q(LUI_2), .clk(CLK));  // open: clr
  Register #(.width(1), .trigger("rising"), .Select("low")) register_14 (
    .D(multiplexer_14_out), .en(not_1_out), .Q(BEQ_2), .clk(CLK));  // open: clr
  Register #(.width(1), .trigger("rising"), .Select("low")) register_15 (
    .D(multiplexer_15_out), .en(not_1_out), .Q(BNE_2), .clk(CLK));  // open: clr
  Register #(.width(1), .trigger("rising"), .Select("low")) register_16 (
    .D(multiplexer_16_out), .en(not_1_out), .Q(MemToReg_2), .clk(CLK));  // open: clr
  Register #(.width(1), .trigger("rising"), .Select("low")) register_17 (
    .D(multiplexer_17_out), .en(not_1_out), .Q(MemWrite_2), .clk(CLK));  // open: clr
  Register #(.width(4), .trigger("rising"), .Select("low")) register_18 (
    .D(multiplexer_18_out), .en(not_1_out), .Q(ALU_OP_2), .clk(CLK));  // open: clr
  Register #(.width(1), .trigger("rising"), .Select("low")) register_19 (
    .D(multiplexer_19_out), .en(not_1_out), .Q(ALU_SrcB_2), .clk(CLK));  // open: clr
  Register #(.width(1), .trigger("rising"), .Select("low")) register_20 (
    .D(multiplexer_20_out), .en(not_1_out), .Q(RegWrite_2), .clk(CLK));  // open: clr
  Register #(.width(1), .trigger("rising"), .Select("low")) register_21 (
    .D(multiplexer_21_out), .en(not_1_out), .Q(JAL_2), .clk(CLK));  // open: clr
  Register #(.width(1), .trigger("rising"), .Select("low")) register_22 (
    .D(multiplexer_22_out), .en(not_1_out), .Q(Syscall_2), .clk(CLK));  // open: clr
  Register #(.width(2), .trigger("rising"), .Select("low")) register_23 (
    .D(multiplexer_23_out), .en(not_1_out), .Q(RsForward_2), .clk(CLK));  // open: clr
  Register #(.width(2), .trigger("rising"), .Select("low")) register_24 (
    .D(multiplexer_24_out), .en(not_1_out), .Q(RtForward_2), .clk(CLK));  // open: clr
  Register #(.width(1), .trigger("rising"), .Select("low")) register_25 (
    .D(multiplexer_25_out), .en(not_1_out), .Q(MISS_2), .clk(CLK));  // open: clr
  Register #(.width(1), .trigger("rising"), .Select("low")) register_26 (
    .D(multiplexer_26_out), .en(not_1_out), .Q(Branch_Pre_2), .clk(CLK));  // open: clr
  Register #(.width(2), .trigger("rising"), .Select("low")) register_27 (
    .D(multiplexer_27_out), .en(not_1_out), .Q(Now_State_Pre_2), .clk(CLK));  // open: clr
  Register #(.width(8), .trigger("rising"), .Select("low")) register_28 (
    .D(multiplexer_28_out), .en(not_1_out), .Q(Row_Pre_2), .clk(CLK));  // open: clr
endmodule

module EX_MEM (
  input  \使能端_低电平有效 ,
  input  \同步清零_高电平有效 ,
  input  CLK,
  input  [31:0] IR,
  input  [4:0] W_num,
  input  [31:0] Write_Data,
  input  [31:0] SIGN_IMM,
  input  [31:0] ALU_RESULT,
  input  [31:0] PC,
  input  LH,
  input  LUI,
  input  MemToReg,
  input  MemWrite,
  input  RegWrite,
  input  [31:0] PC_4,
  input  JAL,
  input  Syscall,
  input  Ledout,
  output [31:0] IR_2,
  output [4:0] W_num_2,
  output [31:0] Write_Data_2,
  output [31:0] SIGN_IMM_2,
  output [31:0] ALU_RESULT_2,
  output [31:0] PC_2,
  output LH_2,
  output LUI_2,
  output MemToReg_2,
  output MemWrite_2,
  output RegWrite_2,
  output [31:0] PC_4_2,
  output JAL_2,
  output Syscall_2,
  output Ledout_2
);

  wire multiplexer_7_out, multiplexer_8_out, multiplexer_9_out, multiplexer_10_out, multiplexer_11_out,
       multiplexer_13_out, multiplexer_14_out, multiplexer_15_out, not_1_out;
  wire [4:0] multiplexer_2_out;
  wire [31:0] multiplexer_1_out, multiplexer_3_out, multiplexer_4_out, multiplexer_5_out, multiplexer_6_out,
       multiplexer_12_out;

  not not_1 (not_1_out, \使能端_低电平有效 );
  Multiplexer #(.select(1), .width(32), .disabled("Z"), .enable("false")) multiplexer_1 (
    .in0(IR), .in1({32{1'b0}}), .out(multiplexer_1_out), .sel(\同步清零_高电平有效 ));
  Multiplexer #(.select(1), .width(5), .disabled("Z"), .enable("false")) multiplexer_2 (
    .in0(W_num), .in1({5{1'b0}}), .out(multiplexer_2_out), .sel(\同步清零_高电平有效 ));
  Multiplexer #(.select(1), .width(32), .disabled("Z"), .enable("false")) multiplexer_3 (
    .in0(Write_Data), .in1({32{1'b0}}), .out(multiplexer_3_out), .sel(\同步清零_高电平有效 ));
  Multiplexer #(.select(1), .width(32), .disabled("Z"), .enable("false")) multiplexer_4 (
    .in0(SIGN_IMM), .in1({32{1'b0}}), .out(multiplexer_4_out), .sel(\同步清零_高电平有效 ));
  Multiplexer #(.select(1), .width(32), .disabled("Z"), .enable("false")) multiplexer_5 (
    .in0(ALU_RESULT), .in1({32{1'b0}}), .out(multiplexer_5_out), .sel(\同步清零_高电平有效 ));
  Multiplexer #(.select(1), .width(32), .disabled("Z"), .enable("false")) multiplexer_6 (
    .in0(PC), .in1({32{1'b0}}), .out(multiplexer_6_out), .sel(\同步清零_高电平有效 ));
  Multiplexer #(.select(1), .width(1), .disabled("Z"), .enable("false")) multiplexer_7 (
    .in0(LH), .in1(1'b0), .out(multiplexer_7_out), .sel(\同步清零_高电平有效 ));
  Multiplexer #(.select(1), .width(1), .disabled("Z"), .enable("false")) multiplexer_8 (
    .in0(LUI), .in1(1'b0), .out(multiplexer_8_out), .sel(\同步清零_高电平有效 ));
  Multiplexer #(.select(1), .width(1), .disabled("Z"), .enable("false")) multiplexer_9 (
    .in0(MemToReg), .in1(1'b0), .out(multiplexer_9_out), .sel(\同步清零_高电平有效 ));
  Multiplexer #(.select(1), .width(1), .disabled("Z"), .enable("false")) multiplexer_10 (
    .in0(MemWrite), .in1(1'b0), .out(multiplexer_10_out), .sel(\同步清零_高电平有效 ));
  Multiplexer #(.select(1), .width(1), .disabled("Z"), .enable("false")) multiplexer_11 (
    .in0(RegWrite), .in1(1'b0), .out(multiplexer_11_out), .sel(\同步清零_高电平有效 ));
  Multiplexer #(.select(1), .width(32), .disabled("Z"), .enable("false")) multiplexer_12 (
    .in0(PC_4), .in1({32{1'b0}}), .out(multiplexer_12_out), .sel(\同步清零_高电平有效 ));
  Multiplexer #(.select(1), .width(1), .disabled("Z"), .enable("false")) multiplexer_13 (
    .in0(JAL), .in1(1'b0), .out(multiplexer_13_out), .sel(\同步清零_高电平有效 ));
  Multiplexer #(.select(1), .width(1), .disabled("Z"), .enable("false")) multiplexer_14 (
    .in0(Syscall), .in1(1'b0), .out(multiplexer_14_out), .sel(\同步清零_高电平有效 ));
  Multiplexer #(.select(1), .width(1), .disabled("Z"), .enable("false")) multiplexer_15 (
    .in0(Ledout), .in1(1'b0), .out(multiplexer_15_out), .sel(\同步清零_高电平有效 ));
  Register #(.width(32), .trigger("rising"), .Select("low")) register_1 (
    .D(multiplexer_1_out), .en(not_1_out), .Q(IR_2), .clk(CLK));  // open: clr
  Register #(.width(5), .trigger("rising"), .Select("low")) register_2 (
    .D(multiplexer_2_out), .en(not_1_out), .Q(W_num_2), .clk(CLK));  // open: clr
  Register #(.width(32), .trigger("rising"), .Select("low")) register_3 (
    .D(multiplexer_3_out), .en(not_1_out), .Q(Write_Data_2), .clk(CLK));  // open: clr
  Register #(.width(32), .trigger("rising"), .Select("low")) register_4 (
    .D(multiplexer_4_out), .en(not_1_out), .Q(SIGN_IMM_2), .clk(CLK));  // open: clr
  Register #(.width(32), .trigger("rising"), .Select("low")) register_5 (
    .D(multiplexer_5_out), .en(not_1_out), .Q(ALU_RESULT_2), .clk(CLK));  // open: clr
  Register #(.width(32), .trigger("rising"), .Select("low")) register_6 (
    .D(multiplexer_6_out), .en(not_1_out), .Q(PC_2), .clk(CLK));  // open: clr
  Register #(.width(1), .trigger("rising"), .Select("low")) register_7 (
    .D(multiplexer_7_out), .en(not_1_out), .Q(LH_2), .clk(CLK));  // open: clr
  Register #(.width(1), .trigger("rising"), .Select("low")) register_8 (
    .D(multiplexer_8_out), .en(not_1_out), .Q(LUI_2), .clk(CLK));  // open: clr
  Register #(.width(1), .trigger("rising"), .Select("low")) register_9 (
    .D(multiplexer_9_out), .en(not_1_out), .Q(MemToReg_2), .clk(CLK));  // open: clr
  Register #(.width(1), .trigger("rising"), .Select("low")) register_10 (
    .D(multiplexer_10_out), .en(not_1_out), .Q(MemWrite_2), .clk(CLK));  // open: clr
  Register #(.width(1), .trigger("rising"), .Select("low")) register_11 (
    .D(multiplexer_11_out), .en(not_1_out), .Q(RegWrite_2), .clk(CLK));  // open: clr
  Register #(.width(32), .trigger("rising"), .Select("low")) register_12 (
    .D(multiplexer_12_out), .en(not_1_out), .Q(PC_4_2), .clk(CLK));  // open: clr
  Register #(.width(1), .trigger("rising"), .Select("low")) register_13 (
    .D(multiplexer_13_out), .en(not_1_out), .Q(JAL_2), .clk(CLK));  // open: clr
  Register #(.width(1), .trigger("rising"), .Select("low")) register_14 (
    .D(multiplexer_14_out), .en(not_1_out), .Q(Syscall_2), .clk(CLK));  // open: clr
  Register #(.width(1), .trigger("rising"), .Select("low")) register_15 (
    .D(multiplexer_15_out), .en(not_1_out), .Q(Ledout_2), .clk(CLK));  // open: clr
endmodule

module MEM_WB (
  input  \使能端_低电平有效 ,
  input  \同步清零_高电平有效 ,
  input  CLK,
  input  [31:0] IR,
  input  [4:0] W_num,
  input  [31:0] MEM_Data,
  input  [31:0] SIGN_IMM,
  input  [31:0] ALU_RESULT,
  input  [31:0] PC,
  input  LH,
  input  LUI,
  input  MemToReg,
  input  RegWrite,
  input  [31:0] PC_4,
  input  JAL,
  input  Syscall,
  output [31:0] IR_2,
  output [4:0] W_num_2,
  output [31:0] MEM_Data_2,
  output [31:0] SIGN_IMM_2,
  output [31:0] ALU_RESULT_2,
  output [31:0] PC_2,
  output LH_2,
  output LUI_2,
  output MemToReg_2,
  output RegWrite_2,
  output [31:0] PC_4_2,
  output JAL_2,
  output Syscall_2
);

  wire multiplexer_7_out, multiplexer_8_out, multiplexer_9_out, multiplexer_10_out, multiplexer_12_out,
       multiplexer_13_out, not_1_out;
  wire [4:0] multiplexer_2_out;
  wire [31:0] multiplexer_1_out, multiplexer_3_out, multiplexer_4_out, multiplexer_5_out, multiplexer_6_out,
       multiplexer_11_out;

  not not_1 (not_1_out, \使能端_低电平有效 );
  Multiplexer #(.select(1), .width(32), .disabled("Z"), .enable("false")) multiplexer_1 (
    .in0(IR), .in1({32{1'b0}}), .out(multiplexer_1_out), .sel(\同步清零_高电平有效 ));
  Multiplexer #(.select(1), .width(5), .disabled("Z"), .enable("false")) multiplexer_2 (
    .in0(W_num), .in1({5{1'b0}}), .out(multiplexer_2_out), .sel(\同步清零_高电平有效 ));
  Multiplexer #(.select(1), .width(32), .disabled("Z"), .enable("false")) multiplexer_3 (
    .in0(MEM_Data), .in1({32{1'b0}}), .out(multiplexer_3_out), .sel(\同步清零_高电平有效 ));
  Multiplexer #(.select(1), .width(32), .disabled("Z"), .enable("false")) multiplexer_4 (
    .in0(SIGN_IMM), .in1({32{1'b0}}), .out(multiplexer_4_out), .sel(\同步清零_高电平有效 ));
  Multiplexer #(.select(1), .width(32), .disabled("Z"), .enable("false")) multiplexer_5 (
    .in0(ALU_RESULT), .in1({32{1'b0}}), .out(multiplexer_5_out), .sel(\同步清零_高电平有效 ));
  Multiplexer #(.select(1), .width(32), .disabled("Z"), .enable("false")) multiplexer_6 (
    .in0(PC), .in1({32{1'b0}}), .out(multiplexer_6_out), .sel(\同步清零_高电平有效 ));
  Multiplexer #(.select(1), .width(1), .disabled("Z"), .enable("false")) multiplexer_7 (
    .in0(LH), .in1(1'b0), .out(multiplexer_7_out), .sel(\同步清零_高电平有效 ));
  Multiplexer #(.select(1), .width(1), .disabled("Z"), .enable("false")) multiplexer_8 (
    .in0(LUI), .in1(1'b0), .out(multiplexer_8_out), .sel(\同步清零_高电平有效 ));
  Multiplexer #(.select(1), .width(1), .disabled("Z"), .enable("false")) multiplexer_9 (
    .in0(MemToReg), .in1(1'b0), .out(multiplexer_9_out), .sel(\同步清零_高电平有效 ));
  Multiplexer #(.select(1), .width(1), .disabled("Z"), .enable("false")) multiplexer_10 (
    .in0(RegWrite), .in1(1'b0), .out(multiplexer_10_out), .sel(\同步清零_高电平有效 ));
  Multiplexer #(.select(1), .width(32), .disabled("Z"), .enable("false")) multiplexer_11 (
    .in0(PC_4), .in1({32{1'b0}}), .out(multiplexer_11_out), .sel(\同步清零_高电平有效 ));
  Multiplexer #(.select(1), .width(1), .disabled("Z"), .enable("false")) multiplexer_12 (
    .in0(JAL), .in1(1'b0), .out(multiplexer_12_out), .sel(\同步清零_高电平有效 ));
  Multiplexer #(.select(1), .width(1), .disabled("Z"), .enable("false")) multiplexer_13 (
    .in0(Syscall), .in1(1'b0), .out(multiplexer_13_out), .sel(\同步清零_高电平有效 ));
  Register #(.width(32), .trigger("rising"), .Select("low")) register_1 (
    .D(multiplexer_1_out), .en(not_1_out), .Q(IR_2), .clk(CLK));  // open: clr
  Register #(.width(5), .trigger("rising"), .Select("low")) register_2 (
    .D(multiplexer_2_out), .en(not_1_out), .Q(W_num_2), .clk(CLK));  // open: clr
  Register #(.width(32), .trigger("rising"), .Select("low")) register_3 (
    .D(multiplexer_3_out), .en(not_1_out), .Q(MEM_Data_2), .clk(CLK));  // open: clr
  Register #(.width(32), .trigger("rising"), .Select("low")) register_4 (
    .D(multiplexer_4_out), .en(not_1_out), .Q(SIGN_IMM_2), .clk(CLK));  // open: clr
  Register #(.width(32), .trigger("rising"), .Select("low")) register_5 (
    .D(multiplexer_5_out), .en(not_1_out), .Q(ALU_RESULT_2), .clk(CLK));  // open: clr
  Register #(.width(32), .trigger("rising"), .Select("low")) register_6 (
    .D(multiplexer_6_out), .en(not_1_out), .Q(PC_2), .clk(CLK));  // open: clr
  Register #(.width(1), .trigger("rising"), .Select("low")) register_7 (
    .D(multiplexer_7_out), .en(not_1_out), .Q(LH_2), .clk(CLK));  // open: clr
  Register #(.width(1), .trigger("rising"), .Select("low")) register_8 (
    .D(multiplexer_8_out), .en(not_1_out), .Q(LUI_2), .clk(CLK));  // open: clr
  Register #(.width(1), .trigger("rising"), .Select("low")) register_9 (
    .D(multiplexer_9_out), .en(not_1_out), .Q(MemToReg_2), .clk(CLK));  // open: clr
  Register #(.width(1), .trigger("rising"), .Select("low")) register_10 (
    .D(multiplexer_10_out), .en(not_1_out), .Q(RegWrite_2), .clk(CLK));  // open: clr
  Register #(.width(32), .trigger("rising"), .Select("low")) register_11 (
    .D(multiplexer_11_out), .en(not_1_out), .Q(PC_4_2), .clk(CLK));  // open: clr
  Register #(.width(1), .trigger("rising"), .Select("low")) register_12 (
    .D(multiplexer_12_out), .en(not_1_out), .Q(JAL_2), .clk(CLK));  // open: clr
  Register #(.width(1), .trigger("rising"), .Select("low")) register_13 (
    .D(multiplexer_13_out), .en(not_1_out), .Q(Syscall_2), .clk(CLK));  // open: clr
endmodule

module \源寄存器使用情况  (
  input  OP0,
  input  OP1,
  input  OP2,
  input  OP3,
  input  OP4,
  input  OP5,
  input  F0,
  input  F1,
  input  F2,
  input  F3,
  input  F4,
  input  F5,
  output R1_used,
  output R2_used
);

  wire and_1_out, and_2_out, and_3_out, and_4_out, and_5_out, and_6_out, and_7_out, and_8_out, and_9_out,
       and_10_out, and_11_out, and_12_out, and_13_out, and_14_out, and_15_out, and_16_out, and_17_out,
       and_18_out, and_19_out, and_20_out, and_21_out, and_22_out, and_23_out, and_24_out, and_25_out,
       and_26_out, and_27_out, and_28_out, and_29_out, and_30_out, and_31_out, and_32_out, and_33_out,
       and_34_out, and_35_out, and_36_out, and_37_out, not_1_out, not_2_out, not_3_out, not_4_out, not_5_out,
       not_6_out, not_7_out, not_8_out, not_9_out, not_10_out, not_11_out, not_12_out, not_13_out,
       not_14_out, not_15_out, not_16_out, not_17_out, not_18_out, not_19_out, not_20_out, not_21_out,
       not_22_out, not_23_out, not_24_out, not_25_out, not_26_out, not_27_out, not_28_out, not_29_out,
       not_30_out, not_31_out, not_32_out, not_33_out, not_34_out, not_35_out, not_36_out, not_37_out,
       not_38_out, not_39_out, not_40_out, not_41_out, not_42_out, not_43_out, not_44_out, not_45_out,
       not_46_out, not_47_out, not_48_out, not_49_out, not_50_out, not_51_out, not_52_out, not_53_out,
       not_54_out, not_55_out, not_56_out, not_57_out, not_58_out, not_59_out, not_60_out, not_61_out,
       not_62_out, not_63_out, not_64_out, not_65_out, not_66_out, not_67_out, not_68_out, not_69_out,
       not_70_out, not_71_out, not_72_out, not_73_out, not_74_out, not_75_out, not_76_out, not_77_out,
       not_78_out, not_79_out, not_80_out, not_81_out, not_82_out, not_83_out, not_84_out, not_85_out,
       not_86_out, not_87_out, not_88_out, not_89_out, not_90_out, not_91_out, not_92_out, not_93_out,
       not_94_out, not_95_out, not_96_out, not_97_out, not_98_out, not_99_out, not_100_out, not_101_out,
       not_102_out, not_103_out, not_104_out, not_105_out, not_106_out, not_107_out, not_108_out,
       not_109_out, not_110_out, not_111_out, not_112_out, not_113_out, not_114_out, not_115_out,
       not_116_out, not_117_out, not_118_out, not_119_out, not_120_out, not_121_out, not_122_out,
       not_123_out, not_124_out, not_125_out, not_126_out, not_127_out, not_128_out, not_129_out,
       not_130_out, not_131_out, not_132_out, not_133_out, not_134_out, not_135_out, not_136_out,
       not_137_out, not_138_out, not_139_out, not_140_out, not_141_out, not_142_out, not_143_out,
       not_144_out, not_145_out, not_146_out, not_147_out, not_148_out, not_149_out, not_150_out,
       not_151_out, not_152_out, not_153_out, not_154_out, not_155_out, not_156_out, not_157_out,
       not_158_out, not_159_out, not_160_out, not_161_out, not_162_out, not_163_out, not_164_out,
       not_165_out, not_166_out, not_167_out, not_168_out, not_169_out, not_170_out, not_171_out,
       not_172_out, not_173_out, not_174_out, not_175_out, not_176_out, not_177_out, not_178_out,
       not_179_out, not_180_out, not_181_out, not_182_out, not_183_out, not_184_out, not_185_out,
       not_186_out, not_187_out, not_188_out, not_189_out, not_190_out, not_191_out, not_192_out,
       not_193_out, not_194_out, not_195_out, not_196_out, not_197_out, not_198_out, not_199_out,
       not_200_out, not_201_out, not_202_out, not_203_out, not_204_out, not_205_out, not_206_out,
       not_207_out, not_208_out, not_209_out, not_210_out, not_211_out, not_212_out, not_213_out,
       not_214_out, not_215_out, not_216_out, not_217_out, not_218_out, not_219_out, not_220_out,
       not_221_out, not_222_out, not_223_out, not_224_out, not_225_out, not_226_out, not_227_out,
       not_228_out, not_229_out, not_230_out, not_231_out, not_232_out, not_233_out, not_234_out,
       not_235_out, not_236_out, not_237_out, not_238_out, not_239_out, not_240_out, not_241_out,
       not_242_out, not_243_out, not_244_out, not_245_out, not_246_out, not_247_out, not_248_out,
       not_249_out, not_250_out, not_251_out, not_252_out, not_253_out, not_254_out, not_255_out,
       not_256_out, not_257_out, not_258_out, not_259_out, not_260_out, not_261_out, not_262_out,
       not_263_out, not_264_out, not_265_out, not_266_out, not_267_out, not_268_out, not_269_out, not_270_out;

  not not_1 (not_1_out, OP5);
  not not_2 (not_2_out, OP4);
  not not_3 (not_3_out, OP3);
  not not_4 (not_4_out, OP2);
  not not_5 (not_5_out, OP1);
  not not_6 (not_6_out, OP0);
  not not_7 (not_7_out, F4);
  not not_8 (not_8_out, F3);
  not not_9 (not_9_out, F2);
  not not_10 (not_10_out, F1);
  not not_11 (not_11_out, F0);
  not not_12 (not_12_out, OP5);
  not not_13 (not_13_out, OP4);
  not not_14 (not_14_out, OP3);
  not not_15 (not_15_out, OP2);
  not not_16 (not_16_out, OP1);
  not not_17 (not_17_out, OP0);
  not not_18 (not_18_out, F4);
  not not_19 (not_19_out, F3);
  not not_20 (not_20_out, F2);
  not not_21 (not_21_out, F1);
  not not_22 (not_22_out, OP5);
  not not_23 (not_23_out, OP4);
  not not_24 (not_24_out, OP3);
  not not_25 (not_25_out, OP2);
  not not_26 (not_26_out, OP1);
  not not_27 (not_27_out, OP0);
  not not_28 (not_28_out, F4);
  not not_29 (not_29_out, F3);
  not not_30 (not_30_out, F2);
  not not_31 (not_31_out, F0);
  not not_32 (not_32_out, OP5);
  not not_33 (not_33_out, OP4);
  not not_34 (not_34_out, OP3);
  not not_35 (not_35_out, OP2);
  not not_36 (not_36_out, OP1);
  not not_37 (not_37_out, OP0);
  not not_38 (not_38_out, F4);
  not not_39 (not_39_out, F3);
  not not_40 (not_40_out, F1);
  not not_41 (not_41_out, F0);
  not not_42 (not_42_out, OP5);
  not not_43 (not_43_out, OP4);
  not not_44 (not_44_out, OP3);
  not not_45 (not_45_out, OP2);
  not not_46 (not_46_out, OP1);
  not not_47 (not_47_out, OP0);
  not not_48 (not_48_out, F4);
  not not_49 (not_49_out, F3);
  not not_50 (not_50_out, F1);
  not not_51 (not_51_out, OP5);
  not not_52 (not_52_out, OP4);
  not not_53 (not_53_out, OP3);
  not not_54 (not_54_out, OP2);
  not not_55 (not_55_out, OP1);
  not not_56 (not_56_out, OP0);
  not not_57 (not_57_out, F4);
  not not_58 (not_58_out, F3);
  not not_59 (not_59_out, OP5);
  not not_60 (not_60_out, OP4);
  not not_61 (not_61_out, OP3);
  not not_62 (not_62_out, OP2);
  not not_63 (not_63_out, OP1);
  not not_64 (not_64_out, OP0);
  not not_65 (not_65_out, F4);
  not not_66 (not_66_out, F2);
  not not_67 (not_67_out, F0);
  not not_68 (not_68_out, OP5);
  not not_69 (not_69_out, OP4);
  not not_70 (not_70_out, OP3);
  not not_71 (not_71_out, OP2);
  not not_72 (not_72_out, OP1);
  not not_73 (not_73_out, OP0);
  not not_74 (not_74_out, F4);
  not not_75 (not_75_out, F2);
  not not_76 (not_76_out, OP5);
  not not_77 (not_77_out, OP4);
  not not_78 (not_78_out, OP3);
  not not_79 (not_79_out, OP2);
  not not_80 (not_80_out, OP1);
  not not_81 (not_81_out, OP0);
  not not_82 (not_82_out, F5);
  not not_83 (not_83_out, F4);
  not not_84 (not_84_out, F2);
  not not_85 (not_85_out, F1);
  not not_86 (not_86_out, F0);
  not not_87 (not_87_out, OP5);
  not not_88 (not_88_out, OP4);
  not not_89 (not_89_out, OP3);
  not not_90 (not_90_out, OP2);
  not not_91 (not_91_out, OP1);
  not not_92 (not_92_out, OP0);
  not not_93 (not_93_out, F5);
  not not_94 (not_94_out, F4);
  not not_95 (not_95_out, F1);
  not not_96 (not_96_out, F0);
  not not_97 (not_97_out, OP5);
  not not_98 (not_98_out, OP4);
  not not_99 (not_99_out, OP3);
  not not_100 (not_100_out, OP1);
  not not_101 (not_101_out, OP0);
  not not_102 (not_102_out, OP5);
  not not_103 (not_103_out, OP4);
  not not_104 (not_104_out, OP3);
  not not_105 (not_105_out, OP1);
  not not_106 (not_106_out, OP5);
  not not_107 (not_107_out, OP4);
  not not_108 (not_108_out, OP2);
  not not_109 (not_109_out, OP1);
  not not_110 (not_110_out, OP0);
  not not_111 (not_111_out, OP5);
  not not_112 (not_112_out, OP4);
  not not_113 (not_113_out, OP1);
  not not_114 (not_114_out, OP0);
  not not_115 (not_115_out, OP5);
  not not_116 (not_116_out, OP4);
  not not_117 (not_117_out, OP2);
  not not_118 (not_118_out, OP1);
  not not_119 (not_119_out, OP5);
  not not_120 (not_120_out, OP4);
  not not_121 (not_121_out, OP2);
  not not_122 (not_122_out, OP0);
  not not_123 (not_123_out, OP5);
  not not_124 (not_124_out, OP4);
  not not_125 (not_125_out, OP1);
  not not_126 (not_126_out, OP4);
  not not_127 (not_127_out, OP3);
  not not_128 (not_128_out, OP2);
  not not_129 (not_129_out, OP4);
  not not_130 (not_130_out, OP2);
  not not_131 (not_131_out, OP5);
  not not_132 (not_132_out, OP4);
  not not_133 (not_133_out, OP2);
  not not_134 (not_134_out, OP4);
  not not_135 (not_135_out, OP3);
  not not_136 (not_136_out, OP2);
  not not_137 (not_137_out, OP1);
  not not_138 (not_138_out, OP5);
  not not_139 (not_139_out, OP4);
  not not_140 (not_140_out, OP3);
  not not_141 (not_141_out, OP0);
  not not_142 (not_142_out, OP5);
  not not_143 (not_143_out, OP4);
  not not_144 (not_144_out, OP3);
  not not_145 (not_145_out, OP2);
  not not_146 (not_146_out, OP1);
  not not_147 (not_147_out, OP0);
  not not_148 (not_148_out, F5);
  not not_149 (not_149_out, F4);
  not not_150 (not_150_out, F3);
  not not_151 (not_151_out, F2);
  not not_152 (not_152_out, F1);
  not not_153 (not_153_out, F0);
  not not_154 (not_154_out, OP5);
  not not_155 (not_155_out, OP4);
  not not_156 (not_156_out, OP3);
  not not_157 (not_157_out, OP2);
  not not_158 (not_158_out, OP1);
  not not_159 (not_159_out, OP0);
  not not_160 (not_160_out, F5);
  not not_161 (not_161_out, F4);
  not not_162 (not_162_out, F3);
  not not_163 (not_163_out, F2);
  not not_164 (not_164_out, OP5);
  not not_165 (not_165_out, OP4);
  not not_166 (not_166_out, OP3);
  not not_167 (not_167_out, OP2);
  not not_168 (not_168_out, OP1);
  not not_169 (not_169_out, OP0);
  not not_170 (not_170_out, F5);
  not not_171 (not_171_out, F4);
  not not_172 (not_172_out, F3);
  not not_173 (not_173_out, F2);
  not not_174 (not_174_out, F0);
  not not_175 (not_175_out, OP5);
  not not_176 (not_176_out, OP4);
  not not_177 (not_177_out, OP3);
  not not_178 (not_178_out, OP2);
  not not_179 (not_179_out, OP1);
  not not_180 (not_180_out, OP0);
  not not_181 (not_181_out, F4);
  not not_182 (not_182_out, F3);
  not not_183 (not_183_out, F2);
  not not_184 (not_184_out, F1);
  not not_185 (not_185_out, F0);
  not not_186 (not_186_out, OP5);
  not not_187 (not_187_out, OP4);
  not not_188 (not_188_out, OP3);
  not not_189 (not_189_out, OP2);
  not not_190 (not_190_out, OP1);
  not not_191 (not_191_out, OP0);
  not not_192 (not_192_out, F4);
  not not_193 (not_193_out, F3);
  not not_194 (not_194_out, F2);
  not not_195 (not_195_out, F1);
  not not_196 (not_196_out, OP5);
  not not_197 (not_197_out, OP4);
  not not_198 (not_198_out, OP3);
  not not_199 (not_199_out, OP2);
  not not_200 (not_200_out, OP1);
  not not_201 (not_201_out, OP0);
  not not_202 (not_202_out, F4);
  not not_203 (not_203_out, F3);
  not not_204 (not_204_out, F2);
  not not_205 (not_205_out, F0);
  not not_206 (not_206_out, OP5);
  not not_207 (not_207_out, OP4);
  not not_208 (not_208_out, OP3);
  not not_209 (not_209_out, OP2);
  not not_210 (not_210_out, OP1);
  not not_211 (not_211_out, OP0);
  not not_212 (not_212_out, F4);
  not not_213 (not_213_out, F3);
  not not_214 (not_214_out, F1);
  not not_215 (not_215_out, F0);
  not not_216 (not_216_out, OP5);
  not not_217 (not_217_out, OP4);
  not not_218 (not_218_out, OP3);
  not not_219 (not_219_out, OP2);
  not not_220 (not_220_out, OP1);
  not not_221 (not_221_out, OP0);
  not not_222 (not_222_out, F4);
  not not_223 (not_223_out, F3);
  not not_224 (not_224_out, F1);
  not not_225 (not_225_out, OP5);
  not not_226 (not_226_out, OP4);
  not not_227 (not_227_out, OP3);
  not not_228 (not_228_out, OP2);
  not not_229 (not_229_out, OP1);
  not not_230 (not_230_out, OP0);
  not not_231 (not_231_out, F4);
  not not_232 (not_232_out, F3);
  not not_233 (not_233_out, OP5);
  not not_234 (not_234_out, OP4);
  not not_235 (not_235_out, OP3);
  not not_236 (not_236_out, OP2);
  not not_237 (not_237_out, OP1);
  not not_238 (not_238_out, OP0);
  not not_239 (not_239_out, F4);
  not not_240 (not_240_out, F2);
  not not_241 (not_241_out, F0);
  not not_242 (not_242_out, OP5);
  not not_243 (not_243_out, OP4);
  not not_244 (not_244_out, OP3);
  not not_245 (not_245_out, OP2);
  not not_246 (not_246_out, OP1);
  not not_247 (not_247_out, OP0);
  not not_248 (not_248_out, F4);
  not not_249 (not_249_out, F2);
  not not_250 (not_250_out, OP5);
  not not_251 (not_251_out, OP4);
  not not_252 (not_252_out, OP3);
  not not_253 (not_253_out, OP2);
  not not_254 (not_254_out, OP1);
  not not_255 (not_255_out, OP0);
  not not_256 (not_256_out, F5);
  not not_257 (not_257_out, F4);
  not not_258 (not_258_out, F1);
  not not_259 (not_259_out, F0);
  not not_260 (not_260_out, OP5);
  not not_261 (not_261_out, OP4);
  not not_262 (not_262_out, OP3);
  not not_263 (not_263_out, OP1);
  not not_264 (not_264_out, OP0);
  not not_265 (not_265_out, OP5);
  not not_266 (not_266_out, OP4);
  not not_267 (not_267_out, OP3);
  not not_268 (not_268_out, OP1);
  not not_269 (not_269_out, OP4);
  not not_270 (not_270_out, OP2);
  and and_1 (and_1_out, not_1_out, not_2_out, not_3_out, not_4_out, not_5_out, not_6_out, F5, not_7_out, not_8_out, not_9_out, not_10_out, not_11_out);
  and and_2 (and_2_out, not_12_out, not_13_out, not_14_out, not_15_out, not_16_out, not_17_out, F5, not_18_out, not_19_out, not_20_out, not_21_out, F0);
  and and_3 (and_3_out, not_22_out, not_23_out, not_24_out, not_25_out, not_26_out, not_27_out, F5, not_28_out, not_29_out, not_30_out, F1, not_31_out);
  and and_4 (and_4_out, not_32_out, not_33_out, not_34_out, not_35_out, not_36_out, not_37_out, F5, not_38_out, not_39_out, F2, not_40_out, not_41_out);
  and and_5 (and_5_out, not_42_out, not_43_out, not_44_out, not_45_out, not_46_out, not_47_out, F5, not_48_out, not_49_out, F2, not_50_out, F0);
  and and_6 (and_6_out, not_51_out, not_52_out, not_53_out, not_54_out, not_55_out, not_56_out, F5, not_57_out, not_58_out, F2, F1, F0);
  and and_7 (and_7_out, not_59_out, not_60_out, not_61_out, not_62_out, not_63_out, not_64_out, F5, not_65_out, F3, not_66_out, F1, not_67_out);
  and and_8 (and_8_out, not_68_out, not_69_out, not_70_out, not_71_out, not_72_out, not_73_out, F5, not_74_out, F3, not_75_out, F1, F0);
  and and_9 (and_9_out, not_76_out, not_77_out, not_78_out, not_79_out, not_80_out, not_81_out, not_82_out, not_83_out, F3, not_84_out, not_85_out, not_86_out);
  and and_10 (and_10_out, not_87_out, not_88_out, not_89_out, not_90_out, not_91_out, not_92_out, not_93_out, not_94_out, F3, F2, not_95_out, not_96_out);
  and and_11 (and_11_out, not_97_out, not_98_out, not_99_out, OP2, not_100_out, not_101_out);
  and and_12 (and_12_out, not_102_out, not_103_out, not_104_out, OP2, not_105_out, OP0);
  and and_13 (and_13_out, not_106_out, not_107_out, OP3, not_108_out, not_109_out, not_110_out);
  and and_14 (and_14_out, not_111_out, not_112_out, OP3, OP2, not_113_out, not_114_out);
  and and_15 (and_15_out, not_115_out, not_116_out, OP3, not_117_out, not_118_out, OP0);
  and and_16 (and_16_out, not_119_out, not_120_out, OP3, not_121_out, OP1, not_122_out);
  and and_17 (and_17_out, not_123_out, not_124_out, OP3, OP2, not_125_out, OP0);
  and and_18 (and_18_out, OP5, not_126_out, not_127_out, not_128_out, OP1, OP0);
  and and_19 (and_19_out, OP5, not_129_out, OP3, not_130_out, OP1, OP0);
  and and_20 (and_20_out, not_131_out, not_132_out, OP3, not_133_out, OP1, OP0);
  and and_21 (and_21_out, OP5, not_134_out, not_135_out, not_136_out, not_137_out, OP0);
  and and_22 (and_22_out, not_138_out, not_139_out, not_140_out, OP2, OP1, not_141_out);
  and and_23 (and_23_out, not_142_out, not_143_out, not_144_out, not_145_out, not_146_out, not_147_out, not_148_out, not_149_out, not_150_out, not_151_out, not_152_out, not_153_out);
  and and_24 (and_24_out, not_154_out, not_155_out, not_156_out, not_157_out, not_158_out, not_159_out, not_160_out, not_161_out, not_162_out, not_163_out, F1, F0);
  and and_25 (and_25_out, not_164_out, not_165_out, not_166_out, not_167_out, not_168_out, not_169_out, not_170_out, not_171_out, not_172_out, not_173_out, F1, not_174_out);
  and and_26 (and_26_out, not_175_out, not_176_out, not_177_out, not_178_out, not_179_out, not_180_out, F5, not_181_out, not_182_out, not_183_out, not_184_out, not_185_out);
  and and_27 (and_27_out, not_186_out, not_187_out, not_188_out, not_189_out, not_190_out, not_191_out, F5, not_192_out, not_193_out, not_194_out, not_195_out, F0);
  and and_28 (and_28_out, not_196_out, not_197_out, not_198_out, not_199_out, not_200_out, not_201_out, F5, not_202_out, not_203_out, not_204_out, F1, not_205_out);
  and and_29 (and_29_out, not_206_out, not_207_out, not_208_out, not_209_out, not_210_out, not_211_out, F5, not_212_out, not_213_out, F2, not_214_out, not_215_out);
  and and_30 (and_30_out, not_216_out, not_217_out, not_218_out, not_219_out, not_220_out, not_221_out, F5, not_222_out, not_223_out, F2, not_224_out, F0);
  and and_31 (and_31_out, not_225_out, not_226_out, not_227_out, not_228_out, not_229_out, not_230_out, F5, not_231_out, not_232_out, F2, F1, F0);
  and and_32 (and_32_out, not_233_out, not_234_out, not_235_out, not_236_out, not_237_out, not_238_out, F5, not_239_out, F3, not_240_out, F1, not_241_out);
  and and_33 (and_33_out, not_242_out, not_243_out, not_244_out, not_245_out, not_246_out, not_247_out, F5, not_248_out, F3, not_249_out, F1, F0);
  and and_34 (and_34_out, not_250_out, not_251_out, not_252_out, not_253_out, not_254_out, not_255_out, not_256_out, not_257_out, F3, F2, not_258_out, not_259_out);
  and and_35 (and_35_out, not_260_out, not_261_out, not_262_out, OP2, not_263_out, not_264_out);
  and and_36 (and_36_out, not_265_out, not_266_out, not_267_out, OP2, not_268_out, OP0);
  and and_37 (and_37_out, OP5, not_269_out, OP3, not_270_out, OP1, OP0);
  or or_1 (R1_used, and_1_out, and_2_out, and_3_out, and_4_out, and_5_out, and_6_out, and_7_out, and_8_out, and_9_out, and_10_out, and_11_out, and_12_out, and_13_out, and_14_out, and_15_out, and_16_out, and_17_out, and_18_out, and_19_out, and_20_out, and_21_out, and_22_out);
  or or_2 (R2_used, and_23_out, and_24_out, and_25_out, and_26_out, and_27_out, and_28_out, and_29_out, and_30_out, and_31_out, and_32_out, and_33_out, and_34_out, and_35_out, and_36_out, and_37_out);
endmodule

module \数据相关检测  (
  input  [4:0] R1_num,
  input  [4:0] R2_num,
  input  R1_Used,
  input  [4:0] EX_WriteReg_num,
  input  EX_RegWrite,
  input  [4:0] MEM_WriteReg_num,
  input  MEM_RegWrite,
  input  R2_Used,
  output DataHazzard
);

  wire and_1_out, and_2_out, and_3_out, and_4_out, comparator_1_eq, comparator_2_eq, comparator_3_eq,
       comparator_4_eq, comparator_5_eq, comparator_6_eq, not_1_out, not_2_out;

  Comparator #(.width(5), .mode("twosComplement")) comparator_1 (
    .a(R1_num), .b(EX_WriteReg_num), .eq(comparator_1_eq));  // open: gt, lt
  Comparator #(.width(5), .mode("twosComplement")) comparator_2 (
    .a(EX_WriteReg_num), .b(R2_num), .eq(comparator_2_eq));  // open: gt, lt
  Comparator #(.width(5), .mode("twosComplement")) comparator_3 (
    .a(R1_num), .b(MEM_WriteReg_num), .eq(comparator_3_eq));  // open: gt, lt
  Comparator #(.width(5), .mode("twosComplement")) comparator_4 (
    .a(MEM_WriteReg_num), .b(R2_num), .eq(comparator_4_eq));  // open: gt, lt
  not not_1 (not_1_out, comparator_5_eq);
  Comparator #(.width(5), .mode("twosComplement")) comparator_5 (
    .a(R1_num), .b({5{1'b0}}), .eq(comparator_5_eq));  // open: gt, lt
  Comparator #(.width(5), .mode("twosComplement")) comparator_6 (
    .a(R2_num), .b({5{1'b0}}), .eq(comparator_6_eq));  // open: gt, lt
  not not_2 (not_2_out, comparator_6_eq);
  and and_1 (and_1_out, R1_Used, not_1_out, comparator_1_eq, EX_RegWrite);
  and and_2 (and_2_out, R2_Used, EX_RegWrite, comparator_2_eq, not_2_out);
  and and_3 (and_3_out, not_1_out, comparator_3_eq, R1_Used, MEM_RegWrite);
  and and_4 (and_4_out, MEM_RegWrite, not_2_out, comparator_4_eq, R2_Used);
  or or_1 (DataHazzard, and_1_out, and_2_out, and_3_out, and_4_out);
endmodule

module \数据相关检测_重定向  (
  input  R1_Used,
  input  R2_Used,
  input  [4:0] R1_num,
  input  [4:0] R2_num,
  input  EX_MemToReg,
  input  [4:0] EX_WriteReg_num,
  input  EX_RegWrite,
  input  [4:0] MEM_WriteReg_num,
  input  MEM_RegWrite,
  output DataHazzard,
  output LoadUse,
  output [1:0] RsForward,
  output [1:0] RtForward
);

  wire and_1_out, and_2_out, and_3_out, and_4_out, comparator_1_eq, comparator_2_eq, comparator_3_eq,
       comparator_4_eq, comparator_5_eq, comparator_6_eq, not_1_out, not_2_out, or_1_out, or_2_out, or_3_out,
       or_4_out;
  wire [1:0] and_5_out, and_6_out;

  Comparator #(.width(5), .mode("twosComplement")) comparator_1 (
    .a(R1_num), .b({5{1'b0}}), .eq(comparator_1_eq));  // open: gt, lt
  Comparator #(.width(5), .mode("twosComplement")) comparator_2 (
    .a(R2_num), .b({5{1'b0}}), .eq(comparator_2_eq));  // open: gt, lt
  Comparator #(.width(5), .mode("twosComplement")) comparator_3 (
    .a(R1_num), .b(EX_WriteReg_num), .eq(comparator_3_eq));  // open: gt, lt
  Comparator #(.width(5), .mode("twosComplement")) comparator_4 (
    .a(EX_WriteReg_num), .b(R2_num), .eq(comparator_4_eq));  // open: gt, lt
  Comparator #(.width(5), .mode("twosComplement")) comparator_5 (
    .a(R1_num), .b(MEM_WriteReg_num), .eq(comparator_5_eq));  // open: gt, lt
  Comparator #(.width(5), .mode("twosComplement")) comparator_6 (
    .a(MEM_WriteReg_num), .b(R2_num), .eq(comparator_6_eq));  // open: gt, lt
  not not_1 (not_1_out, comparator_1_eq);
  not not_2 (not_2_out, comparator_2_eq);
  and and_1 (and_1_out, not_1_out, comparator_3_eq, EX_RegWrite);
  and and_2 (and_2_out, EX_RegWrite, not_2_out, comparator_4_eq);
  and and_3 (and_3_out, not_1_out, comparator_5_eq, MEM_RegWrite);
  and and_4 (and_4_out, MEM_RegWrite, not_2_out, comparator_6_eq);
  and and_5 (and_5_out[0], and_1_out, R1_Used);
  and and_6 (and_6_out[0], and_2_out, R2_Used);
  and and_7 (and_5_out[1], and_3_out, R1_Used);
  and and_8 (and_6_out[1], and_4_out, R2_Used);
  or or_1 (or_1_out, and_1_out, and_3_out);
  or or_2 (or_2_out, and_2_out, and_4_out);
  or or_3 (or_3_out, and_5_out[0], and_6_out[0]);
  and and_9 (LoadUse, EX_MemToReg, or_3_out);
  or or_4 (or_4_out, or_2_out, or_1_out);
  Multiplexer #(.select(2), .width(1), .disabled("Z"), .enable("false")) multiplexer_1 (
    .in0(1'b0), .in1(or_1_out), .in2(or_2_out), .in3(or_4_out), .out(DataHazzard), .sel({R2_Used, R1_Used}));
  Multiplexer #(.select(1), .width(2), .disabled("Z"), .enable("false")) multiplexer_2 (
    .in0(and_6_out), .in1(2'b00), .out(RtForward), .sel(LoadUse));
  Multiplexer #(.select(1), .width(2), .disabled("Z"), .enable("false")) multiplexer_3 (
    .in0(and_5_out), .in1(2'b00), .out(RsForward), .sel(LoadUse));

  // Notes on the sheet:
  //   EX_Write_R1
  //   EX_Write_R2
  //   MEM_Write_R1
  //   MEM_Write_R2
  //   R1_EX_Relate
  //   R2_EX_Relate
  //   R1_MEM_Relate
  //   R2_MEM_Relate
  //   Only_R1_Used
  //   Only_R2_Used
  //   R1_R2_Used
endmodule
module \重定向流水线_动态分支预测  (
  input  [1:0] \设置为11或者10 ,
  input  [1:0] \设置为11 ,
  output RegWrite,
  output MemWrite,
  output [31:0] IF_PC,
  output [31:0] ID_PC,
  output [31:0] EX_PC,
  output [31:0] M_PC,
  output [31:0] WB_PC,
  output [31:0] RDin,
  output [31:0] MDin,
  output [31:0] LedData
);

  wire and_2_out, and_5_out, and_6_out, and_9_out, and_10_out, Branch, CLK, clock_1_out, clock_2_out,
       comparator_1_eq, comparator_2_eq, comparator_3_eq, comparator_3_lt, comparator_4_eq, comparator_5_eq,
       comparator_5_lt, d_ff_1_q, DataHazzard, END, EX_Branch_Pre, EX_Load, ex_mem_1_jal_2, ex_mem_1_lh_2,
       ex_mem_1_lui_2, ex_mem_1_memtoreg_2, ex_mem_1_syscall_2, EX_MemToReg, EX_MISS, EX_RegWrite, Go, Halt,
       id_ex_1_alu_srcb_2, id_ex_1_beq_2, id_ex_1_blez_2, id_ex_1_bne_2, id_ex_1_jal_2, id_ex_1_lh_2,
       id_ex_1_lui_2, id_ex_1_memwrite_2, id_ex_1_syscall_2, ID_EX_Flush, IF_Branch_Pre,
       if_id_1_branch_pre_2, if_id_1_miss_2, IF_ID_Flush, IF_MISS, IR1, IR2, IR3, IsBranchIR_con, JMP, JR,
       LedOut, LoadUse, MEM_RegWrite, MEM_Syscall, mem_wb_1_jal_2, mem_wb_1_lh_2, mem_wb_1_lui_2,
       mem_wb_1_memtoreg_2, mips_alu_1_equal, nand_1_out, not_1_out, not_2_out, not_3_out, not_4_out,
       or_2_out, or_3_out, or_5_out, or_7_out, Predict_Success, register_1_q, RST, SignedExt, W1, W2, W3,
       xnor_1_out, \单周期硬布线控制器_1_alu_src , \单周期硬布线控制器_1_beq , \单周期硬布线控制器_1_blez , \单周期硬布线控制器_1_bne ,
       \单周期硬布线控制器_1_jal , \单周期硬布线控制器_1_jmp , \单周期硬布线控制器_1_jr , \单周期硬布线控制器_1_lh , \单周期硬布线控制器_1_lui ,
       \单周期硬布线控制器_1_memtoreg , \单周期硬布线控制器_1_memwrite , \单周期硬布线控制器_1_regdst , \单周期硬布线控制器_1_regwrite ,
       \单周期硬布线控制器_1_syscall , \源寄存器使用情况_1_r1_used , \源寄存器使用情况_1_r2_used ;
  wire [1:0] EX_Next_State_Pre, EX_Now_State_Pre, id_ex_1_rsforward_2, id_ex_1_rtforward_2, ID_RsForward,
       ID_RtForward, if_id_1_now_state_pre_2, IF_Now_State_Pre, multiplexer_12_out, multiplexer_14_out,
       \双预测位状态机_1_next_state ;
  wire [3:0] id_ex_1_alu_op_2, \单周期硬布线控制器_1_alu_op ;
  wire [4:0] EX_WriteReg_num, mem_wb_1_w_num_2, MEM_WriteReg_num, multiplexer_6_out, multiplexer_9_out, R1,
       R2;
  wire [5:0] Func;
  wire [7:0] EX_Row_Pre, if_id_1_row_pre_2, IF_Row_Pre;
  wire [12:0] CNT_num;
  wire [15:0] adder_2_out, \LoadUse次数 , multiplexer_21_out, register_2_q, \总周期数 , \插入气泡数 , \无条件分支数 ,
       \条件分支成功数 ;
  wire [27:2] PC_no_condition;
  wire [31:0] adder_1_out, bit_extender_1_out, bit_extender_2_out, bit_extender_3_out, EX_IR,
       ex_mem_1_alu_result_2, ex_mem_1_pc_4_2, ex_mem_1_sign_imm_2, EX_Next_PC_Pre, id_ex_1_rs_2,
       id_ex_1_rt_2, id_ex_1_sign_imm_2, if_id_1_pc_4_2, IF_IR, IF_Next_PC_Pre, MEM_ALU, MEM_IR,
       mem_wb_1_alu_result_2, mem_wb_1_mem_data_2, mem_wb_1_pc_4_2, mem_wb_1_sign_imm_2, mips_alu_1_result,
       mips_regifile_1_r1, mips_regifile_1_r2, multiplexer_1_out, multiplexer_2_out, multiplexer_3_out,
       multiplexer_4_out, multiplexer_5_out, multiplexer_10_out, multiplexer_11_out, multiplexer_15_out,
       multiplexer_16_out, multiplexer_18_out, multiplexer_20_out, multiplexer_22_out, multiplexer_23_out,
       PC_4, PC_condition, ram_1_data, RS, shifter_1_out, shifter_2_out, v0, WB_IR;
  wire [31:6] ID_IR;

  Button \u_总复位  (.out(RST));
  Button _1 (.out(IR1));
  Button _2 (.out(IR2));
  Button _3 (.out(IR3));
  // Probe on \总周期数 
  // Probe on \总周期数 
  Button \u_继续运行  (.out(Go));
  LED #(.active("true")) led_1 (.in(W1));
  LED #(.active("true")) led_2 (.in(W2));
  LED #(.active("true")) led_3 (.in(W3));
  Multiplexer #(.select(1), .width(32), .disabled("Z"), .enable("false")) multiplexer_1 (
    .in0(adder_1_out), .in1(PC_condition), .out(multiplexer_1_out), .sel(Branch));
  Multiplexer #(.select(1), .width(32), .disabled("Z"), .enable("false")) multiplexer_2 (
    .in0(multiplexer_1_out), .in1({EX_PC[31:28], PC_no_condition, 2'b00}), .out(multiplexer_2_out), .sel(JMP));
  Hex_Digit_Display hex_digit_display_1 (.value(LedData[31:28]));  // open: dp
  // Probe on IF_PC[19:0]
  // Mips_Probe mips_probe_1: pin names not known; wires that end beside it: IF_IR
  Multiplexer #(.select(1), .width(32), .disabled("Z"), .enable("false")) multiplexer_3 (
    .in0(multiplexer_2_out), .in1(multiplexer_15_out), .out(multiplexer_3_out), .sel(JR));
  Hex_Digit_Display hex_digit_display_2 (.value(LedData[23:20]));  // open: dp
  Hex_Digit_Display hex_digit_display_3 (.value(LedData[27:24]));  // open: dp
  // Probe on ID_PC[19:0]
  // Mips_Probe mips_probe_2: pin names not known; wires that end beside it: {ID_IR, Func}
  Register #(.width(1), .trigger("rising"), .Select("low")) register_1 (
    .D(1'b1), .Q(register_1_q), .clk(Halt), .clr(Go));  // open: en
  Multiplexer #(.select(2), .width(32), .disabled("Z"), .enable("false")) multiplexer_4 (
    .in0(multiplexer_5_out), .in1(multiplexer_3_out), .in2(multiplexer_5_out), .in3(PC_4),
    .out(multiplexer_4_out), .sel({EX_Branch_Pre, IF_ID_Flush}));
  Hex_Digit_Display hex_digit_display_4 (.value(LedData[15:12]));  // open: dp
  Hex_Digit_Display hex_digit_display_5 (.value(LedData[19:16]));  // open: dp
  and and_1 (END, MEM_Syscall, register_1_q);
  Hex_Digit_Display hex_digit_display_6 (.value(LedData[11:8]));  // open: dp
  Hex_Digit_Display hex_digit_display_7 (.value(LedData[7:4]));  // open: dp
  Clock #(.highDuration(1), .lowDuration(1)) clock_1 (.out(clock_1_out));
  // Probe on EX_PC[19:0]
  // Mips_Probe mips_probe_3: pin names not known; wires that end beside it: clock_1_out, EX_IR, CLK
  not not_1 (not_1_out, END);
  and and_2 (and_2_out, not_1_out, not_2_out);
  Register #(.width(32), .trigger("rising"), .Select("low")) PC (
    .D(multiplexer_4_out), .en(and_2_out), .Q(IF_PC), .clk(CLK));  // open: clr
  Hex_Digit_Display hex_digit_display_8 (.value(LedData[3:0]));  // open: dp
  \源寄存器使用情况  \u_源寄存器使用情况_1  (
    .OP0(ID_IR[26]), .OP1(ID_IR[27]), .OP2(ID_IR[28]), .OP3(ID_IR[29]), .OP4(ID_IR[30]), .OP5(ID_IR[31]),
    .F0(Func[0]), .F1(Func[1]), .F2(Func[2]), .F3(Func[3]), .F4(Func[4]), .F5(Func[5]),
    .R1_used(\源寄存器使用情况_1_r1_used ), .R2_used(\源寄存器使用情况_1_r2_used ));
  not not_2 (not_2_out, LoadUse);
  BTB btb_1 (
    .CLK(CLK), .\读_分支指令地址 (IF_PC), .\IF_Row_选中的哪一行 (IF_Row_Pre), .\欲写标志 (EX_Load), .\写_分支指令地址 (EX_PC),
    .\写_分支目标地址 (EX_Next_PC_Pre), .\分支目标地址 (IF_Next_PC_Pre), .\写_更新_预测历史 (EX_Next_State_Pre),
    .\预测历史 (IF_Now_State_Pre), .\EX_Row_选中的哪一行_更新预测历史 (EX_Row_Pre), .MISS(IF_MISS));
  Comparator #(.width(2), .mode("twosComplement")) comparator_1 (
    .a(IF_Now_State_Pre), .b(2'b10), .eq(comparator_1_eq));  // open: gt, lt
  or or_1 (IF_Branch_Pre, comparator_1_eq, comparator_2_eq);
  Comparator #(.width(2), .mode("twosComplement")) comparator_2 (
    .a(IF_Now_State_Pre), .b(2'b11), .eq(comparator_2_eq));  // open: gt, lt
  // Probe on \总周期数 
  // Probe on M_PC[19:0]
  // Mips_Probe mips_probe_4: pin names not known; wires that end beside it: MEM_IR
  Adder #(.width(32)) adder_1 (.a(IF_PC), .b(32'h4), .out(adder_1_out));  // open: cin, cout
  // Probe on \总周期数 
  // Probe on \无条件分支数 
  // Probe on \条件分支成功数 
  // Probe on \插入气泡数 
  // Probe on \LoadUse次数 
  ROM #(.addrWidth(10), .dataWidth(32), .Select("high")) rom_1 (.addr(IF_PC[11:2]), .data(IF_IR));
  Multiplexer #(.select(1), .width(32), .disabled("Z"), .enable("false")) multiplexer_5 (
    .in0(adder_1_out), .in1(IF_Next_PC_Pre), .out(multiplexer_5_out), .sel(IF_Branch_Pre));
  or or_2 (or_2_out, LoadUse, END);
  // Probe on IF_PC[11:0]
  // Probe on WB_PC[19:0]
  // Mips_Probe mips_probe_5: pin names not known; wires that end beside it: WB_IR
  // Mips_Probe mips_probe_6: pin names not known; wires that end beside it: IF_IR
  // Probe on ID_PC[11:0]
  // Probe on EX_PC[11:0]
  \数据相关检测_重定向  \u_数据相关检测_重定向_1  (
    .R1_Used(\源寄存器使用情况_1_r1_used ), .R2_Used(\源寄存器使用情况_1_r2_used ), .DataHazzard(DataHazzard), .R1_num(R1),
    .R2_num(R2), .LoadUse(LoadUse), .EX_WriteReg_num(EX_WriteReg_num), .EX_RegWrite(EX_RegWrite),
    .MEM_WriteReg_num(MEM_WriteReg_num), .MEM_RegWrite(MEM_RegWrite), .EX_MemToReg(EX_MemToReg),
    .RsForward(ID_RsForward), .RtForward(ID_RtForward));
  IF_ID if_id_1 (
    .CLK(CLK), .PC_4(adder_1_out), .IR(IF_IR), .PC(IF_PC), .PC_4_2(if_id_1_pc_4_2), .IR_2({ID_IR, Func}),
    .PC_2(ID_PC), .\同步清零_高电平有效 (IF_ID_Flush), .\使能端_低电平有效 (or_2_out), .MISS(IF_MISS),
    .MISS_2(if_id_1_miss_2), .Branch_Pre(IF_Branch_Pre), .Branch_Pre_2(if_id_1_branch_pre_2),
    .Now_State_Pre(IF_Now_State_Pre), .Now_State_Pre_2(if_id_1_now_state_pre_2), .Row_Pre(IF_Row_Pre),
    .Row_Pre_2(if_id_1_row_pre_2));
  // Probe on M_PC[11:0]
  D_Flip_Flop #(.trigger("high"), .Pre_Clr_Positions("LEGACY"), .NegatePresetClear("false"), .enable("true"), .NewFFLayout("false")) d_ff_1 (.Q(d_ff_1_q));  // open: clk, D, Qn, preset, en, reset
  // Probe on 13'h57
  // Probe on WB_PC[11:0]
  Comparator #(.width(13), .mode("twosComplement")) comparator_3 (
    .a(CNT_num), .b(13'h57), .eq(comparator_3_eq), .lt(comparator_3_lt));  // open: gt
  Clock #(.highDuration(1), .lowDuration(1)) clock_2 (.out(clock_2_out));
  nand nand_1 (nand_1_out, d_ff_1_q, comparator_3_eq);
  Counter #(.width(13), .max('h1fff), .ongoal("stay"), .trigger("rising"), .behavior("old")) counter_1 (
    .count(comparator_3_lt), .Q(CNT_num), .clk(clock_2_out));  // open: load, D, carry, clr, preset
  Multiplexer #(.select(1), .width(5), .disabled("Z"), .enable("false")) multiplexer_6 (
    .in0(ID_IR[20:16]), .in1(ID_IR[15:11]), .out(multiplexer_6_out), .sel(\单周期硬布线控制器_1_regdst ));
  assign bit_extender_1_out = {{16{1'b0}}, {ID_IR[15:6], Func}};  // Bit_Extender bit_extender_1
  assign bit_extender_2_out = {{16{ID_IR[15]}}, {ID_IR[15:6], Func}};  // Bit_Extender bit_extender_2
  assign CLK = nand_1_out ? clock_2_out : 1'bz;  // Controlled_Buffer controlled_buffer_1
  \单周期硬布线控制器  \u_单周期硬布线控制器_1  (
    .Func(Func), .OP(ID_IR[31:26]), .ALU_OP(\单周期硬布线控制器_1_alu_op ), .MemToReg(\单周期硬布线控制器_1_memtoreg ),
    .MemWrite(\单周期硬布线控制器_1_memwrite ), .ALU_SRC(\单周期硬布线控制器_1_alu_src ), .RegWrite(\单周期硬布线控制器_1_regwrite ),
    .SysCALL(\单周期硬布线控制器_1_syscall ), .SignedExt(SignedExt), .RegDst(\单周期硬布线控制器_1_regdst ),
    .JR(\单周期硬布线控制器_1_jr ), .JMP(\单周期硬布线控制器_1_jmp ), .Beq(\单周期硬布线控制器_1_beq ), .JAL(\单周期硬布线控制器_1_jal ),
    .Bne(\单周期硬布线控制器_1_bne ), .LUI(\单周期硬布线控制器_1_lui ), .LH(\单周期硬布线控制器_1_lh ), .BLEZ(\单周期硬布线控制器_1_blez ));
  Multiplexer #(.select(1), .width(5), .disabled("Z"), .enable("false")) multiplexer_7 (
    .in0(ID_IR[25:21]), .in1(5'b00010), .out(R1), .sel(\单周期硬布线控制器_1_syscall ));
  Multiplexer #(.select(1), .width(5), .disabled("Z"), .enable("false")) multiplexer_8 (
    .in0(ID_IR[20:16]), .in1(5'b00100), .out(R2), .sel(\单周期硬布线控制器_1_syscall ));
  Multiplexer #(.select(1), .width(5), .disabled("Z"), .enable("false")) multiplexer_9 (
    .in0(multiplexer_6_out), .in1({5{1'b1}}), .out(multiplexer_9_out), .sel(\单周期硬布线控制器_1_jal ));
  or or_3 (or_3_out, Branch, JMP);
  Multiplexer #(.select(1), .width(32), .disabled("Z"), .enable("false")) multiplexer_10 (
    .in0({EX_PC[31:28], PC_no_condition, 2'b00}), .in1(RS), .out(multiplexer_10_out), .sel(JR));
  Pull_Resistor #(.pull(1)) pull_resistor_1 (.node(CLK));
  not not_3 (not_3_out, END);
  or or_4 (ID_EX_Flush, IF_ID_Flush, LoadUse);
  MIPS_Regifile mips_regifile_1 (
    .Din(RDin), .Clk(CLK), .R1(mips_regifile_1_r1), .R2(mips_regifile_1_r2), .WE(RegWrite),
    .W_num(mem_wb_1_w_num_2), .R1_num(R1), .R2_num(R2));
  Multiplexer #(.select(1), .width(32), .disabled("Z"), .enable("false")) multiplexer_11 (
    .in0(bit_extender_1_out), .in1(bit_extender_2_out), .out(multiplexer_11_out), .sel(SignedExt));
  \双预测位状态机  \u_双预测位状态机_1  (.Now_State(EX_Now_State_Pre), .Branch(or_3_out), .Next_State(\双预测位状态机_1_next_state ));
  Multiplexer #(.select(1), .width(2), .disabled("Z"), .enable("false")) multiplexer_12 (
    .in0(\设置为11或者10 ), .in1(\设置为11 ), .out(multiplexer_12_out), .sel(IsBranchIR_con));
  Register #(.width(16), .trigger("rising"), .Select("low")) register_2 (
    .D(adder_2_out), .en(not_3_out), .Q(register_2_q), .clk(CLK));  // open: clr
  Multiplexer #(.select(1), .width(32), .disabled("Z"), .enable("false")) multiplexer_13 (
    .in0(multiplexer_10_out), .in1(PC_condition), .out(EX_Next_PC_Pre), .sel(IsBranchIR_con));
  Adder #(.width(16)) adder_2 (.a(16'h1), .b(register_2_q), .out(adder_2_out));  // open: cin, cout
  ID_EX id_ex_1 (
    .CLK(CLK), .RS(mips_regifile_1_r1), .RS_2(id_ex_1_rs_2), .RT(mips_regifile_1_r2), .RT_2(id_ex_1_rt_2),
    .W_num(multiplexer_9_out), .W_num_2(EX_WriteReg_num), .PC_4(if_id_1_pc_4_2), .PC_4_2(PC_4),
    .SIGN_IMM(multiplexer_11_out), .SIGN_IMM_2(id_ex_1_sign_imm_2), .IMM26({ID_IR[25:6], Func}),
    .IMM26_2(PC_no_condition), .PC(ID_PC), .PC_2(EX_PC), .JMP(\单周期硬布线控制器_1_jmp ), .JMP_2(JMP),
    .JR(\单周期硬布线控制器_1_jr ), .JR_2(JR), .BLEZ(\单周期硬布线控制器_1_blez ), .BLEZ_2(id_ex_1_blez_2),
    .LH(\单周期硬布线控制器_1_lh ), .LH_2(id_ex_1_lh_2), .LUI(\单周期硬布线控制器_1_lui ), .LUI_2(id_ex_1_lui_2),
    .BEQ(\单周期硬布线控制器_1_beq ), .BEQ_2(id_ex_1_beq_2), .BNE(\单周期硬布线控制器_1_bne ), .BNE_2(id_ex_1_bne_2),
    .MemToReg(\单周期硬布线控制器_1_memtoreg ), .MemToReg_2(EX_MemToReg), .MemWrite(\单周期硬布线控制器_1_memwrite ),
    .MemWrite_2(id_ex_1_memwrite_2), .ALU_OP(\单周期硬布线控制器_1_alu_op ), .ALU_OP_2(id_ex_1_alu_op_2),
    .ALU_SrcB(\单周期硬布线控制器_1_alu_src ), .ALU_SrcB_2(id_ex_1_alu_srcb_2), .RegWrite(\单周期硬布线控制器_1_regwrite ),
    .RegWrite_2(EX_RegWrite), .JAL(\单周期硬布线控制器_1_jal ), .JAL_2(id_ex_1_jal_2),
    .Syscall(\单周期硬布线控制器_1_syscall ), .Syscall_2(id_ex_1_syscall_2), .\使能端_低电平有效 (END),
    .\同步清零_高电平有效 (ID_EX_Flush), .IR({ID_IR, Func}), .IR_2(EX_IR), .RsForward(ID_RsForward),
    .RsForward_2(id_ex_1_rsforward_2), .RtForward(ID_RtForward), .RtForward_2(id_ex_1_rtforward_2),
    .MISS(if_id_1_miss_2), .MISS_2(EX_MISS), .Branch_Pre(if_id_1_branch_pre_2), .Branch_Pre_2(EX_Branch_Pre),
    .Now_State_Pre(if_id_1_now_state_pre_2), .Now_State_Pre_2(EX_Now_State_Pre), .Row_Pre(if_id_1_row_pre_2),
    .Row_Pre_2(EX_Row_Pre));
  or or_5 (or_5_out, IsBranchIR_con, JMP);
  Multiplexer #(.select(1), .width(2), .disabled("Z"), .enable("false")) multiplexer_14 (
    .in1(multiplexer_12_out), .out(multiplexer_14_out), .sel(or_5_out));  // open: in0
  Adder #(.width(16)) adder_3 (.a(adder_2_out), .b({16{1'b1}}), .out(\总周期数 ));  // open: cin, cout
  or or_6 (IsBranchIR_con, id_ex_1_blez_2, id_ex_1_beq_2, id_ex_1_bne_2);
  Multiplexer #(.select(2), .width(32), .disabled("Z"), .enable("false")) multiplexer_15 (
    .in0(id_ex_1_rs_2), .in1(MEM_ALU), .in2(RDin), .in3(MEM_ALU), .out(multiplexer_15_out),
    .sel(id_ex_1_rsforward_2));
  Multiplexer #(.select(2), .width(32), .disabled("Z"), .enable("false")) multiplexer_16 (
    .in0(id_ex_1_rt_2), .in1(MEM_ALU), .in2(RDin), .in3(MEM_ALU), .out(multiplexer_16_out),
    .sel(id_ex_1_rtforward_2));
  Multiplexer #(.select(1), .width(2), .disabled("Z"), .enable("false")) multiplexer_17 (
    .in0(\双预测位状态机_1_next_state ), .in1(multiplexer_14_out), .out(EX_Next_State_Pre), .sel(EX_MISS));
  xnor xnor_1 (xnor_1_out, or_3_out, EX_Branch_Pre);
  Comparator #(.width(32), .mode("twosComplement")) comparator_4 (
    .a(32'ha), .b(v0), .eq(comparator_4_eq));  // open: gt, lt
  Shifter #(.width(32), .shift("ll")) shifter_1 (.in(id_ex_1_sign_imm_2), .\dist (5'b00010), .out(shifter_1_out));
  and and_3 (Predict_Success, xnor_1_out, or_5_out);
  Register #(.width(32), .trigger("rising"), .Select("low")) register_3 (
    .D(MDin), .en(LedOut), .Q(LedData), .clk(CLK));  // open: clr
  Comparator #(.width(32), .mode("twosComplement")) comparator_5 (
    .a(v0), .b({32{1'b0}}), .eq(comparator_5_eq), .lt(comparator_5_lt));  // open: gt
  and and_4 (Halt, id_ex_1_syscall_2, comparator_4_eq);
  and and_5 (and_5_out, id_ex_1_syscall_2, ~comparator_4_eq);  // AND_Gate
  Register #(.width(32), .trigger("falling"), .Select("low")) register_4 (
    .D(multiplexer_15_out), .Q(v0), .clk(CLK));  // open: en, clr
  Adder #(.width(32)) adder_4 (.a(shifter_1_out), .b(PC_4), .out(PC_condition));  // open: cin, cout
  // Probe on Predict_Success
  or or_7 (or_7_out, comparator_5_eq, comparator_5_lt);
  Multiplexer #(.select(1), .width(32), .disabled("Z"), .enable("false")) multiplexer_18 (
    .in0(multiplexer_16_out), .in1(id_ex_1_sign_imm_2), .out(multiplexer_18_out), .sel(id_ex_1_alu_srcb_2));
  not not_4 (not_4_out, Predict_Success);
  and and_6 (and_6_out, or_7_out, id_ex_1_blez_2);
  MIPS_ALU mips_alu_1 (
    .X(multiplexer_15_out), .Y(multiplexer_18_out), .AluOP(id_ex_1_alu_op_2), .Equal(mips_alu_1_equal),
    .Result(mips_alu_1_result), .shamt(PC_no_condition[12:8]));  // open: Result_2
  and and_7 (EX_Load, EX_MISS, or_5_out);
  and and_8 (IF_ID_Flush, or_5_out, not_4_out);
  and and_9 (and_9_out, mips_alu_1_equal, id_ex_1_beq_2);
  and and_10 (and_10_out, ~mips_alu_1_equal, id_ex_1_bne_2);  // AND_Gate
  Shifter #(.width(32), .shift("ll")) shifter_2 (.in(id_ex_1_sign_imm_2), .\dist (5'b10000), .out(shifter_2_out));
  or or_8 (Branch, and_6_out, and_9_out, and_10_out);
  EX_MEM ex_mem_1 (
    .CLK(CLK), .W_num(EX_WriteReg_num), .W_num_2(MEM_WriteReg_num), .Write_Data(multiplexer_16_out),
    .Write_Data_2(MDin), .SIGN_IMM(shifter_2_out), .SIGN_IMM_2(ex_mem_1_sign_imm_2),
    .ALU_RESULT(mips_alu_1_result), .ALU_RESULT_2(ex_mem_1_alu_result_2), .PC(EX_PC), .PC_2(M_PC),
    .LH(id_ex_1_lh_2), .LH_2(ex_mem_1_lh_2), .LUI(id_ex_1_lui_2), .LUI_2(ex_mem_1_lui_2),
    .MemToReg(EX_MemToReg), .MemToReg_2(ex_mem_1_memtoreg_2), .MemWrite(id_ex_1_memwrite_2),
    .MemWrite_2(MemWrite), .RegWrite(EX_RegWrite), .RegWrite_2(MEM_RegWrite), .PC_4(PC_4),
    .PC_4_2(ex_mem_1_pc_4_2), .JAL(id_ex_1_jal_2), .JAL_2(ex_mem_1_jal_2), .\使能端_低电平有效 (END),
    .\同步清零_高电平有效 (1'b0), .Syscall(id_ex_1_syscall_2), .Syscall_2(ex_mem_1_syscall_2), .IR(EX_IR),
    .IR_2(MEM_IR), .Ledout(and_5_out), .Ledout_2(LedOut));
  Multiplexer #(.select(1), .width(32), .disabled("Z"), .enable("false")) multiplexer_19 (
    .in0(ex_mem_1_alu_result_2), .in1(ex_mem_1_sign_imm_2), .out(MEM_ALU), .sel(ex_mem_1_lui_2));
  RAM #(.addrWidth(10), .dataWidth(32), .bus("separate"), .Select("high")) ram_1 (
    .addr(ex_mem_1_alu_result_2[11:2]), .din(MDin), .data(ram_1_data), .str(MemWrite), .clk(CLK));  // open: sel, ld, clr
  MEM_WB mem_wb_1 (
    .CLK(CLK), .W_num(MEM_WriteReg_num), .W_num_2(mem_wb_1_w_num_2), .MEM_Data(ram_1_data),
    .MEM_Data_2(mem_wb_1_mem_data_2), .SIGN_IMM(ex_mem_1_sign_imm_2), .SIGN_IMM_2(mem_wb_1_sign_imm_2),
    .ALU_RESULT(ex_mem_1_alu_result_2), .ALU_RESULT_2(mem_wb_1_alu_result_2), .PC(M_PC), .PC_2(WB_PC),
    .LH(ex_mem_1_lh_2), .LH_2(mem_wb_1_lh_2), .LUI(ex_mem_1_lui_2), .LUI_2(mem_wb_1_lui_2),
    .MemToReg(ex_mem_1_memtoreg_2), .MemToReg_2(mem_wb_1_memtoreg_2), .RegWrite(MEM_RegWrite),
    .RegWrite_2(RegWrite), .PC_4(ex_mem_1_pc_4_2), .PC_4_2(mem_wb_1_pc_4_2), .JAL(ex_mem_1_jal_2),
    .JAL_2(mem_wb_1_jal_2), .\使能端_低电平有效 (END), .\同步清零_高电平有效 (1'b0), .Syscall(ex_mem_1_syscall_2),
    .Syscall_2(MEM_Syscall), .IR(MEM_IR), .IR_2(WB_IR));
  Multiplexer #(.select(1), .width(32), .disabled("Z"), .enable("false")) multiplexer_20 (
    .in0(mem_wb_1_alu_result_2), .in1(mem_wb_1_mem_data_2), .out(multiplexer_20_out),
    .sel(mem_wb_1_memtoreg_2));
  Multiplexer #(.select(1), .width(16), .disabled("Z"), .enable("false")) multiplexer_21 (
    .in0(multiplexer_20_out[15:0]), .in1(multiplexer_20_out[31:16]), .out(multiplexer_21_out),
    .sel(mem_wb_1_alu_result_2[1]));
  assign bit_extender_3_out = {{16{multiplexer_21_out[15]}}, multiplexer_21_out};  // Bit_Extender bit_extender_3
  Multiplexer #(.select(1), .width(32), .disabled("Z"), .enable("false")) multiplexer_22 (
    .in0(multiplexer_20_out), .in1(bit_extender_3_out), .out(multiplexer_22_out), .sel(mem_wb_1_lh_2));
  Multiplexer #(.select(1), .width(32), .disabled("Z"), .enable("false")) multiplexer_23 (
    .in0(multiplexer_22_out), .in1(mem_wb_1_sign_imm_2), .out(multiplexer_23_out), .sel(mem_wb_1_lui_2));
  Multiplexer #(.select(1), .width(32), .disabled("Z"), .enable("false")) multiplexer_24 (
    .in0(multiplexer_23_out), .in1(mem_wb_1_pc_4_2), .out(RDin), .sel(mem_wb_1_jal_2));

  // Other names for the same wires on the sheet: Insert_Bubble = IF_ID_Flush; B_condition_init[1:0] = \设置为11 ;
  //   B_Nocondition_init[1:0] = \设置为11或者10 ; PC_no_condition[31:28] = EX_PC[31:28]; ID_IR[5:0] = Func;
  //   OP[5:0] = ID_IR[31:26]; MEM_PC[31:0] = M_PC; Stall = LoadUse; WB_WD[31:0] = RDin

  // Notes on the sheet:
  //   中断源
  //   时空图监测，可删除
  //   中断等待指示
  //   数码管输出
  //   若不命中，该值默认为0
  //   指令存储器
  //   contents of rom_1 (hex, n*v repeats v):
  //   20110001 8000c05 20110001 20120002 20130003 8000c09 20110001 20120002 20130003 8000c0d 20110001
  //   20120002 20130003 8000c11 20110001 20120002 20130003 c000cf6 20100001 20110001 118fc0 112020
  //   20020022 c 118882 12200001 8000c15 112020 20020022 c 20110001 118880 112020 20020022 c 12200001
  //   8000c1f 20110001 118fc0 112020 20020022 c 1188c3 112020 20020022 c 118903 112020 20020022 c 118903
  //   112020 20020022 c 118903 112020 20020022 c 118903 112020 20020022 c 118903 112020 20020022 c 118903
  //   112020 20020022 c 118903 112020 20020022 c 20100001 109fc0 139fc3 8021 2012000c 24160003 26100001
  //   3210000f 20080008 20090001 139900 2709825 132020 20020022 c 1094022 1500fff9 22100001 2018000f
  //   2188024 108700 20080008 20090001 139902 2709825 132021 20020022 c 1094022 1500fff9 108702 2c9b022
  //   12c00001 8000c50 4020 1084027 84400 3508ffff 82021 20020022 c 2010ffff 20110000 ae300000 22100001
  //   22310004 ae300000 22100001 22310004 ae300000 22100001 22310004 ae300000 22100001 22310004 ae300000
  //   22100001 22310004 ae300000 22100001 22310004 ae300000 22100001 22310004 ae300000 22100001 22310004
  //   ae300000 22100001 22310004 ae300000 22100001 22310004 ae300000 22100001 22310004 ae300000 22100001
  //   22310004 ae300000 22100001 22310004 ae300000 22100001 22310004 ae300000 22100001 22310004 ae300000
  //   22100001 22310004 22100001 8020 2011003c 8e130000 8e340000 274402a 11000002 ae330000 ae140000
  //   2231fffc 1611fff8 102020 20020022 c 22100004 2011003c 1611fff2 2002000a c 200b0008 3c11fedc 3631ffff
  //   112020 20020022 c 3c11ba98 112020 c 3c117654 112020 c 3c113210 112020 c 216bffff 1560fff0 2002000a c
  //   2008ffff 20090000 20111997 112020 20020022 c 2288820 2e291949 1120fffa 2002000a c 20090000 200b0010
  //   34118483 20120404 118c00 129400 36318281 22520404 ad310000 2328820 21290004 216bffff 1560fffb
  //   200b0020 20090000 85310000 112020 20020022 c 21290002 216bffff 1560fff9 2002000a c 2011fff1 112020
  //   20020022 c 22310001 1a20fffb 2002000a c 20100000 22100001 102020 20020022 c 22100002 102020 20020022
  //   c 22100003 102020 20020022 c 22100004 102020 20020022 c 22100005 102020 20020022 c 22100006 102020
  //   20020022 c 22100007 102020 20020022 c 22100008 102020 20020022 20020022 c 3e00008
  //   缺失时，默认为0，即选择PC+4
  //   控制位
  //   IR
  //   流水调试日志用
  //   暂停节拍，不能为0
  //   戳工具置1进入计数暂停模式，ctrl+k时钟自动运行到对应节拍暂停
  //   ctrl+k关闭时钟连续运行，将控制位置零，进入单步调试模式调试
  //   OP
  //   Func
  //   rs
  //   rt
  //   rd
  //   imm16
  //   imm26
  //   JMP
  //   JR
  //   OP
  //   Func
  //   Syscall
  //   可计数暂停的时钟源
  //   Blez
  //   LH
  //   LUI
  //   Beq
  //   Bne
  //   MemToReg
  //   MemWrite
  //   AluOP
  //   AluSrcB
  //   RegWrite
  //   JAL
  //   RegDst
  //   初值
  //   为方便自动评测，需要输出流水线各段保存的PC值，注意是PC不是PC+4，另外ID段寄存器写入信息，Mem段内存写入信息也要输出
  //   Blez
  //   LH
  //   LUI
  //   Beq
  //   Bne
  //   MemToReg
  //   MemWrite
  //   AluOP
  //   AluSrcB
  //   RegWrite
  //   JAL
  //   Syscall
  //   RS
  //   RT
  //   W#
  //   SIGN_IMM
  //   PC+4
  //   IMM26
  //   shamt
  //   LH
  //   LUI
  //   MemToReg
  //   MemWrite
  //   RegWrite
  //   JAL
  //   Syscall
  //   Ledout
  //   Write_Data
  //   W#
  //   LUI_IMM
  //   PC+4
  //   设置重定向的预测初值
  //   ALU_RESULT
  //   LH
  //   LUI
  //   MemToReg
  //   RegWrite
  //   JAL
  //   Syscall
  //   ALU_RESULT
  //   MEM_Data
  //   W#
  //   LUI_IMM
  //   PC+4
endmodule

module BTB (
  input  [31:0] \读_分支指令地址 ,
  input  [7:0] \EX_Row_选中的哪一行_更新预测历史 ,
  input  [1:0] \写_更新_预测历史 ,
  input  \欲写标志 ,
  input  [31:0] \写_分支目标地址 ,
  input  [31:0] \写_分支指令地址 ,
  input  CLK,
  output [1:0] \预测历史 ,
  output [7:0] \IF_Row_选中的哪一行 ,
  output [31:0] \分支目标地址 ,
  output MISS
);

  wire and_9_out, and_10_out, and_11_out, and_12_out, and_13_out, and_14_out, and_15_out, and_16_out,
       not_1_out, not_2_out, not_3_out, not_4_out, not_5_out, not_6_out, not_7_out, not_8_out, or_1_out,
       or_2_out, or_3_out, or_4_out, or_5_out, or_6_out, or_7_out, or_8_out, ToWriteW0, ToWriteW1, ToWriteW2,
       ToWriteW3, ToWriteW4, ToWriteW5, ToWriteW6, ToWriteW7, V0, V1, V2, V3, V4, V5, V6, V7, W0, W1, W2, W3,
       W4, W5, W6, W7;
  wire [1:0] controlled_buffer_9_out, \预测历史_2_q , \预测历史_3_q , \预测历史_4_q , \预测历史_5_q , \预测历史_6_q , \预测历史_7_q ,
       \预测历史_8_q , \预测历史_q ;
  wire [2:0] \btb写控制_1_towritre_num ;
  wire [15:0] Count0, Count1, Count2, Count3, Count4, Count5, Count6, Count7;
  wire [31:0] controlled_buffer_1_out, \分支指令地址_2_q , \分支指令地址_3_q , \分支指令地址_4_q , \分支指令地址_5_q , \分支指令地址_6_q ,
       \分支指令地址_7_q , \分支指令地址_8_q , \分支指令地址_q , \分支目标地址_2_q , \分支目标地址_3_q , \分支目标地址_4_q , \分支目标地址_5_q ,
       \分支目标地址_6_q , \分支目标地址_7_q , \分支目标地址_8_q , \分支目标地址_q ;

  Register #(.width(1), .trigger("rising"), .Select("low")) VALID (
    .D(1'b1), .en(ToWriteW0), .Q(V0), .clk(CLK));  // open: clr
  and and_1 (ToWriteW0, \欲写标志 , W0);
  Register #(.width(1), .trigger("rising"), .Select("low")) VALID_2 (
    .D(1'b1), .en(ToWriteW1), .Q(V1), .clk(CLK));  // open: clr
  and and_2 (ToWriteW1, \欲写标志 , W1);
  Register #(.width(1), .trigger("rising"), .Select("low")) VALID_3 (
    .D(1'b1), .en(ToWriteW2), .Q(V2), .clk(CLK));  // open: clr
  and and_3 (ToWriteW2, \欲写标志 , W2);
  Register #(.width(1), .trigger("rising"), .Select("low")) VALID_4 (
    .D(1'b1), .en(ToWriteW3), .Q(V3), .clk(CLK));  // open: clr
  and and_4 (ToWriteW3, \欲写标志 , W3);
  Register #(.width(1), .trigger("rising"), .Select("low")) VALID_5 (
    .D(1'b1), .en(ToWriteW4), .Q(V4), .clk(CLK));  // open: clr
  and and_5 (ToWriteW4, \欲写标志 , W4);
  Register #(.width(1), .trigger("rising"), .Select("low")) VALID_6 (
    .D(1'b1), .en(ToWriteW5), .Q(V5), .clk(CLK));  // open: clr
  and and_6 (ToWriteW5, \欲写标志 , W5);
  Register #(.width(1), .trigger("rising"), .Select("low")) VALID_7 (
    .D(1'b1), .en(ToWriteW6), .Q(V6), .clk(CLK));  // open: clr
  and and_7 (ToWriteW6, \欲写标志 , W6);
  Register #(.width(1), .trigger("rising"), .Select("low")) VALID_8 (
    .D(1'b1), .en(ToWriteW7), .Q(V7), .clk(CLK));  // open: clr
  and and_8 (ToWriteW7, \欲写标志 , W7);
  Register #(.width(32), .trigger("rising"), .Select("low")) \u_分支指令地址  (
    .D(\写_分支指令地址 ), .en(ToWriteW0), .Q(\分支指令地址_q ), .clk(CLK));  // open: clr
  Register #(.width(32), .trigger("rising"), .Select("low")) \u_分支指令地址_2  (
    .D(\写_分支指令地址 ), .en(ToWriteW1), .Q(\分支指令地址_2_q ), .clk(CLK));  // open: clr
  Register #(.width(32), .trigger("rising"), .Select("low")) \u_分支指令地址_3  (
    .D(\写_分支指令地址 ), .en(ToWriteW2), .Q(\分支指令地址_3_q ), .clk(CLK));  // open: clr
  Register #(.width(32), .trigger("rising"), .Select("low")) \u_分支指令地址_4  (
    .D(\写_分支指令地址 ), .en(ToWriteW3), .Q(\分支指令地址_4_q ), .clk(CLK));  // open: clr
  Register #(.width(32), .trigger("rising"), .Select("low")) \u_分支指令地址_5  (
    .D(\写_分支指令地址 ), .en(ToWriteW4), .Q(\分支指令地址_5_q ), .clk(CLK));  // open: clr
  Register #(.width(32), .trigger("rising"), .Select("low")) \u_分支指令地址_6  (
    .D(\写_分支指令地址 ), .en(ToWriteW5), .Q(\分支指令地址_6_q ), .clk(CLK));  // open: clr
  Register #(.width(32), .trigger("rising"), .Select("low")) \u_分支指令地址_7  (
    .D(\写_分支指令地址 ), .en(ToWriteW6), .Q(\分支指令地址_7_q ), .clk(CLK));  // open: clr
  Register #(.width(32), .trigger("rising"), .Select("low")) \u_分支指令地址_8  (
    .D(\写_分支指令地址 ), .en(ToWriteW7), .Q(\分支指令地址_8_q ), .clk(CLK));  // open: clr
  \BTB写控制  \btb写控制_1  (
    .V0(V0), .V1(V1), .V2(V2), .V3(V3), .V4(V4), .V5(V5), .V6(V6), .V7(V7), .LRUCount0(Count0),
    .LRUCount1(Count1), .LRUCount2(Count2), .LRUCount3(Count3), .LRUCount4(Count4), .LRUCount5(Count5),
    .LRUCount6(Count6), .LRUCount7(Count7), .ToWritre_num(\btb写控制_1_towritre_num ));
  \八路并发控制  \u_八路并发控制_1  (
    .in_3(\分支指令地址_q ), .in_4(V0), .in_5(\分支指令地址_2_q ), .in_6(V1), .in_7(\分支指令地址_3_q ), .in_8(V2),
    .in_9(\分支指令地址_4_q ), .in_10(V3), .in_11(\分支指令地址_5_q ), .in_12(V4), .in_13(\分支指令地址_6_q ), .in_14(V5),
    .in_15(\分支指令地址_7_q ), .in_16(V6), .in_17(\分支指令地址_8_q ), .in_18(V7), .K0(\IF_Row_选中的哪一行 [0]),
    .K1(\IF_Row_选中的哪一行 [1]), .K2(\IF_Row_选中的哪一行 [2]), .K3(\IF_Row_选中的哪一行 [3]), .K4(\IF_Row_选中的哪一行 [4]),
    .K5(\IF_Row_选中的哪一行 [5]), .K6(\IF_Row_选中的哪一行 [6]), .K7(\IF_Row_选中的哪一行 [7]), .V(1'b1),
    .\分支指令地址 (\读_分支指令地址 ), .Miss(MISS));
  Decoder #(.select(3), .tristate("false"), .disabled("Z"), .enable("false")) decoder_1 (
    .out0(W0), .out1(W1), .out2(W2), .out3(W3), .out4(W4), .out5(W5), .out6(W6), .out7(W7),
    .sel(\btb写控制_1_towritre_num ));
  not not_1 (not_1_out, ToWriteW0);
  and and_9 (and_9_out, not_1_out, V0);
  not not_2 (not_2_out, ToWriteW1);
  and and_10 (and_10_out, not_2_out, V1);
  not not_3 (not_3_out, ToWriteW2);
  and and_11 (and_11_out, not_3_out, V2);
  not not_4 (not_4_out, ToWriteW3);
  and and_12 (and_12_out, not_4_out, V3);
  not not_5 (not_5_out, ToWriteW4);
  and and_13 (and_13_out, not_5_out, V4);
  not not_6 (not_6_out, ToWriteW5);
  and and_14 (and_14_out, not_6_out, V5);
  not not_7 (not_7_out, ToWriteW6);
  and and_15 (and_15_out, not_7_out, V6);
  not not_8 (not_8_out, ToWriteW7);
  and and_16 (and_16_out, not_8_out, V7);
  Counter #(.width(16), .max('hffff), .ongoal("wrap"), .trigger("rising"), .behavior("old")) LRUCount (
    .load(ToWriteW0), .D({16{1'b0}}), .count(and_9_out), .Q(Count0), .clk(CLK), .clr(\IF_Row_选中的哪一行 [0]));  // open: carry, preset
  Counter #(.width(16), .max('hffff), .ongoal("wrap"), .trigger("rising"), .behavior("old")) LRUCount_2 (
    .load(ToWriteW1), .D({16{1'b0}}), .count(and_10_out), .Q(Count1), .clk(CLK), .clr(\IF_Row_选中的哪一行 [1]));  // open: carry, preset
  Counter #(.width(16), .max('hffff), .ongoal("wrap"), .trigger("rising"), .behavior("old")) LRUCount_3 (
    .load(ToWriteW2), .D({16{1'b0}}), .count(and_11_out), .Q(Count2), .clk(CLK), .clr(\IF_Row_选中的哪一行 [2]));  // open: carry, preset
  Counter #(.width(16), .max('hffff), .ongoal("wrap"), .trigger("rising"), .behavior("old")) LRUCount_4 (
    .load(ToWriteW3), .D({16{1'b0}}), .count(and_12_out), .Q(Count3), .clk(CLK), .clr(\IF_Row_选中的哪一行 [3]));  // open: carry, preset
  Counter #(.width(16), .max('hffff), .ongoal("wrap"), .trigger("rising"), .behavior("old")) LRUCount_5 (
    .load(ToWriteW4), .D({16{1'b0}}), .count(and_13_out), .Q(Count4), .clk(CLK), .clr(\IF_Row_选中的哪一行 [4]));  // open: carry, preset
  Counter #(.width(16), .max('hffff), .ongoal("wrap"), .trigger("rising"), .behavior("old")) LRUCount_6 (
    .load(ToWriteW5), .D({16{1'b0}}), .count(and_14_out), .Q(Count5), .clk(CLK), .clr(\IF_Row_选中的哪一行 [5]));  // open: carry, preset
  Counter #(.width(16), .max('hffff), .ongoal("wrap"), .trigger("rising"), .behavior("old")) LRUCount_7 (
    .load(ToWriteW6), .D({16{1'b0}}), .count(and_15_out), .Q(Count6), .clk(CLK), .clr(\IF_Row_选中的哪一行 [6]));  // open: carry, preset
  Counter #(.width(16), .max('hffff), .ongoal("wrap"), .trigger("rising"), .behavior("old")) LRUCount_8 (
    .load(ToWriteW7), .D({16{1'b0}}), .count(and_16_out), .Q(Count7), .clk(CLK), .clr(\IF_Row_选中的哪一行 [7]));  // open: carry, preset
  Register #(.width(32), .trigger("rising"), .Select("low")) \u_分支目标地址  (
    .D(\写_分支目标地址 ), .en(ToWriteW0), .Q(\分支目标地址_q ), .clk(CLK));  // open: clr
  assign controlled_buffer_1_out = \IF_Row_选中的哪一行 [0] ? \分支目标地址_q  : 32'bz;  // Controlled_Buffer controlled_buffer_1
  Register #(.width(32), .trigger("rising"), .Select("low")) \u_分支目标地址_2  (
    .D(\写_分支目标地址 ), .en(ToWriteW1), .Q(\分支目标地址_2_q ), .clk(CLK));  // open: clr
  assign controlled_buffer_1_out = \IF_Row_选中的哪一行 [1] ? \分支目标地址_2_q  : 32'bz;  // Controlled_Buffer controlled_buffer_2
  assign controlled_buffer_1_out = \IF_Row_选中的哪一行 [2] ? \分支目标地址_3_q  : 32'bz;  // Controlled_Buffer controlled_buffer_3
  Register #(.width(32), .trigger("rising"), .Select("low")) \u_分支目标地址_3  (
    .D(\写_分支目标地址 ), .en(ToWriteW2), .Q(\分支目标地址_3_q ), .clk(CLK));  // open: clr
  assign controlled_buffer_1_out = \IF_Row_选中的哪一行 [3] ? \分支目标地址_4_q  : 32'bz;  // Controlled_Buffer controlled_buffer_4
  Register #(.width(32), .trigger("rising"), .Select("low")) \u_分支目标地址_4  (
    .D(\写_分支目标地址 ), .en(ToWriteW3), .Q(\分支目标地址_4_q ), .clk(CLK));  // open: clr
  assign controlled_buffer_1_out = \IF_Row_选中的哪一行 [4] ? \分支目标地址_5_q  : 32'bz;  // Controlled_Buffer controlled_buffer_5
  Register #(.width(32), .trigger("rising"), .Select("low")) \u_分支目标地址_5  (
    .D(\写_分支目标地址 ), .en(ToWriteW4), .Q(\分支目标地址_5_q ), .clk(CLK));  // open: clr
  assign controlled_buffer_1_out = \IF_Row_选中的哪一行 [5] ? \分支目标地址_6_q  : 32'bz;  // Controlled_Buffer controlled_buffer_6
  Register #(.width(32), .trigger("rising"), .Select("low")) \u_分支目标地址_6  (
    .D(\写_分支目标地址 ), .en(ToWriteW5), .Q(\分支目标地址_6_q ), .clk(CLK));  // open: clr
  Register #(.width(32), .trigger("rising"), .Select("low")) \u_分支目标地址_7  (
    .D(\写_分支目标地址 ), .en(ToWriteW6), .Q(\分支目标地址_7_q ), .clk(CLK));  // open: clr
  assign controlled_buffer_1_out = \IF_Row_选中的哪一行 [6] ? \分支目标地址_7_q  : 32'bz;  // Controlled_Buffer controlled_buffer_7
  Register #(.width(32), .trigger("rising"), .Select("low")) \u_分支目标地址_8  (
    .D(\写_分支目标地址 ), .en(ToWriteW7), .Q(\分支目标地址_8_q ), .clk(CLK));  // open: clr
  assign controlled_buffer_1_out = \IF_Row_选中的哪一行 [7] ? \分支目标地址_8_q  : 32'bz;  // Controlled_Buffer controlled_buffer_8
  Multiplexer #(.select(1), .width(32), .disabled("Z"), .enable("false")) multiplexer_1 (
    .in0(controlled_buffer_1_out), .in1({32{1'b0}}), .out(\分支目标地址 ), .sel(MISS));
  or or_1 (or_1_out, \EX_Row_选中的哪一行_更新预测历史 [0], ToWriteW0);
  or or_2 (or_2_out, \EX_Row_选中的哪一行_更新预测历史 [1], ToWriteW1);
  or or_3 (or_3_out, \EX_Row_选中的哪一行_更新预测历史 [2], ToWriteW2);
  or or_4 (or_4_out, \EX_Row_选中的哪一行_更新预测历史 [3], ToWriteW3);
  or or_5 (or_5_out, \EX_Row_选中的哪一行_更新预测历史 [4], ToWriteW4);
  or or_6 (or_6_out, \EX_Row_选中的哪一行_更新预测历史 [5], ToWriteW5);
  or or_7 (or_7_out, \EX_Row_选中的哪一行_更新预测历史 [6], ToWriteW6);
  or or_8 (or_8_out, \EX_Row_选中的哪一行_更新预测历史 [7], ToWriteW7);
  Register #(.width(2), .trigger("rising"), .Select("low")) \u_预测历史  (
    .D(\写_更新_预测历史 ), .en(or_1_out), .Q(\预测历史_q ), .clk(CLK));  // open: clr
  Register #(.width(2), .trigger("rising"), .Select("low")) \u_预测历史_2  (
    .D(\写_更新_预测历史 ), .en(or_2_out), .Q(\预测历史_2_q ), .clk(CLK));  // open: clr
  Register #(.width(2), .trigger("rising"), .Select("low")) \u_预测历史_3  (
    .D(\写_更新_预测历史 ), .en(or_3_out), .Q(\预测历史_3_q ), .clk(CLK));  // open: clr
  Register #(.width(2), .trigger("rising"), .Select("low")) \u_预测历史_4  (
    .D(\写_更新_预测历史 ), .en(or_4_out), .Q(\预测历史_4_q ), .clk(CLK));  // open: clr
  Register #(.width(2), .trigger("rising"), .Select("low")) \u_预测历史_5  (
    .D(\写_更新_预测历史 ), .en(or_5_out), .Q(\预测历史_5_q ), .clk(CLK));  // open: clr
  Register #(.width(2), .trigger("rising"), .Select("low")) \u_预测历史_6  (
    .D(\写_更新_预测历史 ), .en(or_6_out), .Q(\预测历史_6_q ), .clk(CLK));  // open: clr
  Register #(.width(2), .trigger("rising"), .Select("low")) \u_预测历史_7  (
    .D(\写_更新_预测历史 ), .en(or_7_out), .Q(\预测历史_7_q ), .clk(CLK));  // open: clr
  Register #(.width(2), .trigger("rising"), .Select("low")) \u_预测历史_8  (
    .D(\写_更新_预测历史 ), .en(or_8_out), .Q(\预测历史_8_q ), .clk(CLK));  // open: clr
  assign controlled_buffer_9_out = \IF_Row_选中的哪一行 [0] ? \预测历史_q  : 2'bz;  // Controlled_Buffer controlled_buffer_9
  assign controlled_buffer_9_out = \IF_Row_选中的哪一行 [1] ? \预测历史_2_q  : 2'bz;  // Controlled_Buffer controlled_buffer_10
  assign controlled_buffer_9_out = \IF_Row_选中的哪一行 [2] ? \预测历史_3_q  : 2'bz;  // Controlled_Buffer controlled_buffer_11
  assign controlled_buffer_9_out = \IF_Row_选中的哪一行 [3] ? \预测历史_4_q  : 2'bz;  // Controlled_Buffer controlled_buffer_12
  assign controlled_buffer_9_out = \IF_Row_选中的哪一行 [4] ? \预测历史_5_q  : 2'bz;  // Controlled_Buffer controlled_buffer_13
  assign controlled_buffer_9_out = \IF_Row_选中的哪一行 [5] ? \预测历史_6_q  : 2'bz;  // Controlled_Buffer controlled_buffer_14
  assign controlled_buffer_9_out = \IF_Row_选中的哪一行 [6] ? \预测历史_7_q  : 2'bz;  // Controlled_Buffer controlled_buffer_15
  assign controlled_buffer_9_out = \IF_Row_选中的哪一行 [7] ? \预测历史_8_q  : 2'bz;  // Controlled_Buffer controlled_buffer_16
  Multiplexer #(.select(1), .width(2), .disabled("Z"), .enable("false")) multiplexer_2 (
    .in0(controlled_buffer_9_out), .in1(2'b00), .out(\预测历史 ), .sel(MISS));

  // Other names for the same wires on the sheet: L0 = \IF_Row_选中的哪一行 [0]; L1 = \IF_Row_选中的哪一行 [1];
  //   L2 = \IF_Row_选中的哪一行 [2]; L3 = \IF_Row_选中的哪一行 [3]; L4 = \IF_Row_选中的哪一行 [4]; L5 = \IF_Row_选中的哪一行 [5];
  //   L6 = \IF_Row_选中的哪一行 [6]; L7 = \IF_Row_选中的哪一行 [7]; RowToUpdate[7:0] = \EX_Row_选中的哪一行_更新预测历史 ;
  //   Update_L0 = \EX_Row_选中的哪一行_更新预测历史 [0]; Update_L1 = \EX_Row_选中的哪一行_更新预测历史 [1];
  //   Update_L2 = \EX_Row_选中的哪一行_更新预测历史 [2]; Update_L3 = \EX_Row_选中的哪一行_更新预测历史 [3];
  //   Update_L4 = \EX_Row_选中的哪一行_更新预测历史 [4]; Update_L5 = \EX_Row_选中的哪一行_更新预测历史 [5];
  //   Update_L6 = \EX_Row_选中的哪一行_更新预测历史 [6]; Update_L7 = \EX_Row_选中的哪一行_更新预测历史 [7]; ToWrite = \欲写标志 
endmodule

module \八路并发控制  (
  input  V,
  input  [31:0] \分支指令地址 ,
  input  [31:0] in_3,
  input  in_4,
  input  [31:0] in_5,
  input  in_6,
  input  [31:0] in_7,
  input  in_8,
  input  [31:0] in_9,
  input  in_10,
  input  [31:0] in_11,
  input  in_12,
  input  [31:0] in_13,
  input  in_14,
  input  [31:0] in_15,
  input  in_16,
  input  [31:0] in_17,
  input  in_18,
  output K0,
  output K1,
  output K2,
  output K3,
  output K4,
  output K5,
  output K6,
  output K7,
  output Miss
);

  wire and_1_out, and_2_out, and_3_out, and_4_out, and_5_out, and_6_out, and_7_out, and_8_out,
       comparator_1_eq, comparator_2_eq, comparator_3_eq, comparator_4_eq, comparator_5_eq, comparator_6_eq,
       comparator_7_eq, comparator_8_eq;

  Comparator #(.width(32), .mode("twosComplement")) comparator_1 (
    .a(\分支指令地址 ), .b(in_3), .eq(comparator_1_eq));  // open: gt, lt
  and and_1 (and_1_out, V, in_4);
  Comparator #(.width(32), .mode("twosComplement")) comparator_2 (
    .a(\分支指令地址 ), .b(in_5), .eq(comparator_2_eq));  // open: gt, lt
  and and_2 (and_2_out, V, in_6);
  Comparator #(.width(32), .mode("twosComplement")) comparator_3 (
    .a(\分支指令地址 ), .b(in_7), .eq(comparator_3_eq));  // open: gt, lt
  and and_3 (and_3_out, V, in_8);
  Comparator #(.width(32), .mode("twosComplement")) comparator_4 (
    .a(\分支指令地址 ), .b(in_9), .eq(comparator_4_eq));  // open: gt, lt
  and and_4 (and_4_out, V, in_10);
  Comparator #(.width(32), .mode("twosComplement")) comparator_5 (
    .a(\分支指令地址 ), .b(in_11), .eq(comparator_5_eq));  // open: gt, lt
  and and_5 (and_5_out, V, in_12);
  Comparator #(.width(32), .mode("twosComplement")) comparator_6 (
    .a(\分支指令地址 ), .b(in_13), .eq(comparator_6_eq));  // open: gt, lt
  and and_6 (and_6_out, V, in_14);
  Comparator #(.width(32), .mode("twosComplement")) comparator_7 (
    .a(\分支指令地址 ), .b(in_15), .eq(comparator_7_eq));  // open: gt, lt
  and and_7 (and_7_out, V, in_16);
  Comparator #(.width(32), .mode("twosComplement")) comparator_8 (
    .a(\分支指令地址 ), .b(in_17), .eq(comparator_8_eq));  // open: gt, lt
  and and_8 (and_8_out, V, in_18);
  and and_9 (K0, comparator_1_eq, and_1_out);
  and and_10 (K1, comparator_2_eq, and_2_out);
  and and_11 (K2, comparator_3_eq, and_3_out);
  and and_12 (K3, comparator_4_eq, and_4_out);
  and and_13 (K4, comparator_5_eq, and_5_out);
  and and_14 (K5, comparator_6_eq, and_6_out);
  and and_15 (K6, comparator_7_eq, and_7_out);
  and and_16 (K7, comparator_8_eq, and_8_out);
  nor nor_1 (Miss, K0, K1, K2, K3, K4, K5, K6, K7);

  // Notes on the sheet:
  //   增加Valid位一起比较
  //   初始时刻Miss为1
endmodule

module \BTB写控制  (
  input  V0,
  input  V1,
  input  V2,
  input  V3,
  input  V4,
  input  V5,
  input  V6,
  input  V7,
  input  [15:0] LRUCount0,
  input  [15:0] LRUCount1,
  input  [15:0] LRUCount2,
  input  [15:0] LRUCount3,
  input  [15:0] LRUCount4,
  input  [15:0] LRUCount5,
  input  [15:0] LRUCount6,
  input  [15:0] LRUCount7,
  output [2:0] ToWritre_num
);

  wire and_1_out;
  wire [2:0] \max3_归并比较_1_max_num , \max3_归并比较_2_max_num , \max3_归并比较_3_max_num , \max3_归并比较_4_max_num ,
       \max3_归并比较_5_max_num , \max3_归并比较_6_max_num , \max3_归并比较_7_max_num , multiplexer_1_out,
       multiplexer_2_out, multiplexer_3_out, multiplexer_4_out, multiplexer_5_out, multiplexer_6_out,
       multiplexer_7_out, multiplexer_8_out;
  wire [15:0] \max3_归并比较_1_max , \max3_归并比较_2_max , \max3_归并比较_3_max , \max3_归并比较_4_max , \max3_归并比较_5_max ,
       \max3_归并比较_6_max ;

  \MAX3_归并比较  \max3_归并比较_1  (
    .Y(LRUCount0), .X(LRUCount1), .Y_num(3'b000), .X_num(3'b001), .MAX(\max3_归并比较_1_max ),
    .Max_num(\max3_归并比较_1_max_num ));
  Multiplexer #(.select(1), .width(3), .disabled("Z"), .enable("false")) multiplexer_1 (
    .in0(3'b110), .in1(multiplexer_2_out), .out(multiplexer_1_out), .sel(V6));
  Multiplexer #(.select(1), .width(3), .disabled("Z"), .enable("false")) multiplexer_2 (
    .in0(3'b111), .out(multiplexer_2_out), .sel(V7));  // open: in1
  \MAX3_归并比较  \max3_归并比较_2  (
    .Y(\max3_归并比较_1_max ), .X(LRUCount2), .Y_num(\max3_归并比较_1_max_num ), .X_num(3'b010),
    .MAX(\max3_归并比较_2_max ), .Max_num(\max3_归并比较_2_max_num ));
  Multiplexer #(.select(1), .width(3), .disabled("Z"), .enable("false")) multiplexer_3 (
    .in0(3'b101), .in1(multiplexer_1_out), .out(multiplexer_3_out), .sel(V5));
  \MAX3_归并比较  \max3_归并比较_3  (
    .Y(\max3_归并比较_2_max ), .X(LRUCount3), .Y_num(\max3_归并比较_2_max_num ), .X_num(3'b011),
    .MAX(\max3_归并比较_3_max ), .Max_num(\max3_归并比较_3_max_num ));
  Multiplexer #(.select(1), .width(3), .disabled("Z"), .enable("false")) multiplexer_4 (
    .in0(3'b011), .in1(multiplexer_5_out), .out(multiplexer_4_out), .sel(V3));
  Multiplexer #(.select(1), .width(3), .disabled("Z"), .enable("false")) multiplexer_5 (
    .in0(3'b100), .in1(multiplexer_3_out), .out(multiplexer_5_out), .sel(V4));
  \MAX3_归并比较  \max3_归并比较_4  (
    .Y(\max3_归并比较_3_max ), .X(LRUCount4), .Y_num(\max3_归并比较_3_max_num ), .X_num(3'b100),
    .MAX(\max3_归并比较_4_max ), .Max_num(\max3_归并比较_4_max_num ));
  Multiplexer #(.select(1), .width(3), .disabled("Z"), .enable("false")) multiplexer_6 (
    .in0(3'b010), .in1(multiplexer_4_out), .out(multiplexer_6_out), .sel(V2));
  \MAX3_归并比较  \max3_归并比较_5  (
    .Y(\max3_归并比较_4_max ), .X(LRUCount5), .Y_num(\max3_归并比较_4_max_num ), .X_num(3'b101),
    .MAX(\max3_归并比较_5_max ), .Max_num(\max3_归并比较_5_max_num ));
  Multiplexer #(.select(1), .width(3), .disabled("Z"), .enable("false")) multiplexer_7 (
    .in0(3'b000), .in1(multiplexer_8_out), .out(multiplexer_7_out), .sel(V0));
  Multiplexer #(.select(1), .width(3), .disabled("Z"), .enable("false")) multiplexer_8 (
    .in0(3'b001), .in1(multiplexer_6_out), .out(multiplexer_8_out), .sel(V1));
  \MAX3_归并比较  \max3_归并比较_6  (
    .Y(\max3_归并比较_5_max ), .X(LRUCount6), .Y_num(\max3_归并比较_5_max_num ), .X_num(3'b110),
    .MAX(\max3_归并比较_6_max ), .Max_num(\max3_归并比较_6_max_num ));
  and and_1 (and_1_out, V0, V1, V2, V3, V4, V5, V6, V7);
  \MAX3_归并比较  \max3_归并比较_7  (
    .Y(\max3_归并比较_6_max ), .X(LRUCount7), .Y_num(\max3_归并比较_6_max_num ), .X_num(3'b111),
    .Max_num(\max3_归并比较_7_max_num ));  // open: MAX
  Multiplexer #(.select(1), .width(3), .disabled("Z"), .enable("false")) multiplexer_9 (
    .in0(multiplexer_7_out), .in1(\max3_归并比较_7_max_num ), .out(ToWritre_num), .sel(and_1_out));

  // Notes on the sheet:
  //   当BTB充满时，减少时延
endmodule

module \MAX3_归并比较  (
  input  [15:0] Y,
  input  [15:0] X,
  input  [2:0] Y_num,
  input  [2:0] X_num,
  output [15:0] MAX,
  output [2:0] Max_num
);

  wire comparator_1_eq, comparator_1_gt, or_1_out;

  Multiplexer #(.select(1), .width(16), .disabled("Z"), .enable("false")) multiplexer_1 (
    .in0(Y), .in1(X), .out(MAX), .sel(or_1_out));
  Comparator #(.width(16), .mode("unsigned")) comparator_1 (
    .a(X), .b(Y), .gt(comparator_1_gt), .eq(comparator_1_eq));  // open: lt
  or or_1 (or_1_out, comparator_1_gt, comparator_1_eq);
  Multiplexer #(.select(1), .width(3), .disabled("Z"), .enable("false")) multiplexer_2 (
    .in0(Y_num), .in1(X_num), .out(Max_num), .sel(or_1_out));

  // Notes on the sheet:
  //   输出两个输入中的较大值，并输出较大值的3位编号
endmodule

module \双预测位状态机  (
  input  [1:0] Now_State,
  input  Branch,
  output [1:0] Next_State
);

  wire and_1_out, and_2_out, and_3_out, and_4_out, not_1_out, not_2_out, not_3_out, not_4_out, not_5_out;

  not not_1 (not_1_out, Now_State[0]);
  not not_2 (not_2_out, Now_State[1]);
  not not_3 (not_3_out, Now_State[0]);
  not not_4 (not_4_out, Now_State[0]);
  not not_5 (not_5_out, Branch);
  and and_1 (and_1_out, Now_State[0], Branch);
  and and_2 (and_2_out, Now_State[1], not_1_out);
  and and_3 (and_3_out, not_2_out, not_3_out, Branch);
  and and_4 (and_4_out, Now_State[1], not_4_out, not_5_out);
  or or_1 (Next_State[1], and_1_out, and_2_out);
  or or_2 (Next_State[0], and_3_out, and_4_out);
endmodule
