// Logisim project 团队任务成语接龙.circ as structural Verilog: 17 circuits, main circuit ◇单周期MIPS
module \单周期MIPS  (
  input  IR1,
  input  IR2,
  input  IR3,
  output RegWrite,
  output MemWrite,
  output [31:0] PC,
  output [31:0] IR,
  output [31:0] RDin,
  output [31:0] MDin,
  output [31:0] LedData
);

  wire and_1_out, and_4_out, and_5_out, and_6_out, Branch, CLK, clock_2_out, comparator_1_eq,
       comparator_2_eq, comparator_2_lt, comparator_3_eq, comparator_3_lt, d_ff_1_q, Go, Halt, IR1_t, IR2_t,
       IR3_t, IRA, IRB, IRC, JAL, JMP, JR, LedOut, mips_alu_1_equal, nand_1_out, not_1_out, or_4_out,
       SignedExt, Syscall, W1, W2, W3, \单周期硬布线控制器_1_alu_src , \单周期硬布线控制器_1_beq , \单周期硬布线控制器_1_blez ,
       \单周期硬布线控制器_1_bne , \单周期硬布线控制器_1_lh , \单周期硬布线控制器_1_lui , \单周期硬布线控制器_1_memtoreg , \单周期硬布线控制器_1_regdst ;
  wire [3:0] \单周期硬布线控制器_1_alu_op ;
  wire [4:0] multiplexer_4_out, multiplexer_5_out, multiplexer_6_out, multiplexer_8_out;
  wire [12:0] CNT_num;
  wire [15:0] adder_1_out, multiplexer_14_out, register_1_q, \总周期数 ;
  wire [31:0] adder_3_out, adder_4_out, bit_extender_1_out, bit_extender_2_out, bit_extender_3_out,
       mips_alu_1_result, multiplexer_1_out, multiplexer_2_out, multiplexer_3_out, multiplexer_9_out,
       multiplexer_10_out, multiplexer_11_out, multiplexer_12_out, multiplexer_13_out, ram_1_data,
       shifter_1_out, shifter_2_out, v0;

  Clock #(.highDuration(1), .lowDuration(1)) clock_1 ();  // open: out
  Button _1 (.out(IRA));
  Button _2 (.out(IRB));
  Button _3 (.out(IRC));
  Button \u_继续运行  (.out(Go));
  LED #(.active("true")) led_1 (.in(W1));
  LED #(.active("true")) led_2 (.in(W2));
  LED #(.active("true")) led_3 (.in(W3));
  Hex_Digit_Display hex_digit_display_1 (.value(LedData[31:28]));  // open: dp
  Register #(.width(16), .trigger("rising"), .Select("low")) register_1 (
    .D(adder_1_out), .Q(register_1_q), .clk(and_1_out));  // open: en, clr
  and and_1 (and_1_out, CLK, ~Halt);  // AND_Gate
  Multiplexer #(.select(1), .width(32), .disabled("Z"), .enable("false")) multiplexer_1 (
    .in0(adder_3_out), .in1(adder_4_out), .out(multiplexer_1_out), .sel(Branch));
  Hex_Digit_Display hex_digit_display_2 (.value(LedData[23:20]));  // open: dp
  Hex_Digit_Display hex_digit_display_3 (.value(LedData[27:24]));  // open: dp
  Multiplexer #(.select(1), .width(32), .disabled("Z"), .enable("false")) multiplexer_2 (
    .in0(multiplexer_1_out), .in1({PC[31:28], IR[25:0], 2'b00}), .out(multiplexer_2_out), .sel(JMP));
  Multiplexer #(.select(1), .width(32), .disabled("Z"), .enable("false")) multiplexer_3 (
    .in0(multiplexer_2_out), .in1(v0), .out(multiplexer_3_out), .sel(JR));
  Hex_Digit_Display hex_digit_display_4 (.value(LedData[15:12]));  // open: dp
  Hex_Digit_Display hex_digit_display_5 (.value(LedData[19:16]));  // open: dp
  Adder #(.width(16)) adder_1 (.a(16'h1), .b(register_1_q), .out(adder_1_out));  // open: cin, cout
  not not_1 (not_1_out, Halt);
  Hex_Digit_Display hex_digit_display_6 (.value(LedData[11:8]));  // open: dp
  Hex_Digit_Display hex_digit_display_7 (.value(LedData[7:4]));  // open: dp
  // Probe on \总周期数 
  Register #(.width(32), .trigger("rising"), .Select("low")) u_PC (
    .D(multiplexer_3_out), .en(not_1_out), .Q(PC), .clk(CLK));  // open: clr
  Hex_Digit_Display hex_digit_display_8 (.value(LedData[3:0]));  // open: dp
  Adder #(.width(16)) adder_2 (.a({16{1'b1}}), .b(adder_1_out), .out(\总周期数 ));  // open: cin, cout
  Adder #(.width(32)) adder_3 (.a(PC), .b(32'h4), .out(adder_3_out));  // open: cin, cout
  // Mips_Probe mips_probe_1: pin names not known; wires that end beside it: IR
  or or_1 (IR1_t, IR1, IRA);
  ROM #(.addrWidth(10), .dataWidth(32), .Select("high")) rom_1 (.addr(PC[11:2]), .data(IR));
  or or_2 (IR2_t, IR2, IRB);
  \单周期硬布线控制器  \u_单周期硬布线控制器_1  (
    .Func(IR[5:0]), .OP(IR[31:26]), .ALU_OP(\单周期硬布线控制器_1_alu_op ), .MemToReg(\单周期硬布线控制器_1_memtoreg ),
    .MemWrite(MemWrite), .ALU_SRC(\单周期硬布线控制器_1_alu_src ), .RegWrite(RegWrite), .SysCALL(Syscall),
    .SignedExt(SignedExt), .RegDst(\单周期硬布线控制器_1_regdst ), .JR(JR), .JMP(JMP), .Beq(\单周期硬布线控制器_1_beq ),
    .JAL(JAL), .Bne(\单周期硬布线控制器_1_bne ), .LUI(\单周期硬布线控制器_1_lui ), .LH(\单周期硬布线控制器_1_lh ),
    .BLEZ(\单周期硬布线控制器_1_blez ));  // open: ERET
  Multiplexer #(.select(1), .width(5), .disabled("Z"), .enable("false")) multiplexer_4 (
    .in0(IR[25:21]), .in1(5'b00010), .out(multiplexer_4_out), .sel(Syscall));
  Multiplexer #(.select(1), .width(5), .disabled("Z"), .enable("false")) multiplexer_5 (
    .in0(IR[20:16]), .in1(5'b00100), .out(multiplexer_5_out), .sel(Syscall));
  Multiplexer #(.select(1), .width(5), .disabled("Z"), .enable("false")) multiplexer_6 (
    .in0(IR[20:16]), .in1(IR[15:11]), .out(multiplexer_6_out), .sel(\单周期硬布线控制器_1_regdst ));
  Multiplexer #(.select(1), .width(32), .disabled("Z"), .enable("false")) multiplexer_7 (
    .in0(multiplexer_10_out), .in1(adder_3_out), .out(RDin), .sel(JAL));
  or or_3 (IR3_t, IR3, IRC);
  Multiplexer #(.select(1), .width(5), .disabled("Z"), .enable("false")) multiplexer_8 (
    .in0(multiplexer_6_out), .in1({5{1'b1}}), .out(multiplexer_8_out), .sel(JAL));
  assign bit_extender_1_out = {{16{1'b0}}, IR[15:0]};  // Bit_Extender bit_extender_1
  assign bit_extender_2_out = {{16{IR[15]}}, IR[15:0]};  // Bit_Extender bit_extender_2
  MIPS_Regifile mips_regifile_1 (
    .Din(RDin), .Clk(CLK), .R1(v0), .R2(MDin), .WE(RegWrite), .W_num(multiplexer_8_out),
    .R1_num(multiplexer_4_out), .R2_num(multiplexer_5_out));
  Multiplexer #(.select(1), .width(32), .disabled("Z"), .enable("false")) multiplexer_9 (
    .in0(bit_extender_1_out), .in1(bit_extender_2_out), .out(multiplexer_9_out), .sel(SignedExt));
  Comparator #(.width(32), .mode("twosComplement")) comparator_1 (
    .a(32'ha), .b(v0), .eq(comparator_1_eq));  // open: gt, lt
  Multiplexer #(.select(1), .width(32), .disabled("Z"), .enable("false")) multiplexer_10 (
    .in0(multiplexer_12_out), .in1(shifter_2_out), .out(multiplexer_10_out), .sel(\单周期硬布线控制器_1_lui ));
  Shifter #(.width(32), .shift("ll")) shifter_1 (.in(multiplexer_9_out), .\dist (5'b00010), .out(shifter_1_out));
  and and_2 (Halt, Syscall, comparator_1_eq);
  and and_3 (LedOut, Syscall, ~comparator_1_eq);  // AND_Gate
  Shifter #(.width(32), .shift("ll")) shifter_2 (.in(multiplexer_9_out), .\dist (5'b10000), .out(shifter_2_out));
  Adder #(.width(32)) adder_4 (.a(shifter_1_out), .b(adder_3_out), .out(adder_4_out));  // open: cin, cout
  Comparator #(.width(32), .mode("twosComplement")) comparator_2 (
    .a(v0), .b({32{1'b0}}), .eq(comparator_2_eq), .lt(comparator_2_lt));  // open: gt
  Multiplexer #(.select(1), .width(32), .disabled("Z"), .enable("false")) multiplexer_11 (
    .in0(MDin), .in1(multiplexer_9_out), .out(multiplexer_11_out), .sel(\单周期硬布线控制器_1_alu_src ));
  or or_4 (or_4_out, comparator_2_eq, comparator_2_lt);
  and and_4 (and_4_out, or_4_out, \单周期硬布线控制器_1_blez );
  and and_5 (and_5_out, mips_alu_1_equal, \单周期硬布线控制器_1_beq );
  and and_6 (and_6_out, ~mips_alu_1_equal, \单周期硬布线控制器_1_bne );  // AND_Gate
  MIPS_ALU mips_alu_1 (
    .X(v0), .Y(multiplexer_11_out), .AluOP(\单周期硬布线控制器_1_alu_op ), .Equal(mips_alu_1_equal),
    .Result(mips_alu_1_result), .shamt(IR[10:6]));  // open: Result_2
  D_Flip_Flop #(.trigger("high"), .Pre_Clr_Positions("LEGACY"), .NegatePresetClear("false"), .enable("true"), .NewFFLayout("false")) d_ff_1 (.Q(d_ff_1_q));  // open: clk, D, Qn, preset, en, reset
  // Probe on 13'hc
  or or_5 (Branch, and_4_out, and_5_out, and_6_out);
  Register #(.width(32), .trigger("rising"), .Select("low")) register_2 (
    .D(MDin), .en(LedOut), .Q(LedData), .clk(CLK));  // open: clr
  Comparator #(.width(13), .mode("twosComplement")) comparator_3 (
    .a(CNT_num), .b(13'hc), .eq(comparator_3_eq), .lt(comparator_3_lt));  // open: gt
  Clock #(.highDuration(1), .lowDuration(1)) clock_2 (.out(clock_2_out));
  nand nand_1 (nand_1_out, d_ff_1_q, comparator_3_eq);
  Counter #(.width(13), .max('h1fff), .ongoal("stay"), .trigger("rising"), .behavior("old")) counter_1 (
    .count(comparator_3_lt), .Q(CNT_num), .clk(clock_2_out));  // open: load, D, carry, clr, preset
  RAM #(.addrWidth(10), .dataWidth(32), .bus("separate"), .Select("high")) ram_1 (
    .addr(mips_alu_1_result[11:2]), .din(MDin), .data(ram_1_data), .str(MemWrite), .clk(CLK));  // open: sel, ld, clr
  assign CLK = nand_1_out ? clock_2_out : 1'bz;  // Controlled_Buffer controlled_buffer_1
  Multiplexer #(.select(1), .width(32), .disabled("Z"), .enable("false")) multiplexer_12 (
    .in0(multiplexer_13_out), .in1(bit_extender_3_out), .out(multiplexer_12_out), .sel(\单周期硬布线控制器_1_lh ));
  Pull_Resistor #(.pull(1)) pull_resistor_1 (.node(CLK));
  Multiplexer #(.select(1), .width(32), .disabled("Z"), .enable("false")) multiplexer_13 (
    .in0(mips_alu_1_result), .in1(ram_1_data), .out(multiplexer_13_out), .sel(\单周期硬布线控制器_1_memtoreg ));
  Multiplexer #(.select(1), .width(16), .disabled("Z"), .enable("false")) multiplexer_14 (
    .in0(multiplexer_13_out[15:0]), .in1(multiplexer_13_out[31:16]), .out(multiplexer_14_out),
    .sel(mips_alu_1_result[1]));
  assign bit_extender_3_out = {{16{multiplexer_14_out[15]}}, multiplexer_14_out};  // Bit_Extender bit_extender_3

  // Notes on the sheet:
  //   中断源
  //   中断等待指示
  //   总复位信号应将除ROM以外所有存储组件全部清零
  //   数码管输出
  //   数码管输出应该用寄存器锁存，否则显示数据只能一闪而过
  //   指令存储器
  //   指令字
  //   contents of rom_1 (hex, n*v repeats v):
  //   20110001 8000c05 20110001 20120002 20130003 8000c09 20110001 20120002 20130003 8000c0d 20110001
  //   20120002 20130003 8000c11 20110001 20120002 20130003 c000cb8 20100001 20110001 118fc0 112020
  //   20020022 c 118882 12200001 8000c15 112020 20020022 c 20110001 118880 112020 20020022 c 12200001
  //   8000c1f 20110001 118fc0 112020 20020022 c 1188c3 112020 20020022 c 118903 112020 20020022 c 118903
  //   112020 20020022 c 118903 112020 20020022 c 118903 112020 20020022 c 118903 112020 20020022 c 118903
  //   112020 20020022 c 118903 112020 20020022 c 20100001 109fc0 139fc3 8021 2012000c 24160003 26100001
  //   3210000f 20080008 20090001 139900 2709825 132020 20020022 c 1094022 1500fff9 22100001 2018000f
  //   2188024 108700 20080008 20090001 139902 2709825 132021 20020022 c 1094022 1500fff9 108702 2c9b022
  //   12c00001 8000c50 4020 1084027 84400 3508ffff 82021 20020022 c 2010ffff 20110000 ae300000 22100001
  //   22310004 ae300000 22100001 22310004 ae300000 22100001 22310004 ae300000 22100001 22310004 ae300000
  //   22100001 22310004 ae300000 22100001 22310004 ae300000 22100001 22310004 ae300000 22100001 22310004
  //   ae300000 22100001 22310004 ae300000 22100001 22310004 ae300000 22100001 22310004 ae300000 22100001
  //   22310004 ae300000 22100001 22310004 ae300000 22100001 22310004 ae300000 22100001 22310004 ae300000
  //   22100001 22310004 22100001 8020 2011003c 8e130000 8e340000 274402a 11000002 ae330000 ae140000
  //   2231fffc 1611fff8 102020 20020022 c 22100004 2011003c 1611fff2 20020032 c 20100000 22100001 102020
  //   20020022 c 22100002 102020 20020022 c 22100003 102020 20020022 c 22100004 102020 20020022 c 22100005
  //   102020 20020022 c 22100006 102020 20020022 c 22100007 102020 20020022 c 22100008 102020 20020022
  //   20020022 c 3e00008
  //   JMP
  //   JR
  //   OP
  //   OP
  //   Func
  //   Func
  //   rs
  //   rt
  //   rd
  //   imm16
  //   imm26
  //   shamt
  //   Blez
  //   LH
  //   LUI
  //   Beq
  //   Bne
  //   AluOP
  //   AluSrcB
  //   RegWrite
  //   JAL
  //   RegDst
  //   Syscall
  //   MemToReg
  //   MemWrite
  //   为方便自动评测，需要输出PC，IR，寄存器堆写如数据RDin
  //   RAM写使能MemWrite、RAM写入数据MDin等信号
  //   控制位
  //   暂停节拍，不能为0
  //   戳工具置1进入计数暂停模式，ctrl+k时钟自动运行到对应节拍暂停
  //   ctrl+k关闭时钟连续运行，将控制位置零，进入单步调试模式调试
  //   用这个时钟源需要去掉电路中的其他时钟源
  //   可计数暂停的时钟源
endmodule

// 单周期硬布线控制器
module \单周期硬布线控制器  (
  input  [5:0] OP,
  input  [5:0] Func,
  output [3:0] ALU_OP,
  output MemToReg,
  output MemWrite,
  output ERET,
  output ALU_SRC,
  output RegWrite,
  output SysCALL,
  output SignedExt,
  output RegDst,
  output Beq,
  output Bne,
  output JR,
  output JMP,
  output JAL,
  output LUI,
  output LH,
  output BLEZ
);

  \运算控制器自动生成  \u_运算控制器自动生成_1  (
    .OP0(OP[0]), .OP1(OP[1]), .OP2(OP[2]), .OP3(OP[3]), .OP4(OP[4]), .OP5(OP[5]), .F0(Func[0]), .F1(Func[1]),
    .F2(Func[2]), .F3(Func[3]), .F4(Func[4]), .F5(Func[5]), .S0(ALU_OP[0]), .S1(ALU_OP[1]), .S2(ALU_OP[2]),
    .S3(ALU_OP[3]));
  \控制信号自动生成  \u_控制信号自动生成_1  (
    .OP0(OP[0]), .OP1(OP[1]), .OP2(OP[2]), .OP3(OP[3]), .OP4(OP[4]), .OP5(OP[5]), .F0(Func[0]), .F1(Func[1]),
    .F2(Func[2]), .F3(Func[3]), .F4(Func[4]), .F5(Func[5]), .MemToReg(MemToReg), .MemWrite(MemWrite),
    .ERET(ERET), .ALU_SRC(ALU_SRC), .RegWrite(RegWrite), .SysCALL(SysCALL), .SignedExt(SignedExt),
    .RegDst(RegDst), .BEQ(Beq), .BNE(Bne), .JR(JR), .JUMP(JMP), .JAL(JAL), .LUI(LUI), .LH(LH), .BLEZ(BLEZ));

  // Other names for the same wires on the sheet: OP_CODE[5:0] = OP

  // Notes on the sheet:
  //   运算器控制器，根据指令生成运算器功能选择信号
  //   控制信号生成，产生数据通路需要的其他控制信号
endmodule

// 运算器控制器
module \运算控制器自动生成  (
  input  OP0,
  input  OP1,
  input  OP2,
  input  OP3,
  input  OP4,
  input  OP5,
  input  F0,
  input  F1,
  input  F2,
  input  F3,
  input  F4,
  input  F5,
  output S0,
  output S1,
  output S2,
  output S3
);

  wire and_1_out, and_2_out, and_3_out, and_4_out, and_5_out, and_6_out, and_7_out, and_8_out, and_9_out,
       and_10_out, and_11_out, and_12_out, and_13_out, and_14_out, and_15_out, and_16_out, and_17_out,
       and_18_out, and_19_out, and_20_out, and_21_out, and_22_out, and_23_out, and_24_out, and_25_out,
       and_26_out, and_27_out, and_28_out, and_29_out, and_30_out, and_31_out, and_32_out, and_33_out,
       and_34_out, and_35_out, and_36_out, and_37_out, and_38_out, not_1_out, not_2_out, not_3_out,
       not_4_out, not_5_out, not_6_out, not_7_out, not_8_out, not_9_out, not_10_out, not_11_out, not_12_out,
       not_13_out, not_14_out, not_15_out, not_16_out, not_17_out, not_18_out, not_19_out, not_20_out,
       not_21_out, not_22_out, not_23_out, not_24_out, not_25_out, not_26_out, not_27_out, not_28_out,
       not_29_out, not_30_out, not_31_out, not_32_out, not_33_out, not_34_out, not_35_out, not_36_out,
       not_37_out, not_38_out, not_39_out, not_40_out, not_41_out, not_42_out, not_43_out, not_44_out,
       not_45_out, not_46_out, not_47_out, not_48_out, not_49_out, not_50_out, not_51_out, not_52_out,
       not_53_out, not_54_out, not_55_out, not_56_out, not_57_out, not_58_out, not_59_out, not_60_out,
       not_61_out, not_62_out, not_63_out, not_64_out, not_65_out, not_66_out, not_67_out, not_68_out,
       not_69_out, not_70_out, not_71_out, not_72_out, not_73_out, not_74_out, not_75_out, not_76_out,
       not_77_out, not_78_out, not_79_out, not_80_out, not_81_out, not_82_out, not_83_out, not_84_out,
       not_85_out, not_86_out, not_87_out, not_88_out, not_89_out, not_90_out, not_91_out, not_92_out,
       not_93_out, not_94_out, not_95_out, not_96_out, not_97_out, not_98_out, not_99_out, not_100_out,
       not_101_out, not_102_out, not_103_out, not_104_out, not_105_out, not_106_out, not_107_out,
       not_108_out, not_109_out, not_110_out, not_111_out, not_112_out, not_113_out, not_114_out,
       not_115_out, not_116_out, not_117_out, not_118_out, not_119_out, not_120_out, not_121_out,
       not_122_out, not_123_out, not_124_out, not_125_out, not_126_out, not_127_out, not_128_out,
       not_129_out, not_130_out, not_131_out, not_132_out, not_133_out, not_134_out, not_135_out,
       not_136_out, not_137_out, not_138_out, not_139_out, not_140_out, not_141_out, not_142_out,
       not_143_out, not_144_out, not_145_out, not_146_out, not_147_out, not_148_out, not_149_out,
       not_150_out, not_151_out, not_152_out, not_153_out, not_154_out, not_155_out, not_156_out,
       not_157_out, not_158_out, not_159_out, not_160_out, not_161_out, not_162_out, not_163_out,
       not_164_out, not_165_out, not_166_out, not_167_out, not_168_out, not_169_out, not_170_out,
       not_171_out, not_172_out, not_173_out, not_174_out, not_175_out, not_176_out, not_177_out,
       not_178_out, not_179_out, not_180_out, not_181_out, not_182_out, not_183_out, not_184_out,
       not_185_out, not_186_out, not_187_out, not_188_out, not_189_out, not_190_out, not_191_out,
       not_192_out, not_193_out, not_194_out, not_195_out, not_196_out, not_197_out, not_198_out,
       not_199_out, not_200_out, not_201_out, not_202_out, not_203_out, not_204_out, not_205_out,
       not_206_out, not_207_out, not_208_out, not_209_out, not_210_out, not_211_out, not_212_out,
       not_213_out, not_214_out, not_215_out, not_216_out, not_217_out, not_218_out, not_219_out,
       not_220_out, not_221_out, not_222_out, not_223_out, not_224_out, not_225_out, not_226_out,
       not_227_out, not_228_out, not_229_out, not_230_out, not_231_out, not_232_out, not_233_out,
       not_234_out, not_235_out, not_236_out, not_237_out, not_238_out, not_239_out, not_240_out,
       not_241_out, not_242_out, not_243_out, not_244_out, not_245_out, not_246_out, not_247_out,
       not_248_out, not_249_out, not_250_out;

  not not_1 (not_1_out, OP5);
  not not_2 (not_2_out, OP4);
  not not_3 (not_3_out, OP3);
  not not_4 (not_4_out, OP2);
  not not_5 (not_5_out, OP1);
  not not_6 (not_6_out, OP0);
  not not_7 (not_7_out, F5);
  not not_8 (not_8_out, F4);
  not not_9 (not_9_out, F3);
  not not_10 (not_10_out, F2);
  not not_11 (not_11_out, OP5);
  not not_12 (not_12_out, OP4);
  not not_13 (not_13_out, OP3);
  not not_14 (not_14_out, OP2);
  not not_15 (not_15_out, OP1);
  not not_16 (not_16_out, OP0);
  not not_17 (not_17_out, F4);
  not not_18 (not_18_out, F3);
  not not_19 (not_19_out, F2);
  not not_20 (not_20_out, F1);
  not not_21 (not_21_out, F0);
  not not_22 (not_22_out, OP5);
  not not_23 (not_23_out, OP4);
  not not_24 (not_24_out, OP3);
  not not_25 (not_25_out, OP2);
  not not_26 (not_26_out, OP1);
  not not_27 (not_27_out, OP0);
  not not_28 (not_28_out, F4);
  not not_29 (not_29_out, F3);
  not not_30 (not_30_out, F2);
  not not_31 (not_31_out, F1);
  not not_32 (not_32_out, OP5);
  not not_33 (not_33_out, OP4);
  not not_34 (not_34_out, OP3);
  not not_35 (not_35_out, OP2);
  not not_36 (not_36_out, OP1);
  not not_37 (not_37_out, OP0);
  not not_38 (not_38_out, F4);
  not not_39 (not_39_out, F3);
  not not_40 (not_40_out, F1);
  not not_41 (not_41_out, F0);
  not not_42 (not_42_out, OP5);
  not not_43 (not_43_out, OP4);
  not not_44 (not_44_out, OP3);
  not not_45 (not_45_out, OP2);
  not not_46 (not_46_out, OP1);
  not not_47 (not_47_out, OP0);
  not not_48 (not_48_out, F4);
  not not_49 (not_49_out, F2);
  not not_50 (not_50_out, F0);
  not not_51 (not_51_out, OP5);
  not not_52 (not_52_out, OP4);
  not not_53 (not_53_out, OP2);
  not not_54 (not_54_out, OP1);
  not not_55 (not_55_out, OP0);
  not not_56 (not_56_out, OP5);
  not not_57 (not_57_out, OP4);
  not not_58 (not_58_out, OP1);
  not not_59 (not_59_out, OP0);
  not not_60 (not_60_out, OP5);
  not not_61 (not_61_out, OP4);
  not not_62 (not_62_out, OP2);
  not not_63 (not_63_out, OP1);
  not not_64 (not_64_out, OP5);
  not not_65 (not_65_out, OP4);
  not not_66 (not_66_out, OP2);
  not not_67 (not_67_out, OP0);
  not not_68 (not_68_out, OP4);
  not not_69 (not_69_out, OP3);
  not not_70 (not_70_out, OP2);
  not not_71 (not_71_out, OP4);
  not not_72 (not_72_out, OP2);
  not not_73 (not_73_out, OP4);
  not not_74 (not_74_out, OP3);
  not not_75 (not_75_out, OP2);
  not not_76 (not_76_out, OP1);
  not not_77 (not_77_out, OP5);
  not not_78 (not_78_out, OP4);
  not not_79 (not_79_out, OP3);
  not not_80 (not_80_out, OP2);
  not not_81 (not_81_out, OP1);
  not not_82 (not_82_out, OP0);
  not not_83 (not_83_out, F5);
  not not_84 (not_84_out, F4);
  not not_85 (not_85_out, F3);
  not not_86 (not_86_out, F2);
  not not_87 (not_87_out, F0);
  not not_88 (not_88_out, OP5);
  not not_89 (not_89_out, OP4);
  not not_90 (not_90_out, OP3);
  not not_91 (not_91_out, OP2);
  not not_92 (not_92_out, OP1);
  not not_93 (not_93_out, OP0);
  not not_94 (not_94_out, F4);
  not not_95 (not_95_out, F3);
  not not_96 (not_96_out, F2);
  not not_97 (not_97_out, F0);
  not not_98 (not_98_out, OP5);
  not not_99 (not_99_out, OP4);
  not not_100 (not_100_out, OP3);
  not not_101 (not_101_out, OP2);
  not not_102 (not_102_out, OP1);
  not not_103 (not_103_out, OP0);
  not not_104 (not_104_out, F4);
  not not_105 (not_105_out, F3);
  not not_106 (not_106_out, F1);
  not not_107 (not_107_out, F0);
  not not_108 (not_108_out, OP5);
  not not_109 (not_109_out, OP4);
  not not_110 (not_110_out, OP3);
  not not_111 (not_111_out, OP2);
  not not_112 (not_112_out, OP1);
  not not_113 (not_113_out, OP0);
  not not_114 (not_114_out, F4);
  not not_115 (not_115_out, F3);
  not not_116 (not_116_out, OP5);
  not not_117 (not_117_out, OP4);
  not not_118 (not_118_out, OP3);
  not not_119 (not_119_out, OP2);
  not not_120 (not_120_out, OP1);
  not not_121 (not_121_out, OP0);
  not not_122 (not_122_out, F4);
  not not_123 (not_123_out, F2);
  not not_124 (not_124_out, F0);
  not not_125 (not_125_out, OP5);
  not not_126 (not_126_out, OP4);
  not not_127 (not_127_out, OP1);
  not not_128 (not_128_out, OP0);
  not not_129 (not_129_out, OP5);
  not not_130 (not_130_out, OP4);
  not not_131 (not_131_out, OP2);
  not not_132 (not_132_out, OP0);
  not not_133 (not_133_out, OP5);
  not not_134 (not_134_out, OP4);
  not not_135 (not_135_out, OP3);
  not not_136 (not_136_out, OP2);
  not not_137 (not_137_out, OP1);
  not not_138 (not_138_out, OP0);
  not not_139 (not_139_out, F4);
  not not_140 (not_140_out, F3);
  not not_141 (not_141_out, F2);
  not not_142 (not_142_out, F1);
  not not_143 (not_143_out, F0);
  not not_144 (not_144_out, OP5);
  not not_145 (not_145_out, OP4);
  not not_146 (not_146_out, OP3);
  not not_147 (not_147_out, OP2);
  not not_148 (not_148_out, OP1);
  not not_149 (not_149_out, OP0);
  not not_150 (not_150_out, F4);
  not not_151 (not_151_out, F3);
  not not_152 (not_152_out, F2);
  not not_153 (not_153_out, F1);
  not not_154 (not_154_out, OP5);
  not not_155 (not_155_out, OP4);
  not not_156 (not_156_out, OP3);
  not not_157 (not_157_out, OP2);
  not not_158 (not_158_out, OP1);
  not not_159 (not_159_out, OP0);
  not not_160 (not_160_out, F4);
  not not_161 (not_161_out, F3);
  not not_162 (not_162_out, F2);
  not not_163 (not_163_out, F0);
  not not_164 (not_164_out, OP5);
  not not_165 (not_165_out, OP4);
  not not_166 (not_166_out, OP3);
  not not_167 (not_167_out, OP2);
  not not_168 (not_168_out, OP1);
  not not_169 (not_169_out, OP0);
  not not_170 (not_170_out, F4);
  not not_171 (not_171_out, F3);
  not not_172 (not_172_out, F1);
  not not_173 (not_173_out, F0);
  not not_174 (not_174_out, OP5);
  not not_175 (not_175_out, OP4);
  not not_176 (not_176_out, OP3);
  not not_177 (not_177_out, OP2);
  not not_178 (not_178_out, OP1);
  not not_179 (not_179_out, OP0);
  not not_180 (not_180_out, F4);
  not not_181 (not_181_out, F2);
  not not_182 (not_182_out, OP5);
  not not_183 (not_183_out, OP4);
  not not_184 (not_184_out, OP2);
  not not_185 (not_185_out, OP1);
  not not_186 (not_186_out, OP0);
  not not_187 (not_187_out, OP5);
  not not_188 (not_188_out, OP4);
  not not_189 (not_189_out, OP1);
  not not_190 (not_190_out, OP0);
  not not_191 (not_191_out, OP5);
  not not_192 (not_192_out, OP4);
  not not_193 (not_193_out, OP2);
  not not_194 (not_194_out, OP1);
  not not_195 (not_195_out, OP4);
  not not_196 (not_196_out, OP3);
  not not_197 (not_197_out, OP2);
  not not_198 (not_198_out, OP4);
  not not_199 (not_199_out, OP2);
  not not_200 (not_200_out, OP5);
  not not_201 (not_201_out, OP4);
  not not_202 (not_202_out, OP2);
  not not_203 (not_203_out, OP4);
  not not_204 (not_204_out, OP3);
  not not_205 (not_205_out, OP2);
  not not_206 (not_206_out, OP1);
  not not_207 (not_207_out, OP5);
  not not_208 (not_208_out, OP4);
  not not_209 (not_209_out, OP3);
  not not_210 (not_210_out, OP2);
  not not_211 (not_211_out, OP1);
  not not_212 (not_212_out, OP0);
  not not_213 (not_213_out, F4);
  not not_214 (not_214_out, F3);
  not not_215 (not_215_out, F1);
  not not_216 (not_216_out, OP5);
  not not_217 (not_217_out, OP4);
  not not_218 (not_218_out, OP3);
  not not_219 (not_219_out, OP2);
  not not_220 (not_220_out, OP1);
  not not_221 (not_221_out, OP0);
  not not_222 (not_222_out, F4);
  not not_223 (not_223_out, F3);
  not not_224 (not_224_out, OP5);
  not not_225 (not_225_out, OP4);
  not not_226 (not_226_out, OP3);
  not not_227 (not_227_out, OP2);
  not not_228 (not_228_out, OP1);
  not not_229 (not_229_out, OP0);
  not not_230 (not_230_out, F4);
  not not_231 (not_231_out, F2);
  not not_232 (not_232_out, F0);
  not not_233 (not_233_out, OP5);
  not not_234 (not_234_out, OP4);
  not not_235 (not_235_out, OP3);
  not not_236 (not_236_out, OP2);
  not not_237 (not_237_out, OP1);
  not not_238 (not_238_out, OP0);
  not not_239 (not_239_out, F4);
  not not_240 (not_240_out, F2);
  not not_241 (not_241_out, OP5);
  not not_242 (not_242_out, OP4);
  not not_243 (not_243_out, OP2);
  not not_244 (not_244_out, OP0);
  not not_245 (not_245_out, OP5);
  not not_246 (not_246_out, OP4);
  not not_247 (not_247_out, OP1);
  not not_248 (not_248_out, OP5);
  not not_249 (not_249_out, OP4);
  not not_250 (not_250_out, OP2);
  and and_1 (and_1_out, not_1_out, not_2_out, not_3_out, not_4_out, not_5_out, not_6_out, not_7_out, not_8_out, not_9_out, not_10_out, F1, F0);
  and and_2 (and_2_out, not_11_out, not_12_out, not_13_out, not_14_out, not_15_out, not_16_out, F5, not_17_out, not_18_out, not_19_out, not_20_out, not_21_out);
  and and_3 (and_3_out, not_22_out, not_23_out, not_24_out, not_25_out, not_26_out, not_27_out, F5, not_28_out, not_29_out, not_30_out, not_31_out, F0);
  and and_4 (and_4_out, not_32_out, not_33_out, not_34_out, not_35_out, not_36_out, not_37_out, F5, not_38_out, not_39_out, F2, not_40_out, not_41_out);
  and and_5 (and_5_out, not_42_out, not_43_out, not_44_out, not_45_out, not_46_out, not_47_out, F5, not_48_out, F3, not_49_out, F1, not_50_out);
  and and_6 (and_6_out, not_51_out, not_52_out, OP3, not_53_out, not_54_out, not_55_out);
  and and_7 (and_7_out, not_56_out, not_57_out, OP3, OP2, not_58_out, not_59_out);
  and and_8 (and_8_out, not_60_out, not_61_out, OP3, not_62_out, not_63_out, OP0);
  and and_9 (and_9_out, not_64_out, not_65_out, OP3, not_66_out, OP1, not_67_out);
  and and_10 (and_10_out, OP5, not_68_out, not_69_out, not_70_out, OP1, OP0);
  and and_11 (and_11_out, OP5, not_71_out, OP3, not_72_out, OP1, OP0);
  and and_12 (and_12_out, OP5, not_73_out, not_74_out, not_75_out, not_76_out, OP0);
  and and_13 (and_13_out, not_77_out, not_78_out, not_79_out, not_80_out, not_81_out, not_82_out, not_83_out, not_84_out, not_85_out, not_86_out, F1, not_87_out);
  and and_14 (and_14_out, not_88_out, not_89_out, not_90_out, not_91_out, not_92_out, not_93_out, F5, not_94_out, not_95_out, not_96_out, F1, not_97_out);
  and and_15 (and_15_out, not_98_out, not_99_out, not_100_out, not_101_out, not_102_out, not_103_out, F5, not_104_out, not_105_out, F2, not_106_out, not_107_out);
  and and_16 (and_16_out, not_108_out, not_109_out, not_110_out, not_111_out, not_112_out, not_113_out, F5, not_114_out, not_115_out, F2, F1, F0);
  and and_17 (and_17_out, not_116_out, not_117_out, not_118_out, not_119_out, not_120_out, not_121_out, F5, not_122_out, F3, not_123_out, F1, not_124_out);
  and and_18 (and_18_out, not_125_out, not_126_out, OP3, OP2, not_127_out, not_128_out);
  and and_19 (and_19_out, not_129_out, not_130_out, OP3, not_131_out, OP1, not_132_out);
  and and_20 (and_20_out, not_133_out, not_134_out, not_135_out, not_136_out, not_137_out, not_138_out, F5, not_139_out, not_140_out, not_141_out, not_142_out, not_143_out);
  and and_21 (and_21_out, not_144_out, not_145_out, not_146_out, not_147_out, not_148_out, not_149_out, F5, not_150_out, not_151_out, not_152_out, not_153_out, F0);
  and and_22 (and_22_out, not_154_out, not_155_out, not_156_out, not_157_out, not_158_out, not_159_out, F5, not_160_out, not_161_out, not_162_out, F1, not_163_out);
  and and_23 (and_23_out, not_164_out, not_165_out, not_166_out, not_167_out, not_168_out, not_169_out, F5, not_170_out, not_171_out, F2, not_172_out, not_173_out);
  and and_24 (and_24_out, not_174_out, not_175_out, not_176_out, not_177_out, not_178_out, not_179_out, F5, not_180_out, F3, not_181_out, F1, F0);
  and and_25 (and_25_out, not_182_out, not_183_out, OP3, not_184_out, not_185_out, not_186_out);
  and and_26 (and_26_out, not_187_out, not_188_out, OP3, OP2, not_189_out, not_190_out);
  and and_27 (and_27_out, not_191_out, not_192_out, OP3, not_193_out, not_194_out, OP0);
  and and_28 (and_28_out, OP5, not_195_out, not_196_out, not_197_out, OP1, OP0);
  and and_29 (and_29_out, OP5, not_198_out, OP3, not_199_out, OP1, OP0);
  and and_30 (and_30_out, not_200_out, not_201_out, OP3, not_202_out, OP1, OP0);
  and and_31 (and_31_out, OP5, not_203_out, not_204_out, not_205_out, not_206_out, OP0);
  and and_32 (and_32_out, not_207_out, not_208_out, not_209_out, not_210_out, not_211_out, not_212_out, F5, not_213_out, not_214_out, F2, not_215_out, F0);
  and and_33 (and_33_out, not_216_out, not_217_out, not_218_out, not_219_out, not_220_out, not_221_out, F5, not_222_out, not_223_out, F2, F1, F0);
  and and_34 (and_34_out, not_224_out, not_225_out, not_226_out, not_227_out, not_228_out, not_229_out, F5, not_230_out, F3, not_231_out, F1, not_232_out);
  and and_35 (and_35_out, not_233_out, not_234_out, not_235_out, not_236_out, not_237_out, not_238_out, F5, not_239_out, F3, not_240_out, F1, F0);
  and and_36 (and_36_out, not_241_out, not_242_out, OP3, not_243_out, OP1, not_244_out);
  and and_37 (and_37_out, not_245_out, not_246_out, OP3, OP2, not_247_out, OP0);
  and and_38 (and_38_out, not_248_out, not_249_out, OP3, not_250_out, OP1, OP0);
  or or_1 (S1, and_13_out, and_14_out, and_15_out, and_16_out, and_17_out, and_18_out, and_19_out);
  or or_2 (S3, and_32_out, and_33_out, and_34_out, and_35_out, and_36_out, and_37_out, and_38_out);
  or or_3 (S0, and_1_out, and_2_out, and_3_out, and_4_out, and_5_out, and_6_out, and_7_out, and_8_out, and_9_out, and_10_out, and_11_out, and_12_out);
  or or_4 (S2, and_20_out, and_21_out, and_22_out, and_23_out, and_24_out, and_25_out, and_26_out, and_27_out, and_28_out, and_29_out, and_30_out, and_31_out);
endmodule

// 控制信号生成
module \控制信号自动生成  (
  input  OP0,
  input  OP1,
  input  OP2,
  input  OP3,
  input  OP4,
  input  OP5,
  input  F0,
  input  F1,
  input  F2,
  input  F3,
  input  F4,
  input  F5,
  output MemToReg,
  output MemWrite,
  output ERET,
  output ALU_SRC,
  output RegWrite,
  output SysCALL,
  output SignedExt,
  output RegDst,
  output BEQ,
  output BNE,
  output JR,
  output JUMP,
  output JAL,
  output LUI,
  output LH,
  output BLEZ
);

  wire and_1_out, and_2_out, and_5_out, and_6_out, and_7_out, and_8_out, and_9_out, and_10_out, and_11_out,
       and_12_out, and_13_out, and_14_out, and_15_out, and_16_out, and_17_out, and_18_out, and_19_out,
       and_20_out, and_21_out, and_22_out, and_23_out, and_24_out, and_25_out, and_26_out, and_27_out,
       and_28_out, and_29_out, and_30_out, and_31_out, and_32_out, and_33_out, and_34_out, and_36_out,
       and_37_out, and_38_out, and_39_out, and_40_out, and_41_out, and_42_out, and_43_out, and_44_out,
       and_45_out, and_46_out, and_47_out, and_48_out, and_49_out, and_50_out, and_51_out, and_52_out,
       and_53_out, and_54_out, and_55_out, and_56_out, and_60_out, and_61_out, and_62_out, not_1_out,
       not_2_out, not_3_out, not_4_out, not_5_out, not_6_out, not_7_out, not_8_out, not_9_out, not_10_out,
       not_11_out, not_12_out, not_13_out, not_14_out, not_15_out, not_16_out, not_17_out, not_18_out,
       not_19_out, not_20_out, not_21_out, not_22_out, not_23_out, not_24_out, not_25_out, not_26_out,
       not_27_out, not_28_out, not_29_out, not_30_out, not_31_out, not_32_out, not_33_out, not_34_out,
       not_35_out, not_36_out, not_37_out, not_38_out, not_39_out, not_40_out, not_41_out, not_42_out,
       not_43_out, not_44_out, not_45_out, not_46_out, not_47_out, not_48_out, not_49_out, not_50_out,
       not_51_out, not_52_out, not_53_out, not_54_out, not_55_out, not_56_out, not_57_out, not_58_out,
       not_59_out, not_60_out, not_61_out, not_62_out, not_63_out, not_64_out, not_65_out, not_66_out,
       not_67_out, not_68_out, not_69_out, not_70_out, not_71_out, not_72_out, not_73_out, not_74_out,
       not_75_out, not_76_out, not_77_out, not_78_out, not_79_out, not_80_out, not_81_out, not_82_out,
       not_83_out, not_84_out, not_85_out, not_86_out, not_87_out, not_88_out, not_89_out, not_90_out,
       not_91_out, not_92_out, not_93_out, not_94_out, not_95_out, not_96_out, not_97_out, not_98_out,
       not_99_out, not_100_out, not_101_out, not_102_out, not_103_out, not_104_out, not_105_out, not_106_out,
       not_107_out, not_108_out, not_109_out, not_110_out, not_111_out, not_112_out, not_113_out,
       not_114_out, not_115_out, not_116_out, not_117_out, not_118_out, not_119_out, not_120_out,
       not_121_out, not_122_out, not_123_out, not_124_out, not_125_out, not_126_out, not_127_out,
       not_128_out, not_129_out, not_130_out, not_131_out, not_132_out, not_133_out, not_134_out,
       not_135_out, not_136_out, not_137_out, not_138_out, not_139_out, not_140_out, not_141_out,
       not_142_out, not_143_out, not_144_out, not_145_out, not_146_out, not_147_out, not_148_out,
       not_149_out, not_150_out, not_151_out, not_152_out, not_153_out, not_154_out, not_155_out,
       not_156_out, not_157_out, not_158_out, not_159_out, not_160_out, not_161_out, not_162_out,
       not_163_out, not_164_out, not_165_out, not_166_out, not_167_out, not_168_out, not_169_out,
       not_170_out, not_171_out, not_172_out, not_173_out, not_174_out, not_175_out, not_176_out,
       not_177_out, not_178_out, not_179_out, not_180_out, not_181_out, not_182_out, not_183_out,
       not_184_out, not_185_out, not_186_out, not_187_out, not_188_out, not_189_out, not_190_out,
       not_191_out, not_192_out, not_193_out, not_194_out, not_195_out, not_196_out, not_197_out,
       not_198_out, not_199_out, not_200_out, not_201_out, not_202_out, not_203_out, not_204_out,
       not_205_out, not_206_out, not_207_out, not_208_out, not_209_out, not_210_out, not_211_out,
       not_212_out, not_213_out, not_214_out, not_215_out, not_216_out, not_217_out, not_218_out,
       not_219_out, not_220_out, not_221_out, not_222_out, not_223_out, not_224_out, not_225_out,
       not_226_out, not_227_out, not_228_out, not_229_out, not_230_out, not_231_out, not_232_out,
       not_233_out, not_234_out, not_235_out, not_236_out, not_237_out, not_238_out, not_239_out,
       not_240_out, not_241_out, not_242_out, not_243_out, not_244_out, not_245_out, not_246_out,
       not_247_out, not_248_out, not_249_out, not_250_out, not_251_out, not_252_out, not_253_out,
       not_254_out, not_255_out, not_256_out, not_257_out, not_258_out, not_259_out, not_260_out,
       not_261_out, not_262_out, not_263_out, not_264_out, not_265_out, not_266_out, not_267_out,
       not_268_out, not_269_out, not_270_out, not_271_out, not_272_out, not_273_out, not_274_out,
       not_275_out, not_276_out, not_277_out, not_278_out, not_279_out, not_280_out, not_281_out,
       not_282_out, not_283_out, not_284_out, not_285_out, not_286_out, not_287_out, not_288_out,
       not_289_out, not_290_out, not_291_out, not_292_out, not_293_out, not_294_out, not_295_out,
       not_296_out, not_297_out, not_298_out, not_299_out, not_300_out, not_301_out, not_302_out,
       not_303_out, not_304_out, not_305_out, not_306_out, not_307_out, not_308_out, not_309_out,
       not_310_out, not_311_out, not_312_out, not_313_out, not_314_out, not_315_out, not_316_out,
       not_317_out, not_318_out, not_319_out, not_320_out, not_321_out, not_322_out, not_323_out,
       not_324_out, not_325_out, not_326_out, not_327_out, not_328_out, not_329_out, not_330_out,
       not_331_out, not_332_out, not_333_out, not_334_out, not_335_out, not_336_out, not_337_out,
       not_338_out, not_339_out, not_340_out, not_341_out, not_342_out, not_343_out, not_344_out,
       not_345_out, not_346_out, not_347_out, not_348_out, not_349_out, not_350_out, not_351_out,
       not_352_out, not_353_out, not_354_out, not_355_out, not_356_out, not_357_out, not_358_out,
       not_359_out, not_360_out, not_361_out, not_362_out, not_363_out, not_364_out, not_365_out,
       not_366_out, not_367_out, not_368_out, not_369_out, not_370_out, not_371_out, not_372_out,
       not_373_out, not_374_out, not_375_out, not_376_out, not_377_out, not_378_out, not_379_out,
       not_380_out, not_381_out, not_382_out, not_383_out, not_384_out, not_385_out, not_386_out,
       not_387_out, not_388_out, not_389_out, not_390_out, not_391_out, not_392_out, not_393_out,
       not_394_out, not_395_out, not_396_out, not_397_out, not_398_out, not_399_out, not_400_out,
       not_401_out, not_402_out, not_403_out, not_404_out;

  not not_1 (not_1_out, OP4);
  not not_2 (not_2_out, OP3);
  not not_3 (not_3_out, OP2);
  not not_4 (not_4_out, OP4);
  not not_5 (not_5_out, OP3);
  not not_6 (not_6_out, OP2);
  not not_7 (not_7_out, OP1);
  not not_8 (not_8_out, OP4);
  not not_9 (not_9_out, OP2);
  not not_10 (not_10_out, OP5);
  not not_11 (not_11_out, OP3);
  not not_12 (not_12_out, OP2);
  not not_13 (not_13_out, OP1);
  not not_14 (not_14_out, OP0);
  not not_15 (not_15_out, F5);
  not not_16 (not_16_out, F2);
  not not_17 (not_17_out, F1);
  not not_18 (not_18_out, F0);
  not not_19 (not_19_out, OP5);
  not not_20 (not_20_out, OP4);
  not not_21 (not_21_out, OP2);
  not not_22 (not_22_out, OP1);
  not not_23 (not_23_out, OP0);
  not not_24 (not_24_out, OP5);
  not not_25 (not_25_out, OP4);
  not not_26 (not_26_out, OP1);
  not not_27 (not_27_out, OP0);
  not not_28 (not_28_out, OP5);
  not not_29 (not_29_out, OP4);
  not not_30 (not_30_out, OP2);
  not not_31 (not_31_out, OP1);
  not not_32 (not_32_out, OP5);
  not not_33 (not_33_out, OP4);
  not not_34 (not_34_out, OP2);
  not not_35 (not_35_out, OP0);
  not not_36 (not_36_out, OP5);
  not not_37 (not_37_out, OP4);
  not not_38 (not_38_out, OP1);
  not not_39 (not_39_out, OP4);
  not not_40 (not_40_out, OP3);
  not not_41 (not_41_out, OP2);
  not not_42 (not_42_out, OP4);
  not not_43 (not_43_out, OP2);
  not not_44 (not_44_out, OP5);
  not not_45 (not_45_out, OP4);
  not not_46 (not_46_out, OP2);
  not not_47 (not_47_out, OP4);
  not not_48 (not_48_out, OP3);
  not not_49 (not_49_out, OP2);
  not not_50 (not_50_out, OP1);
  not not_51 (not_51_out, OP5);
  not not_52 (not_52_out, OP4);
  not not_53 (not_53_out, OP3);
  not not_54 (not_54_out, OP2);
  not not_55 (not_55_out, OP1);
  not not_56 (not_56_out, OP0);
  not not_57 (not_57_out, F5);
  not not_58 (not_58_out, F4);
  not not_59 (not_59_out, F3);
  not not_60 (not_60_out, F2);
  not not_61 (not_61_out, F1);
  not not_62 (not_62_out, F0);
  not not_63 (not_63_out, OP5);
  not not_64 (not_64_out, OP4);
  not not_65 (not_65_out, OP3);
  not not_66 (not_66_out, OP2);
  not not_67 (not_67_out, OP1);
  not not_68 (not_68_out, OP0);
  not not_69 (not_69_out, F5);
  not not_70 (not_70_out, F4);
  not not_71 (not_71_out, F3);
  not not_72 (not_72_out, F2);
  not not_73 (not_73_out, OP5);
  not not_74 (not_74_out, OP4);
  not not_75 (not_75_out, OP3);
  not not_76 (not_76_out, OP2);
  not not_77 (not_77_out, OP1);
  not not_78 (not_78_out, OP0);
  not not_79 (not_79_out, F5);
  not not_80 (not_80_out, F4);
  not not_81 (not_81_out, F3);
  not not_82 (not_82_out, F2);
  not not_83 (not_83_out, F0);
  not not_84 (not_84_out, OP5);
  not not_85 (not_85_out, OP4);
  not not_86 (not_86_out, OP3);
  not not_87 (not_87_out, OP2);
  not not_88 (not_88_out, OP1);
  not not_89 (not_89_out, OP0);
  not not_90 (not_90_out, F4);
  not not_91 (not_91_out, F3);
  not not_92 (not_92_out, F2);
  not not_93 (not_93_out, F1);
  not not_94 (not_94_out, F0);
  not not_95 (not_95_out, OP5);
  not not_96 (not_96_out, OP4);
  not not_97 (not_97_out, OP3);
  not not_98 (not_98_out, OP2);
  not not_99 (not_99_out, OP1);
  not not_100 (not_100_out, OP0);
  not not_101 (not_101_out, F4);
  not not_102 (not_102_out, F3);
  not not_103 (not_103_out, F2);
  not not_104 (not_104_out, F1);
  not not_105 (not_105_out, OP5);
  not not_106 (not_106_out, OP4);
  not not_107 (not_107_out, OP3);
  not not_108 (not_108_out, OP2);
  not not_109 (not_109_out, OP1);
  not not_110 (not_110_out, OP0);
  not not_111 (not_111_out, F4);
  not not_112 (not_112_out, F3);
  not not_113 (not_113_out, F2);
  not not_114 (not_114_out, F0);
  not not_115 (not_115_out, OP5);
  not not_116 (not_116_out, OP4);
  not not_117 (not_117_out, OP3);
  not not_118 (not_118_out, OP2);
  not not_119 (not_119_out, OP1);
  not not_120 (not_120_out, OP0);
  not not_121 (not_121_out, F4);
  not not_122 (not_122_out, F3);
  not not_123 (not_123_out, F1);
  not not_124 (not_124_out, F0);
  not not_125 (not_125_out, OP5);
  not not_126 (not_126_out, OP4);
  not not_127 (not_127_out, OP3);
  not not_128 (not_128_out, OP2);
  not not_129 (not_129_out, OP1);
  not not_130 (not_130_out, OP0);
  not not_131 (not_131_out, F4);
  not not_132 (not_132_out, F3);
  not not_133 (not_133_out, F1);
  not not_134 (not_134_out, OP5);
  not not_135 (not_135_out, OP4);
  not not_136 (not_136_out, OP3);
  not not_137 (not_137_out, OP2);
  not not_138 (not_138_out, OP1);
  not not_139 (not_139_out, OP0);
  not not_140 (not_140_out, F4);
  not not_141 (not_141_out, F3);
  not not_142 (not_142_out, OP5);
  not not_143 (not_143_out, OP4);
  not not_144 (not_144_out, OP3);
  not not_145 (not_145_out, OP2);
  not not_146 (not_146_out, OP1);
  not not_147 (not_147_out, OP0);
  not not_148 (not_148_out, F4);
  not not_149 (not_149_out, F2);
  not not_150 (not_150_out, F0);
  not not_151 (not_151_out, OP5);
  not not_152 (not_152_out, OP4);
  not not_153 (not_153_out, OP3);
  not not_154 (not_154_out, OP2);
  not not_155 (not_155_out, OP1);
  not not_156 (not_156_out, OP0);
  not not_157 (not_157_out, F4);
  not not_158 (not_158_out, F2);
  not not_159 (not_159_out, OP5);
  not not_160 (not_160_out, OP4);
  not not_161 (not_161_out, OP3);
  not not_162 (not_162_out, OP2);
  not not_163 (not_163_out, OP5);
  not not_164 (not_164_out, OP4);
  not not_165 (not_165_out, OP2);
  not not_166 (not_166_out, OP1);
  not not_167 (not_167_out, OP0);
  not not_168 (not_168_out, OP5);
  not not_169 (not_169_out, OP4);
  not not_170 (not_170_out, OP1);
  not not_171 (not_171_out, OP0);
  not not_172 (not_172_out, OP5);
  not not_173 (not_173_out, OP4);
  not not_174 (not_174_out, OP2);
  not not_175 (not_175_out, OP1);
  not not_176 (not_176_out, OP5);
  not not_177 (not_177_out, OP4);
  not not_178 (not_178_out, OP2);
  not not_179 (not_179_out, OP0);
  not not_180 (not_180_out, OP5);
  not not_181 (not_181_out, OP4);
  not not_182 (not_182_out, OP1);
  not not_183 (not_183_out, OP4);
  not not_184 (not_184_out, OP3);
  not not_185 (not_185_out, OP2);
  not not_186 (not_186_out, OP5);
  not not_187 (not_187_out, OP4);
  not not_188 (not_188_out, OP5);
  not not_189 (not_189_out, OP4);
  not not_190 (not_190_out, OP2);
  not not_191 (not_191_out, OP4);
  not not_192 (not_192_out, OP3);
  not not_193 (not_193_out, OP2);
  not not_194 (not_194_out, OP1);
  not not_195 (not_195_out, OP5);
  not not_196 (not_196_out, OP4);
  not not_197 (not_197_out, OP3);
  not not_198 (not_198_out, OP2);
  not not_199 (not_199_out, OP1);
  not not_200 (not_200_out, OP0);
  not not_201 (not_201_out, F5);
  not not_202 (not_202_out, F4);
  not not_203 (not_203_out, F1);
  not not_204 (not_204_out, F0);
  not not_205 (not_205_out, OP5);
  not not_206 (not_206_out, OP4);
  not not_207 (not_207_out, OP3);
  not not_208 (not_208_out, OP1);
  not not_209 (not_209_out, OP0);
  not not_210 (not_210_out, OP5);
  not not_211 (not_211_out, OP4);
  not not_212 (not_212_out, OP3);
  not not_213 (not_213_out, OP1);
  not not_214 (not_214_out, OP5);
  not not_215 (not_215_out, OP4);
  not not_216 (not_216_out, OP2);
  not not_217 (not_217_out, OP1);
  not not_218 (not_218_out, OP0);
  not not_219 (not_219_out, OP5);
  not not_220 (not_220_out, OP4);
  not not_221 (not_221_out, OP2);
  not not_222 (not_222_out, OP1);
  not not_223 (not_223_out, OP5);
  not not_224 (not_224_out, OP4);
  not not_225 (not_225_out, OP2);
  not not_226 (not_226_out, OP0);
  not not_227 (not_227_out, OP4);
  not not_228 (not_228_out, OP3);
  not not_229 (not_229_out, OP2);
  not not_230 (not_230_out, OP4);
  not not_231 (not_231_out, OP2);
  not not_232 (not_232_out, OP5);
  not not_233 (not_233_out, OP4);
  not not_234 (not_234_out, OP2);
  not not_235 (not_235_out, OP4);
  not not_236 (not_236_out, OP3);
  not not_237 (not_237_out, OP2);
  not not_238 (not_238_out, OP1);
  not not_239 (not_239_out, OP5);
  not not_240 (not_240_out, OP4);
  not not_241 (not_241_out, OP3);
  not not_242 (not_242_out, OP0);
  not not_243 (not_243_out, OP5);
  not not_244 (not_244_out, OP4);
  not not_245 (not_245_out, OP3);
  not not_246 (not_246_out, OP2);
  not not_247 (not_247_out, OP1);
  not not_248 (not_248_out, OP0);
  not not_249 (not_249_out, F5);
  not not_250 (not_250_out, F4);
  not not_251 (not_251_out, F3);
  not not_252 (not_252_out, F2);
  not not_253 (not_253_out, F1);
  not not_254 (not_254_out, F0);
  not not_255 (not_255_out, OP5);
  not not_256 (not_256_out, OP4);
  not not_257 (not_257_out, OP3);
  not not_258 (not_258_out, OP2);
  not not_259 (not_259_out, OP1);
  not not_260 (not_260_out, OP0);
  not not_261 (not_261_out, F5);
  not not_262 (not_262_out, F4);
  not not_263 (not_263_out, F3);
  not not_264 (not_264_out, F2);
  not not_265 (not_265_out, OP5);
  not not_266 (not_266_out, OP4);
  not not_267 (not_267_out, OP3);
  not not_268 (not_268_out, OP2);
  not not_269 (not_269_out, OP1);
  not not_270 (not_270_out, OP0);
  not not_271 (not_271_out, F5);
  not not_272 (not_272_out, F4);
  not not_273 (not_273_out, F3);
  not not_274 (not_274_out, F2);
  not not_275 (not_275_out, F0);
  not not_276 (not_276_out, OP5);
  not not_277 (not_277_out, OP4);
  not not_278 (not_278_out, OP3);
  not not_279 (not_279_out, OP2);
  not not_280 (not_280_out, OP1);
  not not_281 (not_281_out, OP0);
  not not_282 (not_282_out, F4);
  not not_283 (not_283_out, F3);
  not not_284 (not_284_out, F2);
  not not_285 (not_285_out, F1);
  not not_286 (not_286_out, F0);
  not not_287 (not_287_out, OP5);
  not not_288 (not_288_out, OP4);
  not not_289 (not_289_out, OP3);
  not not_290 (not_290_out, OP2);
  not not_291 (not_291_out, OP1);
  not not_292 (not_292_out, OP0);
  not not_293 (not_293_out, F4);
  not not_294 (not_294_out, F3);
  not not_295 (not_295_out, F2);
  not not_296 (not_296_out, F1);
  not not_297 (not_297_out, OP5);
  not not_298 (not_298_out, OP4);
  not not_299 (not_299_out, OP3);
  not not_300 (not_300_out, OP2);
  not not_301 (not_301_out, OP1);
  not not_302 (not_302_out, OP0);
  not not_303 (not_303_out, F4);
  not not_304 (not_304_out, F3);
  not not_305 (not_305_out, F2);
  not not_306 (not_306_out, F0);
  not not_307 (not_307_out, OP5);
  not not_308 (not_308_out, OP4);
  not not_309 (not_309_out, OP3);
  not not_310 (not_310_out, OP2);
  not not_311 (not_311_out, OP1);
  not not_312 (not_312_out, OP0);
  not not_313 (not_313_out, F4);
  not not_314 (not_314_out, F3);
  not not_315 (not_315_out, F1);
  not not_316 (not_316_out, F0);
  not not_317 (not_317_out, OP5);
  not not_318 (not_318_out, OP4);
  not not_319 (not_319_out, OP3);
  not not_320 (not_320_out, OP2);
  not not_321 (not_321_out, OP1);
  not not_322 (not_322_out, OP0);
  not not_323 (not_323_out, F4);
  not not_324 (not_324_out, F3);
  not not_325 (not_325_out, F1);
  not not_326 (not_326_out, OP5);
  not not_327 (not_327_out, OP4);
  not not_328 (not_328_out, OP3);
  not not_329 (not_329_out, OP2);
  not not_330 (not_330_out, OP1);
  not not_331 (not_331_out, OP0);
  not not_332 (not_332_out, F4);
  not not_333 (not_333_out, F3);
  not not_334 (not_334_out, OP5);
  not not_335 (not_335_out, OP4);
  not not_336 (not_336_out, OP3);
  not not_337 (not_337_out, OP2);
  not not_338 (not_338_out, OP1);
  not not_339 (not_339_out, OP0);
  not not_340 (not_340_out, F4);
  not not_341 (not_341_out, F2);
  not not_342 (not_342_out, F0);
  not not_343 (not_343_out, OP5);
  not not_344 (not_344_out, OP4);
  not not_345 (not_345_out, OP3);
  not not_346 (not_346_out, OP2);
  not not_347 (not_347_out, OP1);
  not not_348 (not_348_out, OP0);
  not not_349 (not_349_out, F4);
  not not_350 (not_350_out, F2);
  not not_351 (not_351_out, OP5);
  not not_352 (not_352_out, OP4);
  not not_353 (not_353_out, OP3);
  not not_354 (not_354_out, OP1);
  not not_355 (not_355_out, OP0);
  not not_356 (not_356_out, OP5);
  not not_357 (not_357_out, OP4);
  not not_358 (not_358_out, OP3);
  not not_359 (not_359_out, OP1);
  not not_360 (not_360_out, OP5);
  not not_361 (not_361_out, OP4);
  not not_362 (not_362_out, OP3);
  not not_363 (not_363_out, OP2);
  not not_364 (not_364_out, OP1);
  not not_365 (not_365_out, OP0);
  not not_366 (not_366_out, F5);
  not not_367 (not_367_out, F4);
  not not_368 (not_368_out, F2);
  not not_369 (not_369_out, F1);
  not not_370 (not_370_out, F0);
  not not_371 (not_371_out, OP5);
  not not_372 (not_372_out, OP4);
  not not_373 (not_373_out, OP3);
  not not_374 (not_374_out, OP2);
  not not_375 (not_375_out, OP1);
  not not_376 (not_376_out, OP0);
  not not_377 (not_377_out, F5);
  not not_378 (not_378_out, F4);
  not not_379 (not_379_out, F2);
  not not_380 (not_380_out, F1);
  not not_381 (not_381_out, F0);
  not not_382 (not_382_out, OP5);
  not not_383 (not_383_out, OP4);
  not not_384 (not_384_out, OP3);
  not not_385 (not_385_out, OP2);
  not not_386 (not_386_out, OP0);
  not not_387 (not_387_out, OP5);
  not not_388 (not_388_out, OP4);
  not not_389 (not_389_out, OP3);
  not not_390 (not_390_out, OP2);
  not not_391 (not_391_out, OP5);
  not not_392 (not_392_out, OP4);
  not not_393 (not_393_out, OP3);
  not not_394 (not_394_out, OP2);
  not not_395 (not_395_out, OP5);
  not not_396 (not_396_out, OP4);
  not not_397 (not_397_out, OP4);
  not not_398 (not_398_out, OP3);
  not not_399 (not_399_out, OP2);
  not not_400 (not_400_out, OP1);
  not not_401 (not_401_out, OP5);
  not not_402 (not_402_out, OP4);
  not not_403 (not_403_out, OP3);
  not not_404 (not_404_out, OP0);
  and and_1 (and_1_out, OP5, not_1_out, not_2_out, not_3_out, OP1, OP0);
  and and_2 (and_2_out, OP5, not_4_out, not_5_out, not_6_out, not_7_out, OP0);
  and and_3 (MemWrite, OP5, not_8_out, OP3, not_9_out, OP1, OP0);
  and and_4 (ERET, not_10_out, OP4, not_11_out, not_12_out, not_13_out, not_14_out, not_15_out, F4, F3, not_16_out, not_17_out, not_18_out);
  and and_5 (and_5_out, not_19_out, not_20_out, OP3, not_21_out, not_22_out, not_23_out);
  and and_6 (and_6_out, not_24_out, not_25_out, OP3, OP2, not_26_out, not_27_out);
  and and_7 (and_7_out, not_28_out, not_29_out, OP3, not_30_out, not_31_out, OP0);
  and and_8 (and_8_out, not_32_out, not_33_out, OP3, not_34_out, OP1, not_35_out);
  and and_9 (and_9_out, not_36_out, not_37_out, OP3, OP2, not_38_out, OP0);
  and and_10 (and_10_out, OP5, not_39_out, not_40_out, not_41_out, OP1, OP0);
  and and_11 (and_11_out, OP5, not_42_out, OP3, not_43_out, OP1, OP0);
  and and_12 (and_12_out, not_44_out, not_45_out, OP3, not_46_out, OP1, OP0);
  and and_13 (and_13_out, OP5, not_47_out, not_48_out, not_49_out, not_50_out, OP0);
  and and_14 (and_14_out, not_51_out, not_52_out, not_53_out, not_54_out, not_55_out, not_56_out, not_57_out, not_58_out, not_59_out, not_60_out, not_61_out, not_62_out);
  and and_15 (and_15_out, not_63_out, not_64_out, not_65_out, not_66_out, not_67_out, not_68_out, not_69_out, not_70_out, not_71_out, not_72_out, F1, F0);
  and and_16 (and_16_out, not_73_out, not_74_out, not_75_out, not_76_out, not_77_out, not_78_out, not_79_out, not_80_out, not_81_out, not_82_out, F1, not_83_out);
  and and_17 (and_17_out, not_84_out, not_85_out, not_86_out, not_87_out, not_88_out, not_89_out, F5, not_90_out, not_91_out, not_92_out, not_93_out, not_94_out);
  and and_18 (and_18_out, not_95_out, not_96_out, not_97_out, not_98_out, not_99_out, not_100_out, F5, not_101_out, not_102_out, not_103_out, not_104_out, F0);
  and and_19 (and_19_out, not_105_out, not_106_out, not_107_out, not_108_out, not_109_out, not_110_out, F5, not_111_out, not_112_out, not_113_out, F1, not_114_out);
  and and_20 (and_20_out, not_115_out, not_116_out, not_117_out, not_118_out, not_119_out, not_120_out, F5, not_121_out, not_122_out, F2, not_123_out, not_124_out);
  and and_21 (and_21_out, not_125_out, not_126_out, not_127_out, not_128_out, not_129_out, not_130_out, F5, not_131_out, not_132_out, F2, not_133_out, F0);
  and and_22 (and_22_out, not_134_out, not_135_out, not_136_out, not_137_out, not_138_out, not_139_out, F5, not_140_out, not_141_out, F2, F1, F0);
  and and_23 (and_23_out, not_142_out, not_143_out, not_144_out, not_145_out, not_146_out, not_147_out, F5, not_148_out, F3, not_149_out, F1, not_150_out);
  and and_24 (and_24_out, not_151_out, not_152_out, not_153_out, not_154_out, not_155_out, not_156_out, F5, not_157_out, F3, not_158_out, F1, F0);
  and and_25 (and_25_out, not_159_out, not_160_out, not_161_out, not_162_out, OP1, OP0);
  and and_26 (and_26_out, not_163_out, not_164_out, OP3, not_165_out, not_166_out, not_167_out);
  and and_27 (and_27_out, not_168_out, not_169_out, OP3, OP2, not_170_out, not_171_out);
  and and_28 (and_28_out, not_172_out, not_173_out, OP3, not_174_out, not_175_out, OP0);
  and and_29 (and_29_out, not_176_out, not_177_out, OP3, not_178_out, OP1, not_179_out);
  and and_30 (and_30_out, not_180_out, not_181_out, OP3, OP2, not_182_out, OP0);
  and and_31 (and_31_out, OP5, not_183_out, not_184_out, not_185_out, OP1, OP0);
  and and_32 (and_32_out, not_186_out, not_187_out, OP3, OP2, OP1, OP0);
  and and_33 (and_33_out, not_188_out, not_189_out, OP3, not_190_out, OP1, OP0);
  and and_34 (and_34_out, OP5, not_191_out, not_192_out, not_193_out, not_194_out, OP0);
  and and_35 (SysCALL, not_195_out, not_196_out, not_197_out, not_198_out, not_199_out, not_200_out, not_201_out, not_202_out, F3, F2, not_203_out, not_204_out);
  and and_36 (and_36_out, not_205_out, not_206_out, not_207_out, OP2, not_208_out, not_209_out);
  and and_37 (and_37_out, not_210_out, not_211_out, not_212_out, OP2, not_213_out, OP0);
  and and_38 (and_38_out, not_214_out, not_215_out, OP3, not_216_out, not_217_out, not_218_out);
  and and_39 (and_39_out, not_219_out, not_220_out, OP3, not_221_out, not_222_out, OP0);
  and and_40 (and_40_out, not_223_out, not_224_out, OP3, not_225_out, OP1, not_226_out);
  and and_41 (and_41_out, OP5, not_227_out, not_228_out, not_229_out, OP1, OP0);
  and and_42 (and_42_out, OP5, not_230_out, OP3, not_231_out, OP1, OP0);
  and and_43 (and_43_out, not_232_out, not_233_out, OP3, not_234_out, OP1, OP0);
  and and_44 (and_44_out, OP5, not_235_out, not_236_out, not_237_out, not_238_out, OP0);
  and and_45 (and_45_out, not_239_out, not_240_out, not_241_out, OP2, OP1, not_242_out);
  and and_46 (and_46_out, not_243_out, not_244_out, not_245_out, not_246_out, not_247_out, not_248_out, not_249_out, not_250_out, not_251_out, not_252_out, not_253_out, not_254_out);
  and and_47 (and_47_out, not_255_out, not_256_out, not_257_out, not_258_out, not_259_out, not_260_out, not_261_out, not_262_out, not_263_out, not_264_out, F1, F0);
  and and_48 (and_48_out, not_265_out, not_266_out, not_267_out, not_268_out, not_269_out, not_270_out, not_271_out, not_272_out, not_273_out, not_274_out, F1, not_275_out);
  and and_49 (and_49_out, not_276_out, not_277_out, not_278_out, not_279_out, not_280_out, not_281_out, F5, not_282_out, not_283_out, not_284_out, not_285_out, not_286_out);
  and and_50 (and_50_out, not_287_out, not_288_out, not_289_out, not_290_out, not_291_out, not_292_out, F5, not_293_out, not_294_out, not_295_out, not_296_out, F0);
  and and_51 (and_51_out, not_297_out, not_298_out, not_299_out, not_300_out, not_301_out, not_302_out, F5, not_303_out, not_304_out, not_305_out, F1, not_306_out);
  and and_52 (and_52_out, not_307_out, not_308_out, not_309_out, not_310_out, not_311_out, not_312_out, F5, not_313_out, not_314_out, F2, not_315_out, not_316_out);
  and and_53 (and_53_out, not_317_out, not_318_out, not_319_out, not_320_out, not_321_out, not_322_out, F5, not_323_out, not_324_out, F2, not_325_out, F0);
  and and_54 (and_54_out, not_326_out, not_327_out, not_328_out, not_329_out, not_330_out, not_331_out, F5, not_332_out, not_333_out, F2, F1, F0);
  and and_55 (and_55_out, not_334_out, not_335_out, not_336_out, not_337_out, not_338_out, not_339_out, F5, not_340_out, F3, not_341_out, F1, not_342_out);
  and and_56 (and_56_out, not_343_out, not_344_out, not_345_out, not_346_out, not_347_out, not_348_out, F5, not_349_out, F3, not_350_out, F1, F0);
  and and_57 (BEQ, not_351_out, not_352_out, not_353_out, OP2, not_354_out, not_355_out);
  and and_58 (BNE, not_356_out, not_357_out, not_358_out, OP2, not_359_out, OP0);
  and and_59 (JR, not_360_out, not_361_out, not_362_out, not_363_out, not_364_out, not_365_out, not_366_out, not_367_out, F3, not_368_out, not_369_out, not_370_out);
  and and_60 (and_60_out, not_371_out, not_372_out, not_373_out, not_374_out, not_375_out, not_376_out, not_377_out, not_378_out, F3, not_379_out, not_380_out, not_381_out);
  and and_61 (and_61_out, not_382_out, not_383_out, not_384_out, not_385_out, OP1, not_386_out);
  and and_62 (and_62_out, not_387_out, not_388_out, not_389_out, not_390_out, OP1, OP0);
  and and_63 (JAL, not_391_out, not_392_out, not_393_out, not_394_out, OP1, OP0);
  and and_64 (LUI, not_395_out, not_396_out, OP3, OP2, OP1, OP0);
  and and_65 (LH, OP5, not_397_out, not_398_out, not_399_out, not_400_out, OP0);
  and and_66 (BLEZ, not_401_out, not_402_out, not_403_out, OP2, OP1, not_404_out);
  or or_1 (MemToReg, and_1_out, and_2_out);
  or or_2 (ALU_SRC, and_5_out, and_6_out, and_7_out, and_8_out, and_9_out, and_10_out, and_11_out, and_12_out, and_13_out);
  or or_3 (SignedExt, and_36_out, and_37_out, and_38_out, and_39_out, and_40_out, and_41_out, and_42_out, and_43_out, and_44_out, and_45_out);
  or or_4 (RegDst, and_46_out, and_47_out, and_48_out, and_49_out, and_50_out, and_51_out, and_52_out, and_53_out, and_54_out, and_55_out, and_56_out);
  or or_5 (JUMP, and_60_out, and_61_out, and_62_out);
  or or_6 (RegWrite, and_14_out, and_15_out, and_16_out, and_17_out, and_18_out, and_19_out, and_20_out, and_21_out, and_22_out, and_23_out, and_24_out, and_25_out, and_26_out, and_27_out, and_28_out, and_29_out, and_30_out, and_31_out, and_32_out, and_33_out, and_34_out);
endmodule

// ALU
module MIPS_ALU (
  input  [4:0] shamt,
  input  [31:0] X,
  input  [31:0] Y,
  input  [3:0] AluOP,
  output Equal,
  output [31:0] Result,
  output [31:0] Result_2
);

  wire [0:0] comparator_1_lt, comparator_2_lt;
  wire [31:0] adder_1_out, AND_out, divider_1_out, divider_1_rem, multiplier_1_cout, multiplier_1_out,
       NOR_out, OR_out, shifter_1_out, shifter_2_out, shifter_3_out, subtractor_1_out, XOR_out;

  assign AND_out = X & Y;  // AND_Gate AND, 32 bits wide
  assign OR_out = X | Y;  // OR_Gate OR, 32 bits wide
  Shifter #(.width(32), .shift("ll")) shifter_1 (.in(Y), .\dist (shamt), .out(shifter_1_out));
  Shifter #(.width(32), .shift("ar")) shifter_2 (.in(Y), .\dist (shamt), .out(shifter_2_out));
  Shifter #(.width(32), .shift("lr")) shifter_3 (.in(Y), .\dist (shamt), .out(shifter_3_out));
  Multiplier #(.width(32)) multiplier_1 (.a(X), .b(Y), .out(multiplier_1_out), .cout(multiplier_1_cout));  // open: cin
  Divider #(.width(32)) divider_1 (.a(X), .b(Y), .out(divider_1_out), .rem(divider_1_rem));  // open: upper
  Adder #(.width(32)) adder_1 (.a(X), .b(Y), .out(adder_1_out));  // open: cin, cout
  Subtractor #(.width(32)) subtractor_1 (.a(X), .b(Y), .out(subtractor_1_out));  // open: bin, bout
  assign XOR_out = X ^ Y;  // XOR_Gate XOR, 32 bits wide
  assign NOR_out = ~(X | Y);  // NOR_Gate NOR, 32 bits wide
  Comparator #(.width(32), .mode("twosComplement")) comparator_1 (
    .a(X), .b(Y), .eq(Equal), .lt(comparator_1_lt[0]));  // open: gt
  Comparator #(.width(32), .mode("unsigned")) comparator_2 (.a(X), .b(Y), .lt(comparator_2_lt[0]));  // open: gt, eq
  Multiplexer #(.select(4), .width(32), .disabled("Z"), .enable("false")) multiplexer_1 (
    .in0(shifter_1_out), .in1(shifter_2_out), .in2(shifter_3_out), .in3(multiplier_1_out),
    .in4(divider_1_out), .in5(adder_1_out), .in6(subtractor_1_out), .in7(AND_out), .in8(OR_out),
    .in9(XOR_out), .in10(NOR_out), .in11({{31{1'b0}}, comparator_1_lt[0]}),
    .in12({{31{1'b0}}, comparator_2_lt[0]}), .in13({32{1'b0}}), .in14({32{1'b0}}), .in15({32{1'b0}}),
    .out(Result), .sel(AluOP));
  Multiplexer #(.select(4), .width(32), .disabled("Z"), .enable("false")) multiplexer_2 (
    .in0({32{1'b0}}), .in1({32{1'b0}}), .in2({32{1'b0}}), .in3(multiplier_1_cout), .in4(divider_1_rem),
    .in5({32{1'b0}}), .in6({32{1'b0}}), .in7({32{1'b0}}), .in8({32{1'b0}}), .in9({32{1'b0}}),
    .in10({32{1'b0}}), .in11({32{1'b0}}), .in12({32{1'b0}}), .in13({32{1'b0}}), .in14({32{1'b0}}),
    .in15({32{1'b0}}), .out(Result_2), .sel(AluOP));

  // Other names for the same wires on the sheet: Result2[31:0] = Result_2; S[3:0] = AluOP

  // Notes on the sheet:
  //   不要改变此引脚区域内容，也不要改变ALU封装形式
  //   输入引脚
  //   输出引脚
endmodule

module MIPS_Regifile (
  input  [31:0] Din,
  input  Clk,
  input  WE,
  input  [4:0] R1_num,
  input  [4:0] W_num,
  input  [4:0] R2_num,
  output [31:0] R1,
  output [31:0] R2
);

  // RegisterFile registerfile_1: pin names not known; wires that end beside it: Din, Clk, WE, W_num, R1_num, R2_num, R1, R2
endmodule

module \理想流水线  (
  output RegWrite,
  output MemWrite,
  output [31:0] IF_PC,
  output [31:0] ID_PC,
  output [31:0] EX_PC,
  output [31:0] M_PC,
  output [31:0] WB_PC,
  output [31:0] RDin,
  output [31:0] MDin,
  output [31:0] LedData
);

  wire CLK, clock_1_out, clock_2_out, comparator_1_eq, comparator_1_lt, d_ff_1_q, Go, IR1, IR2, IR3,
       nand_1_out, RST, W1, W2, W3;
  wire [12:0] CNT_num;
  wire [15:0] \LoadUse次数 , \总周期数 , \插入气泡数 , \无条件分支数 , \条件分支成功数 ;
  wire [31:0] EX_IR, ID_IR, IF_IR, MEM_IR, WB_IR;

  Button \u_总复位  (.out(RST));
  Button _1 (.out(IR1));
  Button _2 (.out(IR2));
  Button _3 (.out(IR3));
  // Probe on \总周期数 
  // Probe on \总周期数 
  Button \u_继续运行  (.out(Go));
  LED #(.active("true")) led_1 (.in(W1));
  LED #(.active("true")) led_2 (.in(W2));
  LED #(.active("true")) led_3 (.in(W3));
  Hex_Digit_Display hex_digit_display_1 (.value(LedData[31:28]));  // open: dp
  // Probe on IF_PC[19:0]
  // Mips_Probe mips_probe_1: pin names not known; wires that end beside it: IF_IR
  Hex_Digit_Display hex_digit_display_2 (.value(LedData[23:20]));  // open: dp
  Hex_Digit_Display hex_digit_display_3 (.value(LedData[27:24]));  // open: dp
  // Probe on ID_PC[19:0]
  // Mips_Probe mips_probe_2: pin names not known; wires that end beside it: ID_IR
  Hex_Digit_Display hex_digit_display_4 (.value(LedData[15:12]));  // open: dp
  Hex_Digit_Display hex_digit_display_5 (.value(LedData[19:16]));  // open: dp
  Hex_Digit_Display hex_digit_display_6 (.value(LedData[7:4]));  // open: dp
  Hex_Digit_Display hex_digit_display_7 (.value(LedData[11:8]));  // open: dp
  Clock #(.highDuration(1), .lowDuration(1)) clock_1 (.out(clock_1_out));
  // Probe on EX_PC[19:0]
  // Mips_Probe mips_probe_3: pin names not known; wires that end beside it: clock_1_out, EX_IR, CLK
  Hex_Digit_Display hex_digit_display_8 (.value(LedData[3:0]));  // open: dp
  // Probe on \总周期数 
  // Probe on M_PC[19:0]
  // Mips_Probe mips_probe_4: pin names not known; wires that end beside it: MEM_IR
  // Probe on \总周期数 
  // Probe on \无条件分支数 
  // Probe on \条件分支成功数 
  // Probe on \插入气泡数 
  // Probe on \LoadUse次数 
  // Probe on IF_PC[11:0]
  // Probe on WB_PC[19:0]
  // Mips_Probe mips_probe_5: pin names not known; wires that end beside it: WB_IR
  // Probe on EX_PC[11:0]
  // Probe on ID_PC[11:0]
  // Probe on M_PC[11:0]
  D_Flip_Flop #(.trigger("high"), .Pre_Clr_Positions("LEGACY"), .NegatePresetClear("false"), .enable("true"), .NewFFLayout("false")) d_ff_1 (.Q(d_ff_1_q));  // open: clk, D, Qn, preset, en, reset
  // Probe on 13'hc
  // Probe on WB_PC[11:0]
  Comparator #(.width(13), .mode("twosComplement")) comparator_1 (
    .a(CNT_num), .b(13'hc), .eq(comparator_1_eq), .lt(comparator_1_lt));  // open: gt
  Clock #(.highDuration(1), .lowDuration(1)) clock_2 (.out(clock_2_out));
  nand nand_1 (nand_1_out, d_ff_1_q, comparator_1_eq);
  Counter #(.width(13), .max('h1fff), .ongoal("stay"), .trigger("rising"), .behavior("old")) counter_1 (
    .count(comparator_1_lt), .Q(CNT_num), .clk(clock_2_out));  // open: load, D, carry, clr, preset
  assign CLK = nand_1_out ? clock_2_out : 1'bz;  // Controlled_Buffer controlled_buffer_1
  Pull_Resistor #(.pull(1)) pull_resistor_1 (.node(CLK));

  // Other names for the same wires on the sheet: MEM_PC[31:0] = M_PC

  // Notes on the sheet:
  //   中断源
  //   时空图监测，可删除
  //   中断等待指示
  //   数码管输出
  //   控制位
  //   流水调试日志用
  //   暂停节拍，不能为0
  //   戳工具置1进入计数暂停模式，ctrl+k时钟自动运行到对应节拍暂停
  //   ctrl+k关闭时钟连续运行，将控制位置零，进入单步调试模式调试
  //   用这个时钟源需要去掉电路中的其他时钟源
  //   可计数暂停的时钟源
  //   为方便自动评测，需要输出流水线各段保存的PC值，注意是PC不是PC+4，另外ID段寄存器写入信息，Mem段内存写入信息也要输出
endmodule

module \气泡流水线  (
  output RegWrite,
  output MemWrite,
  output [31:0] IF_PC,
  output [31:0] ID_PC,
  output [31:0] EX_PC,
  output [31:0] M_PC,
  output [31:0] WB_PC,
  output [31:0] RDin,
  output [31:0] MDin,
  output [31:0] LedData
);

  wire CLK, clock_2_out, comparator_1_eq, comparator_1_lt, d_ff_1_q, Go, IR1, IR2, IR3, nand_1_out, RST, W1,
       W2, W3;
  wire [12:0] CNT_num;
  wire [15:0] \LoadUse次数 , \总周期数 , \插入气泡数 , \无条件分支数 , \条件分支成功数 ;
  wire [31:0] EX_IR, ID_IR, IF_IR, MEM_IR, WB_IR;

  Button \u_总复位  (.out(RST));
  Button _1 (.out(IR1));
  Button _2 (.out(IR2));
  Button _3 (.out(IR3));
  // Probe on \总周期数 
  // Probe on \总周期数 
  Button \u_继续运行  (.out(Go));
  LED #(.active("true")) led_1 (.in(W1));
  LED #(.active("true")) led_2 (.in(W2));
  LED #(.active("true")) led_3 (.in(W3));
  Hex_Digit_Display hex_digit_display_1 (.value(LedData[31:28]));  // open: dp
  // Probe on IF_PC[19:0]
  // Mips_Probe mips_probe_1: pin names not known; wires that end beside it: IF_IR
  Hex_Digit_Display hex_digit_display_2 (.value(LedData[27:24]));  // open: dp
  Hex_Digit_Display hex_digit_display_3 (.value(LedData[23:20]));  // open: dp
  // Probe on ID_PC[19:0]
  // Mips_Probe mips_probe_2: pin names not known; wires that end beside it: ID_IR
  Hex_Digit_Display hex_digit_display_4 (.value(LedData[19:16]));  // open: dp
  Hex_Digit_Display hex_digit_display_5 (.value(LedData[15:12]));  // open: dp
  Hex_Digit_Display hex_digit_display_6 (.value(LedData[11:8]));  // open: dp
  Hex_Digit_Display hex_digit_display_7 (.value(LedData[7:4]));  // open: dp
  Clock #(.highDuration(1), .lowDuration(1)) clock_1 (.out(CLK));
  // Probe on EX_PC[19:0]
  // Mips_Probe mips_probe_3: pin names not known; wires that end beside it: EX_IR
  Hex_Digit_Display hex_digit_display_8 (.value(LedData[3:0]));  // open: dp
  // Probe on \总周期数 
  // Probe on M_PC[19:0]
  // Mips_Probe mips_probe_4: pin names not known; wires that end beside it: MEM_IR
  // Probe on \总周期数 
  // Probe on \无条件分支数 
  // Probe on \条件分支成功数 
  // Probe on \插入气泡数 
  // Probe on \LoadUse次数 
  // Probe on IF_PC[11:0]
  // Probe on WB_PC[19:0]
  // Mips_Probe mips_probe_5: pin names not known; wires that end beside it: WB_IR
  // Probe on ID_PC[11:0]
  // Probe on EX_PC[11:0]
  // Probe on M_PC[11:0]
  D_Flip_Flop #(.trigger("high"), .Pre_Clr_Positions("LEGACY"), .NegatePresetClear("false"), .enable("true"), .NewFFLayout("false")) d_ff_1 (.Q(d_ff_1_q));  // open: clk, D, Qn, preset, en, reset
  // Probe on 13'hc
  // Probe on WB_PC[11:0]
  Comparator #(.width(13), .mode("twosComplement")) comparator_1 (
    .a(CNT_num), .b(13'hc), .eq(comparator_1_eq), .lt(comparator_1_lt));  // open: gt
  Clock #(.highDuration(1), .lowDuration(1)) clock_2 (.out(clock_2_out));
  nand nand_1 (nand_1_out, d_ff_1_q, comparator_1_eq);
  Counter #(.width(13), .max('h1fff), .ongoal("stay"), .trigger("rising"), .behavior("old")) counter_1 (
    .count(comparator_1_lt), .Q(CNT_num), .clk(clock_2_out));  // open: load, D, carry, clr, preset
  assign CLK = nand_1_out ? clock_2_out : 1'bz;  // Controlled_Buffer controlled_buffer_1
  Pull_Resistor #(.pull(1)) pull_resistor_1 (.node(CLK));

  // Other names for the same wires on the sheet: MEM_PC[31:0] = M_PC

  // Notes on the sheet:
  //   中断源
  //   时空图监测，可删除
  //   中断等待指示
  //   数码管输出
  //   控制位
  //   流水调试日志用
  //   暂停节拍，不能为0
  //   戳工具置1进入计数暂停模式，ctrl+k时钟自动运行到对应节拍暂停
  //   ctrl+k关闭时钟连续运行，将控制位置零，进入单步调试模式调试
  //   可计数暂停的时钟源
  //   为方便自动评测，需要输出流水线各段保存的PC值，注意是PC不是PC+4，另外ID段寄存器写入信息，Mem段内存写入信息也要输出
endmodule

module \重定向流水线  (
  output RegWrite,
  output MemWrite,
  output [31:0] IF_PC,
  output [31:0] ID_PC,
  output [31:0] EX_PC,
  output [31:0] M_PC,
  output [31:0] WB_PC,
  output [31:0] RDin,
  output [31:0] MDin,
  output [31:0] LedData
);

  wire CLK, clock_2_out, comparator_1_eq, comparator_1_lt, d_ff_1_q, Go, IR1, IR2, IR3, nand_1_out, RST, W1,
       W2, W3;
  wire [12:0] CNT_num;
  wire [15:0] \LoadUse次数 , \总周期数 , \插入气泡数 , \无条件分支数 , \条件分支成功数 ;
  wire [31:0] EX_IR, ID_IR, IF_IR, MEM_IR, WB_IR;

  Button \u_总复位  (.out(RST));
  Button _1 (.out(IR1));
  Button _2 (.out(IR2));
  Button _3 (.out(IR3));
  // Probe on \总周期数 
  // Probe on \总周期数 
  Button \u_继续运行  (.out(Go));
  LED #(.active("true")) led_1 (.in(W1));
  LED #(.active("true")) led_2 (.in(W2));
  LED #(.active("true")) led_3 (.in(W3));
  Hex_Digit_Display hex_digit_display_1 (.value(LedData[31:28]));  // open: dp
  // Probe on IF_PC[19:0]
  // Mips_Probe mips_probe_1: pin names not known; wires that end beside it: IF_IR
  Hex_Digit_Display hex_digit_display_2 (.value(LedData[27:24]));  // open: dp
  Hex_Digit_Display hex_digit_display_3 (.value(LedData[23:20]));  // open: dp
  // Probe on ID_PC[19:0]
  // Mips_Probe mips_probe_2: pin names not known; wires that end beside it: ID_IR
  Hex_Digit_Display hex_digit_display_4 (.value(LedData[19:16]));  // open: dp
  Hex_Digit_Display hex_digit_display_5 (.value(LedData[15:12]));  // open: dp
  Hex_Digit_Display hex_digit_display_6 (.value(LedData[11:8]));  // open: dp
  Hex_Digit_Display hex_digit_display_7 (.value(LedData[7:4]));  // open: dp
  Clock #(.highDuration(1), .lowDuration(1)) clock_1 (.out(CLK));
  // Probe on EX_PC[19:0]
  // Mips_Probe mips_probe_3: pin names not known; wires that end beside it: EX_IR
  Hex_Digit_Display hex_digit_display_8 (.value(LedData[3:0]));  // open: dp
  // Probe on \总周期数 
  // Probe on M_PC[19:0]
  // Mips_Probe mips_probe_4: pin names not known; wires that end beside it: MEM_IR
  // Probe on \总周期数 
  // Probe on \无条件分支数 
  // Probe on \条件分支成功数 
  // Probe on \插入气泡数 
  // Probe on \LoadUse次数 
  // Probe on IF_PC[11:0]
  // Probe on WB_PC[19:0]
  // Mips_Probe mips_probe_5: pin names not known; wires that end beside it: WB_IR
  // Probe on ID_PC[11:0]
  // Probe on EX_PC[11:0]
  // Probe on M_PC[11:0]
  D_Flip_Flop #(.trigger("high"), .Pre_Clr_Positions("LEGACY"), .NegatePresetClear("false"), .enable("true"), .NewFFLayout("false")) d_ff_1 (.Q(d_ff_1_q));  // open: clk, D, Qn, preset, en, reset
  // Probe on 13'hc
  // Probe on WB_PC[11:0]
  Comparator #(.width(13), .mode("twosComplement")) comparator_1 (
    .a(CNT_num), .b(13'hc), .eq(comparator_1_eq), .lt(comparator_1_lt));  // open: gt
  Clock #(.highDuration(1), .lowDuration(1)) clock_2 (.out(clock_2_out));
  nand nand_1 (nand_1_out, d_ff_1_q, comparator_1_eq);
  Counter #(.width(13), .max('h1fff), .ongoal("stay"), .trigger("rising"), .behavior("old")) counter_1 (
    .count(comparator_1_lt), .Q(CNT_num), .clk(clock_2_out));  // open: load, D, carry, clr, preset
  assign CLK = nand_1_out ? clock_2_out : 1'bz;  // Controlled_Buffer controlled_buffer_1
  Pull_Resistor #(.pull(1)) pull_resistor_1 (.node(CLK));

  // Other names for the same wires on the sheet: MEM_PC[31:0] = M_PC

  // Notes on the sheet:
  //   中断源
  //   时空图监测，可删除
  //   中断等待指示
  //   数码管输出
  //   控制位
  //   流水调试日志用
  //   暂停节拍，不能为0
  //   戳工具置1进入计数暂停模式，ctrl+k时钟自动运行到对应节拍暂停
  //   ctrl+k关闭时钟连续运行，将控制位置零，进入单步调试模式调试
  //   可计数暂停的时钟源
  //   为方便自动评测，需要输出流水线各段保存的PC值，注意是PC不是PC+4，另外ID段寄存器写入信息，Mem段内存写入信息也要输出
endmodule

module \中断按键参考电路  (
  input  \同步清零信号 ,
  output \与中断屏蔽位与 
);

  wire \_1号中断_out , and_1_out, clock_1_out, d_ff_1_q, or_1_out, or_2_out;

  Clock #(.highDuration(1), .lowDuration(1)) clock_1 (.out(clock_1_out));
  Button \_1号中断  (.out(\_1号中断_out ));
  LED #(.active("true")) \_1号中断等待指示灯  (.in(or_1_out));
  or or_1 (or_1_out, \与中断屏蔽位与 , d_ff_1_q);
  D_Flip_Flop #(.trigger("rising"), .Pre_Clr_Positions("LEGACY"), .NegatePresetClear("false"), .enable("true"), .NewFFLayout("false")) d_ff_1 (
    .clk(\_1号中断_out ), .D(1'b1), .Q(d_ff_1_q), .reset(\与中断屏蔽位与 ));  // open: Qn, preset, en
  or or_2 (or_2_out, d_ff_1_q, \与中断屏蔽位与 );
  and and_1 (and_1_out, or_2_out, ~\同步清零信号 );  // AND_Gate
  D_Flip_Flop #(.trigger("rising"), .Pre_Clr_Positions("LEGACY"), .NegatePresetClear("false"), .enable("true"), .NewFFLayout("false")) IR1 (
    .clk(clock_1_out), .D(and_1_out), .Q(\与中断屏蔽位与 ));  // open: Qn, preset, en, reset
  \单周期硬布线控制器  \u_单周期硬布线控制器_1  ();  // open: Func, OP, ALU_OP, MemToReg, MemWrite, ALU_SRC, RegWrite, SysCALL, SignedExt, RegDst, JR, JMP, Beq, JAL, Bne, LUI, LH, BLEZ, ERET

  // Notes on the sheet:
  //   中断信号采样参考电路
  //   Reset 
endmodule

module \单周期MIPS_单级中断  (
  input  IR1,
  input  IR2,
  input  IR3,
  output RegWrite,
  output MemWrite,
  output [31:0] PC,
  output [31:0] IR,
  output [31:0] RDin,
  output [31:0] MDin,
  output [31:0] LedData
);

  wire and_1_out, and_2_out, and_3_out, and_6_out, and_8_out, and_9_out, and_13_out, Branch, clear1, clear2,
       clear3, CLK, clock_2_out, comparator_1_eq, comparator_2_eq, comparator_3_eq, comparator_4_eq,
       comparator_5_eq, comparator_6_eq, comparator_6_lt, comparator_7_eq, comparator_7_lt, d_ff_1_q,
       d_ff_2_q, d_ff_3_q, d_ff_4_q, decoder_1_out0, decoder_1_out1, decoder_1_out2, ERET, Go, Halt, IE,
       IE_q, INT, INT1, INT2, INT3, IR1_t, IR2_t, IR3_t, IRA, IRB, IRC, JAL, JMP, JR, LedOut,
       mips_alu_1_equal, nand_1_out, not_1_out, not_2_out, not_3_out, or_1_out, or_7_out, or_8_out, or_9_out,
       or_11_out, priority_encoder_1_gs, register_1_q, register_2_q, SignedExt, Syscall, W1, W2, W3,
       \单周期硬布线控制器_1_alu_src , \单周期硬布线控制器_1_beq , \单周期硬布线控制器_1_blez , \单周期硬布线控制器_1_bne , \单周期硬布线控制器_1_lh ,
       \单周期硬布线控制器_1_lui , \单周期硬布线控制器_1_memtoreg , \单周期硬布线控制器_1_regdst ;
  wire [1:0] priority_encoder_1_out, \锁存当前中断号_q ;
  wire [3:0] \单周期硬布线控制器_1_alu_op ;
  wire [4:0] multiplexer_6_out, multiplexer_7_out, multiplexer_8_out, multiplexer_10_out;
  wire [12:0] CNT_num;
  wire [15:0] adder_3_out, multiplexer_17_out, register_4_q, \总周期数 ;
  wire [31:0] adder_2_out, bit_extender_1_out, bit_extender_2_out, bit_extender_3_out, INT_PC,
       mips_alu_1_result, multiplexer_1_out, multiplexer_2_out, multiplexer_3_out, multiplexer_5_out,
       multiplexer_11_out, multiplexer_12_out, multiplexer_13_out, multiplexer_15_out, multiplexer_16_out,
       Next_PC, PC_4, ram_1_data, Ret_PC, shifter_1_out, shifter_2_out, v0;

  Clock #(.highDuration(1), .lowDuration(1)) clock_1 ();  // open: out
  Button _1 ();  // open: out
  Button _2 ();  // open: out
  Button _3 ();  // open: out
  Button \u_继续运行  (.out(Go));
  LED #(.active("true")) led_1 (.in(W1));
  LED #(.active("true")) led_2 (.in(W2));
  LED #(.active("true")) led_3 (.in(W3));
  Multiplexer #(.select(1), .width(32), .disabled("Z"), .enable("false")) multiplexer_1 (
    .in0(PC_4), .in1(adder_2_out), .out(multiplexer_1_out), .sel(Branch));
  Hex_Digit_Display hex_digit_display_1 (.value(LedData[31:28]));  // open: dp
  Comparator #(.width(16), .mode("twosComplement")) comparator_1 (
    .a(16'h23b), .b(\总周期数 ), .eq(comparator_1_eq));  // open: gt, lt
  Comparator #(.width(16), .mode("twosComplement")) comparator_2 (
    .a(\总周期数 ), .b(16'h1), .eq(comparator_2_eq));  // open: gt, lt
  Comparator #(.width(16), .mode("twosComplement")) comparator_3 (
    .a(\总周期数 ), .b(16'h4), .eq(comparator_3_eq));  // open: gt, lt
  Comparator #(.width(16), .mode("twosComplement")) comparator_4 (
    .a(\总周期数 ), .b(16'h7), .eq(comparator_4_eq));  // open: gt, lt
  Register #(.width(1), .trigger("rising"), .Select("low")) register_1 (
    .D(1'b1), .Q(register_1_q), .clk(INT), .clr(register_2_q));  // open: en
  Multiplexer #(.select(1), .width(32), .disabled("Z"), .enable("false")) multiplexer_2 (
    .in0(multiplexer_1_out), .in1({PC[31:28], IR[25:0], 2'b00}), .out(multiplexer_2_out), .sel(JMP));
  Multiplexer #(.select(1), .width(32), .disabled("Z"), .enable("false")) multiplexer_3 (
    .in0(multiplexer_2_out), .in1(v0), .out(multiplexer_3_out), .sel(JR));
  Hex_Digit_Display hex_digit_display_2 (.value(LedData[23:20]));  // open: dp
  Hex_Digit_Display hex_digit_display_3 (.value(LedData[27:24]));  // open: dp
  or or_1 (or_1_out, comparator_1_eq, comparator_2_eq);
  assign IRA = or_1_out ? ~CLK : 1'bz;  // Controlled_Inverter controlled_inverter_1
  assign IRB = comparator_3_eq ? ~CLK : 1'bz;  // Controlled_Inverter controlled_inverter_2
  assign IRC = comparator_4_eq ? ~CLK : 1'bz;  // Controlled_Inverter controlled_inverter_3
  Multiplexer #(.select(1), .width(32), .disabled("Z"), .enable("false")) multiplexer_4 (
    .in0(multiplexer_3_out), .in1(Ret_PC), .out(Next_PC), .sel(ERET));
  Hex_Digit_Display hex_digit_display_4 (.value(LedData[15:12]));  // open: dp
  Hex_Digit_Display hex_digit_display_5 (.value(LedData[19:16]));  // open: dp
  Pull_Resistor #(.pull(0)) pull_resistor_1 (.node(IRA));
  Pull_Resistor #(.pull(0)) pull_resistor_2 (.node(IRB));
  Pull_Resistor #(.pull(0)) pull_resistor_3 (.node(IRC));
  Register #(.width(32), .trigger("falling"), .Select("low")) EPC (
    .D(Next_PC), .Q(Ret_PC), .clk(register_1_q));  // open: en, clr
  Register #(.width(1), .trigger("rising"), .Select("low")) register_2 (
    .D(register_1_q), .Q(register_2_q), .clk(CLK));  // open: en, clr
  Multiplexer #(.select(1), .width(32), .disabled("Z"), .enable("false")) multiplexer_5 (
    .in0(Next_PC), .in1(INT_PC), .out(multiplexer_5_out), .sel(register_1_q));
  Register #(.width(32), .trigger("rising"), .Select("low")) u_PC (
    .D(multiplexer_5_out), .en(not_1_out), .Q(PC), .clk(CLK));  // open: clr
  not not_1 (not_1_out, Halt);
  Hex_Digit_Display hex_digit_display_6 (.value(LedData[11:8]));  // open: dp
  Hex_Digit_Display hex_digit_display_7 (.value(LedData[7:4]));  // open: dp
  // Probe on \总周期数 
  Hex_Digit_Display hex_digit_display_8 (.value(LedData[3:0]));  // open: dp
  Adder #(.width(32)) adder_1 (.a(PC), .b(32'h4), .out(PC_4));  // open: cin, cout
  // Mips_Probe mips_probe_1: pin names not known; wires that end beside it: IR
  ROM #(.addrWidth(10), .dataWidth(32), .Select("high")) rom_1 (.addr(PC[11:2]), .data(IR));
  or or_2 (IR1_t, IR1, IRA);
  or or_3 (W1, INT1, d_ff_1_q);
  or or_4 (W2, INT2, d_ff_2_q);
  or or_5 (W3, INT3, d_ff_3_q);
  or or_6 (IR2_t, IR2, IRB);
  D_Flip_Flop #(.trigger("rising"), .Pre_Clr_Positions("LEGACY"), .NegatePresetClear("false"), .enable("true"), .NewFFLayout("false")) d_ff_1 (
    .clk(IR1_t), .D(1'b1), .Q(d_ff_1_q), .reset(INT1));  // open: Qn, preset, en
  D_Flip_Flop #(.trigger("rising"), .Pre_Clr_Positions("LEGACY"), .NegatePresetClear("false"), .enable("true"), .NewFFLayout("false")) d_ff_2 (
    .clk(IR2_t), .D(1'b1), .Q(d_ff_2_q), .reset(INT2));  // open: Qn, preset, en
  D_Flip_Flop #(.trigger("rising"), .Pre_Clr_Positions("LEGACY"), .NegatePresetClear("false"), .enable("true"), .NewFFLayout("false")) d_ff_3 (
    .clk(IR3_t), .D(1'b1), .Q(d_ff_3_q), .reset(INT3));  // open: Qn, preset, en
  or or_7 (or_7_out, d_ff_1_q, INT1);
  or or_8 (or_8_out, d_ff_2_q, INT2);
  or or_9 (or_9_out, d_ff_3_q, INT3);
  \单周期硬布线控制器  \u_单周期硬布线控制器_1  (
    .Func(IR[5:0]), .OP(IR[31:26]), .ALU_OP(\单周期硬布线控制器_1_alu_op ), .MemToReg(\单周期硬布线控制器_1_memtoreg ),
    .MemWrite(MemWrite), .ALU_SRC(\单周期硬布线控制器_1_alu_src ), .RegWrite(RegWrite), .SysCALL(Syscall),
    .SignedExt(SignedExt), .RegDst(\单周期硬布线控制器_1_regdst ), .JR(JR), .JMP(JMP), .Beq(\单周期硬布线控制器_1_beq ),
    .JAL(JAL), .Bne(\单周期硬布线控制器_1_bne ), .LUI(\单周期硬布线控制器_1_lui ), .LH(\单周期硬布线控制器_1_lh ),
    .BLEZ(\单周期硬布线控制器_1_blez ), .ERET(ERET));
  Multiplexer #(.select(1), .width(5), .disabled("Z"), .enable("false")) multiplexer_6 (
    .in0(IR[25:21]), .in1(5'b00010), .out(multiplexer_6_out), .sel(Syscall));
  Multiplexer #(.select(1), .width(5), .disabled("Z"), .enable("false")) multiplexer_7 (
    .in0(IR[20:16]), .in1(5'b00100), .out(multiplexer_7_out), .sel(Syscall));
  Multiplexer #(.select(1), .width(5), .disabled("Z"), .enable("false")) multiplexer_8 (
    .in0(IR[20:16]), .in1(IR[15:11]), .out(multiplexer_8_out), .sel(\单周期硬布线控制器_1_regdst ));
  Multiplexer #(.select(1), .width(32), .disabled("Z"), .enable("false")) multiplexer_9 (
    .in0(multiplexer_12_out), .in1(PC_4), .out(RDin), .sel(JAL));
  or or_10 (IR3_t, IR3, IRC);
  and and_1 (and_1_out, or_7_out, ~clear1);  // AND_Gate
  and and_2 (and_2_out, or_8_out, ~clear2);  // AND_Gate
  and and_3 (and_3_out, or_9_out, ~clear3);  // AND_Gate
  Multiplexer #(.select(1), .width(5), .disabled("Z"), .enable("false")) multiplexer_10 (
    .in0(multiplexer_8_out), .in1({5{1'b1}}), .out(multiplexer_10_out), .sel(JAL));
  assign bit_extender_1_out = {{16{1'b0}}, IR[15:0]};  // Bit_Extender bit_extender_1
  assign bit_extender_2_out = {{16{IR[15]}}, IR[15:0]};  // Bit_Extender bit_extender_2
  D_Flip_Flop #(.trigger("rising"), .Pre_Clr_Positions("LEGACY"), .NegatePresetClear("false"), .enable("true"), .NewFFLayout("false")) u_IR1 (
    .clk(CLK), .D(and_1_out), .Q(INT1));  // open: Qn, preset, en, reset
  D_Flip_Flop #(.trigger("rising"), .Pre_Clr_Positions("LEGACY"), .NegatePresetClear("false"), .enable("true"), .NewFFLayout("false")) u_IR2 (
    .clk(CLK), .D(and_2_out), .Q(INT2));  // open: Qn, preset, en, reset
  D_Flip_Flop #(.trigger("rising"), .Pre_Clr_Positions("LEGACY"), .NegatePresetClear("false"), .enable("true"), .NewFFLayout("false")) u_IR3 (
    .clk(CLK), .D(and_3_out), .Q(INT3));  // open: Qn, preset, en, reset
  MIPS_Regifile mips_regifile_1 (
    .Din(RDin), .Clk(CLK), .R1(v0), .R2(MDin), .WE(RegWrite), .W_num(multiplexer_10_out),
    .R1_num(multiplexer_6_out), .R2_num(multiplexer_7_out));
  Multiplexer #(.select(1), .width(32), .disabled("Z"), .enable("false")) multiplexer_11 (
    .in0(bit_extender_1_out), .in1(bit_extender_2_out), .out(multiplexer_11_out), .sel(SignedExt));
  Comparator #(.width(32), .mode("twosComplement")) comparator_5 (
    .a(32'ha), .b(v0), .eq(comparator_5_eq));  // open: gt, lt
  Multiplexer #(.select(1), .width(32), .disabled("Z"), .enable("false")) multiplexer_12 (
    .in0(multiplexer_15_out), .in1(shifter_2_out), .out(multiplexer_12_out), .sel(\单周期硬布线控制器_1_lui ));
  Shifter #(.width(32), .shift("ll")) shifter_1 (.in(multiplexer_11_out), .\dist (5'b00010), .out(shifter_1_out));
  Comparator #(.width(32), .mode("twosComplement")) comparator_6 (
    .a(v0), .b({32{1'b0}}), .eq(comparator_6_eq), .lt(comparator_6_lt));  // open: gt
  and and_4 (Halt, Syscall, comparator_5_eq);
  and and_5 (LedOut, Syscall, ~comparator_5_eq);  // AND_Gate
  Shifter #(.width(32), .shift("ll")) shifter_2 (.in(multiplexer_11_out), .\dist (5'b10000), .out(shifter_2_out));
  Adder #(.width(32)) adder_2 (.a(shifter_1_out), .b(PC_4), .out(adder_2_out));  // open: cin, cout
  or or_11 (or_11_out, comparator_6_eq, comparator_6_lt);
  Multiplexer #(.select(1), .width(32), .disabled("Z"), .enable("false")) multiplexer_13 (
    .in0(MDin), .in1(multiplexer_11_out), .out(multiplexer_13_out), .sel(\单周期硬布线控制器_1_alu_src ));
  not not_2 (not_2_out, 1'b0);
  and and_6 (and_6_out, or_11_out, \单周期硬布线控制器_1_blez );
  MIPS_ALU mips_alu_1 (
    .X(v0), .Y(multiplexer_13_out), .AluOP(\单周期硬布线控制器_1_alu_op ), .Equal(mips_alu_1_equal),
    .Result(mips_alu_1_result), .shamt(IR[10:6]));  // open: Result_2
  Priority_Encoder #(.select(2), .disabled("Z")) priority_encoder_1 (
    .in0(INT1), .in1(INT2), .in2(INT3), .in3(1'b0), .out(priority_encoder_1_out), .gs(priority_encoder_1_gs),
    .en_in(not_2_out));  // open: en_out
  and and_7 (INT, priority_encoder_1_gs, IE);
  and and_8 (and_8_out, mips_alu_1_equal, \单周期硬布线控制器_1_beq );
  and and_9 (and_9_out, ~mips_alu_1_equal, \单周期硬布线控制器_1_bne );  // AND_Gate
  D_Flip_Flop #(.trigger("high"), .Pre_Clr_Positions("LEGACY"), .NegatePresetClear("false"), .enable("true"), .NewFFLayout("false")) d_ff_4 (.Q(d_ff_4_q));  // open: clk, D, Qn, preset, en, reset
  // Probe on 13'hbc
  Register #(.width(1), .trigger("rising"), .Select("low")) u_IE (
    .D(1'b0), .Q(IE_q), .clk(not_3_out), .preset(INT));  // open: en, clr, cs
  not not_3 (not_3_out, ERET);
  or or_12 (Branch, and_6_out, and_8_out, and_9_out);
  Register #(.width(32), .trigger("rising"), .Select("low")) register_3 (
    .D(MDin), .en(LedOut), .Q(LedData), .clk(CLK));  // open: clr
  Comparator #(.width(13), .mode("twosComplement")) comparator_7 (
    .a(CNT_num), .b(13'hbc), .eq(comparator_7_eq), .lt(comparator_7_lt));  // open: gt
  Clock #(.highDuration(1), .lowDuration(1)) clock_2 (.out(clock_2_out));
  not not_4 (IE, IE_q);
  RAM #(.addrWidth(10), .dataWidth(32), .bus("separate"), .Select("high")) ram_1 (
    .addr(mips_alu_1_result[11:2]), .din(MDin), .data(ram_1_data), .str(MemWrite), .clk(CLK));  // open: sel, ld, clr
  nand nand_1 (nand_1_out, d_ff_4_q, comparator_7_eq);
  Counter #(.width(13), .max('h1fff), .ongoal("stay"), .trigger("rising"), .behavior("old")) counter_1 (
    .count(comparator_7_lt), .Q(CNT_num), .clk(clock_2_out));  // open: load, D, carry, clr, preset
  Multiplexer #(.select(2), .width(32), .disabled("Z"), .enable("false")) multiplexer_14 (
    .in0(32'h30ac), .in1(32'h3150), .in2(32'h31f4), .out(INT_PC), .sel(priority_encoder_1_out));  // open: in3
  Multiplexer #(.select(1), .width(32), .disabled("Z"), .enable("false")) multiplexer_15 (
    .in0(multiplexer_16_out), .in1(bit_extender_3_out), .out(multiplexer_15_out), .sel(\单周期硬布线控制器_1_lh ));
  assign CLK = nand_1_out ? clock_2_out : 1'bz;  // Controlled_Buffer controlled_buffer_1
  Multiplexer #(.select(1), .width(32), .disabled("Z"), .enable("false")) multiplexer_16 (
    .in0(mips_alu_1_result), .in1(ram_1_data), .out(multiplexer_16_out), .sel(\单周期硬布线控制器_1_memtoreg ));
  Pull_Resistor #(.pull(1)) pull_resistor_4 (.node(CLK));
  Register #(.width(2), .trigger("rising"), .Select("low")) \u_锁存当前中断号  (
    .D(priority_encoder_1_out), .Q(\锁存当前中断号_q ), .clk(INT));  // open: en, clr
  Decoder #(.select(2), .tristate("false"), .disabled("Z"), .enable("false")) decoder_1 (
    .out0(decoder_1_out0), .out1(decoder_1_out1), .out2(decoder_1_out2), .sel(\锁存当前中断号_q ));  // open: out3
  and and_10 (clear1, decoder_1_out0, ERET);
  and and_11 (clear2, decoder_1_out1, ERET);
  and and_12 (clear3, decoder_1_out2, ERET);
  Register #(.width(16), .trigger("rising"), .Select("low")) register_4 (
    .D(adder_3_out), .Q(register_4_q), .clk(and_13_out));  // open: en, clr
  and and_13 (and_13_out, CLK, ~Halt);  // AND_Gate
  Multiplexer #(.select(1), .width(16), .disabled("Z"), .enable("false")) multiplexer_17 (
    .in0(multiplexer_16_out[15:0]), .in1(multiplexer_16_out[31:16]), .out(multiplexer_17_out),
    .sel(mips_alu_1_result[1]));
  assign bit_extender_3_out = {{16{multiplexer_17_out[15]}}, multiplexer_17_out};  // Bit_Extender bit_extender_3
  Adder #(.width(16)) adder_3 (.a(16'h1), .b(register_4_q), .out(adder_3_out));  // open: cin, cout
  Adder #(.width(16)) adder_4 (.a({16{1'b1}}), .b(adder_3_out), .out(\总周期数 ));  // open: cin, cout

  // Notes on the sheet:
  //   中断源
  //   中断等待指示
  //   总复位信号应将除ROM以外所有存储组件全部清零
  //   单级中断测试信号模拟器
  //   数码管输出
  //   数码管输出应该用寄存器锁存，否则显示数据只能一闪而过
  //   指令存储器
  //   contents of rom_1 (hex, n*v repeats v):
  //   201d07d0 20100001 109fc0 139fc3 8021 2012000c 24160008 26100001 3210000f 20080008 20090001 139900
  //   2709825 132020 20020022 c 1094022 1500fff9 22100001 2018000f 2188024 108700 20080008 20090001 139902
  //   2709825 132021 20020022 c 1094022 1500fff9 108702 2c9b022 12c00001 8000c07 4020 1084027 84400
  //   3508ffff 82021 20020022 c 8000c01 afa20000 23bd0004 afa40000 23bd0004 afb00000 23bd0004 afb30000
  //   23bd0004 afb40000 23bd0004 afb50000 23bd0004 afb60000 23bd0004 20160001 20140003 20150001 168020
  //   108100 2149825 132020 20020022 c 1600fffa 295a022 1680fff7 23bdfffc 8fb60000 23bdfffc 8fb50000
  //   23bdfffc 8fb40000 23bdfffc 8fb30000 23bdfffc 8fb00000 23bdfffc 8fa40000 23bdfffc 8fa20000 42000018
  //   afa20000 23bd0004 afa40000 23bd0004 afb00000 23bd0004 afb30000 23bd0004 afb40000 23bd0004 afb50000
  //   23bd0004 afb60000 23bd0004 20160002 20140003 20150001 168020 108100 2149825 132020 20020022 c
  //   1600fffa 295a022 1680fff7 23bdfffc 8fb60000 23bdfffc 8fb50000 23bdfffc 8fb40000 23bdfffc 8fb30000
  //   23bdfffc 8fb00000 23bdfffc 8fa40000 23bdfffc 8fa20000 42000018 afa20000 23bd0004 afa40000 23bd0004
  //   afb00000 23bd0004 afb30000 23bd0004 afb40000 23bd0004 afb50000 23bd0004 afb60000 23bd0004 20160003
  //   20140003 20150001 168020 108100 2149825 132020 20020022 c 1600fffa 295a022 1680fff7 23bdfffc
  //   8fb60000 23bdfffc 8fb50000 23bdfffc 8fb40000 23bdfffc 8fb30000 23bdfffc 8fb00000 23bdfffc 8fa40000
  //   23bdfffc 8fa20000 42000018
  //   OP
  //   Func
  //   rs
  //   指令字
  //   rt
  //   rd
  //   shamt
  //   JMP
  //   JR
  //   OP
  //   Func
  //   Syscall
  //   imm16
  //   imm26
  //   Blez
  //   LH
  //   LUI
  //   Beq
  //   Bne
  //   MemToReg
  //   MemWrite
  //   AluOP
  //   AluSrcB
  //   RegWrite
  //   JAL
  //   RegDst
  //   Reset 
  //   Reset 
  //   Reset 
  //   为方便自动评测，需要输出PC，IR，寄存器堆写如数据RDin
  //   RAM写使能MemWrite、RAM写入数据MDin等信号
  //   控制位
  //   用这个时钟源需要去掉电路中的其他时钟源
  //   暂停节拍，不能为0
  //   戳工具置1进入计数暂停模式，ctrl+k时钟自动运行到对应节拍暂停
  //   ctrl+k关闭时钟连续运行，将控制位置零，进入单步调试模式调试
  //   可计数暂停的时钟源
endmodule

module \单周期MIPS_多级中断  (
  input  IR1,
  input  IR2,
  input  IR3,
  output RegWrite,
  output MemWrite,
  output [31:0] PC,
  output [31:0] IR,
  output [31:0] RDin,
  output [31:0] MDin,
  output [31:0] LedData
);

  wire CLK, comparator_1_eq, comparator_2_eq, comparator_3_eq, comparator_4_eq, comparator_5_eq, Go, IR1_t,
       IR2_t, IR3_t, IRA, IRB, IRC, or_1_out, or_2_out, W1, W2, W3;
  wire [15:0] \总周期数 ;

  Clock #(.highDuration(1), .lowDuration(1)) clock_1 (.out(CLK));
  Button _1 ();  // open: out
  Button _2 ();  // open: out
  Button _3 ();  // open: out
  Button \u_继续运行  (.out(Go));
  LED #(.active("true")) led_1 (.in(W1));
  LED #(.active("true")) led_2 (.in(W2));
  LED #(.active("true")) led_3 (.in(W3));
  Hex_Digit_Display hex_digit_display_1 (.value(LedData[31:28]));  // open: dp
  Comparator #(.width(16), .mode("twosComplement")) comparator_1 (
    .a(\总周期数 ), .b(16'h7), .eq(comparator_1_eq));  // open: gt, lt
  Comparator #(.width(16), .mode("twosComplement")) comparator_2 (
    .a(\总周期数 ), .b(16'h241), .eq(comparator_2_eq));  // open: gt, lt
  Hex_Digit_Display hex_digit_display_2 (.value(LedData[27:24]));  // open: dp
  Hex_Digit_Display hex_digit_display_3 (.value(LedData[23:20]));  // open: dp
  Comparator #(.width(16), .mode("twosComplement")) comparator_3 (
    .a(16'h258), .b(\总周期数 ), .eq(comparator_3_eq));  // open: gt, lt
  or or_1 (or_1_out, comparator_3_eq, comparator_4_eq);
  Comparator #(.width(16), .mode("twosComplement")) comparator_4 (
    .a(\总周期数 ), .b(16'h1), .eq(comparator_4_eq));  // open: gt, lt
  Comparator #(.width(16), .mode("twosComplement")) comparator_5 (
    .a(\总周期数 ), .b(16'h4), .eq(comparator_5_eq));  // open: gt, lt
  or or_2 (or_2_out, comparator_1_eq, comparator_2_eq);
  Hex_Digit_Display hex_digit_display_4 (.value(LedData[15:12]));  // open: dp
  Hex_Digit_Display hex_digit_display_5 (.value(LedData[19:16]));  // open: dp
  Pull_Resistor #(.pull(0)) pull_resistor_1 (.node(IRA));
  assign IRA = or_1_out ? ~CLK : 1'bz;  // Controlled_Inverter controlled_inverter_1
  Pull_Resistor #(.pull(0)) pull_resistor_2 (.node(IRB));
  assign IRB = comparator_5_eq ? ~CLK : 1'bz;  // Controlled_Inverter controlled_inverter_2
  Pull_Resistor #(.pull(0)) pull_resistor_3 (.node(IRC));
  assign IRC = or_2_out ? ~CLK : 1'bz;  // Controlled_Inverter controlled_inverter_3
  Hex_Digit_Display hex_digit_display_6 (.value(LedData[11:8]));  // open: dp
  Hex_Digit_Display hex_digit_display_7 (.value(LedData[7:4]));  // open: dp
  // Probe on \总周期数 
  Hex_Digit_Display hex_digit_display_8 (.value(LedData[3:0]));  // open: dp
  or or_3 (IR1_t, IR1, IRA);
  or or_4 (IR2_t, IR2, IRB);
  or or_5 (IR3_t, IR3, IRC);

  // Notes on the sheet:
  //   中断源
  //   中断等待指示
  //   总复位信号应将除ROM以外所有存储组件全部清零
  //   多级中断测试信号模拟器
  //   数码管输出
  //   数码管输出应该用寄存器锁存，否则显示数据只能一闪而过
  //   为方便自动评测，需要输出PC，IR，寄存器堆写如数据RDin
  //   RAM写使能MemWrite、RAM写入数据MDin等信号
endmodule

module \封装正确性测试  (
);

  wire IR1, IR2, IR3, MemW, RegW;
  wire [31:0] EX_PC, ID_PC, IF_PC, IR, LED, MDin, MDinr, MEM_PC, PC, RDin, RDinr, WB_PC;

  \单周期MIPS  \u_单周期mips_1  (
    .IR1(IR1), .IR2(IR2), .IR3(IR3), .RegWrite(RegW), .MemWrite(MemW), .PC(PC), .IR(IR), .RDin(RDin),
    .MDin(MDin), .LedData(LED));
  \气泡流水线  \u_气泡流水线_1  (
    .RegWrite(RegW), .MemWrite(MemW), .IF_PC(IF_PC), .ID_PC(ID_PC), .EX_PC(EX_PC), .M_PC(MEM_PC),
    .WB_PC(WB_PC), .RDin(RDinr), .MDin(MDinr), .LedData(LED));
  \单周期MIPS_单级中断  \u_单周期mips_单级中断_1  (
    .IR1(IR1), .IR2(IR2), .IR3(IR3), .RegWrite(RegW), .MemWrite(MemW), .PC(PC), .IR(IR), .RDin(RDin),
    .MDin(MDin), .LedData(LED));
  \理想流水线  \u_理想流水线_1  (
    .RegWrite(RegW), .MemWrite(MemW), .IF_PC(IF_PC), .ID_PC(ID_PC), .EX_PC(EX_PC), .M_PC(MEM_PC),
    .WB_PC(WB_PC), .RDin(RDinr), .MDin(MDinr), .LedData(LED));
  \重定向流水线  \u_重定向流水线_1  (
    .RegWrite(RegW), .MemWrite(MemW), .IF_PC(IF_PC), .ID_PC(ID_PC), .EX_PC(EX_PC), .M_PC(MEM_PC),
    .WB_PC(WB_PC), .RDin(RDinr), .MDin(MDinr), .LedData(LED));
  \单周期MIPS_多级中断  \u_单周期mips_多级中断_1  (
    .IR1(IR1), .IR2(IR2), .IR3(IR3), .RegWrite(RegW), .MemWrite(MemW), .PC(PC), .IR(IR), .RDin(RDin),
    .MDin(MDin), .LedData(LED));

  // Notes on the sheet:
  //   单周期封装测试
  //   气泡流水封装测试
  //   单周期+单级中断封装测试
  //   请检查上面封装有无位宽不匹配，引脚标签是否和连接的标签相对应，否则无法在educoder平台上正确测试
  //   理想流水封装测试
  //   重定向流水封装测试
  //   单周期+多级中断封装测试
endmodule

module \交互界面  (
  input  EN
);

  wire and_1_out, and_3_out, and_4_out, CLK, comparator_1_eq, comparator_2_eq, comparator_3_eq,
       comparator_4_eq, comparator_5_eq, EN_t, has_data, load, lose, mipscpu_1_not_used, mipscpu_1_used,
       not_1_out, not_2_out, not_used, or_1_out, or_6_out, output_CLK, pause, RST, used, \键盘输入逻辑_1_next_word ;
  wire [1:0] or_2_out;
  wire [2:0] random_1_out;
  wire [4:0] mipscpu_1_first_letter_2, multiplexer_1_out, multiplexer_2_out, \键盘输入逻辑_1_last_letter ;
  wire [5:0] counter_1_q;
  wire [6:0] ascii, first_letter, last_letter, \output , register_1_q;
  wire [15:0] counter_2_q, mipscpu_1_addr;

  TTY #(.Char_bit_width(7), .rows(8), .cols(32), .trigger("rising")) tty_1 (
    .data(\output ), .clk(output_CLK), .clr(RST));  // open: we
  Keyboard #(.Char_bit_width(7), .buflen(32), .trigger("rising")) keyboard_1 (
    .clk(CLK), .re(EN_t), .avail(has_data), .data(ascii));  // open: clr
  LED #(.active("true")) led_1 (.in(lose));
  Button button_1 (.out(RST));
  Comparator #(.width(7), .mode("twosComplement")) comparator_1 (
    .a(\output ), .b({7{1'b0}}), .eq(comparator_1_eq));  // open: gt, lt
  Comparator #(.width(7), .mode("twosComplement")) comparator_2 (
    .a(\output ), .b(7'b0100000), .eq(comparator_2_eq));  // open: gt, lt
  Register #(.width(7), .trigger("rising"), .Select("low")) register_1 (
    .D(last_letter), .Q(register_1_q), .clk(has_data), .clr(RST));  // open: en
  \键盘输入逻辑  \u_键盘输入逻辑_1  (
    .CLK(CLK), .RST(RST), .has_data(has_data), .ascii(ascii), .next_word(\键盘输入逻辑_1_next_word ),
    .last_letter(\键盘输入逻辑_1_last_letter ), .first_letter(first_letter));  // open: EN
  not not_1 (not_1_out, comparator_1_eq);
  and and_1 (and_1_out, not_1_out, not_2_out);
  not not_2 (not_2_out, comparator_2_eq);
  Comparator #(.width(7), .mode("twosComplement")) comparator_3 (
    .a(register_1_q), .b({7{1'b0}}), .eq(comparator_3_eq));  // open: gt, lt
  Comparator #(.width(7), .mode("twosComplement")) comparator_4 (
    .a(register_1_q), .b(first_letter), .eq(comparator_4_eq));  // open: gt, lt
  Clock #(.highDuration(1), .lowDuration(1)) clock_1 (.out(CLK));
  and and_2 (lose, ~comparator_3_eq, ~comparator_4_eq);  // AND_Gate
  or or_1 (or_1_out, RST, \键盘输入逻辑_1_next_word );
  Random #(.width(3), .seed(0), .trigger("rising")) random_1 (.clk(or_1_out), .out(random_1_out));  // open: next, clr
  Register #(.width(7), .trigger("rising"), .Select("low")) register_2 (
    .D(\output ), .en(and_1_out), .Q(last_letter), .clk(CLK), .clr(RST));
  Register #(.width(1), .trigger("falling"), .Select("low")) register_3 (
    .D(1'b1), .Q(not_used), .clk(mipscpu_1_not_used), .clr(pause));  // open: en
  MIPScpu mipscpu_1 (
    .CLK(CLK), .IR1(\键盘输入逻辑_1_next_word ), .first_letter(\键盘输入逻辑_1_last_letter ), .random_num(random_1_out),
    .NOT_USED(mipscpu_1_not_used), .USED(mipscpu_1_used), .first_letter_2(mipscpu_1_first_letter_2),
    .addr(mipscpu_1_addr), .MEM_RST(RST));  // open: IR2, IR3
  Register #(.width(1), .trigger("falling"), .Select("low")) register_4 (
    .D(1'b1), .Q(used), .clk(mipscpu_1_used), .clr(pause));  // open: en
  or or_2 (or_2_out[0], not_used, mipscpu_1_not_used);
  not not_3 (EN_t, EN);
  and and_3 (and_3_out, not_used, CLK);
  and and_4 (and_4_out, used, CLK);
  or or_3 (or_2_out[1], used, mipscpu_1_used);
  Multiplexer #(.select(2), .width(5), .disabled("Z"), .enable("false")) multiplexer_1 (
    .in0({5{1'b1}}), .in1(mipscpu_1_first_letter_2), .in2(5'b11110), .out(multiplexer_1_out), .sel(or_2_out));  // open: in3
  or or_4 (output_CLK, and_3_out, and_4_out);
  or or_5 (load, mipscpu_1_used, mipscpu_1_not_used);
  Multiplexer #(.select(1), .width(5), .disabled("Z"), .enable("false")) multiplexer_2 (
    .in0(multiplexer_1_out), .in1(5'b11101), .out(multiplexer_2_out), .sel(lose));
  Counter #(.width(6), .max('h3f), .ongoal("wrap"), .trigger("rising"), .behavior("new")) counter_1 (
    .Q(counter_1_q), .clk(output_CLK), .clr(pause));  // open: load, D, count, carry, preset, down
  or or_6 (or_6_out, load, output_CLK);
  Comparator #(.width(6), .mode("twosComplement")) comparator_5 (
    .a(counter_1_q), .b(6'b100000), .eq(comparator_5_eq));  // open: gt, lt
  Counter #(.width(16), .max('hffff), .ongoal("wrap"), .trigger("rising"), .behavior("new")) counter_2 (
    .load(load), .D(mipscpu_1_addr), .Q(counter_2_q), .clk(or_6_out), .clr(RST), .preset(mipscpu_1_used));  // open: count, carry, down
  or or_7 (pause, comparator_5_eq, lose, RST);
  \ROM阵列  \rom阵列_1  (.ADDR(counter_2_q), .First_Letter(multiplexer_2_out), .ascii(\output ));

  // Notes on the sheet:
  //   失败提示
  //   在这里输入一个单词以开始游戏
  //   欢迎来到英语成语接龙游戏
  //   游戏规则：类似中文版的成语接龙，你需要与人机对战
  //   人机每个字母开头的单词只会8个，且每个单词只会使用一次
  //   在每轮回答中，当人机随机到之前使用过的单词就会认输，屏幕上会有胜利提示
  //   当你输入的单词首字母不正确时，你就失败了，屏幕上方的灯会亮
  //   再来一局
  //   注意：每次输入前请暂停时钟，在一个时钟周期内完成输入
endmodule
module \ROM阵列  (
  input  [15:0] ADDR,
  input  [4:0] First_Letter,
  output [6:0] ascii
);

  wire [6:0] LINE0, LINE1, LINE2, LINE3, LINE4, LINE5, LINE6, LINE7, LINE8, LINE9, LINE10, LINE11, LINE12,
       LINE13, LINE14, LINE15, LINE16, LINE17, LINE18, LINE19, LINE20, LINE21, LINE22, LINE23, LINE24,
       LINE25, LINE26, LINE27, LINE28, LINE29, LINE30, LINE31;

  ROM #(.addrWidth(16), .dataWidth(7), .Select("low")) A (.addr(ADDR), .data(LINE0));
  ROM #(.addrWidth(16), .dataWidth(7), .Select("low")) B (.addr(ADDR), .data(LINE1));
  ROM #(.addrWidth(16), .dataWidth(7), .Select("low")) C (.addr(ADDR), .data(LINE2));
  ROM #(.addrWidth(16), .dataWidth(7), .Select("low")) D (.addr(ADDR), .data(LINE3));
  ROM #(.addrWidth(16), .dataWidth(7), .Select("low")) E (.addr(ADDR), .data(LINE4));
  ROM #(.addrWidth(16), .dataWidth(7), .Select("low")) F (.addr(ADDR), .data(LINE5));
  ROM #(.addrWidth(16), .dataWidth(7), .Select("low")) G (.addr(ADDR), .data(LINE6));
  ROM #(.addrWidth(16), .dataWidth(7), .Select("low")) H (.addr(ADDR), .data(LINE7));
  ROM #(.addrWidth(16), .dataWidth(7), .Select("low")) I (.addr(ADDR), .data(LINE8));
  ROM #(.addrWidth(16), .dataWidth(7), .Select("low")) J (.addr(ADDR), .data(LINE9));
  ROM #(.addrWidth(16), .dataWidth(7), .Select("low")) K (.addr(ADDR), .data(LINE10));
  ROM #(.addrWidth(16), .dataWidth(7), .Select("low")) L (.addr(ADDR), .data(LINE11));
  ROM #(.addrWidth(16), .dataWidth(7), .Select("low")) M (.addr(ADDR), .data(LINE12));
  ROM #(.addrWidth(16), .dataWidth(7), .Select("low")) N (.addr(ADDR), .data(LINE13));
  ROM #(.addrWidth(16), .dataWidth(7), .Select("low")) O (.addr(ADDR), .data(LINE14));
  ROM #(.addrWidth(16), .dataWidth(7), .Select("low")) P (.addr(ADDR), .data(LINE15));
  ROM #(.addrWidth(16), .dataWidth(7), .Select("low")) Q (.addr(ADDR), .data(LINE16));
  ROM #(.addrWidth(16), .dataWidth(7), .Select("low")) R (.addr(ADDR), .data(LINE17));
  ROM #(.addrWidth(16), .dataWidth(7), .Select("low")) S (.addr(ADDR), .data(LINE18));
  ROM #(.addrWidth(16), .dataWidth(7), .Select("low")) T (.addr(ADDR), .data(LINE19));
  ROM #(.addrWidth(16), .dataWidth(7), .Select("low")) U (.addr(ADDR), .data(LINE20));
  ROM #(.addrWidth(16), .dataWidth(7), .Select("low")) V (.addr(ADDR), .data(LINE21));
  ROM #(.addrWidth(16), .dataWidth(7), .Select("low")) W (.addr(ADDR), .data(LINE22));
  ROM #(.addrWidth(16), .dataWidth(7), .Select("low")) X (.addr(ADDR), .data(LINE23));
  ROM #(.addrWidth(16), .dataWidth(7), .Select("low")) Y (.addr(ADDR), .data(LINE24));
  ROM #(.addrWidth(16), .dataWidth(7), .Select("low")) Z (.addr(ADDR), .data(LINE25));
  ROM #(.addrWidth(16), .dataWidth(7), .Select("low")) rom_1 (.addr(ADDR), .data(LINE26));
  ROM #(.addrWidth(16), .dataWidth(7), .Select("low")) rom_2 (.addr(ADDR), .data(LINE27));
  ROM #(.addrWidth(16), .dataWidth(7), .Select("low")) rom_3 (.addr(ADDR), .data(LINE28));
  ROM #(.addrWidth(16), .dataWidth(7), .Select("low")) LOSE (.addr(ADDR), .data(LINE29));
  ROM #(.addrWidth(16), .dataWidth(7), .Select("low")) WIN (.addr(ADDR), .data(LINE30));
  ROM #(.addrWidth(16), .dataWidth(7), .Select("low")) \u_空白  (.addr(ADDR), .data(LINE31));
  Multiplexer #(.select(5), .width(7), .disabled("Z"), .enable("false")) multiplexer_1 (
    .in0(LINE0), .in1(LINE1), .in2(LINE2), .in3(LINE3), .in4(LINE4), .in5(LINE5), .in6(LINE6), .in7(LINE7),
    .in8(LINE8), .in9(LINE9), .in10(LINE10), .in11(LINE11), .in12(LINE12), .in13(LINE13), .in14(LINE14),
    .in15(LINE15), .in16(LINE16), .in17(LINE17), .in18(LINE18), .in19(LINE19), .in20(LINE20), .in21(LINE21),
    .in22(LINE22), .in23(LINE23), .in24(LINE24), .in25(LINE25), .in26(LINE26), .in27(LINE27), .in28(LINE28),
    .in29(LINE29), .in30(LINE30), .in31(LINE31), .out(ascii), .sel(First_Letter));

  // Notes on the sheet:
  //   contents of A (hex, n*v repeats v):
  //   61 6d 6e 65 73 69 61 25*20 61 70 6c 6f 6d 62 26*20 61 6c 63 6f 68 6f 6c 69 63 23*20 61 69 72 66 69
  //   65 6c 64 24*20 61 6d 61 7a 65 27*20 61 6c 6f 6f 66 27*20 61 69 72 69 6e 67 26*20 61 6d 62 75 73 68
  //   26*20 61 6c 69 62 69 27*20 61 69 72 73 69 63 6b 25*20 61 6c 63 6f 68 6f 6c 25*20 61 69 6d 29*20 61
  //   67 61 69 6e 27*20 61 67 6f 29*20 61 69 72 73 68 69 70 25*20 61 69 72 29*20 61 6c 62 61 74 72 6f 73
  //   73 23*20 61 69 72 70 6f 72 74 25*20 61 64 69 65 75 27*20 61 6c 6c 6f 77 27*20 61 6e 6e 65 78 27*20
  //   61 67 65 6e 63 79 26*20 69 20 63 61 6e 6e 6f 74 20 61 6e 73 77 65 72 2c 73 74 61 72 74 20 77 69 74
  //   68 20 65 61 74 20 20 69 20 63 61 6e 6e 6f 74 20 61 6e 73 77 65 72 2c 73 74 61 72 74 20 77 69 74 68
  //   20 65 61 74 20 20 69 20 63 61 6e 6e 6f 74 20 61 6e 73 77 65 72 2c 73 74 61 72 74 20 77 69 74 68 20
  //   65 61 74 20 20 69 20 63 61 6e 6e 6f 74 20 61 6e 73 77 65 72 2c 73 74 61 72 74 20 77 69 74 68 20 65
  //   61 74 20 20 69 20 63 61 6e 6e 6f 74 20 61 6e 73 77 65 72 2c 73 74 61 72 74 20 77 69 74 68 20 65 61
  //   74 20 20 69 20 63 61 6e 6e 6f 74 20 61 6e 73 77 65 72 2c 73 74 61 72 74 20 77 69 74 68 20 65 61 74
  //   20 20 69 20 63 61 6e 6e 6f 74 20 61 6e 73 77 65 72 2c 73 74 61 72 74 20 77 69 74 68 20 65 61 74 20
  //   20 69 20 63 61 6e 6e 6f 74 20 61 6e 73 77 65 72 2c 73 74 61 72 74 20 77 69 74 68 20 65 61 74 20 20
  //   69 20 63 61 6e 6e 6f 74 20 61 6e 73 77 65 72 2c 73 74 61 72 74 20 77 69 74 68 20 65 61 74 20 20 69
  //   20 63 61 6e 6e 6f 74 20 61 6e 73 77 65 72 2c 73 74 61 72 74 20 77 69 74 68 20 65 61 74 20 20 69 20
  //   63 61 6e 6e 6f 74 20 61 6e 73 77 65 72 2c 73 74 61 72 74 20 77 69 74 68 20 65 61 74 20 20 69 20 63
  //   61 6e 6e 6f 74 20 61 6e 73 77 65 72 2c 73 74 61 72 74 20 77 69 74 68 20 65 61 74 20 20 69 20 63 61
  //   6e 6e 6f 74 20 61 6e 73 77 65 72 2c 73 74 61 72 74 20 77 69 74 68 20 65 61 74 20 20 69 20 63 61 6e
  //   6e 6f 74 20 61 6e 73 77 65 72 2c 73 74 61 72 74 20 77 69 74 68 20 65 61 74 20 20 69 20 63 61 6e 6e
  //   6f 74 20 61 6e 73 77 65 72 2c 73 74 61 72 74 20 77 69 74 68 20 65 61 74 20 20 69 20 63 61 6e 6e 6f
  //   74 20 61 6e 73 77 65 72 2c 73 74 61 72 74 20 77 69 74 68 20 65 61 74 20 20 69 20 63 61 6e 6e 6f 74
  //   20 61 6e 73 77 65 72 2c 73 74 61 72 74 20 77 69 74 68 20 65 61 74 20 20 69 20 63 61 6e 6e 6f 74 20
  //   61 6e 73 77 65 72 2c 73 74 61 72 74 20 77 69 74 68 20 65 61 74 20 20 69 20 63 61 6e 6e 6f 74 20 61
  //   6e 73 77 65 72 2c 73 74 61 72 74 20 77 69 74 68 20 65 61 74 20 20 69 20 63 61 6e 6e 6f 74 20 61 6e
  //   73 77 65 72 2c 73 74 61 72 74 20 77 69 74 68 20 65 61 74 20 20 69 20 63 61 6e 6e 6f 74 20 61 6e 73
  //   77 65 72 2c 73 74 61 72 74 20 77 69 74 68 20 65 61 74 20 20 69 20 63 61 6e 6e 6f 74 20 61 6e 73 77
  //   65 72 2c 73 74 61 72 74 20 77 69 74 68 20 65 61 74 20 20 69 20 63 61 6e 6e 6f 74 20 61 6e 73 77 65
  //   72 2c 73 74 61 72 74 20 77 69 74 68 20 65 61 74 20 20 69 20 63 61 6e 6e 6f 74 20 61 6e 73 77 65 72
  //   2c 73 74 61 72 74 20 77 69 74 68 20 65 61 74 20 20 69 20 63 61 6e 6e 6f 74 20 61 6e 73 77 65 72 2c
  //   73 74 61 72 74 20 77 69 74 68 20 65 61 74 20 20 69 20 63 61 6e 6e 6f 74 20 61 6e 73 77 65 72 2c 73
  //   74 61 72 74 20 77 69 74 68 20 65 61 74 20 20 69 20 63 61 6e 6e 6f 74 20 61 6e 73 77 65 72 2c 73 74
  //   61 72 74 20 77 69 74 68 20 65 61 74 20 20 69 20 63 61 6e 6e 6f 74 20 61 6e 73 77 65 72 2c 73 74 61
  //   72 74 20 77 69 74 68 20 65 61 74 20 20 69 20 63 61 6e 6e 6f 74 20 61 6e 73 77 65 72 2c 73 74 61 72
  //   74 20 77 69 74 68 20 65 61 74 20 20 69 20 63 61 6e 6e 6f 74 20 61 6e 73 77 65 72 2c 73 74 61 72 74
  //   20 77 69 74 68 20 65 61 74 20 20 69 20 63 61 6e 6e 6f 74 20 61 6e 73 77 65 72 2c 73 74 61 72 74 20
  //   77 69 74 68 20 65 61 74 20 20 69 20 63 61 6e 6e 6f 74 20 61 6e 73 77 65 72 2c 73 74 61 72 74 20 77
  //   69 74 68 20 65 61 74 20 20
  //   contents of B (hex, n*v repeats v):
  //   62 61 63 74 65 72 69 61 24*20 62 61 74 68 74 75 62 25*20 62 69 76 6f 75 61 63 25*20 62 61 64 29*20
  //   62 72 61 65 28*20 62 65 68 61 6c 66 26*20 62 61 67 29*20 62 69 72 74 68 27*20 62 61 6e 6b 28*20 62
  //   65 76 65 6c 27*20 62 72 69 6d 28*20 62 61 69 72 6e 27*20 69 20 63 61 6e 6e 6f 74 20 61 6e 73 77 65
  //   72 2c 73 74 61 72 74 20 77 69 74 68 20 65 61 74 20 20 69 20 63 61 6e 6e 6f 74 20 61 6e 73 77 65 72
  //   2c 73 74 61 72 74 20 77 69 74 68 20 65 61 74 20 20 69 20 63 61 6e 6e 6f 74 20 61 6e 73 77 65 72 2c
  //   73 74 61 72 74 20 77 69 74 68 20 65 61 74 20 20 69 20 63 61 6e 6e 6f 74 20 61 6e 73 77 65 72 2c 73
  //   74 61 72 74 20 77 69 74 68 20 65 61 74 20 20 69 20 63 61 6e 6e 6f 74 20 61 6e 73 77 65 72 2c 73 74
  //   61 72 74 20 77 69 74 68 20 65 61 74 20 20 69 20 63 61 6e 6e 6f 74 20 61 6e 73 77 65 72 2c 73 74 61
  //   72 74 20 77 69 74 68 20 65 61 74 20 20 69 20 63 61 6e 6e 6f 74 20 61 6e 73 77 65 72 2c 73 74 61 72
  //   74 20 77 69 74 68 20 65 61 74 20 20 69 20 63 61 6e 6e 6f 74 20 61 6e 73 77 65 72 2c 73 74 61 72 74
  //   20 77 69 74 68 20 65 61 74 20 20 69 20 63 61 6e 6e 6f 74 20 61 6e 73 77 65 72 2c 73 74 61 72 74 20
  //   77 69 74 68 20 65 61 74 20 20 69 20 63 61 6e 6e 6f 74 20 61 6e 73 77 65 72 2c 73 74 61 72 74 20 77
  //   69 74 68 20 65 61 74 20 20 69 20 63 61 6e 6e 6f 74 20 61 6e 73 77 65 72 2c 73 74 61 72 74 20 77 69
  //   74 68 20 65 61 74 20 20 69 20 63 61 6e 6e 6f 74 20 61 6e 73 77 65 72 2c 73 74 61 72 74 20 77 69 74
  //   68 20 65 61 74 20 20 69 20 63 61 6e 6e 6f 74 20 61 6e 73 77 65 72 2c 73 74 61 72 74 20 77 69 74 68
  //   20 65 61 74 20 20 69 20 63 61 6e 6e 6f 74 20 61 6e 73 77 65 72 2c 73 74 61 72 74 20 77 69 74 68 20
  //   65 61 74 20 20 69 20 63 61 6e 6e 6f 74 20 61 6e 73 77 65 72 2c 73 74 61 72 74 20 77 69 74 68 20 65
  //   61 74 20 20 69 20 63 61 6e 6e 6f 74 20 61 6e 73 77 65 72 2c 73 74 61 72 74 20 77 69 74 68 20 65 61
  //   74 20 20 69 20 63 61 6e 6e 6f 74 20 61 6e 73 77 65 72 2c 73 74 61 72 74 20 77 69 74 68 20 65 61 74
  //   20 20 69 20 63 61 6e 6e 6f 74 20 61 6e 73 77 65 72 2c 73 74 61 72 74 20 77 69 74 68 20 65 61 74 20
  //   20 69 20 63 61 6e 6e 6f 74 20 61 6e 73 77 65 72 2c 73 74 61 72 74 20 77 69 74 68 20 65 61 74 20 20
  //   69 20 63 61 6e 6e 6f 74 20 61 6e 73 77 65 72 2c 73 74 61 72 74 20 77 69 74 68 20 65 61 74 20 20 69
  //   20 63 61 6e 6e 6f 74 20 61 6e 73 77 65 72 2c 73 74 61 72 74 20 77 69 74 68 20 65 61 74 20 20 69 20
  //   63 61 6e 6e 6f 74 20 61 6e 73 77 65 72 2c 73 74 61 72 74 20 77 69 74 68 20 65 61 74 20 20 69 20 63
  //   61 6e 6e 6f 74 20 61 6e 73 77 65 72 2c 73 74 61 72 74 20 77 69 74 68 20 65 61 74 20 20 69 20 63 61
  //   6e 6e 6f 74 20 61 6e 73 77 65 72 2c 73 74 61 72 74 20 77 69 74 68 20 65 61 74 20 20 69 20 63 61 6e
  //   6e 6f 74 20 61 6e 73 77 65 72 2c 73 74 61 72 74 20 77 69 74 68 20 65 61 74 20 20 69 20 63 61 6e 6e
  //   6f 74 20 61 6e 73 77 65 72 2c 73 74 61 72 74 20 77 69 74 68 20 65 61 74 20 20 69 20 63 61 6e 6e 6f
  //   74 20 61 6e 73 77 65 72 2c 73 74 61 72 74 20 77 69 74 68 20 65 61 74 20 20 69 20 63 61 6e 6e 6f 74
  //   20 61 6e 73 77 65 72 2c 73 74 61 72 74 20 77 69 74 68 20 65 61 74 20 20 69 20 63 61 6e 6e 6f 74 20
  //   61 6e 73 77 65 72 2c 73 74 61 72 74 20 77 69 74 68 20 65 61 74 20 20 69 20 63 61 6e 6e 6f 74 20 61
  //   6e 73 77 65 72 2c 73 74 61 72 74 20 77 69 74 68 20 65 61 74 20 20 69 20 63 61 6e 6e 6f 74 20 61 6e
  //   73 77 65 72 2c 73 74 61 72 74 20 77 69 74 68 20 65 61 74 20 20 69 20 63 61 6e 6e 6f 74 20 61 6e 73
  //   77 65 72 2c 73 74 61 72 74 20 77 69 74 68 20 65 61 74 20 20
  //   contents of C (hex, n*v repeats v):
  //   63 61 61 63 28*20 63 61 62 29*20 63 61 62 61 6c 27*20 63 61 62 62 61 67 65 25*20 63 61 62 69 6e
  //   27*20 63 61 62 69 6e 65 74 25*20 63 61 62 6c 65 27*20 63 61 62 6c 65 67 72 61 6d 23*20 63 61 62 6f
  //   6f 73 65 25*20 63 61 63 61 6f 27*20 63 61 63 68 65 27*20 63 61 63 6b 6c 65 20 6e 24*20 63 61 63 6f
  //   70 68 6f 6e 6f 75 73 21*20 63 61 63 6f 70 68 6f 6e 79 23*20 69 20 63 61 6e 6e 6f 74 20 61 6e 73 77
  //   65 72 2c 73 74 61 72 74 20 77 69 74 68 20 65 61 74 20 20 69 20 63 61 6e 6e 6f 74 20 61 6e 73 77 65
  //   72 2c 73 74 61 72 74 20 77 69 74 68 20 65 61 74 20 20 69 20 63 61 6e 6e 6f 74 20 61 6e 73 77 65 72
  //   2c 73 74 61 72 74 20 77 69 74 68 20 65 61 74 20 20 69 20 63 61 6e 6e 6f 74 20 61 6e 73 77 65 72 2c
  //   73 74 61 72 74 20 77 69 74 68 20 65 61 74 20 20 69 20 63 61 6e 6e 6f 74 20 61 6e 73 77 65 72 2c 73
  //   74 61 72 74 20 77 69 74 68 20 65 61 74 20 20 69 20 63 61 6e 6e 6f 74 20 61 6e 73 77 65 72 2c 73 74
  //   61 72 74 20 77 69 74 68 20 65 61 74 20 20 69 20 63 61 6e 6e 6f 74 20 61 6e 73 77 65 72 2c 73 74 61
  //   72 74 20 77 69 74 68 20 65 61 74 20 20 69 20 63 61 6e 6e 6f 74 20 61 6e 73 77 65 72 2c 73 74 61 72
  //   74 20 77 69 74 68 20 65 61 74 20 20 69 20 63 61 6e 6e 6f 74 20 61 6e 73 77 65 72 2c 73 74 61 72 74
  //   20 77 69 74 68 20 65 61 74 20 20 69 20 63 61 6e 6e 6f 74 20 61 6e 73 77 65 72 2c 73 74 61 72 74 20
  //   77 69 74 68 20 65 61 74 20 20 69 20 63 61 6e 6e 6f 74 20 61 6e 73 77 65 72 2c 73 74 61 72 74 20 77
  //   69 74 68 20 65 61 74 20 20 69 20 63 61 6e 6e 6f 74 20 61 6e 73 77 65 72 2c 73 74 61 72 74 20 77 69
  //   74 68 20 65 61 74 20 20 69 20 63 61 6e 6e 6f 74 20 61 6e 73 77 65 72 2c 73 74 61 72 74 20 77 69 74
  //   68 20 65 61 74 20 20 69 20 63 61 6e 6e 6f 74 20 61 6e 73 77 65 72 2c 73 74 61 72 74 20 77 69 74 68
  //   20 65 61 74 20 20 69 20 63 61 6e 6e 6f 74 20 61 6e 73 77 65 72 2c 73 74 61 72 74 20 77 69 74 68 20
  //   65 61 74 20 20 69 20 63 61 6e 6e 6f 74 20 61 6e 73 77 65 72 2c 73 74 61 72 74 20 77 69 74 68 20 65
  //   61 74 20 20 69 20 63 61 6e 6e 6f 74 20 61 6e 73 77 65 72 2c 73 74 61 72 74 20 77 69 74 68 20 65 61
  //   74 20 20 69 20 63 61 6e 6e 6f 74 20 61 6e 73 77 65 72 2c 73 74 61 72 74 20 77 69 74 68 20 65 61 74
  //   20 20 69 20 63 61 6e 6e 6f 74 20 61 6e 73 77 65 72 2c 73 74 61 72 74 20 77 69 74 68 20 65 61 74 20
  //   20 69 20 63 61 6e 6e 6f 74 20 61 6e 73 77 65 72 2c 73 74 61 72 74 20 77 69 74 68 20 65 61 74 20 20
  //   69 20 63 61 6e 6e 6f 74 20 61 6e 73 77 65 72 2c 73 74 61 72 74 20 77 69 74 68 20 65 61 74 20 20 69
  //   20 63 61 6e 6e 6f 74 20 61 6e 73 77 65 72 2c 73 74 61 72 74 20 77 69 74 68 20 65 61 74 20 20 69 20
  //   63 61 6e 6e 6f 74 20 61 6e 73 77 65 72 2c 73 74 61 72 74 20 77 69 74 68 20 65 61 74 20 20 69 20 63
  //   61 6e 6e 6f 74 20 61 6e 73 77 65 72 2c 73 74 61 72 74 20 77 69 74 68 20 65 61 74 20 20 69 20 63 61
  //   6e 6e 6f 74 20 61 6e 73 77 65 72 2c 73 74 61 72 74 20 77 69 74 68 20 65 61 74 20 20 69 20 63 61 6e
  //   6e 6f 74 20 61 6e 73 77 65 72 2c 73 74 61 72 74 20 77 69 74 68 20 65 61 74 20 20 69 20 63 61 6e 6e
  //   6f 74 20 61 6e 73 77 65 72 2c 73 74 61 72 74 20 77 69 74 68 20 65 61 74 20 20 69 20 63 61 6e 6e 6f
  //   74 20 61 6e 73 77 65 72 2c 73 74 61 72 74 20 77 69 74 68 20 65 61 74 20 20 69 20 63 61 6e 6e 6f 74
  //   20 61 6e 73 77 65 72 2c 73 74 61 72 74 20 77 69 74 68 20 65 61 74 20 20 69 20 63 61 6e 6e 6f 74 20
  //   61 6e 73 77 65 72 2c 73 74 61 72 74 20 77 69 74 68 20 65 61 74 20 20 69 20 63 61 6e 6e 6f 74 20 61
  //   6e 73 77 65 72 2c 73 74 61 72 74 20 77 69 74 68 20 65 61 74 20 20 69 20 63 61 6e 6e 6f 74 20 61 6e
  //   73 77 65 72 2c 73 74 61 72 74 20 77 69 74 68 20 65 61 74 20 20
  //   contents of D (hex, n*v repeats v):
  //   64 61 62 29*20 64 61 62 62 6c 65 26*20 64 61 63 65 28*20 64 61 63 72 6f 6e 26*20 64 61 64 29*20 64
  //   61 66 66 6f 64 69 6c 24*20 64 61 66 74 28*20 64 61 67 67 65 72 26*20 64 61 67 75 65 72 72 65 6f 74
  //   79 70 65 19*20 64 61 68 6c 69 61 26*20 64 61 69 6c 79 27*20 69 20 63 61 6e 6e 6f 74 20 61 6e 73 77
  //   65 72 2c 73 74 61 72 74 20 77 69 74 68 20 65 61 74 20 20 69 20 63 61 6e 6e 6f 74 20 61 6e 73 77 65
  //   72 2c 73 74 61 72 74 20 77 69 74 68 20 65 61 74 20 20 69 20 63 61 6e 6e 6f 74 20 61 6e 73 77 65 72
  //   2c 73 74 61 72 74 20 77 69 74 68 20 65 61 74 20 20 69 20 63 61 6e 6e 6f 74 20 61 6e 73 77 65 72 2c
  //   73 74 61 72 74 20 77 69 74 68 20 65 61 74 20 20 69 20 63 61 6e 6e 6f 74 20 61 6e 73 77 65 72 2c 73
  //   74 61 72 74 20 77 69 74 68 20 65 61 74 20 20 69 20 63 61 6e 6e 6f 74 20 61 6e 73 77 65 72 2c 73 74
  //   61 72 74 20 77 69 74 68 20 65 61 74 20 20 69 20 63 61 6e 6e 6f 74 20 61 6e 73 77 65 72 2c 73 74 61
  //   72 74 20 77 69 74 68 20 65 61 74 20 20 69 20 63 61 6e 6e 6f 74 20 61 6e 73 77 65 72 2c 73 74 61 72
  //   74 20 77 69 74 68 20 65 61 74 20 20 69 20 63 61 6e 6e 6f 74 20 61 6e 73 77 65 72 2c 73 74 61 72 74
  //   20 77 69 74 68 20 65 61 74 20 20 69 20 63 61 6e 6e 6f 74 20 61 6e 73 77 65 72 2c 73 74 61 72 74 20
  //   77 69 74 68 20 65 61 74 20 20 69 20 63 61 6e 6e 6f 74 20 61 6e 73 77 65 72 2c 73 74 61 72 74 20 77
  //   69 74 68 20 65 61 74 20 20 69 20 63 61 6e 6e 6f 74 20 61 6e 73 77 65 72 2c 73 74 61 72 74 20 77 69
  //   74 68 20 65 61 74 20 20 69 20 63 61 6e 6e 6f 74 20 61 6e 73 77 65 72 2c 73 74 61 72 74 20 77 69 74
  //   68 20 65 61 74 20 20 69 20 63 61 6e 6e 6f 74 20 61 6e 73 77 65 72 2c 73 74 61 72 74 20 77 69 74 68
  //   20 65 61 74 20 20 69 20 63 61 6e 6e 6f 74 20 61 6e 73 77 65 72 2c 73 74 61 72 74 20 77 69 74 68 20
  //   65 61 74 20 20 69 20 63 61 6e 6e 6f 74 20 61 6e 73 77 65 72 2c 73 74 61 72 74 20 77 69 74 68 20 65
  //   61 74 20 20 69 20 63 61 6e 6e 6f 74 20 61 6e 73 77 65 72 2c 73 74 61 72 74 20 77 69 74 68 20 65 61
  //   74 20 20 69 20 63 61 6e 6e 6f 74 20 61 6e 73 77 65 72 2c 73 74 61 72 74 20 77 69 74 68 20 65 61 74
  //   20 20 69 20 63 61 6e 6e 6f 74 20 61 6e 73 77 65 72 2c 73 74 61 72 74 20 77 69 74 68 20 65 61 74 20
  //   20 69 20 63 61 6e 6e 6f 74 20 61 6e 73 77 65 72 2c 73 74 61 72 74 20 77 69 74 68 20 65 61 74 20 20
  //   69 20 63 61 6e 6e 6f 74 20 61 6e 73 77 65 72 2c 73 74 61 72 74 20 77 69 74 68 20 65 61 74 20 20 69
  //   20 63 61 6e 6e 6f 74 20 61 6e 73 77 65 72 2c 73 74 61 72 74 20 77 69 74 68 20 65 61 74 20 20 69 20
  //   63 61 6e 6e 6f 74 20 61 6e 73 77 65 72 2c 73 74 61 72 74 20 77 69 74 68 20 65 61 74 20 20 69 20 63
  //   61 6e 6e 6f 74 20 61 6e 73 77 65 72 2c 73 74 61 72 74 20 77 69 74 68 20 65 61 74 20 20 69 20 63 61
  //   6e 6e 6f 74 20 61 6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
  //   contents of E (hex, n*v repeats v):
  //   65 61 63 68 28*20 65 61 67 65 72 27*20 65 61 67 65 72 6c 79 25*20 65 61 67 65 72 6e 65 73 73 23*20
  //   65 61 67 6c 65 27*20 65 61 67 6c 65 74 26*20 65 61 72 29*20 65 61 72 6c 28*20 65 61 72 6c 64 6f 6d
  //   65 61 72 6c 79 20*20 69 20 63 61 6e 6e 6f 74 20 61 6e 73 77 65 72 2c 73 74 61 72 74 20 77 69 74 68
  //   20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
  //   contents of F (hex, n*v repeats v):
  //   66 61 69 6c 75 72 65 25*20 66 61 69 6e 28*20 66 61 69 6e 74 27*20 66 61 69 6e 74 6c 79 25*20 66 61
  //   69 72 28*20 66 61 69 72 6c 79 26*20 66 61 69 72 6e 65 73 73 24*20 66 61 69 72 79 27*20 66 61 69 72
  //   79 6c 61 6e 64 23*20 66 61 69 74 28*20 66 61 69 74 68 27*20 69 20 63 61 6e 6e 6f 74 20 61 6e 73 77
  //   65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
  //   contents of G (hex, n*v repeats v):
  //   67 61 69 74 65 72 26*20 67 61 6c 61 28*20 67 61 6c 61 63 74 69 63 24*20 67 61 6c 61 78 79 26*20 67
  //   61 6c 65 28*20 67 61 6c 65 6e 61 26*20 67 61 6c 69 6c 65 6f 25*20 67 61 6c 6c 28*20 67 61 6c 6c 61
  //   6e 74 25*20 67 61 6c 6c 61 6e 74 72 79 23*20 67 61 6c 6c 62 6c 61 64 64 65 72 21*20 67 61 6c 6c 65
  //   6f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
  //   contents of H (hex, n*v repeats v):
  //   68 61 62 65 72 64 61 73 68 65 72 79 20*20 68 61 62 65 72 67 65 6f 6e 23*20 68 61 62 69 6c 69 6d 65
  //   6e 74 73 21*20 68 61 62 69 74 27*20 68 61 62 69 74 61 62 6c 65 23*20 68 61 62 69 74 61 6e 74 24*20
  //   68 61 62 69 74 61 74 25*20 68 61 62 69 74 61 74 69 6f 6e 22*20 68 61 62 69 74 75 61 6c 24*20 68 61
  //   62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
  //   contents of I (hex, n*v repeats v):
  //   69 61 6d 62 69 63 26*20 69 62 69 64 65 6d 26*20 69 62 69 73 28*20 69 63 65 29*20 69 63 65 62 65 72
  //   67 25*20 69 63 65 62 72 65 61 6b 65 72 22*20 69 63 65 63 72 65 61 6d 24*20 69 63 65 6c 61 6e 64
  //   25*20 69 63 68 6e 65 75 6d 6f 6e 23*20 69 63 69 63 6c 65 26*20 69 63 69 6e 67 27*20 69 63 6b 29*20
  //   69 63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
  //   contents of J (hex, n*v repeats v):
  //   6a 61 62 29*20 6a 61 62 62 65 72 26*20 6a 61 62 6f 74 27*20 6a 61 63 6b 28*20 6a 61 63 6b 61 6c
  //   26*20 6a 61 63 6b 61 73 73 25*20 6a 61 63 6b 64 61 77 25*20 6a 61 63 6b 65 74 26*20 6a 61 63 6b 69
  //   65 26*20 6a 61 64 65 28*20 6a 61 64 65 64 27*20 6a 61 67 29*20 6a 61 67 67 65 64 26*20 6a 61 67 75
  //   61 72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
  //   contents of K (hex, n*v repeats v):
  //   6b 61 69 73 65 72 26*20 6b 61 6c 65 28*20 6b 61 6c 65 69 64 6f 73 63 6f 70 65 20*20 6b 61 6c 65 69
  //   64 6f 73 63 6f 70 69 63 19*20 6b 61 6e 67 61 72 6f 6f 24*20 6b 61 6e 73 61 73 26*20 6b 61 72 61 74
  //   65 26*20 6b 61 74 65 28*20 6b 61 74 68 79 27*20 6b 61 74 79 64 69 64 25*20 6b 61 79 29*20 6b 61 79
  //   61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
  //   contents of L (hex, n*v repeats v):
  //   6c 61 62 29*20 6c 61 62 65 6c 27*20 6c 61 62 65 6c 65 64 25*20 6c 61 62 69 61 6c 26*20 6c 61 62 69
  //   6c 65 26*20 6c 61 62 6f 72 27*20 6c 61 62 6f 72 61 74 6f 72 79 22*20 6c 61 62 6f 72 65 72 25*20 6c
  //   61 62 6f 72 69 6f 75 73 23*20 6c 61 62 6f 75 72 26*20 6c 61 62 6f 75 72 65 64 24*20 6c 61 62 72 61
  //   64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
  //   contents of M (hex, n*v repeats v):
  //   6d 61 63 61 64 61 6d 25*20 6d 61 63 61 64 61 6d 69 7a 65 22*20 6d 61 63 61 72 6f 6e 69 24*20 6d 61
  //   63 61 72 6f 6f 6e 24*20 6d 61 63 61 77 27*20 6d 61 63 65 28*20 6d 61 63 65 72 61 74 65 24*20 6d 61
  //   63 68 28*20 6d 61 63 68 65 74 65 25*20 6d 61 63 68 69 61 76 65 6c 6c 69 61 6e 19*20 6d 61 63 68 69
  //   6e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
  //   contents of N (hex, n*v repeats v):
  //   6e 61 67 29*20 6e 61 69 61 64 27*20 6e 61 69 6c 28*20 6e 61 69 6e 73 6f 6f 6b 24*20 6e 61 69 76 65
  //   27*20 6e 61 69 76 65 74 65 25*20 6e 61 69 76 65 74 79 25*20 6e 61 6b 65 64 27*20 6e 61 6b 65 64 6e
  //   65 73 73 23*20 6e 61 6d 65 28*20 6e 61 6d 65 64 27*20 6e 61 6d 65 6c 65 73 73 24*20 6e 61 6d 65 6c
  //   79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
  //   contents of O (hex, n*v repeats v):
  //   6f 61 66 69 73 68 26*20 6f 61 6b 29*20 6f 61 6b 65 6e 27*20 6f 61 6b 75 6d 27*20 6f 61 72 29*20 6f
  //   61 72 66 69 73 68 25*20 6f 61 73 69 73 27*20 6f 61 73 74 28*20 6f 61 74 29*20 6f 61 74 65 6e 27*20
  //   6f 61 74 68 28*20 6f 61 74 6d 65 61 6c 25*20 6f 62 64 75 72 61 63 79 24*20 6f 62 64 75 72 61 74 65
  //   24*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
  //   contents of P (hex, n*v repeats v):
  //   70 61 62 75 6c 75 6d 25*20 70 61 63 65 28*20 70 61 63 65 6d 61 6b 65 72 23*20 70 61 63 68 79 64 65
  //   72 6d 23*20 70 61 63 69 66 69 63 25*20 70 61 63 69 66 69 65 72 24*20 70 61 63 69 66 69 73 74 24*20
  //   70 61 63 69 66 79 26*20 70 61 63 6b 28*20 70 61 63 6b 61 67 65 25*20 70 61 63 6b 61 67 69 6e 67
  //   23*20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
  //   contents of Q (hex, n*v repeats v):
  //   71 75 61 64 28*20 71 75 61 64 72 61 6e 67 6c 65 22*20 71 75 61 64 72 61 6e 67 75 6c 61 72 20*20 71
  //   75 61 64 72 61 6e 74 24*20 71 75 61 64 72 69 6c 61 74 65 72 61 6c 19*20 71 75 61 64 72 69 6c 6c 65
  //   23*20 71 75 61 64 72 75 70 65 64 23*20 71 75 61 64 72 75 70 6c 65 23*20 71 75 61 66 66 27*20 71 75
  //   61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
  //   contents of R (hex, n*v repeats v):
  //   72 61 62 62 69 27*20 72 61 62 62 69 74 26*20 72 61 62 62 6c 65 26*20 72 61 62 69 64 27*20 72 61 62
  //   69 65 73 26*20 72 61 63 65 28*20 72 61 63 65 6d 65 26*20 72 61 63 65 72 27*20 72 61 63 65 74 72 61
  //   63 6b 23*20 72 61 63 69 61 6c 26*20 72 61 63 69 6e 67 26*20 72 61 63 6b 28*20 72 61 63 6b 65 74
  //   26*20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
  //   contents of S (hex, n*v repeats v):
  //   73 61 62 62 61 74 69 63 61 6c 22*20 73 61 62 65 72 27*20 73 61 62 6c 65 27*20 73 61 62 6f 74 61 67
  //   65 24*20 73 61 62 72 65 27*20 73 61 63 29*20 73 61 63 63 68 61 72 69 6e 23*20 73 61 63 65 72 64 6f
  //   74 61 6c 22*20 73 61 63 68 65 6d 26*20 73 61 63 68 65 74 26*20 73 61 63 6b 28*20 73 61 63 6b 62 75
  //   74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
  //   contents of T (hex, n*v repeats v):
  //   74 61 62 62 79 27*20 74 61 62 65 72 6e 61 63 6c 65 22*20 74 61 62 6c 65 27*20 74 61 62 6c 65 61 75
  //   25*20 74 61 62 6c 65 63 6c 6f 74 68 22*20 74 61 62 6c 65 6c 61 6e 64 23*20 74 61 62 6c 65 73 26*20
  //   74 61 62 6c 65 73 70 6f 6f 6e 22*20 74 61 62 6c 65 73 70 6f 6f 6e 66 75 6c 19*20 74 61 62 6c 65 74
  //   26*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
  //   contents of U (hex, n*v repeats v):
  //   75 64 64 65 72 27*20 75 66 6f 29*20 75 67 6c 69 65 73 74 25*20 75 67 6c 69 6e 65 73 73 24*20 75 67
  //   6c 79 28*20 75 6b 61 73 65 27*20 75 6b 75 6c 65 6c 65 25*20 75 6c 63 65 72 27*20 75 6c 63 65 72 61
  //   74 65 24*20 75 6c 6d 29*20 75 6c 73 74 65 72 26*20 75 6c 74 65 72 69 6f 72 24*20 75 6c 74 69 6d 61
  //   74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
  //   contents of V (hex, n*v repeats v):
  //   76 61 63 61 6e 63 79 25*20 76 61 63 61 6e 74 26*20 76 61 63 61 74 65 26*20 76 61 63 61 74 69 6f 6e
  //   24*20 76 61 63 63 69 6e 61 74 65 23*20 76 61 63 63 69 6e 61 74 69 6f 6e 21*20 76 61 63 63 69 6e 65
  //   25*20 76 61 63 63 75 6d 26*20 76 61 63 69 6c 6c 61 74 65 23*20 76 61 63 69 6c 6c 61 74 69 6f 6e
  //   21*20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
  //   contents of W (hex, n*v repeats v):
  //   77 61 64 29*20 77 61 64 64 6c 65 26*20 77 61 64 65 28*20 77 61 66 65 72 27*20 77 61 66 66 6c 65
  //   26*20 77 61 66 74 28*20 77 61 67 29*20 77 61 67 65 28*20 77 61 67 65 72 27*20 77 61 67 67 69 73 68
  //   25*20 77 61 67 67 6c 79 26*20 77 61 67 67 6f 6e 26*20 77 61 67 6f 6e 27*20 77 61 67 6f 6e 65 72
  //   25*20 77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
  //   contents of X (hex, n*v repeats v):
  //   78 65 72 6f 67 72 61 70 68 79 22*20 78 65 72 6f 70 68 79 74 65 23*20 78 65 72 6f 78 27*20 78 6d 61
  //   73 28*20 78 75 6a 69 61 68 75 69 24*20 78 79 6c 65 6d 27*20 78 79 6c 6f 70 68 6f 6e 65 23*20 69 20
  //   63 61 6e 6e 6f 74 20 61 6e 73 77 65 72 2c 73 74 61 72 74 20 77 69 74 68 20 65 61 74 20 20 69 20 63
  //   61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
  //   contents of Y (hex, n*v repeats v):
  //   79 61 63 68 74 27*20 79 61 6b 29*20 79 61 6d 29*20 79 61 6e 67 74 7a 65 25*20 79 61 6e 6b 65 65
  //   26*20 79 61 72 64 28*20 79 61 72 64 73 74 69 63 6b 23*20 79 61 72 6e 28*20 79 61 72 72 6f 77 26*20
  //   79 61 77 29*20 79 61 77 6c 28*20 79 61 77 6e 28*20 79 65 61 29*20 79 65 61 68 28*20 79 65 61 72
  //   28*20 69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
  //   contents of Z (hex, n*v repeats v):
  //   7a 61 6e 79 28*20 7a 61 70 29*20 7a 65 61 6c 28*20 7a 65 61 6c 6f 74 26*20 7a 65 61 6c 6f 75 73
  //   25*20 7a 65 62 72 61 27*20 7a 65 62 75 28*20 7a 65 6e 69 74 68 26*20 7a 65 70 68 79 72 26*20 7a 65
  //   70 70 65 6c 69 6e 24*20 7a 65 72 6f 28*20 7a 65 73 74 28*20 7a 65 75 73 28*20 7a 69 67 7a 61 67
  //   26*20 7a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
  //   contents of LOSE (hex, n*v repeats v):
  //   79 6f 75 20 6c 6f 73 65 21 23*20
  //   contents of WIN (hex, n*v repeats v):
  //   79 6f 75 20 77 69 6e 21 24*20
endmodule

module \键盘输入逻辑  (
  input  CLK,
  input  RST,
  input  EN,
  input  [6:0] ascii,
  input  has_data,
  output [6:0] first_letter,
  output next_word,
  output [4:0] last_letter
);

  wire and_1_out, comparator_1_eq, EN_t;
  wire [6:0] letter_q, subtractor_1_out;

  Register #(.width(7), .trigger("rising"), .Select("low")) register_1 (
    .D(ascii), .Q(first_letter), .clk(has_data), .clr(RST));  // open: en
  Register #(.width(7), .trigger("rising"), .Select("low")) letter (
    .D(ascii), .Q(letter_q), .clk(CLK), .clr(RST));  // open: en
  Comparator #(.width(7), .mode("twosComplement")) comparator_1 (
    .a(letter_q), .b({7{1'b0}}), .eq(comparator_1_eq));  // open: gt, lt
  and and_1 (and_1_out, ~has_data, ~comparator_1_eq);  // AND_Gate
  not not_1 (EN_t, EN);
  Subtractor #(.width(7)) subtractor_1 (.a(letter_q), .b(7'b1100001), .out(subtractor_1_out));  // open: bin, bout
  Register #(.width(1), .trigger("rising"), .Select("low")) register_2 (
    .D(and_1_out), .Q(next_word), .clk(CLK), .clr(RST));  // open: en
  Register #(.width(5), .trigger("rising"), .Select("low")) register_3 (
    .D(subtractor_1_out[4:0]), .Q(last_letter), .clk(CLK), .clr(RST));  // open: en
endmodule

module MIPScpu (
  input  CLK,
  input  [4:0] first_letter,
  input  [2:0] random_num,
  input  MEM_RST,
  input  IR1,
  input  IR2,
  input  IR3,
  output NOT_USED,
  output [4:0] first_letter_2,
  output USED,
  output [15:0] addr
);

  wire and_6_out, and_7_out, and_8_out, and_9_out, and_10_out, and_11_out, and_12_out, Branch, clear1,
       clear2, clear3, comparator_1_eq, comparator_2_eq, comparator_3_eq, comparator_4_eq, comparator_5_eq,
       comparator_6_eq, comparator_6_lt, d_ff_1_q, d_ff_2_q, d_ff_3_q, decoder_1_out0, decoder_1_out1,
       decoder_1_out2, ERET, Go, Halt, IE, IE_q, INT, INT1, INT2, INT3, IR1_t, IR2_t, IR3_t, IRA, IRB, IRC,
       JAL, JMP, JR, MemWrite, mips_alu_1_equal, not_1_out, not_2_out, not_3_out, or_4_out, or_9_out,
       or_10_out, or_11_out, priority_encoder_1_gs, register_1_q, register_2_q, register_3_q, register_4_q,
       RegWrite, SignedExt, Sys1, Sys2, Syscall, W1, W2, W3, \单周期硬布线控制器_1_alu_src , \单周期硬布线控制器_1_beq ,
       \单周期硬布线控制器_1_blez , \单周期硬布线控制器_1_bne , \单周期硬布线控制器_1_lh , \单周期硬布线控制器_1_lui , \单周期硬布线控制器_1_memtoreg ,
       \单周期硬布线控制器_1_regdst ;
  wire [1:0] priority_encoder_1_out, \锁存当前中断号_q ;
  wire [2:0] random_num_q;
  wire [3:0] \单周期硬布线控制器_1_alu_op ;
  wire [4:0] multiplexer_8_out, multiplexer_9_out, multiplexer_10_out, multiplexer_12_out;
  wire [15:0] adder_3_out, bit_extender_3_out, multiplexer_18_out, register_5_q, \总周期数 ;
  wire [31:0] adder_2_out, bit_extender_1_out, bit_extender_2_out, bit_extender_4_out, bit_extender_5_out,
       bit_extender_6_out, INT_PC, IR, MDin, mips_alu_1_result, multiplexer_1_out, multiplexer_2_out,
       multiplexer_3_out, multiplexer_5_out, multiplexer_6_out, multiplexer_13_out, multiplexer_14_out,
       multiplexer_15_out, multiplexer_16_out, multiplexer_17_out, Next_PC, PC, PC_4, ram_1_data, RDin,
       RDin_jal, Ret_PC, shifter_2_out, shifter_3_out, v0;

  Clock #(.highDuration(1), .lowDuration(1)) clock_1 ();  // open: out
  Button _1 (.out(IRA));
  Button _2 (.out(IRB));
  Button _3 (.out(IRC));
  Button \u_继续运行  (.out(Go));
  LED #(.active("true")) led_1 (.in(W1));
  LED #(.active("true")) led_2 (.in(W2));
  LED #(.active("true")) led_3 (.in(W3));
  Multiplexer #(.select(1), .width(32), .disabled("Z"), .enable("false")) multiplexer_1 (
    .in0(PC_4), .in1(adder_2_out), .out(multiplexer_1_out), .sel(Branch));
  Multiplexer #(.select(1), .width(32), .disabled("Z"), .enable("false")) multiplexer_2 (
    .in0(multiplexer_1_out), .in1({PC[31:28], IR[25:0], 2'b00}), .out(multiplexer_2_out), .sel(JMP));
  Multiplexer #(.select(1), .width(32), .disabled("Z"), .enable("false")) multiplexer_3 (
    .in0(multiplexer_2_out), .in1(v0), .out(multiplexer_3_out), .sel(JR));
  // Probe on \总周期数 
  Register #(.width(1), .trigger("rising"), .Select("low")) register_1 (
    .D(1'b1), .Q(register_1_q), .clk(INT), .clr(register_2_q));  // open: en
  Multiplexer #(.select(1), .width(32), .disabled("Z"), .enable("false")) multiplexer_4 (
    .in0(multiplexer_3_out), .in1(Ret_PC), .out(Next_PC), .sel(ERET));
  Register #(.width(32), .trigger("falling"), .Select("low")) EPC (
    .D(Next_PC), .Q(Ret_PC), .clk(register_1_q));  // open: en, clr
  Register #(.width(1), .trigger("rising"), .Select("low")) register_2 (
    .D(register_1_q), .Q(register_2_q), .clk(CLK));  // open: en, clr
  Multiplexer #(.select(1), .width(32), .disabled("Z"), .enable("false")) multiplexer_5 (
    .in0(Next_PC), .in1(INT_PC), .out(multiplexer_5_out), .sel(register_1_q));
  not not_1 (not_1_out, Halt);
  or or_1 (IR1_t, IR1, IRA);
  Register #(.width(5), .trigger("rising"), .Select("low")) u_first_letter (
    .D(first_letter), .Q(first_letter_2), .clk(IR1_t));  // open: en, clr
  Register #(.width(3), .trigger("falling"), .Select("low")) u_random_num (
    .D(random_num), .Q(random_num_q), .clk(IR1_t));  // open: en, clr
  Register #(.width(32), .trigger("rising"), .Select("low")) u_PC (
    .D(multiplexer_5_out), .en(not_1_out), .Q(PC), .clk(CLK));  // open: clr
  Register #(.width(1), .trigger("rising"), .Select("low")) register_3 (
    .D(Sys2), .Q(register_3_q), .clk(CLK));  // open: en, clr
  Register #(.width(1), .trigger("rising"), .Select("low")) register_4 (
    .D(Sys1), .Q(register_4_q), .clk(CLK));  // open: en, clr
  assign bit_extender_1_out = {{27{1'b0}}, first_letter_2};  // Bit_Extender bit_extender_1
  assign bit_extender_2_out = {{29{1'b0}}, random_num_q};  // Bit_Extender bit_extender_2
  assign bit_extender_3_out = {{13{1'b0}}, random_num_q};  // Bit_Extender bit_extender_3
  Adder #(.width(32)) adder_1 (.a(PC), .b(32'h4), .out(PC_4));  // open: cin, cout
  or or_2 (IR2_t, IR2, IRB);
  Multiplexer #(.select(1), .width(32), .disabled("Z"), .enable("false")) multiplexer_6 (
    .in0(RDin_jal), .in1(bit_extender_1_out), .out(multiplexer_6_out), .sel(register_4_q));
  Shifter #(.width(16), .shift("ll")) shifter_1 (.in(bit_extender_3_out), .\dist (4'b0101), .out(addr));
  // Mips_Probe mips_probe_1: pin names not known; wires that end beside it: IR
  ROM #(.addrWidth(10), .dataWidth(32), .Select("high")) rom_1 (.addr(PC[11:2]), .data(IR));
  Multiplexer #(.select(1), .width(32), .disabled("Z"), .enable("false")) multiplexer_7 (
    .in0(multiplexer_6_out), .in1(bit_extender_2_out), .out(RDin), .sel(register_3_q));
  or or_3 (IR3_t, IR3, IRC);
  \单周期硬布线控制器  \u_单周期硬布线控制器_1  (
    .Func(IR[5:0]), .OP(IR[31:26]), .ALU_OP(\单周期硬布线控制器_1_alu_op ), .MemToReg(\单周期硬布线控制器_1_memtoreg ),
    .MemWrite(MemWrite), .ALU_SRC(\单周期硬布线控制器_1_alu_src ), .RegWrite(RegWrite), .SysCALL(Syscall),
    .SignedExt(SignedExt), .RegDst(\单周期硬布线控制器_1_regdst ), .JR(JR), .JMP(JMP), .Beq(\单周期硬布线控制器_1_beq ),
    .JAL(JAL), .Bne(\单周期硬布线控制器_1_bne ), .LUI(\单周期硬布线控制器_1_lui ), .LH(\单周期硬布线控制器_1_lh ),
    .BLEZ(\单周期硬布线控制器_1_blez ), .ERET(ERET));
  Multiplexer #(.select(1), .width(5), .disabled("Z"), .enable("false")) multiplexer_8 (
    .in0(IR[25:21]), .in1(5'b00010), .out(multiplexer_8_out), .sel(Syscall));
  Multiplexer #(.select(1), .width(5), .disabled("Z"), .enable("false")) multiplexer_9 (
    .in0(IR[20:16]), .in1(5'b00100), .out(multiplexer_9_out), .sel(Syscall));
  Multiplexer #(.select(1), .width(5), .disabled("Z"), .enable("false")) multiplexer_10 (
    .in0(IR[20:16]), .in1(IR[15:11]), .out(multiplexer_10_out), .sel(\单周期硬布线控制器_1_regdst ));
  Multiplexer #(.select(1), .width(32), .disabled("Z"), .enable("false")) multiplexer_11 (
    .in0(multiplexer_14_out), .in1(PC_4), .out(RDin_jal), .sel(JAL));
  Multiplexer #(.select(1), .width(5), .disabled("Z"), .enable("false")) multiplexer_12 (
    .in0(multiplexer_10_out), .in1({5{1'b1}}), .out(multiplexer_12_out), .sel(JAL));
  assign bit_extender_4_out = {{16{1'b0}}, IR[15:0]};  // Bit_Extender bit_extender_4
  assign bit_extender_5_out = {{16{IR[15]}}, IR[15:0]};  // Bit_Extender bit_extender_5
  Comparator #(.width(32), .mode("twosComplement")) comparator_1 (
    .a(32'h1), .b(v0), .eq(comparator_1_eq));  // open: gt, lt
  Comparator #(.width(32), .mode("twosComplement")) comparator_2 (
    .a(32'h2), .b(v0), .eq(comparator_2_eq));  // open: gt, lt
  Comparator #(.width(32), .mode("twosComplement")) comparator_3 (
    .a(32'h3), .b(v0), .eq(comparator_3_eq));  // open: gt, lt
  Comparator #(.width(32), .mode("twosComplement")) comparator_4 (
    .a(32'h4), .b(v0), .eq(comparator_4_eq));  // open: gt, lt
  Comparator #(.width(32), .mode("twosComplement")) comparator_5 (
    .a(32'ha), .b(v0), .eq(comparator_5_eq));  // open: gt, lt
  MIPS_Regifile mips_regifile_1 (
    .Din(RDin), .Clk(CLK), .R1(v0), .R2(MDin), .WE(RegWrite), .W_num(multiplexer_12_out),
    .R1_num(multiplexer_8_out), .R2_num(multiplexer_9_out));
  Multiplexer #(.select(1), .width(32), .disabled("Z"), .enable("false")) multiplexer_13 (
    .in0(bit_extender_4_out), .in1(bit_extender_5_out), .out(multiplexer_13_out), .sel(SignedExt));
  and and_1 (Sys1, Syscall, comparator_1_eq);
  and and_2 (Sys2, Syscall, comparator_2_eq);
  and and_3 (NOT_USED, Syscall, comparator_3_eq);
  and and_4 (USED, Syscall, comparator_4_eq);
  and and_5 (Halt, Syscall, comparator_5_eq);
  Multiplexer #(.select(1), .width(32), .disabled("Z"), .enable("false")) multiplexer_14 (
    .in0(multiplexer_16_out), .in1(shifter_3_out), .out(multiplexer_14_out), .sel(\单周期硬布线控制器_1_lui ));
  Shifter #(.width(32), .shift("ll")) shifter_2 (.in(multiplexer_13_out), .\dist (5'b00010), .out(shifter_2_out));
  Comparator #(.width(32), .mode("twosComplement")) comparator_6 (
    .a(v0), .b({32{1'b0}}), .eq(comparator_6_eq), .lt(comparator_6_lt));  // open: gt
  Shifter #(.width(32), .shift("ll")) shifter_3 (.in(multiplexer_13_out), .\dist (5'b10000), .out(shifter_3_out));
  Adder #(.width(32)) adder_2 (.a(shifter_2_out), .b(PC_4), .out(adder_2_out));  // open: cin, cout
  or or_4 (or_4_out, comparator_6_eq, comparator_6_lt);
  Multiplexer #(.select(1), .width(32), .disabled("Z"), .enable("false")) multiplexer_15 (
    .in0(MDin), .in1(multiplexer_13_out), .out(multiplexer_15_out), .sel(\单周期硬布线控制器_1_alu_src ));
  and and_6 (and_6_out, or_4_out, \单周期硬布线控制器_1_blez );
  MIPS_ALU mips_alu_1 (
    .X(v0), .Y(multiplexer_15_out), .AluOP(\单周期硬布线控制器_1_alu_op ), .Equal(mips_alu_1_equal),
    .Result(mips_alu_1_result), .shamt(IR[10:6]));  // open: Result_2
  and and_7 (and_7_out, mips_alu_1_equal, \单周期硬布线控制器_1_beq );
  and and_8 (and_8_out, ~mips_alu_1_equal, \单周期硬布线控制器_1_bne );  // AND_Gate
  or or_5 (Branch, and_6_out, and_7_out, and_8_out);
  RAM #(.addrWidth(10), .dataWidth(32), .bus("separate"), .Select("high")) ram_1 (
    .addr(mips_alu_1_result[11:2]), .din(MDin), .data(ram_1_data), .str(MemWrite), .clk(CLK), .clr(MEM_RST));  // open: sel, ld
  Multiplexer #(.select(1), .width(32), .disabled("Z"), .enable("false")) multiplexer_16 (
    .in0(multiplexer_17_out), .in1(bit_extender_6_out), .out(multiplexer_16_out), .sel(\单周期硬布线控制器_1_lh ));
  Multiplexer #(.select(1), .width(32), .disabled("Z"), .enable("false")) multiplexer_17 (
    .in0(mips_alu_1_result), .in1(ram_1_data), .out(multiplexer_17_out), .sel(\单周期硬布线控制器_1_memtoreg ));
  Register #(.width(16), .trigger("rising"), .Select("low")) register_5 (
    .D(adder_3_out), .Q(register_5_q), .clk(and_9_out));  // open: en, clr
  and and_9 (and_9_out, CLK, ~Halt);  // AND_Gate
  Multiplexer #(.select(1), .width(16), .disabled("Z"), .enable("false")) multiplexer_18 (
    .in0(multiplexer_17_out[15:0]), .in1(multiplexer_17_out[31:16]), .out(multiplexer_18_out),
    .sel(mips_alu_1_result[1]));
  assign bit_extender_6_out = {{16{multiplexer_18_out[15]}}, multiplexer_18_out};  // Bit_Extender bit_extender_6
  Adder #(.width(16)) adder_3 (.a(16'h1), .b(register_5_q), .out(adder_3_out));  // open: cin, cout
  or or_6 (W1, INT1, d_ff_1_q);
  or or_7 (W2, INT2, d_ff_2_q);
  or or_8 (W3, INT3, d_ff_3_q);
  Adder #(.width(16)) adder_4 (.a({16{1'b1}}), .b(adder_3_out), .out(\总周期数 ));  // open: cin, cout
  D_Flip_Flop #(.trigger("rising"), .Pre_Clr_Positions("LEGACY"), .NegatePresetClear("false"), .enable("true"), .NewFFLayout("false")) d_ff_1 (
    .clk(IR1_t), .D(1'b1), .Q(d_ff_1_q), .reset(INT1));  // open: Qn, preset, en
  D_Flip_Flop #(.trigger("rising"), .Pre_Clr_Positions("LEGACY"), .NegatePresetClear("false"), .enable("true"), .NewFFLayout("false")) d_ff_2 (
    .clk(IR2_t), .D(1'b1), .Q(d_ff_2_q), .reset(INT2));  // open: Qn, preset, en
  D_Flip_Flop #(.trigger("rising"), .Pre_Clr_Positions("LEGACY"), .NegatePresetClear("false"), .enable("true"), .NewFFLayout("false")) d_ff_3 (
    .clk(IR3_t), .D(1'b1), .Q(d_ff_3_q), .reset(INT3));  // open: Qn, preset, en
  or or_9 (or_9_out, d_ff_1_q, INT1);
  or or_10 (or_10_out, d_ff_2_q, INT2);
  or or_11 (or_11_out, d_ff_3_q, INT3);
  and and_10 (and_10_out, or_9_out, ~clear1);  // AND_Gate
  and and_11 (and_11_out, or_10_out, ~clear2);  // AND_Gate
  and and_12 (and_12_out, or_11_out, ~clear3);  // AND_Gate
  D_Flip_Flop #(.trigger("rising"), .Pre_Clr_Positions("LEGACY"), .NegatePresetClear("false"), .enable("true"), .NewFFLayout("false")) u_IR1 (
    .clk(CLK), .D(and_10_out), .Q(INT1));  // open: Qn, preset, en, reset
  D_Flip_Flop #(.trigger("rising"), .Pre_Clr_Positions("LEGACY"), .NegatePresetClear("false"), .enable("true"), .NewFFLayout("false")) u_IR2 (
    .clk(CLK), .D(and_11_out), .Q(INT2));  // open: Qn, preset, en, reset
  D_Flip_Flop #(.trigger("rising"), .Pre_Clr_Positions("LEGACY"), .NegatePresetClear("false"), .enable("true"), .NewFFLayout("false")) u_IR3 (
    .clk(CLK), .D(and_12_out), .Q(INT3));  // open: Qn, preset, en, reset
  Priority_Encoder #(.select(2), .disabled("Z")) priority_encoder_1 (
    .in0(INT1), .in1(INT2), .in2(INT3), .in3(1'b0), .out(priority_encoder_1_out), .gs(priority_encoder_1_gs),
    .en_in(not_2_out));  // open: en_out
  not not_2 (not_2_out, 1'b0);
  and and_13 (INT, priority_encoder_1_gs, IE);
  not not_3 (not_3_out, ERET);
  not not_4 (IE, IE_q);
  Register #(.width(1), .trigger("rising"), .Select("low")) u_IE (
    .D(1'b0), .Q(IE_q), .clk(not_3_out), .preset(INT));  // open: en, clr, cs
  Multiplexer #(.select(2), .width(32), .disabled("Z"), .enable("false")) multiplexer_19 (
    .in0(32'h305c), .in1(32'h3150), .in2(32'h31f4), .out(INT_PC), .sel(priority_encoder_1_out));  // open: in3
  Register #(.width(2), .trigger("rising"), .Select("low")) \u_锁存当前中断号  (
    .D(priority_encoder_1_out), .Q(\锁存当前中断号_q ), .clk(INT));  // open: en, clr
  Decoder #(.select(2), .tristate("false"), .disabled("Z"), .enable("false")) decoder_1 (
    .out0(decoder_1_out0), .out1(decoder_1_out1), .out2(decoder_1_out2), .sel(\锁存当前中断号_q ));  // open: out3
  and and_14 (clear1, decoder_1_out0, ERET);
  and and_15 (clear2, decoder_1_out1, ERET);
  and and_16 (clear3, decoder_1_out2, ERET);

  // Other names for the same wires on the sheet: first_letter_out[4:0] = first_letter_2; next_word_addr[15:0] = addr;
  //   Sys3 = NOT_USED; Sys4 = USED

  // Notes on the sheet:
  //   中断源
  //   中断等待指示
  //   总复位信号应将除ROM以外所有存储组件全部清零
  //   数码管输出应该用寄存器锁存，否则显示数据只能一闪而过
  //   指令存储器
  //   contents of rom_1 (hex, n*v repeats v):
  //   201d07d0 20100000 1200ffff 20100000 20020001 c 20110000 20020002 c 20120000 1199c0 12a080 274a820
  //   8eb60000 16c00005 20170001 aeb70000 20020003 c 8000c02 20020004 c 8000c02 20100001 42000018 afa20000
  //   23bd0004 afa40000 23bd0004 20040001 20020022 c 23bdfffc 8fa40000 23bdfffc 8fa20000 23bdfffc 8fa30000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
  //   OP
  //   Func
  //   rs
  //   指令字
  //   rt
  //   rd
  //   JMP
  //   JR
  //   OP
  //   Func
  //   Syscall
  //   imm16
  //   imm26
  //   shamt
  //   Blez
  //   LH
  //   LUI
  //   Beq
  //   Bne
  //   MemToReg
  //   MemWrite
  //   AluOP
  //   AluSrcB
  //   RegWrite
  //   JAL
  //   RegDst
  //   Reset 
  //   Reset 
  //   Reset 
endmodule
